// Logisim project basicgates.circ as structural Verilog: 66 circuits, main circuit main
module main (
);

  wire [63:0] multiplier_1_cout, multiplier_1_out;

  // Probe on multiplier_1_out
  Multiplier #(.width(64)) multiplier_1 (
    .a(64'hfffffffff), .b(64'hffffffffffffffee), .out(multiplier_1_out), .cin(64'h1234),
    .cout(multiplier_1_cout));
  // Probe on multiplier_1_cout
  // Probe on nothing
  // Probe on nothing
endmodule

module adder1bit (
  input  inflow,
  input  input1,
  input  input2,
  output overflow,
  output output1
);

  wire and_1_out, and_2_out, xor_1_out;

  and and_1 (and_1_out, input1, input2);
  xor xor_1 (xor_1_out, input1, input2);
  and and_2 (and_2_out, inflow, xor_1_out);
  xor xor_2 (output1, inflow, xor_1_out);
  or or_1 (overflow, and_1_out, and_2_out);
endmodule

module adder2bit (
  input  inflow,
  input  [1:0] input1,
  input  [1:0] input2,
  output overflow,
  output [1:0] output1
);

  wire adder1bit_1_overflow;

  adder1bit adder1bit_1 (
    .inflow(inflow), .input1(input1[0]), .input2(input2[0]), .overflow(adder1bit_1_overflow),
    .output1(output1[0]));
  adder1bit adder1bit_2 (
    .inflow(adder1bit_1_overflow), .input1(input1[1]), .input2(input2[1]), .overflow(overflow),
    .output1(output1[1]));
endmodule

module adder4bit (
  input  inflow,
  input  [3:0] input1,
  input  [3:0] input2,
  output overflow,
  output [3:0] output1
);

  wire adder2bit_1_overflow;

  adder2bit adder2bit_1 (
    .inflow(inflow), .input1(input1[1:0]), .input2(input2[1:0]), .overflow(adder2bit_1_overflow),
    .output1(output1[1:0]));
  adder2bit adder2bit_2 (
    .inflow(adder2bit_1_overflow), .input1(input1[3:2]), .input2(input2[3:2]), .overflow(overflow),
    .output1(output1[3:2]));
endmodule

module adder8bit (
  input  inflow,
  input  [7:0] input1,
  input  [7:0] input2,
  output overflow,
  output [7:0] output1
);

  wire adder4bit_1_overflow;

  adder4bit adder4bit_1 (
    .inflow(inflow), .input1(input1[3:0]), .input2(input2[3:0]), .overflow(adder4bit_1_overflow),
    .output1(output1[3:0]));
  adder4bit adder4bit_2 (
    .inflow(adder4bit_1_overflow), .input1(input1[7:4]), .input2(input2[7:4]), .overflow(overflow),
    .output1(output1[7:4]));
endmodule

module adder16bit (
  input  inflow,
  input  [15:0] input1,
  input  [15:0] input2,
  output overflow,
  output [15:0] output1
);

  wire adder8bit_1_overflow;

  adder8bit adder8bit_1 (
    .inflow(inflow), .input1(input1[7:0]), .input2(input2[7:0]), .overflow(adder8bit_1_overflow),
    .output1(output1[7:0]));
  adder8bit adder8bit_2 (
    .inflow(adder8bit_1_overflow), .input1(input1[15:8]), .input2(input2[15:8]), .overflow(overflow),
    .output1(output1[15:8]));
endmodule

module adder32bit (
  input  inflow,
  input  [31:0] input1,
  input  [31:0] input2,
  output overflow,
  output [31:0] output1
);

  wire adder16bit_1_overflow;

  adder16bit adder16bit_1 (
    .inflow(inflow), .input1(input1[15:0]), .input2(input2[15:0]), .overflow(adder16bit_1_overflow),
    .output1(output1[15:0]));
  adder16bit adder16bit_2 (
    .inflow(adder16bit_1_overflow), .input1(input1[31:16]), .input2(input2[31:16]), .overflow(overflow),
    .output1(output1[31:16]));
endmodule

module adder64bit (
  input  inflow,
  input  [63:0] input1,
  input  [63:0] input2,
  output overflow,
  output [63:0] output1
);

  wire adder32bit_1_overflow;

  adder32bit adder32bit_1 (
    .inflow(inflow), .input1(input1[31:0]), .input2(input2[31:0]), .overflow(adder32bit_1_overflow),
    .output1(output1[31:0]));
  adder32bit adder32bit_2 (
    .inflow(adder32bit_1_overflow), .input1(input1[63:32]), .input2(input2[63:32]), .overflow(overflow),
    .output1(output1[63:32]));
endmodule

module negate1bit (
  input  input1,
  output output1
);


  assign output1 = input1;
endmodule

module negate2bit (
  input  [1:0] input1,
  output [1:0] output1
);

  wire [1:0] not_1_out;

  assign not_1_out = ~input1;  // NOT_Gate not_1, 2 bits wide
  adder2bit adder2bit_1 (.input1(2'b01), .input2(not_1_out), .output1(output1));  // open: inflow, overflow
endmodule

module negate4bit (
  input  [3:0] input1,
  output [3:0] output1
);

  wire [3:0] not_1_out;

  assign not_1_out = ~input1;  // NOT_Gate not_1, 4 bits wide
  adder4bit adder4bit_1 (.input1(4'b0001), .input2(not_1_out), .output1(output1));  // open: inflow, overflow
endmodule

module negate8bit (
  input  [7:0] input1,
  output [7:0] output1
);

  wire [7:0] not_1_out;

  assign not_1_out = ~input1;  // NOT_Gate not_1, 8 bits wide
  adder8bit adder8bit_1 (.input1(8'h1), .input2(not_1_out), .output1(output1));  // open: inflow, overflow
endmodule

module negate16bit (
  input  [15:0] input1,
  output [15:0] output1
);

  wire [15:0] not_1_out;

  assign not_1_out = ~input1;  // NOT_Gate not_1, 16 bits wide
  adder16bit adder16bit_1 (.input1(16'h1), .input2(not_1_out), .output1(output1));  // open: inflow, overflow
endmodule

module negate32bit (
  input  [31:0] input1,
  output [31:0] output1
);

  wire [31:0] not_1_out;

  assign not_1_out = ~input1;  // NOT_Gate not_1, 32 bits wide
  adder32bit adder32bit_1 (.input1(32'h1), .input2(not_1_out), .output1(output1));  // open: inflow, overflow
endmodule

module negate64bit (
  input  [63:0] input1,
  output [63:0] output1
);

  wire [63:0] not_1_out;

  assign not_1_out = ~input1;  // NOT_Gate not_1, 64 bits wide
  adder64bit adder64bit_1 (.input1(64'h1), .input2(not_1_out), .output1(output1));  // open: inflow, overflow
endmodule

module subtractor1bit (
  input  inborrow,
  input  input1,
  input  input2,
  output borrow,
  output output1
);

  wire and_1_out, and_2_out, not_1_out, not_2_out, xor_1_out;

  not not_1 (not_1_out, input1);
  xor xor_1 (xor_1_out, input1, input2);
  and and_1 (and_1_out, not_1_out, input2);
  and and_2 (and_2_out, inborrow, not_2_out);
  not not_2 (not_2_out, xor_1_out);
  xor xor_2 (output1, inborrow, xor_1_out);
  or or_1 (borrow, and_1_out, and_2_out);
endmodule

module subtractor2bit (
  input  inborrow,
  input  [1:0] input1,
  input  [1:0] input2,
  output borrow,
  output [1:0] output1
);

  wire subtractor1bit_1_borrow;

  subtractor1bit subtractor1bit_1 (
    .inborrow(inborrow), .input1(input1[0]), .input2(input2[0]), .borrow(subtractor1bit_1_borrow),
    .output1(output1[0]));
  subtractor1bit subtractor1bit_2 (
    .inborrow(subtractor1bit_1_borrow), .input1(input1[1]), .input2(input2[1]), .borrow(borrow),
    .output1(output1[1]));
endmodule

module subtractor4bit (
  input  inborrow,
  input  [3:0] input1,
  input  [3:0] input2,
  output borrow,
  output [3:0] output1
);

  wire subtractor2bit_1_borrow;

  subtractor2bit subtractor2bit_1 (
    .inborrow(inborrow), .input1(input1[1:0]), .input2(input2[1:0]), .borrow(subtractor2bit_1_borrow),
    .output1(output1[1:0]));
  subtractor2bit subtractor2bit_2 (
    .inborrow(subtractor2bit_1_borrow), .input1(input1[3:2]), .input2(input2[3:2]), .borrow(borrow),
    .output1(output1[3:2]));
endmodule

module subtractor8bit (
  input  inborrow,
  input  [7:0] input1,
  input  [7:0] input2,
  output borrow,
  output [7:0] output1
);

  wire subtractor4bit_1_borrow;

  subtractor4bit subtractor4bit_1 (
    .inborrow(inborrow), .input1(input1[3:0]), .input2(input2[3:0]), .borrow(subtractor4bit_1_borrow),
    .output1(output1[3:0]));
  subtractor4bit subtractor4bit_2 (
    .inborrow(subtractor4bit_1_borrow), .input1(input1[7:4]), .input2(input2[7:4]), .borrow(borrow),
    .output1(output1[7:4]));
endmodule

module subtractor16bit (
  input  inborrow,
  input  [15:0] input1,
  input  [15:0] input2,
  output borrow,
  output [15:0] output1
);

  wire subtractor8bit_1_borrow;

  subtractor8bit subtractor8bit_1 (
    .inborrow(inborrow), .input1(input1[7:0]), .input2(input2[7:0]), .borrow(subtractor8bit_1_borrow),
    .output1(output1[7:0]));
  subtractor8bit subtractor8bit_2 (
    .inborrow(subtractor8bit_1_borrow), .input1(input1[15:8]), .input2(input2[15:8]), .borrow(borrow),
    .output1(output1[15:8]));
endmodule

module subtractor32bit (
  input  inborrow,
  input  [31:0] input1,
  input  [31:0] input2,
  output borrow,
  output [31:0] output1
);

  wire subtractor16bit_1_borrow;

  subtractor16bit subtractor16bit_1 (
    .inborrow(inborrow), .input1(input1[15:0]), .input2(input2[15:0]), .borrow(subtractor16bit_1_borrow),
    .output1(output1[15:0]));
  subtractor16bit subtractor16bit_2 (
    .inborrow(subtractor16bit_1_borrow), .input1(input1[31:16]), .input2(input2[31:16]), .borrow(borrow),
    .output1(output1[31:16]));
endmodule

module subtractor64bit (
  input  inborrow,
  input  [63:0] input1,
  input  [63:0] input2,
  output borrow,
  output [63:0] output1
);

  wire subtractor32bit_1_borrow;

  subtractor32bit subtractor32bit_1 (
    .inborrow(inborrow), .input1(input1[31:0]), .input2(input2[31:0]), .borrow(subtractor32bit_1_borrow),
    .output1(output1[31:0]));
  subtractor32bit subtractor32bit_2 (
    .inborrow(subtractor32bit_1_borrow), .input1(input1[63:32]), .input2(input2[63:32]), .borrow(borrow),
    .output1(output1[63:32]));
endmodule

module adder128bit (
  input  inflow,
  input  [63:0] input1a,
  input  [63:0] input1b,
  input  [63:0] input2a,
  input  [63:0] input2b,
  output overflow,
  output [63:0] output1a,
  output [63:0] output1b
);

  wire adder64bit_1_overflow;

  adder64bit adder64bit_1 (
    .inflow(inflow), .input1(input1a), .input2(input2a), .overflow(adder64bit_1_overflow), .output1(output1a));
  adder64bit adder64bit_2 (
    .inflow(adder64bit_1_overflow), .input1(input1b), .input2(input2b), .overflow(overflow),
    .output1(output1b));
endmodule

module negate128bit (
  input  [63:0] input1a,
  input  [63:0] input1b,
  output [63:0] output1a,
  output [63:0] output1b
);

  wire [63:0] not_1_out, not_2_out;

  assign not_1_out = ~input1a;  // NOT_Gate not_1, 64 bits wide
  assign not_2_out = ~input1b;  // NOT_Gate not_2, 64 bits wide
  adder128bit adder128bit_1 (
    .input1a(64'h1), .input2a(not_1_out), .input2b(not_2_out), .output1a(output1a), .output1b(output1b));  // open: inflow, input1b, overflow
endmodule

module subtractor128bit (
  input  inborrow,
  input  [63:0] input1a,
  input  [63:0] input1b,
  input  [63:0] input2a,
  input  [63:0] input2b,
  output borrow,
  output [63:0] output1a,
  output [63:0] output1b
);

  wire subtractor64bit_1_borrow;

  subtractor64bit subtractor64bit_1 (
    .inborrow(inborrow), .input1(input1a), .input2(input2a), .borrow(subtractor64bit_1_borrow),
    .output1(output1a));
  subtractor64bit subtractor64bit_2 (
    .inborrow(subtractor64bit_1_borrow), .input1(input1b), .input2(input2b), .borrow(borrow),
    .output1(output1b));
endmodule

module cbuffer1bit (
  input  buffer1,
  input  input1,
  output output1
);

  and and_1 (output1, buffer1, input1);
endmodule

module cbuffer2bit (
  input  buffer1,
  input  [1:0] input1,
  output [1:0] output1
);

  assign output1 = {2{buffer1}} & input1;  // AND_Gate and_1, 2 bits wide
endmodule

module cbuffer4bit (
  input  buffer1,
  input  [3:0] input1,
  output [3:0] output1
);

  assign output1 = {4{buffer1}} & input1;  // AND_Gate and_1, 4 bits wide
endmodule

module cbuffer8bit (
  input  buffer1,
  input  [7:0] input1,
  output [7:0] output1
);

  assign output1 = {8{buffer1}} & input1;  // AND_Gate and_1, 8 bits wide
endmodule

module cbuffer16bit (
  input  buffer1,
  input  [15:0] input1,
  output [15:0] output1
);

  assign output1 = {16{buffer1}} & input1;  // AND_Gate and_1, 16 bits wide
endmodule

module cbuffer32bit (
  input  buffer1,
  input  [31:0] input1,
  output [31:0] output1
);

  assign output1 = {32{buffer1}} & input1;  // AND_Gate and_1, 32 bits wide
endmodule

module cbuffer64bit (
  input  buffer1,
  input  [63:0] input1,
  output [63:0] output1
);

  assign output1 = {64{buffer1}} & input1;  // AND_Gate and_1, 64 bits wide
endmodule

module cbuffer128bit (
  input  buffer1,
  input  [63:0] input1a,
  input  [63:0] input1b,
  output [63:0] output1a,
  output [63:0] output1b
);

  assign output1a = {64{buffer1}} & input1a;  // AND_Gate and_1, 64 bits wide
  assign output1b = {64{buffer1}} & input1b;  // AND_Gate and_2, 64 bits wide
endmodule

module multiplier1bit (
  input  inflow,
  input  input1,
  input  input2,
  output overflow,
  output output1
);

  wire and_1_out;

  and and_1 (and_1_out, input1, input2);
  xor xor_1 (output1, inflow, and_1_out);
  and and_2 (overflow, inflow, and_1_out);
endmodule

module multiplier2bit (
  input  [1:0] inflow,
  input  [1:0] input1,
  input  [1:0] input2,
  output [1:0] overflow,
  output [1:0] output1
);

  wire [3:0] adder4bit_2_output1, cbuffer4bit_1_output1, cbuffer4bit_2_output1;

  adder4bit adder4bit_1 (
    .input1({2'b00, inflow}), .input2(adder4bit_2_output1), .output1({overflow, output1}));  // open: inflow, overflow
  cbuffer4bit cbuffer4bit_1 (.buffer1(input1[0]), .input1({2'b00, input2}), .output1(cbuffer4bit_1_output1));
  adder4bit adder4bit_2 (
    .input1(cbuffer4bit_1_output1), .input2(cbuffer4bit_2_output1), .output1(adder4bit_2_output1));  // open: inflow, overflow
  cbuffer4bit cbuffer4bit_2 (.buffer1(input1[1]), .input1({1'b0, input2, 1'b0}), .output1(cbuffer4bit_2_output1));
endmodule

module multiplier4bit (
  input  [3:0] inflow,
  input  [3:0] input1,
  input  [3:0] input2,
  output [3:0] overflow,
  output [3:0] output1
);

  wire [1:0] multiplier2bit_1_output1, multiplier2bit_1_overflow;
  wire [5:2] multiplier2bit_2_output1, multiplier2bit_3_output1;
  wire [7:0] adder8bit_1_output1, adder8bit_3_output1, adder8bit_4_output1;
  wire [7:4] multiplier2bit_4_output1;

  adder8bit adder8bit_1 (
    .input1({4'b0000, multiplier2bit_1_overflow, multiplier2bit_1_output1}),
    .input2({2'b00, multiplier2bit_2_output1, 2'b00}), .output1(adder8bit_1_output1));  // open: inflow, overflow
  multiplier2bit multiplier2bit_1 (
    .input1(input1[1:0]), .input2(input2[1:0]), .overflow(multiplier2bit_1_overflow),
    .output1(multiplier2bit_1_output1));  // open: inflow
  adder8bit adder8bit_2 (
    .input1({4'b0000, inflow}), .input2(adder8bit_3_output1), .output1({overflow, output1}));  // open: inflow, overflow
  adder8bit adder8bit_3 (
    .input1(adder8bit_1_output1), .input2(adder8bit_4_output1), .output1(adder8bit_3_output1));  // open: inflow, overflow
  adder8bit adder8bit_4 (
    .input1({2'b00, multiplier2bit_3_output1, 2'b00}), .input2({multiplier2bit_4_output1, 4'b0000}),
    .output1(adder8bit_4_output1));  // open: inflow, overflow
  multiplier2bit multiplier2bit_2 (
    .input1(input1[1:0]), .input2(input2[3:2]), .overflow(multiplier2bit_2_output1[5:4]),
    .output1(multiplier2bit_2_output1[3:2]));  // open: inflow
  multiplier2bit multiplier2bit_3 (
    .input1(input1[3:2]), .input2(input2[1:0]), .overflow(multiplier2bit_3_output1[5:4]),
    .output1(multiplier2bit_3_output1[3:2]));  // open: inflow
  multiplier2bit multiplier2bit_4 (
    .input1(input1[3:2]), .input2(input2[3:2]), .overflow(multiplier2bit_4_output1[7:6]),
    .output1(multiplier2bit_4_output1[5:4]));  // open: inflow
endmodule

module multiplier8bit (
  input  [7:0] inflow,
  input  [7:0] input1,
  input  [7:0] input2,
  output [7:0] overflow,
  output [7:0] output1
);

  wire [3:0] multiplier4bit_1_output1, multiplier4bit_1_overflow;
  wire [11:4] multiplier4bit_2_output1, multiplier4bit_3_output1;
  wire [15:0] adder16bit_1_output1, adder16bit_3_output1, adder16bit_4_output1;
  wire [15:8] multiplier4bit_4_output1;

  adder16bit adder16bit_1 (
    .input1({{8{1'b0}}, multiplier4bit_1_overflow, multiplier4bit_1_output1}),
    .input2({4'b0000, multiplier4bit_2_output1, 4'b0000}), .output1(adder16bit_1_output1));  // open: inflow, overflow
  multiplier4bit multiplier4bit_1 (
    .input1(input1[3:0]), .input2(input2[3:0]), .overflow(multiplier4bit_1_overflow),
    .output1(multiplier4bit_1_output1));  // open: inflow
  adder16bit adder16bit_2 (
    .input1({{8{1'b0}}, inflow}), .input2(adder16bit_3_output1), .output1({overflow, output1}));  // open: inflow, overflow
  adder16bit adder16bit_3 (
    .input1(adder16bit_1_output1), .input2(adder16bit_4_output1), .output1(adder16bit_3_output1));  // open: inflow, overflow
  adder16bit adder16bit_4 (
    .input1({4'b0000, multiplier4bit_3_output1, 4'b0000}), .input2({multiplier4bit_4_output1, {8{1'b0}}}),
    .output1(adder16bit_4_output1));  // open: inflow, overflow
  multiplier4bit multiplier4bit_2 (
    .input1(input1[3:0]), .input2(input2[7:4]), .overflow(multiplier4bit_2_output1[11:8]),
    .output1(multiplier4bit_2_output1[7:4]));  // open: inflow
  multiplier4bit multiplier4bit_3 (
    .input1(input1[7:4]), .input2(input2[3:0]), .overflow(multiplier4bit_3_output1[11:8]),
    .output1(multiplier4bit_3_output1[7:4]));  // open: inflow
  multiplier4bit multiplier4bit_4 (
    .input1(input1[7:4]), .input2(input2[7:4]), .overflow(multiplier4bit_4_output1[15:12]),
    .output1(multiplier4bit_4_output1[11:8]));  // open: inflow
endmodule

module multiplier16bit (
  input  [15:0] inflow,
  input  [15:0] input1,
  input  [15:0] input2,
  output [15:0] overflow,
  output [15:0] output1
);

  wire [7:0] multiplier8bit_1_output1, multiplier8bit_1_overflow;
  wire [23:8] multiplier8bit_2_output1, multiplier8bit_3_output1;
  wire [31:0] adder32bit_1_output1, adder32bit_3_output1, adder32bit_4_output1;
  wire [31:16] multiplier8bit_4_output1;

  adder32bit adder32bit_1 (
    .input1({{16{1'b0}}, multiplier8bit_1_overflow, multiplier8bit_1_output1}),
    .input2({{8{1'b0}}, multiplier8bit_2_output1, {8{1'b0}}}), .output1(adder32bit_1_output1));  // open: inflow, overflow
  multiplier8bit multiplier8bit_1 (
    .input1(input1[7:0]), .input2(input2[7:0]), .overflow(multiplier8bit_1_overflow),
    .output1(multiplier8bit_1_output1));  // open: inflow
  adder32bit adder32bit_2 (
    .input1({{16{1'b0}}, inflow}), .input2(adder32bit_3_output1), .output1({overflow, output1}));  // open: inflow, overflow
  adder32bit adder32bit_3 (
    .input1(adder32bit_1_output1), .input2(adder32bit_4_output1), .output1(adder32bit_3_output1));  // open: inflow, overflow
  adder32bit adder32bit_4 (
    .input1({{8{1'b0}}, multiplier8bit_3_output1, {8{1'b0}}}),
    .input2({multiplier8bit_4_output1, {16{1'b0}}}), .output1(adder32bit_4_output1));  // open: inflow, overflow
  multiplier8bit multiplier8bit_2 (
    .input1(input1[7:0]), .input2(input2[15:8]), .overflow(multiplier8bit_2_output1[23:16]),
    .output1(multiplier8bit_2_output1[15:8]));  // open: inflow
  multiplier8bit multiplier8bit_3 (
    .input1(input1[15:8]), .input2(input2[7:0]), .overflow(multiplier8bit_3_output1[23:16]),
    .output1(multiplier8bit_3_output1[15:8]));  // open: inflow
  multiplier8bit multiplier8bit_4 (
    .input1(input1[15:8]), .input2(input2[15:8]), .overflow(multiplier8bit_4_output1[31:24]),
    .output1(multiplier8bit_4_output1[23:16]));  // open: inflow
endmodule

module multiplier32bit (
  input  [31:0] inflow,
  input  [31:0] input1,
  input  [31:0] input2,
  output [31:0] overflow,
  output [31:0] output1
);

  wire [15:0] multiplier16bit_1_output1, multiplier16bit_1_overflow;
  wire [47:16] multiplier16bit_2_output1, multiplier16bit_3_output1;
  wire [63:0] adder64bit_1_output1, adder64bit_3_output1, adder64bit_4_output1;
  wire [63:32] multiplier16bit_4_output1;

  adder64bit adder64bit_1 (
    .input1({{32{1'b0}}, multiplier16bit_1_overflow, multiplier16bit_1_output1}),
    .input2({{16{1'b0}}, multiplier16bit_2_output1, {16{1'b0}}}), .output1(adder64bit_1_output1));  // open: inflow, overflow
  multiplier16bit multiplier16bit_1 (
    .input1(input1[15:0]), .input2(input2[15:0]), .overflow(multiplier16bit_1_overflow),
    .output1(multiplier16bit_1_output1));  // open: inflow
  adder64bit adder64bit_2 (
    .input1({{32{1'b0}}, inflow}), .input2(adder64bit_3_output1), .output1({overflow, output1}));  // open: inflow, overflow
  adder64bit adder64bit_3 (
    .input1(adder64bit_1_output1), .input2(adder64bit_4_output1), .output1(adder64bit_3_output1));  // open: inflow, overflow
  adder64bit adder64bit_4 (
    .input1({{16{1'b0}}, multiplier16bit_3_output1, {16{1'b0}}}),
    .input2({multiplier16bit_4_output1, {32{1'b0}}}), .output1(adder64bit_4_output1));  // open: inflow, overflow
  multiplier16bit multiplier16bit_2 (
    .input1(input1[15:0]), .input2(input2[31:16]), .overflow(multiplier16bit_2_output1[47:32]),
    .output1(multiplier16bit_2_output1[31:16]));  // open: inflow
  multiplier16bit multiplier16bit_3 (
    .input1(input1[31:16]), .input2(input2[15:0]), .overflow(multiplier16bit_3_output1[47:32]),
    .output1(multiplier16bit_3_output1[31:16]));  // open: inflow
  multiplier16bit multiplier16bit_4 (
    .input1(input1[31:16]), .input2(input2[31:16]), .overflow(multiplier16bit_4_output1[63:48]),
    .output1(multiplier16bit_4_output1[47:32]));  // open: inflow
endmodule

module multiplier64bit (
  input  [63:0] inflow,
  input  [63:0] input1,
  input  [63:0] input2,
  output [63:0] overflow,
  output [63:0] output1
);

  wire [31:0] multiplier32bit_2_overflow, multiplier32bit_3_overflow;
  wire [63:0] adder128bit_1_output1a, adder128bit_1_output1b, adder128bit_3_output1a, adder128bit_3_output1b,
       adder128bit_4_output1a, adder128bit_4_output1b, multiplier32bit_1_output1, multiplier32bit_4_output1;
  wire [63:32] multiplier32bit_2_output1, multiplier32bit_3_output1;

  adder128bit adder128bit_1 (
    .input1a(multiplier32bit_1_output1), .input1b({64{1'b0}}),
    .input2a({multiplier32bit_2_output1, {32{1'b0}}}), .input2b({{32{1'b0}}, multiplier32bit_2_overflow}),
    .output1a(adder128bit_1_output1a), .output1b(adder128bit_1_output1b));  // open: inflow, overflow
  multiplier32bit multiplier32bit_1 (
    .input1(input1[31:0]), .input2(input2[31:0]), .overflow(multiplier32bit_1_output1[63:32]),
    .output1(multiplier32bit_1_output1[31:0]));  // open: inflow
  adder128bit adder128bit_2 (
    .input1a(inflow), .input2a(adder128bit_3_output1a), .input2b(adder128bit_3_output1b), .output1a(output1),
    .output1b(overflow));  // open: inflow, input1b, overflow
  adder128bit adder128bit_3 (
    .input1a(adder128bit_1_output1a), .input1b(adder128bit_1_output1b), .input2a(adder128bit_4_output1a),
    .input2b(adder128bit_4_output1b), .output1a(adder128bit_3_output1a), .output1b(adder128bit_3_output1b));  // open: inflow, overflow
  multiplier32bit multiplier32bit_2 (
    .input1(input1[31:0]), .input2(input2[63:32]), .overflow(multiplier32bit_2_overflow),
    .output1(multiplier32bit_2_output1));  // open: inflow
  adder128bit adder128bit_4 (
    .input1a({multiplier32bit_3_output1, {32{1'b0}}}), .input1b({{32{1'b0}}, multiplier32bit_3_overflow}),
    .input2a({64{1'b0}}), .input2b(multiplier32bit_4_output1), .output1a(adder128bit_4_output1a),
    .output1b(adder128bit_4_output1b));  // open: inflow, overflow
  multiplier32bit multiplier32bit_3 (
    .input1(input1[63:32]), .input2(input2[31:0]), .overflow(multiplier32bit_3_overflow),
    .output1(multiplier32bit_3_output1));  // open: inflow
  multiplier32bit multiplier32bit_4 (
    .input1(input1[63:32]), .input2(input2[63:32]), .overflow(multiplier32bit_4_output1[63:32]),
    .output1(multiplier32bit_4_output1[31:0]));  // open: inflow
endmodule

module divider1bit (
  input  inupper,
  input  input1,
  input  input2,
  output remainder,
  output output1
);


  assign output1 = input1;
  assign remainder = 1'b0;
endmodule

module divideru2bit (
  input  [1:0] inupper,
  input  [1:0] input1,
  input  [1:0] input2,
  output [1:0] remainder,
  output [1:0] output1
);

  wire comparatoru2bit_1_equal1, comparatoru8bit_1_equal1, comparatoru8bit_1_greater1,
       comparatoru8bit_2_equal1, comparatoru8bit_2_greater1, comparatoru8bit_3_equal1,
       comparatoru8bit_3_greater1, comparatoru8bit_4_equal1, comparatoru8bit_4_greater1, not_1_out, or_1_out,
       or_2_out, or_3_out, or_4_out;
  wire [3:2] and_2_out;
  wire [7:0] cbuffer8bit_1_output1, cbuffer8bit_2_output1, cbuffer8bit_3_output1, cbuffer8bit_4_output1,
       subtractor8bit_1_output1, subtractor8bit_2_output1, subtractor8bit_3_output1;
  wire [7:2] subtractor8bit_4_output1;

  // Probe on inupper
  // Probe on inupper
  // Probe on input1
  // Probe on input1
  not not_1 (not_1_out, comparatoru2bit_1_equal1);
  comparatoru2bit comparatoru2bit_1 (
    .input1(input2), .input2(2'b00), .equal1(comparatoru2bit_1_equal1));  // open: greater1, less1
  // Probe on input2
  // Probe on input2
  // Probe on {4'b0000, inupper, input1}
  // Probe on {4'b0000, inupper, input1}
  subtractor8bit subtractor8bit_1 (
    .input1({4'b0000, inupper, input1}), .input2(cbuffer8bit_1_output1), .output1(subtractor8bit_1_output1));  // open: inborrow, borrow
  cbuffer8bit cbuffer8bit_1 (
    .buffer1(and_2_out[3]), .input1({3'b000, input2, 3'b000}), .output1(cbuffer8bit_1_output1));
  and and_1 (and_2_out[3], not_1_out, or_1_out);
  or or_1 (or_1_out, comparatoru8bit_1_greater1, comparatoru8bit_1_equal1);
  comparatoru8bit comparatoru8bit_1 (
    .input1({4'b0000, inupper, input1}), .input2({3'b000, input2, 3'b000}),
    .greater1(comparatoru8bit_1_greater1), .equal1(comparatoru8bit_1_equal1));  // open: less1
  // Probe on subtractor8bit_1_output1
  // Probe on subtractor8bit_1_output1
  subtractor8bit subtractor8bit_2 (
    .input1(subtractor8bit_1_output1), .input2(cbuffer8bit_2_output1), .output1(subtractor8bit_2_output1));  // open: inborrow, borrow
  cbuffer8bit cbuffer8bit_2 (
    .buffer1(and_2_out[2]), .input1({4'b0000, input2, 2'b00}), .output1(cbuffer8bit_2_output1));
  and and_2 (and_2_out[2], not_1_out, or_2_out);
  or or_2 (or_2_out, comparatoru8bit_2_greater1, comparatoru8bit_2_equal1);
  comparatoru8bit comparatoru8bit_2 (
    .input1(subtractor8bit_1_output1), .input2({4'b0000, input2, 2'b00}),
    .greater1(comparatoru8bit_2_greater1), .equal1(comparatoru8bit_2_equal1));  // open: less1
  // Probe on subtractor8bit_2_output1
  // Probe on subtractor8bit_2_output1
  subtractor8bit subtractor8bit_3 (
    .input1(subtractor8bit_2_output1), .input2(cbuffer8bit_3_output1), .output1(subtractor8bit_3_output1));  // open: inborrow, borrow
  cbuffer8bit cbuffer8bit_3 (.buffer1(output1[1]), .input1({{5{1'b0}}, input2, 1'b0}), .output1(cbuffer8bit_3_output1));
  and and_3 (output1[1], not_1_out, or_3_out);
  or or_3 (or_3_out, comparatoru8bit_3_greater1, comparatoru8bit_3_equal1);
  comparatoru8bit comparatoru8bit_3 (
    .input1(subtractor8bit_2_output1), .input2({{5{1'b0}}, input2, 1'b0}),
    .greater1(comparatoru8bit_3_greater1), .equal1(comparatoru8bit_3_equal1));  // open: less1
  // Probe on subtractor8bit_3_output1
  // Probe on subtractor8bit_3_output1
  subtractor8bit subtractor8bit_4 (
    .input1(subtractor8bit_3_output1), .input2(cbuffer8bit_4_output1),
    .output1({subtractor8bit_4_output1, remainder}));  // open: inborrow, borrow
  cbuffer8bit cbuffer8bit_4 (.buffer1(output1[0]), .input1({{6{1'b0}}, input2}), .output1(cbuffer8bit_4_output1));
  and and_4 (output1[0], not_1_out, or_4_out);
  or or_4 (or_4_out, comparatoru8bit_4_greater1, comparatoru8bit_4_equal1);
  comparatoru8bit comparatoru8bit_4 (
    .input1(subtractor8bit_3_output1), .input2({{6{1'b0}}, input2}), .greater1(comparatoru8bit_4_greater1),
    .equal1(comparatoru8bit_4_equal1));  // open: less1
  // Probe on {subtractor8bit_4_output1, remainder}
  // Probe on {subtractor8bit_4_output1, remainder}
  // Probe on {4'b0000, and_2_out, output1}
  // Probe on {4'b0000, and_2_out, output1}
  // Probe on remainder
  // Probe on remainder
  // Probe on output1
  // Probe on output1

  // Notes on the sheet:
  //   input2: initial=0x2
  //   input1: initial=0x3
endmodule

module divideru4bit (
  input  [3:0] inupper,
  input  [3:0] input1,
  input  [3:0] input2,
  output [3:0] remainder,
  output [3:0] output1
);

  wire comparatoru4bit_1_equal1, comparatoru16bit_1_equal1, comparatoru16bit_1_greater1,
       comparatoru16bit_2_equal1, comparatoru16bit_2_greater1, comparatoru16bit_3_equal1,
       comparatoru16bit_3_greater1, comparatoru16bit_4_equal1, comparatoru16bit_4_greater1,
       comparatoru16bit_5_equal1, comparatoru16bit_5_greater1, comparatoru16bit_6_equal1,
       comparatoru16bit_6_greater1, comparatoru16bit_7_equal1, comparatoru16bit_7_greater1,
       comparatoru16bit_8_equal1, comparatoru16bit_8_greater1, not_1_out, or_1_out, or_2_out, or_3_out,
       or_4_out, or_5_out, or_6_out, or_7_out, or_8_out;
  wire [3:0] divider_1_out, divider_1_rem;
  wire [7:4] and_4_out;
  wire [15:0] cbuffer16bit_1_output1, cbuffer16bit_2_output1, cbuffer16bit_3_output1, cbuffer16bit_4_output1,
       cbuffer16bit_5_output1, cbuffer16bit_6_output1, cbuffer16bit_7_output1, cbuffer16bit_8_output1,
       subtractor16bit_1_output1, subtractor16bit_2_output1, subtractor16bit_3_output1,
       subtractor16bit_4_output1, subtractor16bit_5_output1, subtractor16bit_6_output1,
       subtractor16bit_7_output1;
  wire [15:4] subtractor16bit_8_output1;

  // Probe on inupper
  // Probe on inupper
  // Probe on input1
  // Probe on input1
  // Probe on divider_1_out
  // Probe on divider_1_out
  Divider #(.width(4)) divider_1 (.a(input1), .b(input2), .out(divider_1_out), .upper(inupper), .rem(divider_1_rem));
  // Probe on divider_1_rem
  // Probe on divider_1_rem
  not not_1 (not_1_out, comparatoru4bit_1_equal1);
  comparatoru4bit comparatoru4bit_1 (
    .input1(input2), .input2(4'b0000), .equal1(comparatoru4bit_1_equal1));  // open: greater1, less1
  // Probe on input2
  // Probe on input2
  // Probe on {{8{1'b0}}, inupper, input1}
  // Probe on {{8{1'b0}}, inupper, input1}
  subtractor16bit subtractor16bit_1 (
    .input1({{8{1'b0}}, inupper, input1}), .input2(cbuffer16bit_1_output1),
    .output1(subtractor16bit_1_output1));  // open: inborrow, borrow
  cbuffer16bit cbuffer16bit_1 (
    .buffer1(and_4_out[7]), .input1({{5{1'b0}}, input2, {7{1'b0}}}), .output1(cbuffer16bit_1_output1));
  and and_1 (and_4_out[7], not_1_out, or_1_out);
  or or_1 (or_1_out, comparatoru16bit_1_greater1, comparatoru16bit_1_equal1);
  comparatoru16bit comparatoru16bit_1 (
    .input1({{8{1'b0}}, inupper, input1}), .input2({{5{1'b0}}, input2, {7{1'b0}}}),
    .greater1(comparatoru16bit_1_greater1), .equal1(comparatoru16bit_1_equal1));  // open: less1
  // Probe on subtractor16bit_1_output1
  // Probe on subtractor16bit_1_output1
  subtractor16bit subtractor16bit_2 (
    .input1(subtractor16bit_1_output1), .input2(cbuffer16bit_2_output1), .output1(subtractor16bit_2_output1));  // open: inborrow, borrow
  cbuffer16bit cbuffer16bit_2 (
    .buffer1(and_4_out[6]), .input1({{6{1'b0}}, input2, {6{1'b0}}}), .output1(cbuffer16bit_2_output1));
  and and_2 (and_4_out[6], not_1_out, or_2_out);
  or or_2 (or_2_out, comparatoru16bit_2_greater1, comparatoru16bit_2_equal1);
  comparatoru16bit comparatoru16bit_2 (
    .input1(subtractor16bit_1_output1), .input2({{6{1'b0}}, input2, {6{1'b0}}}),
    .greater1(comparatoru16bit_2_greater1), .equal1(comparatoru16bit_2_equal1));  // open: less1
  // Probe on subtractor16bit_2_output1
  // Probe on subtractor16bit_2_output1
  subtractor16bit subtractor16bit_3 (
    .input1(subtractor16bit_2_output1), .input2(cbuffer16bit_3_output1), .output1(subtractor16bit_3_output1));  // open: inborrow, borrow
  cbuffer16bit cbuffer16bit_3 (
    .buffer1(and_4_out[5]), .input1({{7{1'b0}}, input2, {5{1'b0}}}), .output1(cbuffer16bit_3_output1));
  and and_3 (and_4_out[5], not_1_out, or_3_out);
  or or_3 (or_3_out, comparatoru16bit_3_greater1, comparatoru16bit_3_equal1);
  comparatoru16bit comparatoru16bit_3 (
    .input1(subtractor16bit_2_output1), .input2({{7{1'b0}}, input2, {5{1'b0}}}),
    .greater1(comparatoru16bit_3_greater1), .equal1(comparatoru16bit_3_equal1));  // open: less1
  // Probe on subtractor16bit_3_output1
  // Probe on subtractor16bit_3_output1
  subtractor16bit subtractor16bit_4 (
    .input1(subtractor16bit_3_output1), .input2(cbuffer16bit_4_output1), .output1(subtractor16bit_4_output1));  // open: inborrow, borrow
  cbuffer16bit cbuffer16bit_4 (
    .buffer1(and_4_out[4]), .input1({{8{1'b0}}, input2, 4'b0000}), .output1(cbuffer16bit_4_output1));
  and and_4 (and_4_out[4], not_1_out, or_4_out);
  or or_4 (or_4_out, comparatoru16bit_4_greater1, comparatoru16bit_4_equal1);
  comparatoru16bit comparatoru16bit_4 (
    .input1(subtractor16bit_3_output1), .input2({{8{1'b0}}, input2, 4'b0000}),
    .greater1(comparatoru16bit_4_greater1), .equal1(comparatoru16bit_4_equal1));  // open: less1
  // Probe on subtractor16bit_4_output1
  // Probe on subtractor16bit_4_output1
  subtractor16bit subtractor16bit_5 (
    .input1(subtractor16bit_4_output1), .input2(cbuffer16bit_5_output1), .output1(subtractor16bit_5_output1));  // open: inborrow, borrow
  cbuffer16bit cbuffer16bit_5 (
    .buffer1(output1[3]), .input1({{9{1'b0}}, input2, 3'b000}), .output1(cbuffer16bit_5_output1));
  and and_5 (output1[3], not_1_out, or_5_out);
  or or_5 (or_5_out, comparatoru16bit_5_greater1, comparatoru16bit_5_equal1);
  comparatoru16bit comparatoru16bit_5 (
    .input1(subtractor16bit_4_output1), .input2({{9{1'b0}}, input2, 3'b000}),
    .greater1(comparatoru16bit_5_greater1), .equal1(comparatoru16bit_5_equal1));  // open: less1
  // Probe on subtractor16bit_5_output1
  // Probe on subtractor16bit_5_output1
  subtractor16bit subtractor16bit_6 (
    .input1(subtractor16bit_5_output1), .input2(cbuffer16bit_6_output1), .output1(subtractor16bit_6_output1));  // open: inborrow, borrow
  cbuffer16bit cbuffer16bit_6 (
    .buffer1(output1[2]), .input1({{10{1'b0}}, input2, 2'b00}), .output1(cbuffer16bit_6_output1));
  and and_6 (output1[2], not_1_out, or_6_out);
  or or_6 (or_6_out, comparatoru16bit_6_greater1, comparatoru16bit_6_equal1);
  comparatoru16bit comparatoru16bit_6 (
    .input1(subtractor16bit_5_output1), .input2({{10{1'b0}}, input2, 2'b00}),
    .greater1(comparatoru16bit_6_greater1), .equal1(comparatoru16bit_6_equal1));  // open: less1
  // Probe on subtractor16bit_6_output1
  // Probe on subtractor16bit_6_output1
  subtractor16bit subtractor16bit_7 (
    .input1(subtractor16bit_6_output1), .input2(cbuffer16bit_7_output1), .output1(subtractor16bit_7_output1));  // open: inborrow, borrow
  cbuffer16bit cbuffer16bit_7 (
    .buffer1(output1[1]), .input1({{11{1'b0}}, input2, 1'b0}), .output1(cbuffer16bit_7_output1));
  and and_7 (output1[1], not_1_out, or_7_out);
  or or_7 (or_7_out, comparatoru16bit_7_greater1, comparatoru16bit_7_equal1);
  comparatoru16bit comparatoru16bit_7 (
    .input1(subtractor16bit_6_output1), .input2({{11{1'b0}}, input2, 1'b0}),
    .greater1(comparatoru16bit_7_greater1), .equal1(comparatoru16bit_7_equal1));  // open: less1
  // Probe on subtractor16bit_7_output1
  // Probe on subtractor16bit_7_output1
  subtractor16bit subtractor16bit_8 (
    .input1(subtractor16bit_7_output1), .input2(cbuffer16bit_8_output1),
    .output1({subtractor16bit_8_output1, remainder}));  // open: inborrow, borrow
  cbuffer16bit cbuffer16bit_8 (.buffer1(output1[0]), .input1({{12{1'b0}}, input2}), .output1(cbuffer16bit_8_output1));
  and and_8 (output1[0], not_1_out, or_8_out);
  or or_8 (or_8_out, comparatoru16bit_8_greater1, comparatoru16bit_8_equal1);
  comparatoru16bit comparatoru16bit_8 (
    .input1(subtractor16bit_7_output1), .input2({{12{1'b0}}, input2}),
    .greater1(comparatoru16bit_8_greater1), .equal1(comparatoru16bit_8_equal1));  // open: less1
  // Probe on {subtractor16bit_8_output1, remainder}
  // Probe on {subtractor16bit_8_output1, remainder}
  // Probe on {and_4_out, output1}
  // Probe on {and_4_out, output1}
  // Probe on remainder
  // Probe on remainder
  // Probe on output1
  // Probe on output1

  // Notes on the sheet:
  //   input2: initial=0x3
  //   inupper: initial=0xc
  //   input1: initial=0x8
endmodule

module divideru8bit (
  input  [7:0] inupper,
  input  [7:0] input1,
  input  [7:0] input2,
  output [7:0] remainder,
  output [7:0] output1
);

  wire comparatoru8bit_1_equal1, comparatoru32bit_1_equal1, comparatoru32bit_1_greater1,
       comparatoru32bit_2_equal1, comparatoru32bit_2_greater1, comparatoru32bit_3_equal1,
       comparatoru32bit_3_greater1, comparatoru32bit_4_equal1, comparatoru32bit_4_greater1,
       comparatoru32bit_5_equal1, comparatoru32bit_5_greater1, comparatoru32bit_6_equal1,
       comparatoru32bit_6_greater1, comparatoru32bit_7_equal1, comparatoru32bit_7_greater1,
       comparatoru32bit_8_equal1, comparatoru32bit_8_greater1, comparatoru32bit_9_equal1,
       comparatoru32bit_9_greater1, comparatoru32bit_10_equal1, comparatoru32bit_10_greater1,
       comparatoru32bit_11_equal1, comparatoru32bit_11_greater1, comparatoru32bit_12_equal1,
       comparatoru32bit_12_greater1, comparatoru32bit_13_equal1, comparatoru32bit_13_greater1,
       comparatoru32bit_14_equal1, comparatoru32bit_14_greater1, comparatoru32bit_15_equal1,
       comparatoru32bit_15_greater1, comparatoru32bit_16_equal1, comparatoru32bit_16_greater1, not_1_out,
       or_1_out, or_2_out, or_3_out, or_4_out, or_5_out, or_6_out, or_7_out, or_8_out, or_9_out, or_10_out,
       or_11_out, or_12_out, or_13_out, or_14_out, or_15_out, or_16_out;
  wire [7:0] divider_1_out, divider_1_rem;
  wire [15:8] and_8_out;
  wire [31:0] cbuffer32bit_1_output1, cbuffer32bit_2_output1, cbuffer32bit_3_output1, cbuffer32bit_4_output1,
       cbuffer32bit_5_output1, cbuffer32bit_6_output1, cbuffer32bit_7_output1, cbuffer32bit_8_output1,
       cbuffer32bit_9_output1, cbuffer32bit_10_output1, cbuffer32bit_11_output1, cbuffer32bit_12_output1,
       cbuffer32bit_13_output1, cbuffer32bit_14_output1, cbuffer32bit_15_output1, cbuffer32bit_16_output1,
       subtractor32bit_1_output1, subtractor32bit_2_output1, subtractor32bit_3_output1,
       subtractor32bit_4_output1, subtractor32bit_5_output1, subtractor32bit_6_output1,
       subtractor32bit_7_output1, subtractor32bit_8_output1, subtractor32bit_9_output1,
       subtractor32bit_10_output1, subtractor32bit_11_output1, subtractor32bit_12_output1,
       subtractor32bit_13_output1, subtractor32bit_14_output1, subtractor32bit_15_output1;
  wire [31:8] subtractor32bit_16_output1;

  // Probe on inupper
  // Probe on inupper
  // Probe on input1
  // Probe on input1
  // Probe on divider_1_out
  // Probe on divider_1_out
  Divider divider_1 (.a(input1), .b(input2), .out(divider_1_out), .upper(inupper), .rem(divider_1_rem));
  // Probe on divider_1_rem
  // Probe on divider_1_rem
  not not_1 (not_1_out, comparatoru8bit_1_equal1);
  comparatoru8bit comparatoru8bit_1 (
    .input1(input2), .input2({8{1'b0}}), .equal1(comparatoru8bit_1_equal1));  // open: greater1, less1
  // Probe on input2
  // Probe on input2
  // Probe on {{16{1'b0}}, inupper, input1}
  // Probe on {{16{1'b0}}, inupper, input1}
  subtractor32bit subtractor32bit_1 (
    .input1({{16{1'b0}}, inupper, input1}), .input2(cbuffer32bit_1_output1),
    .output1(subtractor32bit_1_output1));  // open: inborrow, borrow
  cbuffer32bit cbuffer32bit_1 (
    .buffer1(and_8_out[15]), .input1({{9{1'b0}}, input2, {15{1'b0}}}), .output1(cbuffer32bit_1_output1));
  and and_1 (and_8_out[15], not_1_out, or_1_out);
  or or_1 (or_1_out, comparatoru32bit_1_greater1, comparatoru32bit_1_equal1);
  comparatoru32bit comparatoru32bit_1 (
    .input1({{16{1'b0}}, inupper, input1}), .input2({{9{1'b0}}, input2, {15{1'b0}}}),
    .greater1(comparatoru32bit_1_greater1), .equal1(comparatoru32bit_1_equal1));  // open: less1
  // Probe on subtractor32bit_1_output1
  // Probe on subtractor32bit_1_output1
  subtractor32bit subtractor32bit_2 (
    .input1(subtractor32bit_1_output1), .input2(cbuffer32bit_2_output1), .output1(subtractor32bit_2_output1));  // open: inborrow, borrow
  cbuffer32bit cbuffer32bit_2 (
    .buffer1(and_8_out[14]), .input1({{10{1'b0}}, input2, {14{1'b0}}}), .output1(cbuffer32bit_2_output1));
  and and_2 (and_8_out[14], not_1_out, or_2_out);
  or or_2 (or_2_out, comparatoru32bit_2_greater1, comparatoru32bit_2_equal1);
  comparatoru32bit comparatoru32bit_2 (
    .input1(subtractor32bit_1_output1), .input2({{10{1'b0}}, input2, {14{1'b0}}}),
    .greater1(comparatoru32bit_2_greater1), .equal1(comparatoru32bit_2_equal1));  // open: less1
  // Probe on subtractor32bit_2_output1
  // Probe on subtractor32bit_2_output1
  subtractor32bit subtractor32bit_3 (
    .input1(subtractor32bit_2_output1), .input2(cbuffer32bit_3_output1), .output1(subtractor32bit_3_output1));  // open: inborrow, borrow
  cbuffer32bit cbuffer32bit_3 (
    .buffer1(and_8_out[13]), .input1({{11{1'b0}}, input2, {13{1'b0}}}), .output1(cbuffer32bit_3_output1));
  and and_3 (and_8_out[13], not_1_out, or_3_out);
  or or_3 (or_3_out, comparatoru32bit_3_greater1, comparatoru32bit_3_equal1);
  comparatoru32bit comparatoru32bit_3 (
    .input1(subtractor32bit_2_output1), .input2({{11{1'b0}}, input2, {13{1'b0}}}),
    .greater1(comparatoru32bit_3_greater1), .equal1(comparatoru32bit_3_equal1));  // open: less1
  // Probe on subtractor32bit_3_output1
  // Probe on subtractor32bit_3_output1
  subtractor32bit subtractor32bit_4 (
    .input1(subtractor32bit_3_output1), .input2(cbuffer32bit_4_output1), .output1(subtractor32bit_4_output1));  // open: inborrow, borrow
  cbuffer32bit cbuffer32bit_4 (
    .buffer1(and_8_out[12]), .input1({{12{1'b0}}, input2, {12{1'b0}}}), .output1(cbuffer32bit_4_output1));
  and and_4 (and_8_out[12], not_1_out, or_4_out);
  or or_4 (or_4_out, comparatoru32bit_4_greater1, comparatoru32bit_4_equal1);
  comparatoru32bit comparatoru32bit_4 (
    .input1(subtractor32bit_3_output1), .input2({{12{1'b0}}, input2, {12{1'b0}}}),
    .greater1(comparatoru32bit_4_greater1), .equal1(comparatoru32bit_4_equal1));  // open: less1
  // Probe on subtractor32bit_4_output1
  // Probe on subtractor32bit_4_output1
  subtractor32bit subtractor32bit_5 (
    .input1(subtractor32bit_4_output1), .input2(cbuffer32bit_5_output1), .output1(subtractor32bit_5_output1));  // open: inborrow, borrow
  cbuffer32bit cbuffer32bit_5 (
    .buffer1(and_8_out[11]), .input1({{13{1'b0}}, input2, {11{1'b0}}}), .output1(cbuffer32bit_5_output1));
  and and_5 (and_8_out[11], not_1_out, or_5_out);
  or or_5 (or_5_out, comparatoru32bit_5_greater1, comparatoru32bit_5_equal1);
  comparatoru32bit comparatoru32bit_5 (
    .input1(subtractor32bit_4_output1), .input2({{13{1'b0}}, input2, {11{1'b0}}}),
    .greater1(comparatoru32bit_5_greater1), .equal1(comparatoru32bit_5_equal1));  // open: less1
  // Probe on subtractor32bit_5_output1
  // Probe on subtractor32bit_5_output1
  subtractor32bit subtractor32bit_6 (
    .input1(subtractor32bit_5_output1), .input2(cbuffer32bit_6_output1), .output1(subtractor32bit_6_output1));  // open: inborrow, borrow
  cbuffer32bit cbuffer32bit_6 (
    .buffer1(and_8_out[10]), .input1({{14{1'b0}}, input2, {10{1'b0}}}), .output1(cbuffer32bit_6_output1));
  and and_6 (and_8_out[10], not_1_out, or_6_out);
  or or_6 (or_6_out, comparatoru32bit_6_greater1, comparatoru32bit_6_equal1);
  comparatoru32bit comparatoru32bit_6 (
    .input1(subtractor32bit_5_output1), .input2({{14{1'b0}}, input2, {10{1'b0}}}),
    .greater1(comparatoru32bit_6_greater1), .equal1(comparatoru32bit_6_equal1));  // open: less1
  // Probe on subtractor32bit_6_output1
  // Probe on subtractor32bit_6_output1
  subtractor32bit subtractor32bit_7 (
    .input1(subtractor32bit_6_output1), .input2(cbuffer32bit_7_output1), .output1(subtractor32bit_7_output1));  // open: inborrow, borrow
  cbuffer32bit cbuffer32bit_7 (
    .buffer1(and_8_out[9]), .input1({{15{1'b0}}, input2, {9{1'b0}}}), .output1(cbuffer32bit_7_output1));
  and and_7 (and_8_out[9], not_1_out, or_7_out);
  or or_7 (or_7_out, comparatoru32bit_7_greater1, comparatoru32bit_7_equal1);
  comparatoru32bit comparatoru32bit_7 (
    .input1(subtractor32bit_6_output1), .input2({{15{1'b0}}, input2, {9{1'b0}}}),
    .greater1(comparatoru32bit_7_greater1), .equal1(comparatoru32bit_7_equal1));  // open: less1
  // Probe on subtractor32bit_7_output1
  // Probe on subtractor32bit_7_output1
  subtractor32bit subtractor32bit_8 (
    .input1(subtractor32bit_7_output1), .input2(cbuffer32bit_8_output1), .output1(subtractor32bit_8_output1));  // open: inborrow, borrow
  cbuffer32bit cbuffer32bit_8 (
    .buffer1(and_8_out[8]), .input1({{16{1'b0}}, input2, {8{1'b0}}}), .output1(cbuffer32bit_8_output1));
  and and_8 (and_8_out[8], not_1_out, or_8_out);
  or or_8 (or_8_out, comparatoru32bit_8_greater1, comparatoru32bit_8_equal1);
  comparatoru32bit comparatoru32bit_8 (
    .input1(subtractor32bit_7_output1), .input2({{16{1'b0}}, input2, {8{1'b0}}}),
    .greater1(comparatoru32bit_8_greater1), .equal1(comparatoru32bit_8_equal1));  // open: less1
  // Probe on subtractor32bit_8_output1
  // Probe on subtractor32bit_8_output1
  subtractor32bit subtractor32bit_9 (
    .input1(subtractor32bit_8_output1), .input2(cbuffer32bit_9_output1), .output1(subtractor32bit_9_output1));  // open: inborrow, borrow
  cbuffer32bit cbuffer32bit_9 (
    .buffer1(output1[7]), .input1({{17{1'b0}}, input2, {7{1'b0}}}), .output1(cbuffer32bit_9_output1));
  and and_9 (output1[7], not_1_out, or_9_out);
  or or_9 (or_9_out, comparatoru32bit_9_greater1, comparatoru32bit_9_equal1);
  comparatoru32bit comparatoru32bit_9 (
    .input1(subtractor32bit_8_output1), .input2({{17{1'b0}}, input2, {7{1'b0}}}),
    .greater1(comparatoru32bit_9_greater1), .equal1(comparatoru32bit_9_equal1));  // open: less1
  // Probe on subtractor32bit_9_output1
  // Probe on subtractor32bit_9_output1
  subtractor32bit subtractor32bit_10 (
    .input1(subtractor32bit_9_output1), .input2(cbuffer32bit_10_output1), .output1(subtractor32bit_10_output1));  // open: inborrow, borrow
  cbuffer32bit cbuffer32bit_10 (
    .buffer1(output1[6]), .input1({{18{1'b0}}, input2, {6{1'b0}}}), .output1(cbuffer32bit_10_output1));
  and and_10 (output1[6], not_1_out, or_10_out);
  or or_10 (or_10_out, comparatoru32bit_10_greater1, comparatoru32bit_10_equal1);
  comparatoru32bit comparatoru32bit_10 (
    .input1(subtractor32bit_9_output1), .input2({{18{1'b0}}, input2, {6{1'b0}}}),
    .greater1(comparatoru32bit_10_greater1), .equal1(comparatoru32bit_10_equal1));  // open: less1
  // Probe on subtractor32bit_10_output1
  // Probe on subtractor32bit_10_output1
  subtractor32bit subtractor32bit_11 (
    .input1(subtractor32bit_10_output1), .input2(cbuffer32bit_11_output1),
    .output1(subtractor32bit_11_output1));  // open: inborrow, borrow
  cbuffer32bit cbuffer32bit_11 (
    .buffer1(output1[5]), .input1({{19{1'b0}}, input2, {5{1'b0}}}), .output1(cbuffer32bit_11_output1));
  and and_11 (output1[5], not_1_out, or_11_out);
  or or_11 (or_11_out, comparatoru32bit_11_greater1, comparatoru32bit_11_equal1);
  comparatoru32bit comparatoru32bit_11 (
    .input1(subtractor32bit_10_output1), .input2({{19{1'b0}}, input2, {5{1'b0}}}),
    .greater1(comparatoru32bit_11_greater1), .equal1(comparatoru32bit_11_equal1));  // open: less1
  // Probe on subtractor32bit_11_output1
  // Probe on subtractor32bit_11_output1
  subtractor32bit subtractor32bit_12 (
    .input1(subtractor32bit_11_output1), .input2(cbuffer32bit_12_output1),
    .output1(subtractor32bit_12_output1));  // open: inborrow, borrow
  cbuffer32bit cbuffer32bit_12 (
    .buffer1(output1[4]), .input1({{20{1'b0}}, input2, 4'b0000}), .output1(cbuffer32bit_12_output1));
  and and_12 (output1[4], not_1_out, or_12_out);
  or or_12 (or_12_out, comparatoru32bit_12_greater1, comparatoru32bit_12_equal1);
  comparatoru32bit comparatoru32bit_12 (
    .input1(subtractor32bit_11_output1), .input2({{20{1'b0}}, input2, 4'b0000}),
    .greater1(comparatoru32bit_12_greater1), .equal1(comparatoru32bit_12_equal1));  // open: less1
  // Probe on subtractor32bit_12_output1
  // Probe on subtractor32bit_12_output1
  subtractor32bit subtractor32bit_13 (
    .input1(subtractor32bit_12_output1), .input2(cbuffer32bit_13_output1),
    .output1(subtractor32bit_13_output1));  // open: inborrow, borrow
  cbuffer32bit cbuffer32bit_13 (
    .buffer1(output1[3]), .input1({{21{1'b0}}, input2, 3'b000}), .output1(cbuffer32bit_13_output1));
  and and_13 (output1[3], not_1_out, or_13_out);
  or or_13 (or_13_out, comparatoru32bit_13_greater1, comparatoru32bit_13_equal1);
  comparatoru32bit comparatoru32bit_13 (
    .input1(subtractor32bit_12_output1), .input2({{21{1'b0}}, input2, 3'b000}),
    .greater1(comparatoru32bit_13_greater1), .equal1(comparatoru32bit_13_equal1));  // open: less1
  // Probe on subtractor32bit_13_output1
  // Probe on subtractor32bit_13_output1
  subtractor32bit subtractor32bit_14 (
    .input1(subtractor32bit_13_output1), .input2(cbuffer32bit_14_output1),
    .output1(subtractor32bit_14_output1));  // open: inborrow, borrow
  cbuffer32bit cbuffer32bit_14 (
    .buffer1(output1[2]), .input1({{22{1'b0}}, input2, 2'b00}), .output1(cbuffer32bit_14_output1));
  and and_14 (output1[2], not_1_out, or_14_out);
  or or_14 (or_14_out, comparatoru32bit_14_greater1, comparatoru32bit_14_equal1);
  comparatoru32bit comparatoru32bit_14 (
    .input1(subtractor32bit_13_output1), .input2({{22{1'b0}}, input2, 2'b00}),
    .greater1(comparatoru32bit_14_greater1), .equal1(comparatoru32bit_14_equal1));  // open: less1
  // Probe on subtractor32bit_14_output1
  // Probe on subtractor32bit_14_output1
  subtractor32bit subtractor32bit_15 (
    .input1(subtractor32bit_14_output1), .input2(cbuffer32bit_15_output1),
    .output1(subtractor32bit_15_output1));  // open: inborrow, borrow
  cbuffer32bit cbuffer32bit_15 (
    .buffer1(output1[1]), .input1({{23{1'b0}}, input2, 1'b0}), .output1(cbuffer32bit_15_output1));
  and and_15 (output1[1], not_1_out, or_15_out);
  or or_15 (or_15_out, comparatoru32bit_15_greater1, comparatoru32bit_15_equal1);
  comparatoru32bit comparatoru32bit_15 (
    .input1(subtractor32bit_14_output1), .input2({{23{1'b0}}, input2, 1'b0}),
    .greater1(comparatoru32bit_15_greater1), .equal1(comparatoru32bit_15_equal1));  // open: less1
  // Probe on subtractor32bit_15_output1
  // Probe on subtractor32bit_15_output1
  subtractor32bit subtractor32bit_16 (
    .input1(subtractor32bit_15_output1), .input2(cbuffer32bit_16_output1),
    .output1({subtractor32bit_16_output1, remainder}));  // open: inborrow, borrow
  cbuffer32bit cbuffer32bit_16 (.buffer1(output1[0]), .input1({{24{1'b0}}, input2}), .output1(cbuffer32bit_16_output1));
  and and_16 (output1[0], not_1_out, or_16_out);
  or or_16 (or_16_out, comparatoru32bit_16_greater1, comparatoru32bit_16_equal1);
  comparatoru32bit comparatoru32bit_16 (
    .input1(subtractor32bit_15_output1), .input2({{24{1'b0}}, input2}),
    .greater1(comparatoru32bit_16_greater1), .equal1(comparatoru32bit_16_equal1));  // open: less1
  // Probe on {subtractor32bit_16_output1, remainder}
  // Probe on {subtractor32bit_16_output1, remainder}
  // Probe on {and_8_out, output1}
  // Probe on {and_8_out, output1}
  // Probe on remainder
  // Probe on remainder
  // Probe on output1
  // Probe on output1

  // Notes on the sheet:
  //   input2: initial=0x7a
  //   inupper: initial=0xc
  //   input1: initial=0xfa
endmodule

module divideru16bit (
  input  [15:0] inupper,
  input  [15:0] input1,
  input  [15:0] input2,
  output [15:0] remainder,
  output [15:0] output1
);

  wire comparatoru16bit_1_equal1, comparatoru64bit_1_equal1, comparatoru64bit_1_greater1,
       comparatoru64bit_2_equal1, comparatoru64bit_2_greater1, comparatoru64bit_3_equal1,
       comparatoru64bit_3_greater1, comparatoru64bit_4_equal1, comparatoru64bit_4_greater1,
       comparatoru64bit_5_equal1, comparatoru64bit_5_greater1, comparatoru64bit_6_equal1,
       comparatoru64bit_6_greater1, comparatoru64bit_7_equal1, comparatoru64bit_7_greater1,
       comparatoru64bit_8_equal1, comparatoru64bit_8_greater1, comparatoru64bit_9_equal1,
       comparatoru64bit_9_greater1, comparatoru64bit_10_equal1, comparatoru64bit_10_greater1,
       comparatoru64bit_11_equal1, comparatoru64bit_11_greater1, comparatoru64bit_12_equal1,
       comparatoru64bit_12_greater1, comparatoru64bit_13_equal1, comparatoru64bit_13_greater1,
       comparatoru64bit_14_equal1, comparatoru64bit_14_greater1, comparatoru64bit_15_equal1,
       comparatoru64bit_15_greater1, comparatoru64bit_16_equal1, comparatoru64bit_16_greater1,
       comparatoru64bit_17_equal1, comparatoru64bit_17_greater1, comparatoru64bit_18_equal1,
       comparatoru64bit_18_greater1, comparatoru64bit_19_equal1, comparatoru64bit_19_greater1,
       comparatoru64bit_20_equal1, comparatoru64bit_20_greater1, comparatoru64bit_21_equal1,
       comparatoru64bit_21_greater1, comparatoru64bit_22_equal1, comparatoru64bit_22_greater1,
       comparatoru64bit_23_equal1, comparatoru64bit_23_greater1, comparatoru64bit_24_equal1,
       comparatoru64bit_24_greater1, comparatoru64bit_25_equal1, comparatoru64bit_25_greater1,
       comparatoru64bit_26_equal1, comparatoru64bit_26_greater1, comparatoru64bit_27_equal1,
       comparatoru64bit_27_greater1, comparatoru64bit_28_equal1, comparatoru64bit_28_greater1,
       comparatoru64bit_29_equal1, comparatoru64bit_29_greater1, comparatoru64bit_30_equal1,
       comparatoru64bit_30_greater1, comparatoru64bit_31_equal1, comparatoru64bit_31_greater1,
       comparatoru64bit_32_equal1, comparatoru64bit_32_greater1, not_1_out, or_1_out, or_2_out, or_3_out,
       or_4_out, or_5_out, or_6_out, or_7_out, or_8_out, or_9_out, or_10_out, or_11_out, or_12_out,
       or_13_out, or_14_out, or_15_out, or_16_out, or_17_out, or_18_out, or_19_out, or_20_out, or_21_out,
       or_22_out, or_23_out, or_24_out, or_25_out, or_26_out, or_27_out, or_28_out, or_29_out, or_30_out,
       or_31_out, or_32_out;
  wire [15:0] divider_1_out, divider_1_rem;
  wire [31:16] and_16_out;
  wire [63:0] cbuffer64bit_1_output1, cbuffer64bit_2_output1, cbuffer64bit_3_output1, cbuffer64bit_4_output1,
       cbuffer64bit_5_output1, cbuffer64bit_6_output1, cbuffer64bit_7_output1, cbuffer64bit_8_output1,
       cbuffer64bit_9_output1, cbuffer64bit_10_output1, cbuffer64bit_11_output1, cbuffer64bit_12_output1,
       cbuffer64bit_13_output1, cbuffer64bit_14_output1, cbuffer64bit_15_output1, cbuffer64bit_16_output1,
       cbuffer64bit_17_output1, cbuffer64bit_18_output1, cbuffer64bit_19_output1, cbuffer64bit_20_output1,
       cbuffer64bit_21_output1, cbuffer64bit_22_output1, cbuffer64bit_23_output1, cbuffer64bit_24_output1,
       cbuffer64bit_25_output1, cbuffer64bit_26_output1, cbuffer64bit_27_output1, cbuffer64bit_28_output1,
       cbuffer64bit_29_output1, cbuffer64bit_30_output1, cbuffer64bit_31_output1, cbuffer64bit_32_output1,
       subtractor64bit_1_output1, subtractor64bit_2_output1, subtractor64bit_3_output1,
       subtractor64bit_4_output1, subtractor64bit_5_output1, subtractor64bit_6_output1,
       subtractor64bit_7_output1, subtractor64bit_8_output1, subtractor64bit_9_output1,
       subtractor64bit_10_output1, subtractor64bit_11_output1, subtractor64bit_12_output1,
       subtractor64bit_13_output1, subtractor64bit_14_output1, subtractor64bit_15_output1,
       subtractor64bit_16_output1, subtractor64bit_17_output1, subtractor64bit_18_output1,
       subtractor64bit_19_output1, subtractor64bit_20_output1, subtractor64bit_21_output1,
       subtractor64bit_22_output1, subtractor64bit_23_output1, subtractor64bit_24_output1,
       subtractor64bit_25_output1, subtractor64bit_26_output1, subtractor64bit_27_output1,
       subtractor64bit_28_output1, subtractor64bit_29_output1, subtractor64bit_30_output1,
       subtractor64bit_31_output1;
  wire [63:16] subtractor64bit_32_output1;

  // Probe on inupper
  // Probe on inupper
  // Probe on input1
  // Probe on input1
  // Probe on divider_1_out
  // Probe on divider_1_out
  Divider #(.width(16)) divider_1 (.a(input1), .b(input2), .out(divider_1_out), .upper(inupper), .rem(divider_1_rem));
  // Probe on divider_1_rem
  // Probe on divider_1_rem
  not not_1 (not_1_out, comparatoru16bit_1_equal1);
  comparatoru16bit comparatoru16bit_1 (
    .input1(input2), .input2({16{1'b0}}), .equal1(comparatoru16bit_1_equal1));  // open: greater1, less1
  // Probe on input2
  // Probe on input2
  // Probe on {{32{1'b0}}, inupper, input1}
  // Probe on {{32{1'b0}}, inupper, input1}
  subtractor64bit subtractor64bit_1 (
    .input1({{32{1'b0}}, inupper, input1}), .input2(cbuffer64bit_1_output1),
    .output1(subtractor64bit_1_output1));  // open: inborrow, borrow
  cbuffer64bit cbuffer64bit_1 (
    .buffer1(and_16_out[31]), .input1({{17{1'b0}}, input2, {31{1'b0}}}), .output1(cbuffer64bit_1_output1));
  and and_1 (and_16_out[31], not_1_out, or_1_out);
  or or_1 (or_1_out, comparatoru64bit_1_greater1, comparatoru64bit_1_equal1);
  comparatoru64bit comparatoru64bit_1 (
    .input1({{32{1'b0}}, inupper, input1}), .input2({{17{1'b0}}, input2, {31{1'b0}}}),
    .greater1(comparatoru64bit_1_greater1), .equal1(comparatoru64bit_1_equal1));  // open: less1
  // Probe on subtractor64bit_1_output1
  // Probe on subtractor64bit_1_output1
  subtractor64bit subtractor64bit_2 (
    .input1(subtractor64bit_1_output1), .input2(cbuffer64bit_2_output1), .output1(subtractor64bit_2_output1));  // open: inborrow, borrow
  cbuffer64bit cbuffer64bit_2 (
    .buffer1(and_16_out[30]), .input1({{18{1'b0}}, input2, {30{1'b0}}}), .output1(cbuffer64bit_2_output1));
  and and_2 (and_16_out[30], not_1_out, or_2_out);
  or or_2 (or_2_out, comparatoru64bit_2_greater1, comparatoru64bit_2_equal1);
  comparatoru64bit comparatoru64bit_2 (
    .input1(subtractor64bit_1_output1), .input2({{18{1'b0}}, input2, {30{1'b0}}}),
    .greater1(comparatoru64bit_2_greater1), .equal1(comparatoru64bit_2_equal1));  // open: less1
  // Probe on subtractor64bit_2_output1
  // Probe on subtractor64bit_2_output1
  subtractor64bit subtractor64bit_3 (
    .input1(subtractor64bit_2_output1), .input2(cbuffer64bit_3_output1), .output1(subtractor64bit_3_output1));  // open: inborrow, borrow
  cbuffer64bit cbuffer64bit_3 (
    .buffer1(and_16_out[29]), .input1({{19{1'b0}}, input2, {29{1'b0}}}), .output1(cbuffer64bit_3_output1));
  and and_3 (and_16_out[29], not_1_out, or_3_out);
  or or_3 (or_3_out, comparatoru64bit_3_greater1, comparatoru64bit_3_equal1);
  comparatoru64bit comparatoru64bit_3 (
    .input1(subtractor64bit_2_output1), .input2({{19{1'b0}}, input2, {29{1'b0}}}),
    .greater1(comparatoru64bit_3_greater1), .equal1(comparatoru64bit_3_equal1));  // open: less1
  // Probe on subtractor64bit_3_output1
  // Probe on subtractor64bit_3_output1
  subtractor64bit subtractor64bit_4 (
    .input1(subtractor64bit_3_output1), .input2(cbuffer64bit_4_output1), .output1(subtractor64bit_4_output1));  // open: inborrow, borrow
  cbuffer64bit cbuffer64bit_4 (
    .buffer1(and_16_out[28]), .input1({{20{1'b0}}, input2, {28{1'b0}}}), .output1(cbuffer64bit_4_output1));
  and and_4 (and_16_out[28], not_1_out, or_4_out);
  or or_4 (or_4_out, comparatoru64bit_4_greater1, comparatoru64bit_4_equal1);
  comparatoru64bit comparatoru64bit_4 (
    .input1(subtractor64bit_3_output1), .input2({{20{1'b0}}, input2, {28{1'b0}}}),
    .greater1(comparatoru64bit_4_greater1), .equal1(comparatoru64bit_4_equal1));  // open: less1
  // Probe on subtractor64bit_4_output1
  // Probe on subtractor64bit_4_output1
  subtractor64bit subtractor64bit_5 (
    .input1(subtractor64bit_4_output1), .input2(cbuffer64bit_5_output1), .output1(subtractor64bit_5_output1));  // open: inborrow, borrow
  cbuffer64bit cbuffer64bit_5 (
    .buffer1(and_16_out[27]), .input1({{21{1'b0}}, input2, {27{1'b0}}}), .output1(cbuffer64bit_5_output1));
  and and_5 (and_16_out[27], not_1_out, or_5_out);
  or or_5 (or_5_out, comparatoru64bit_5_greater1, comparatoru64bit_5_equal1);
  comparatoru64bit comparatoru64bit_5 (
    .input1(subtractor64bit_4_output1), .input2({{21{1'b0}}, input2, {27{1'b0}}}),
    .greater1(comparatoru64bit_5_greater1), .equal1(comparatoru64bit_5_equal1));  // open: less1
  // Probe on subtractor64bit_5_output1
  // Probe on subtractor64bit_5_output1
  subtractor64bit subtractor64bit_6 (
    .input1(subtractor64bit_5_output1), .input2(cbuffer64bit_6_output1), .output1(subtractor64bit_6_output1));  // open: inborrow, borrow
  cbuffer64bit cbuffer64bit_6 (
    .buffer1(and_16_out[26]), .input1({{22{1'b0}}, input2, {26{1'b0}}}), .output1(cbuffer64bit_6_output1));
  and and_6 (and_16_out[26], not_1_out, or_6_out);
  or or_6 (or_6_out, comparatoru64bit_6_greater1, comparatoru64bit_6_equal1);
  comparatoru64bit comparatoru64bit_6 (
    .input1(subtractor64bit_5_output1), .input2({{22{1'b0}}, input2, {26{1'b0}}}),
    .greater1(comparatoru64bit_6_greater1), .equal1(comparatoru64bit_6_equal1));  // open: less1
  // Probe on subtractor64bit_6_output1
  // Probe on subtractor64bit_6_output1
  subtractor64bit subtractor64bit_7 (
    .input1(subtractor64bit_6_output1), .input2(cbuffer64bit_7_output1), .output1(subtractor64bit_7_output1));  // open: inborrow, borrow
  cbuffer64bit cbuffer64bit_7 (
    .buffer1(and_16_out[25]), .input1({{23{1'b0}}, input2, {25{1'b0}}}), .output1(cbuffer64bit_7_output1));
  and and_7 (and_16_out[25], not_1_out, or_7_out);
  or or_7 (or_7_out, comparatoru64bit_7_greater1, comparatoru64bit_7_equal1);
  comparatoru64bit comparatoru64bit_7 (
    .input1(subtractor64bit_6_output1), .input2({{23{1'b0}}, input2, {25{1'b0}}}),
    .greater1(comparatoru64bit_7_greater1), .equal1(comparatoru64bit_7_equal1));  // open: less1
  // Probe on subtractor64bit_7_output1
  // Probe on subtractor64bit_7_output1
  subtractor64bit subtractor64bit_8 (
    .input1(subtractor64bit_7_output1), .input2(cbuffer64bit_8_output1), .output1(subtractor64bit_8_output1));  // open: inborrow, borrow
  cbuffer64bit cbuffer64bit_8 (
    .buffer1(and_16_out[24]), .input1({{24{1'b0}}, input2, {24{1'b0}}}), .output1(cbuffer64bit_8_output1));
  and and_8 (and_16_out[24], not_1_out, or_8_out);
  or or_8 (or_8_out, comparatoru64bit_8_greater1, comparatoru64bit_8_equal1);
  comparatoru64bit comparatoru64bit_8 (
    .input1(subtractor64bit_7_output1), .input2({{24{1'b0}}, input2, {24{1'b0}}}),
    .greater1(comparatoru64bit_8_greater1), .equal1(comparatoru64bit_8_equal1));  // open: less1
  // Probe on subtractor64bit_8_output1
  // Probe on subtractor64bit_8_output1
  subtractor64bit subtractor64bit_9 (
    .input1(subtractor64bit_8_output1), .input2(cbuffer64bit_9_output1), .output1(subtractor64bit_9_output1));  // open: inborrow, borrow
  cbuffer64bit cbuffer64bit_9 (
    .buffer1(and_16_out[23]), .input1({{25{1'b0}}, input2, {23{1'b0}}}), .output1(cbuffer64bit_9_output1));
  and and_9 (and_16_out[23], not_1_out, or_9_out);
  or or_9 (or_9_out, comparatoru64bit_9_greater1, comparatoru64bit_9_equal1);
  comparatoru64bit comparatoru64bit_9 (
    .input1(subtractor64bit_8_output1), .input2({{25{1'b0}}, input2, {23{1'b0}}}),
    .greater1(comparatoru64bit_9_greater1), .equal1(comparatoru64bit_9_equal1));  // open: less1
  // Probe on subtractor64bit_9_output1
  // Probe on subtractor64bit_9_output1
  subtractor64bit subtractor64bit_10 (
    .input1(subtractor64bit_9_output1), .input2(cbuffer64bit_10_output1), .output1(subtractor64bit_10_output1));  // open: inborrow, borrow
  cbuffer64bit cbuffer64bit_10 (
    .buffer1(and_16_out[22]), .input1({{26{1'b0}}, input2, {22{1'b0}}}), .output1(cbuffer64bit_10_output1));
  and and_10 (and_16_out[22], not_1_out, or_10_out);
  or or_10 (or_10_out, comparatoru64bit_10_greater1, comparatoru64bit_10_equal1);
  comparatoru64bit comparatoru64bit_10 (
    .input1(subtractor64bit_9_output1), .input2({{26{1'b0}}, input2, {22{1'b0}}}),
    .greater1(comparatoru64bit_10_greater1), .equal1(comparatoru64bit_10_equal1));  // open: less1
  // Probe on subtractor64bit_10_output1
  // Probe on subtractor64bit_10_output1
  subtractor64bit subtractor64bit_11 (
    .input1(subtractor64bit_10_output1), .input2(cbuffer64bit_11_output1),
    .output1(subtractor64bit_11_output1));  // open: inborrow, borrow
  cbuffer64bit cbuffer64bit_11 (
    .buffer1(and_16_out[21]), .input1({{27{1'b0}}, input2, {21{1'b0}}}), .output1(cbuffer64bit_11_output1));
  and and_11 (and_16_out[21], not_1_out, or_11_out);
  or or_11 (or_11_out, comparatoru64bit_11_greater1, comparatoru64bit_11_equal1);
  comparatoru64bit comparatoru64bit_11 (
    .input1(subtractor64bit_10_output1), .input2({{27{1'b0}}, input2, {21{1'b0}}}),
    .greater1(comparatoru64bit_11_greater1), .equal1(comparatoru64bit_11_equal1));  // open: less1
  // Probe on subtractor64bit_11_output1
  // Probe on subtractor64bit_11_output1
  subtractor64bit subtractor64bit_12 (
    .input1(subtractor64bit_11_output1), .input2(cbuffer64bit_12_output1),
    .output1(subtractor64bit_12_output1));  // open: inborrow, borrow
  cbuffer64bit cbuffer64bit_12 (
    .buffer1(and_16_out[20]), .input1({{28{1'b0}}, input2, {20{1'b0}}}), .output1(cbuffer64bit_12_output1));
  and and_12 (and_16_out[20], not_1_out, or_12_out);
  or or_12 (or_12_out, comparatoru64bit_12_greater1, comparatoru64bit_12_equal1);
  comparatoru64bit comparatoru64bit_12 (
    .input1(subtractor64bit_11_output1), .input2({{28{1'b0}}, input2, {20{1'b0}}}),
    .greater1(comparatoru64bit_12_greater1), .equal1(comparatoru64bit_12_equal1));  // open: less1
  // Probe on subtractor64bit_12_output1
  // Probe on subtractor64bit_12_output1
  subtractor64bit subtractor64bit_13 (
    .input1(subtractor64bit_12_output1), .input2(cbuffer64bit_13_output1),
    .output1(subtractor64bit_13_output1));  // open: inborrow, borrow
  cbuffer64bit cbuffer64bit_13 (
    .buffer1(and_16_out[19]), .input1({{29{1'b0}}, input2, {19{1'b0}}}), .output1(cbuffer64bit_13_output1));
  and and_13 (and_16_out[19], not_1_out, or_13_out);
  or or_13 (or_13_out, comparatoru64bit_13_greater1, comparatoru64bit_13_equal1);
  comparatoru64bit comparatoru64bit_13 (
    .input1(subtractor64bit_12_output1), .input2({{29{1'b0}}, input2, {19{1'b0}}}),
    .greater1(comparatoru64bit_13_greater1), .equal1(comparatoru64bit_13_equal1));  // open: less1
  // Probe on subtractor64bit_13_output1
  // Probe on subtractor64bit_13_output1
  subtractor64bit subtractor64bit_14 (
    .input1(subtractor64bit_13_output1), .input2(cbuffer64bit_14_output1),
    .output1(subtractor64bit_14_output1));  // open: inborrow, borrow
  cbuffer64bit cbuffer64bit_14 (
    .buffer1(and_16_out[18]), .input1({{30{1'b0}}, input2, {18{1'b0}}}), .output1(cbuffer64bit_14_output1));
  and and_14 (and_16_out[18], not_1_out, or_14_out);
  or or_14 (or_14_out, comparatoru64bit_14_greater1, comparatoru64bit_14_equal1);
  comparatoru64bit comparatoru64bit_14 (
    .input1(subtractor64bit_13_output1), .input2({{30{1'b0}}, input2, {18{1'b0}}}),
    .greater1(comparatoru64bit_14_greater1), .equal1(comparatoru64bit_14_equal1));  // open: less1
  // Probe on subtractor64bit_14_output1
  // Probe on subtractor64bit_14_output1
  subtractor64bit subtractor64bit_15 (
    .input1(subtractor64bit_14_output1), .input2(cbuffer64bit_15_output1),
    .output1(subtractor64bit_15_output1));  // open: inborrow, borrow
  cbuffer64bit cbuffer64bit_15 (
    .buffer1(and_16_out[17]), .input1({{31{1'b0}}, input2, {17{1'b0}}}), .output1(cbuffer64bit_15_output1));
  and and_15 (and_16_out[17], not_1_out, or_15_out);
  or or_15 (or_15_out, comparatoru64bit_15_greater1, comparatoru64bit_15_equal1);
  comparatoru64bit comparatoru64bit_15 (
    .input1(subtractor64bit_14_output1), .input2({{31{1'b0}}, input2, {17{1'b0}}}),
    .greater1(comparatoru64bit_15_greater1), .equal1(comparatoru64bit_15_equal1));  // open: less1
  // Probe on subtractor64bit_15_output1
  // Probe on subtractor64bit_15_output1
  subtractor64bit subtractor64bit_16 (
    .input1(subtractor64bit_15_output1), .input2(cbuffer64bit_16_output1),
    .output1(subtractor64bit_16_output1));  // open: inborrow, borrow
  cbuffer64bit cbuffer64bit_16 (
    .buffer1(and_16_out[16]), .input1({{32{1'b0}}, input2, {16{1'b0}}}), .output1(cbuffer64bit_16_output1));
  and and_16 (and_16_out[16], not_1_out, or_16_out);
  or or_16 (or_16_out, comparatoru64bit_16_greater1, comparatoru64bit_16_equal1);
  comparatoru64bit comparatoru64bit_16 (
    .input1(subtractor64bit_15_output1), .input2({{32{1'b0}}, input2, {16{1'b0}}}),
    .greater1(comparatoru64bit_16_greater1), .equal1(comparatoru64bit_16_equal1));  // open: less1
  // Probe on subtractor64bit_16_output1
  // Probe on subtractor64bit_16_output1
  subtractor64bit subtractor64bit_17 (
    .input1(subtractor64bit_16_output1), .input2(cbuffer64bit_17_output1),
    .output1(subtractor64bit_17_output1));  // open: inborrow, borrow
  cbuffer64bit cbuffer64bit_17 (
    .buffer1(output1[15]), .input1({{33{1'b0}}, input2, {15{1'b0}}}), .output1(cbuffer64bit_17_output1));
  and and_17 (output1[15], not_1_out, or_17_out);
  or or_17 (or_17_out, comparatoru64bit_17_greater1, comparatoru64bit_17_equal1);
  comparatoru64bit comparatoru64bit_17 (
    .input1(subtractor64bit_16_output1), .input2({{33{1'b0}}, input2, {15{1'b0}}}),
    .greater1(comparatoru64bit_17_greater1), .equal1(comparatoru64bit_17_equal1));  // open: less1
  // Probe on subtractor64bit_17_output1
  // Probe on subtractor64bit_17_output1
  subtractor64bit subtractor64bit_18 (
    .input1(subtractor64bit_17_output1), .input2(cbuffer64bit_18_output1),
    .output1(subtractor64bit_18_output1));  // open: inborrow, borrow
  cbuffer64bit cbuffer64bit_18 (
    .buffer1(output1[14]), .input1({{34{1'b0}}, input2, {14{1'b0}}}), .output1(cbuffer64bit_18_output1));
  and and_18 (output1[14], not_1_out, or_18_out);
  or or_18 (or_18_out, comparatoru64bit_18_greater1, comparatoru64bit_18_equal1);
  comparatoru64bit comparatoru64bit_18 (
    .input1(subtractor64bit_17_output1), .input2({{34{1'b0}}, input2, {14{1'b0}}}),
    .greater1(comparatoru64bit_18_greater1), .equal1(comparatoru64bit_18_equal1));  // open: less1
  // Probe on subtractor64bit_18_output1
  // Probe on subtractor64bit_18_output1
  subtractor64bit subtractor64bit_19 (
    .input1(subtractor64bit_18_output1), .input2(cbuffer64bit_19_output1),
    .output1(subtractor64bit_19_output1));  // open: inborrow, borrow
  cbuffer64bit cbuffer64bit_19 (
    .buffer1(output1[13]), .input1({{35{1'b0}}, input2, {13{1'b0}}}), .output1(cbuffer64bit_19_output1));
  and and_19 (output1[13], not_1_out, or_19_out);
  or or_19 (or_19_out, comparatoru64bit_19_greater1, comparatoru64bit_19_equal1);
  comparatoru64bit comparatoru64bit_19 (
    .input1(subtractor64bit_18_output1), .input2({{35{1'b0}}, input2, {13{1'b0}}}),
    .greater1(comparatoru64bit_19_greater1), .equal1(comparatoru64bit_19_equal1));  // open: less1
  // Probe on subtractor64bit_19_output1
  // Probe on subtractor64bit_19_output1
  subtractor64bit subtractor64bit_20 (
    .input1(subtractor64bit_19_output1), .input2(cbuffer64bit_20_output1),
    .output1(subtractor64bit_20_output1));  // open: inborrow, borrow
  cbuffer64bit cbuffer64bit_20 (
    .buffer1(output1[12]), .input1({{36{1'b0}}, input2, {12{1'b0}}}), .output1(cbuffer64bit_20_output1));
  and and_20 (output1[12], not_1_out, or_20_out);
  or or_20 (or_20_out, comparatoru64bit_20_greater1, comparatoru64bit_20_equal1);
  comparatoru64bit comparatoru64bit_20 (
    .input1(subtractor64bit_19_output1), .input2({{36{1'b0}}, input2, {12{1'b0}}}),
    .greater1(comparatoru64bit_20_greater1), .equal1(comparatoru64bit_20_equal1));  // open: less1
  // Probe on subtractor64bit_20_output1
  // Probe on subtractor64bit_20_output1
  subtractor64bit subtractor64bit_21 (
    .input1(subtractor64bit_20_output1), .input2(cbuffer64bit_21_output1),
    .output1(subtractor64bit_21_output1));  // open: inborrow, borrow
  cbuffer64bit cbuffer64bit_21 (
    .buffer1(output1[11]), .input1({{37{1'b0}}, input2, {11{1'b0}}}), .output1(cbuffer64bit_21_output1));
  and and_21 (output1[11], not_1_out, or_21_out);
  or or_21 (or_21_out, comparatoru64bit_21_greater1, comparatoru64bit_21_equal1);
  comparatoru64bit comparatoru64bit_21 (
    .input1(subtractor64bit_20_output1), .input2({{37{1'b0}}, input2, {11{1'b0}}}),
    .greater1(comparatoru64bit_21_greater1), .equal1(comparatoru64bit_21_equal1));  // open: less1
  // Probe on subtractor64bit_21_output1
  // Probe on subtractor64bit_21_output1
  subtractor64bit subtractor64bit_22 (
    .input1(subtractor64bit_21_output1), .input2(cbuffer64bit_22_output1),
    .output1(subtractor64bit_22_output1));  // open: inborrow, borrow
  cbuffer64bit cbuffer64bit_22 (
    .buffer1(output1[10]), .input1({{38{1'b0}}, input2, {10{1'b0}}}), .output1(cbuffer64bit_22_output1));
  and and_22 (output1[10], not_1_out, or_22_out);
  or or_22 (or_22_out, comparatoru64bit_22_greater1, comparatoru64bit_22_equal1);
  comparatoru64bit comparatoru64bit_22 (
    .input1(subtractor64bit_21_output1), .input2({{38{1'b0}}, input2, {10{1'b0}}}),
    .greater1(comparatoru64bit_22_greater1), .equal1(comparatoru64bit_22_equal1));  // open: less1
  // Probe on subtractor64bit_22_output1
  // Probe on subtractor64bit_22_output1
  subtractor64bit subtractor64bit_23 (
    .input1(subtractor64bit_22_output1), .input2(cbuffer64bit_23_output1),
    .output1(subtractor64bit_23_output1));  // open: inborrow, borrow
  cbuffer64bit cbuffer64bit_23 (
    .buffer1(output1[9]), .input1({{39{1'b0}}, input2, {9{1'b0}}}), .output1(cbuffer64bit_23_output1));
  and and_23 (output1[9], not_1_out, or_23_out);
  or or_23 (or_23_out, comparatoru64bit_23_greater1, comparatoru64bit_23_equal1);
  comparatoru64bit comparatoru64bit_23 (
    .input1(subtractor64bit_22_output1), .input2({{39{1'b0}}, input2, {9{1'b0}}}),
    .greater1(comparatoru64bit_23_greater1), .equal1(comparatoru64bit_23_equal1));  // open: less1
  // Probe on subtractor64bit_23_output1
  // Probe on subtractor64bit_23_output1
  subtractor64bit subtractor64bit_24 (
    .input1(subtractor64bit_23_output1), .input2(cbuffer64bit_24_output1),
    .output1(subtractor64bit_24_output1));  // open: inborrow, borrow
  cbuffer64bit cbuffer64bit_24 (
    .buffer1(output1[8]), .input1({{40{1'b0}}, input2, {8{1'b0}}}), .output1(cbuffer64bit_24_output1));
  and and_24 (output1[8], not_1_out, or_24_out);
  or or_24 (or_24_out, comparatoru64bit_24_greater1, comparatoru64bit_24_equal1);
  comparatoru64bit comparatoru64bit_24 (
    .input1(subtractor64bit_23_output1), .input2({{40{1'b0}}, input2, {8{1'b0}}}),
    .greater1(comparatoru64bit_24_greater1), .equal1(comparatoru64bit_24_equal1));  // open: less1
  // Probe on subtractor64bit_24_output1
  // Probe on subtractor64bit_24_output1
  subtractor64bit subtractor64bit_25 (
    .input1(subtractor64bit_24_output1), .input2(cbuffer64bit_25_output1),
    .output1(subtractor64bit_25_output1));  // open: inborrow, borrow
  cbuffer64bit cbuffer64bit_25 (
    .buffer1(output1[7]), .input1({{41{1'b0}}, input2, {7{1'b0}}}), .output1(cbuffer64bit_25_output1));
  and and_25 (output1[7], not_1_out, or_25_out);
  or or_25 (or_25_out, comparatoru64bit_25_greater1, comparatoru64bit_25_equal1);
  comparatoru64bit comparatoru64bit_25 (
    .input1(subtractor64bit_24_output1), .input2({{41{1'b0}}, input2, {7{1'b0}}}),
    .greater1(comparatoru64bit_25_greater1), .equal1(comparatoru64bit_25_equal1));  // open: less1
  // Probe on subtractor64bit_25_output1
  // Probe on subtractor64bit_25_output1
  subtractor64bit subtractor64bit_26 (
    .input1(subtractor64bit_25_output1), .input2(cbuffer64bit_26_output1),
    .output1(subtractor64bit_26_output1));  // open: inborrow, borrow
  cbuffer64bit cbuffer64bit_26 (
    .buffer1(output1[6]), .input1({{42{1'b0}}, input2, {6{1'b0}}}), .output1(cbuffer64bit_26_output1));
  and and_26 (output1[6], not_1_out, or_26_out);
  or or_26 (or_26_out, comparatoru64bit_26_greater1, comparatoru64bit_26_equal1);
  comparatoru64bit comparatoru64bit_26 (
    .input1(subtractor64bit_25_output1), .input2({{42{1'b0}}, input2, {6{1'b0}}}),
    .greater1(comparatoru64bit_26_greater1), .equal1(comparatoru64bit_26_equal1));  // open: less1
  // Probe on subtractor64bit_26_output1
  // Probe on subtractor64bit_26_output1
  subtractor64bit subtractor64bit_27 (
    .input1(subtractor64bit_26_output1), .input2(cbuffer64bit_27_output1),
    .output1(subtractor64bit_27_output1));  // open: inborrow, borrow
  cbuffer64bit cbuffer64bit_27 (
    .buffer1(output1[5]), .input1({{43{1'b0}}, input2, {5{1'b0}}}), .output1(cbuffer64bit_27_output1));
  and and_27 (output1[5], not_1_out, or_27_out);
  or or_27 (or_27_out, comparatoru64bit_27_greater1, comparatoru64bit_27_equal1);
  comparatoru64bit comparatoru64bit_27 (
    .input1(subtractor64bit_26_output1), .input2({{43{1'b0}}, input2, {5{1'b0}}}),
    .greater1(comparatoru64bit_27_greater1), .equal1(comparatoru64bit_27_equal1));  // open: less1
  // Probe on subtractor64bit_27_output1
  // Probe on subtractor64bit_27_output1
  subtractor64bit subtractor64bit_28 (
    .input1(subtractor64bit_27_output1), .input2(cbuffer64bit_28_output1),
    .output1(subtractor64bit_28_output1));  // open: inborrow, borrow
  cbuffer64bit cbuffer64bit_28 (
    .buffer1(output1[4]), .input1({{44{1'b0}}, input2, 4'b0000}), .output1(cbuffer64bit_28_output1));
  and and_28 (output1[4], not_1_out, or_28_out);
  or or_28 (or_28_out, comparatoru64bit_28_greater1, comparatoru64bit_28_equal1);
  comparatoru64bit comparatoru64bit_28 (
    .input1(subtractor64bit_27_output1), .input2({{44{1'b0}}, input2, 4'b0000}),
    .greater1(comparatoru64bit_28_greater1), .equal1(comparatoru64bit_28_equal1));  // open: less1
  // Probe on subtractor64bit_28_output1
  // Probe on subtractor64bit_28_output1
  subtractor64bit subtractor64bit_29 (
    .input1(subtractor64bit_28_output1), .input2(cbuffer64bit_29_output1),
    .output1(subtractor64bit_29_output1));  // open: inborrow, borrow
  cbuffer64bit cbuffer64bit_29 (
    .buffer1(output1[3]), .input1({{45{1'b0}}, input2, 3'b000}), .output1(cbuffer64bit_29_output1));
  and and_29 (output1[3], not_1_out, or_29_out);
  or or_29 (or_29_out, comparatoru64bit_29_greater1, comparatoru64bit_29_equal1);
  comparatoru64bit comparatoru64bit_29 (
    .input1(subtractor64bit_28_output1), .input2({{45{1'b0}}, input2, 3'b000}),
    .greater1(comparatoru64bit_29_greater1), .equal1(comparatoru64bit_29_equal1));  // open: less1
  // Probe on subtractor64bit_29_output1
  // Probe on subtractor64bit_29_output1
  subtractor64bit subtractor64bit_30 (
    .input1(subtractor64bit_29_output1), .input2(cbuffer64bit_30_output1),
    .output1(subtractor64bit_30_output1));  // open: inborrow, borrow
  cbuffer64bit cbuffer64bit_30 (
    .buffer1(output1[2]), .input1({{46{1'b0}}, input2, 2'b00}), .output1(cbuffer64bit_30_output1));
  and and_30 (output1[2], not_1_out, or_30_out);
  or or_30 (or_30_out, comparatoru64bit_30_greater1, comparatoru64bit_30_equal1);
  comparatoru64bit comparatoru64bit_30 (
    .input1(subtractor64bit_29_output1), .input2({{46{1'b0}}, input2, 2'b00}),
    .greater1(comparatoru64bit_30_greater1), .equal1(comparatoru64bit_30_equal1));  // open: less1
  // Probe on subtractor64bit_30_output1
  // Probe on subtractor64bit_30_output1
  subtractor64bit subtractor64bit_31 (
    .input1(subtractor64bit_30_output1), .input2(cbuffer64bit_31_output1),
    .output1(subtractor64bit_31_output1));  // open: inborrow, borrow
  cbuffer64bit cbuffer64bit_31 (
    .buffer1(output1[1]), .input1({{47{1'b0}}, input2, 1'b0}), .output1(cbuffer64bit_31_output1));
  and and_31 (output1[1], not_1_out, or_31_out);
  or or_31 (or_31_out, comparatoru64bit_31_greater1, comparatoru64bit_31_equal1);
  comparatoru64bit comparatoru64bit_31 (
    .input1(subtractor64bit_30_output1), .input2({{47{1'b0}}, input2, 1'b0}),
    .greater1(comparatoru64bit_31_greater1), .equal1(comparatoru64bit_31_equal1));  // open: less1
  // Probe on subtractor64bit_31_output1
  // Probe on subtractor64bit_31_output1
  subtractor64bit subtractor64bit_32 (
    .input1(subtractor64bit_31_output1), .input2(cbuffer64bit_32_output1),
    .output1({subtractor64bit_32_output1, remainder}));  // open: inborrow, borrow
  cbuffer64bit cbuffer64bit_32 (.buffer1(output1[0]), .input1({{48{1'b0}}, input2}), .output1(cbuffer64bit_32_output1));
  and and_32 (output1[0], not_1_out, or_32_out);
  or or_32 (or_32_out, comparatoru64bit_32_greater1, comparatoru64bit_32_equal1);
  comparatoru64bit comparatoru64bit_32 (
    .input1(subtractor64bit_31_output1), .input2({{48{1'b0}}, input2}),
    .greater1(comparatoru64bit_32_greater1), .equal1(comparatoru64bit_32_equal1));  // open: less1
  // Probe on {subtractor64bit_32_output1, remainder}
  // Probe on {subtractor64bit_32_output1, remainder}
  // Probe on {and_16_out, output1}
  // Probe on {and_16_out, output1}
  // Probe on remainder
  // Probe on remainder
  // Probe on output1
  // Probe on output1

  // Notes on the sheet:
  //   input2: initial=0xb7a
  //   inupper: initial=0xfedc
  //   input1: initial=0xfa3d
endmodule
module divideru32bit (
  input  [31:0] inupper,
  input  [31:0] input1,
  input  [31:0] input2,
  output [31:0] remainder,
  output [31:0] output1
);

  wire comparatoru32bit_1_equal1, comparatoru128bit_1_equal1, comparatoru128bit_1_greater1,
       comparatoru128bit_2_equal1, comparatoru128bit_2_greater1, comparatoru128bit_3_equal1,
       comparatoru128bit_3_greater1, comparatoru128bit_4_equal1, comparatoru128bit_4_greater1,
       comparatoru128bit_5_equal1, comparatoru128bit_5_greater1, comparatoru128bit_6_equal1,
       comparatoru128bit_6_greater1, comparatoru128bit_7_equal1, comparatoru128bit_7_greater1,
       comparatoru128bit_8_equal1, comparatoru128bit_8_greater1, comparatoru128bit_9_equal1,
       comparatoru128bit_9_greater1, comparatoru128bit_10_equal1, comparatoru128bit_10_greater1,
       comparatoru128bit_11_equal1, comparatoru128bit_11_greater1, comparatoru128bit_12_equal1,
       comparatoru128bit_12_greater1, comparatoru128bit_13_equal1, comparatoru128bit_13_greater1,
       comparatoru128bit_14_equal1, comparatoru128bit_14_greater1, comparatoru128bit_15_equal1,
       comparatoru128bit_15_greater1, comparatoru128bit_16_equal1, comparatoru128bit_16_greater1,
       comparatoru128bit_17_equal1, comparatoru128bit_17_greater1, comparatoru128bit_18_equal1,
       comparatoru128bit_18_greater1, comparatoru128bit_19_equal1, comparatoru128bit_19_greater1,
       comparatoru128bit_20_equal1, comparatoru128bit_20_greater1, comparatoru128bit_21_equal1,
       comparatoru128bit_21_greater1, comparatoru128bit_22_equal1, comparatoru128bit_22_greater1,
       comparatoru128bit_23_equal1, comparatoru128bit_23_greater1, comparatoru128bit_24_equal1,
       comparatoru128bit_24_greater1, comparatoru128bit_25_equal1, comparatoru128bit_25_greater1,
       comparatoru128bit_26_equal1, comparatoru128bit_26_greater1, comparatoru128bit_27_equal1,
       comparatoru128bit_27_greater1, comparatoru128bit_28_equal1, comparatoru128bit_28_greater1,
       comparatoru128bit_29_equal1, comparatoru128bit_29_greater1, comparatoru128bit_30_equal1,
       comparatoru128bit_30_greater1, comparatoru128bit_31_equal1, comparatoru128bit_31_greater1,
       comparatoru128bit_32_equal1, comparatoru128bit_32_greater1, comparatoru128bit_33_equal1,
       comparatoru128bit_33_greater1, comparatoru128bit_34_equal1, comparatoru128bit_34_greater1,
       comparatoru128bit_35_equal1, comparatoru128bit_35_greater1, comparatoru128bit_36_equal1,
       comparatoru128bit_36_greater1, comparatoru128bit_37_equal1, comparatoru128bit_37_greater1,
       comparatoru128bit_38_equal1, comparatoru128bit_38_greater1, comparatoru128bit_39_equal1,
       comparatoru128bit_39_greater1, comparatoru128bit_40_equal1, comparatoru128bit_40_greater1,
       comparatoru128bit_41_equal1, comparatoru128bit_41_greater1, comparatoru128bit_42_equal1,
       comparatoru128bit_42_greater1, comparatoru128bit_43_equal1, comparatoru128bit_43_greater1,
       comparatoru128bit_44_equal1, comparatoru128bit_44_greater1, comparatoru128bit_45_equal1,
       comparatoru128bit_45_greater1, comparatoru128bit_46_equal1, comparatoru128bit_46_greater1,
       comparatoru128bit_47_equal1, comparatoru128bit_47_greater1, comparatoru128bit_48_equal1,
       comparatoru128bit_48_greater1, comparatoru128bit_49_equal1, comparatoru128bit_49_greater1,
       comparatoru128bit_50_equal1, comparatoru128bit_50_greater1, comparatoru128bit_51_equal1,
       comparatoru128bit_51_greater1, comparatoru128bit_52_equal1, comparatoru128bit_52_greater1,
       comparatoru128bit_53_equal1, comparatoru128bit_53_greater1, comparatoru128bit_54_equal1,
       comparatoru128bit_54_greater1, comparatoru128bit_55_equal1, comparatoru128bit_55_greater1,
       comparatoru128bit_56_equal1, comparatoru128bit_56_greater1, comparatoru128bit_57_equal1,
       comparatoru128bit_57_greater1, comparatoru128bit_58_equal1, comparatoru128bit_58_greater1,
       comparatoru128bit_59_equal1, comparatoru128bit_59_greater1, comparatoru128bit_60_equal1,
       comparatoru128bit_60_greater1, comparatoru128bit_61_equal1, comparatoru128bit_61_greater1,
       comparatoru128bit_62_equal1, comparatoru128bit_62_greater1, comparatoru128bit_63_equal1,
       comparatoru128bit_63_greater1, comparatoru128bit_64_equal1, comparatoru128bit_64_greater1, not_1_out,
       or_1_out, or_2_out, or_3_out, or_4_out, or_5_out, or_6_out, or_7_out, or_8_out, or_9_out, or_10_out,
       or_11_out, or_12_out, or_13_out, or_14_out, or_15_out, or_16_out, or_17_out, or_18_out, or_19_out,
       or_20_out, or_21_out, or_22_out, or_23_out, or_24_out, or_25_out, or_26_out, or_27_out, or_28_out,
       or_29_out, or_30_out, or_31_out, or_32_out, or_33_out, or_34_out, or_35_out, or_36_out, or_37_out,
       or_38_out, or_39_out, or_40_out, or_41_out, or_42_out, or_43_out, or_44_out, or_45_out, or_46_out,
       or_47_out, or_48_out, or_49_out, or_50_out, or_51_out, or_52_out, or_53_out, or_54_out, or_55_out,
       or_56_out, or_57_out, or_58_out, or_59_out, or_60_out, or_61_out, or_62_out, or_63_out, or_64_out;
  wire [31:0] divider_1_out, divider_1_rem;
  wire [63:0] cbuffer128bit_1_output1a, cbuffer128bit_1_output1b, cbuffer128bit_2_output1a,
       cbuffer128bit_2_output1b, cbuffer128bit_3_output1a, cbuffer128bit_3_output1b,
       cbuffer128bit_4_output1a, cbuffer128bit_4_output1b, cbuffer128bit_5_output1a,
       cbuffer128bit_5_output1b, cbuffer128bit_6_output1a, cbuffer128bit_6_output1b,
       cbuffer128bit_7_output1a, cbuffer128bit_7_output1b, cbuffer128bit_8_output1a,
       cbuffer128bit_8_output1b, cbuffer128bit_9_output1a, cbuffer128bit_9_output1b,
       cbuffer128bit_10_output1a, cbuffer128bit_10_output1b, cbuffer128bit_11_output1a,
       cbuffer128bit_11_output1b, cbuffer128bit_12_output1a, cbuffer128bit_12_output1b,
       cbuffer128bit_13_output1a, cbuffer128bit_13_output1b, cbuffer128bit_14_output1a,
       cbuffer128bit_14_output1b, cbuffer128bit_15_output1a, cbuffer128bit_15_output1b,
       cbuffer128bit_16_output1a, cbuffer128bit_16_output1b, cbuffer128bit_17_output1a,
       cbuffer128bit_17_output1b, cbuffer128bit_18_output1a, cbuffer128bit_18_output1b,
       cbuffer128bit_19_output1a, cbuffer128bit_19_output1b, cbuffer128bit_20_output1a,
       cbuffer128bit_20_output1b, cbuffer128bit_21_output1a, cbuffer128bit_21_output1b,
       cbuffer128bit_22_output1a, cbuffer128bit_22_output1b, cbuffer128bit_23_output1a,
       cbuffer128bit_23_output1b, cbuffer128bit_24_output1a, cbuffer128bit_24_output1b,
       cbuffer128bit_25_output1a, cbuffer128bit_25_output1b, cbuffer128bit_26_output1a,
       cbuffer128bit_26_output1b, cbuffer128bit_27_output1a, cbuffer128bit_27_output1b,
       cbuffer128bit_28_output1a, cbuffer128bit_28_output1b, cbuffer128bit_29_output1a,
       cbuffer128bit_29_output1b, cbuffer128bit_30_output1a, cbuffer128bit_30_output1b,
       cbuffer128bit_31_output1a, cbuffer128bit_31_output1b, cbuffer128bit_32_output1a,
       cbuffer128bit_32_output1b, cbuffer128bit_33_output1a, cbuffer128bit_33_output1b,
       cbuffer128bit_34_output1a, cbuffer128bit_34_output1b, cbuffer128bit_35_output1a,
       cbuffer128bit_35_output1b, cbuffer128bit_36_output1a, cbuffer128bit_36_output1b,
       cbuffer128bit_37_output1a, cbuffer128bit_37_output1b, cbuffer128bit_38_output1a,
       cbuffer128bit_38_output1b, cbuffer128bit_39_output1a, cbuffer128bit_39_output1b,
       cbuffer128bit_40_output1a, cbuffer128bit_40_output1b, cbuffer128bit_41_output1a,
       cbuffer128bit_41_output1b, cbuffer128bit_42_output1a, cbuffer128bit_42_output1b,
       cbuffer128bit_43_output1a, cbuffer128bit_43_output1b, cbuffer128bit_44_output1a,
       cbuffer128bit_44_output1b, cbuffer128bit_45_output1a, cbuffer128bit_45_output1b,
       cbuffer128bit_46_output1a, cbuffer128bit_46_output1b, cbuffer128bit_47_output1a,
       cbuffer128bit_47_output1b, cbuffer128bit_48_output1a, cbuffer128bit_48_output1b,
       cbuffer128bit_49_output1a, cbuffer128bit_49_output1b, cbuffer128bit_50_output1a,
       cbuffer128bit_50_output1b, cbuffer128bit_51_output1a, cbuffer128bit_51_output1b,
       cbuffer128bit_52_output1a, cbuffer128bit_52_output1b, cbuffer128bit_53_output1a,
       cbuffer128bit_53_output1b, cbuffer128bit_54_output1a, cbuffer128bit_54_output1b,
       cbuffer128bit_55_output1a, cbuffer128bit_55_output1b, cbuffer128bit_56_output1a,
       cbuffer128bit_56_output1b, cbuffer128bit_57_output1a, cbuffer128bit_57_output1b,
       cbuffer128bit_58_output1a, cbuffer128bit_58_output1b, cbuffer128bit_59_output1a,
       cbuffer128bit_59_output1b, cbuffer128bit_60_output1a, cbuffer128bit_60_output1b,
       cbuffer128bit_61_output1a, cbuffer128bit_61_output1b, cbuffer128bit_62_output1a,
       cbuffer128bit_62_output1b, cbuffer128bit_63_output1a, cbuffer128bit_63_output1b,
       cbuffer128bit_64_output1a, cbuffer128bit_64_output1b, subtractor128bit_1_output1a,
       subtractor128bit_1_output1b, subtractor128bit_2_output1a, subtractor128bit_2_output1b,
       subtractor128bit_3_output1a, subtractor128bit_3_output1b, subtractor128bit_4_output1a,
       subtractor128bit_4_output1b, subtractor128bit_5_output1a, subtractor128bit_5_output1b,
       subtractor128bit_6_output1a, subtractor128bit_6_output1b, subtractor128bit_7_output1a,
       subtractor128bit_7_output1b, subtractor128bit_8_output1a, subtractor128bit_8_output1b,
       subtractor128bit_9_output1a, subtractor128bit_9_output1b, subtractor128bit_10_output1a,
       subtractor128bit_10_output1b, subtractor128bit_11_output1a, subtractor128bit_11_output1b,
       subtractor128bit_12_output1a, subtractor128bit_12_output1b, subtractor128bit_13_output1a,
       subtractor128bit_13_output1b, subtractor128bit_14_output1a, subtractor128bit_14_output1b,
       subtractor128bit_15_output1a, subtractor128bit_15_output1b, subtractor128bit_16_output1a,
       subtractor128bit_16_output1b, subtractor128bit_17_output1a, subtractor128bit_17_output1b,
       subtractor128bit_18_output1a, subtractor128bit_18_output1b, subtractor128bit_19_output1a,
       subtractor128bit_19_output1b, subtractor128bit_20_output1a, subtractor128bit_20_output1b,
       subtractor128bit_21_output1a, subtractor128bit_21_output1b, subtractor128bit_22_output1a,
       subtractor128bit_22_output1b, subtractor128bit_23_output1a, subtractor128bit_23_output1b,
       subtractor128bit_24_output1a, subtractor128bit_24_output1b, subtractor128bit_25_output1a,
       subtractor128bit_25_output1b, subtractor128bit_26_output1a, subtractor128bit_26_output1b,
       subtractor128bit_27_output1a, subtractor128bit_27_output1b, subtractor128bit_28_output1a,
       subtractor128bit_28_output1b, subtractor128bit_29_output1a, subtractor128bit_29_output1b,
       subtractor128bit_30_output1a, subtractor128bit_30_output1b, subtractor128bit_31_output1a,
       subtractor128bit_31_output1b, subtractor128bit_32_output1a, subtractor128bit_32_output1b,
       subtractor128bit_33_output1a, subtractor128bit_33_output1b, subtractor128bit_34_output1a,
       subtractor128bit_34_output1b, subtractor128bit_35_output1a, subtractor128bit_35_output1b,
       subtractor128bit_36_output1a, subtractor128bit_36_output1b, subtractor128bit_37_output1a,
       subtractor128bit_37_output1b, subtractor128bit_38_output1a, subtractor128bit_38_output1b,
       subtractor128bit_39_output1a, subtractor128bit_39_output1b, subtractor128bit_40_output1a,
       subtractor128bit_40_output1b, subtractor128bit_41_output1a, subtractor128bit_41_output1b,
       subtractor128bit_42_output1a, subtractor128bit_42_output1b, subtractor128bit_43_output1a,
       subtractor128bit_43_output1b, subtractor128bit_44_output1a, subtractor128bit_44_output1b,
       subtractor128bit_45_output1a, subtractor128bit_45_output1b, subtractor128bit_46_output1a,
       subtractor128bit_46_output1b, subtractor128bit_47_output1a, subtractor128bit_47_output1b,
       subtractor128bit_48_output1a, subtractor128bit_48_output1b, subtractor128bit_49_output1a,
       subtractor128bit_49_output1b, subtractor128bit_50_output1a, subtractor128bit_50_output1b,
       subtractor128bit_51_output1a, subtractor128bit_51_output1b, subtractor128bit_52_output1a,
       subtractor128bit_52_output1b, subtractor128bit_53_output1a, subtractor128bit_53_output1b,
       subtractor128bit_54_output1a, subtractor128bit_54_output1b, subtractor128bit_55_output1a,
       subtractor128bit_55_output1b, subtractor128bit_56_output1a, subtractor128bit_56_output1b,
       subtractor128bit_57_output1a, subtractor128bit_57_output1b, subtractor128bit_58_output1a,
       subtractor128bit_58_output1b, subtractor128bit_59_output1a, subtractor128bit_59_output1b,
       subtractor128bit_60_output1a, subtractor128bit_60_output1b, subtractor128bit_61_output1a,
       subtractor128bit_61_output1b, subtractor128bit_62_output1a, subtractor128bit_62_output1b,
       subtractor128bit_63_output1a, subtractor128bit_63_output1b, subtractor128bit_64_output1b;
  wire [63:32] and_32_out, subtractor128bit_64_output1a;

  // Probe on inupper
  // Probe on inupper
  // Probe on input1
  // Probe on input1
  // Probe on divider_1_out
  // Probe on divider_1_out
  Divider #(.width(32)) divider_1 (.a(input1), .b(input2), .out(divider_1_out), .upper(inupper), .rem(divider_1_rem));
  // Probe on divider_1_rem
  // Probe on divider_1_rem
  not not_1 (not_1_out, comparatoru32bit_1_equal1);
  comparatoru32bit comparatoru32bit_1 (
    .input1(input2), .input2({32{1'b0}}), .equal1(comparatoru32bit_1_equal1));  // open: greater1, less1
  // Probe on input2
  // Probe on input2
  // Probe on {inupper, input1}
  // Probe on {inupper, input1}
  subtractor128bit subtractor128bit_1 (
    .input1a({inupper, input1}), .input1b({64{1'b0}}), .input2a(cbuffer128bit_1_output1a),
    .input2b(cbuffer128bit_1_output1b), .output1a(subtractor128bit_1_output1a),
    .output1b(subtractor128bit_1_output1b));  // open: inborrow, borrow
  cbuffer128bit cbuffer128bit_1 (
    .buffer1(and_32_out[63]), .input1a({input2[0], {63{1'b0}}}), .input1b({{33{1'b0}}, input2[31:1]}),
    .output1a(cbuffer128bit_1_output1a), .output1b(cbuffer128bit_1_output1b));
  and and_1 (and_32_out[63], not_1_out, or_1_out);
  or or_1 (or_1_out, comparatoru128bit_1_greater1, comparatoru128bit_1_equal1);
  comparatoru128bit comparatoru128bit_1 (
    .input1a({inupper, input1}), .input1b({64{1'b0}}), .input2a({input2[0], {63{1'b0}}}),
    .input2b({{33{1'b0}}, input2[31:1]}), .greater1(comparatoru128bit_1_greater1),
    .equal1(comparatoru128bit_1_equal1));  // open: less1
  // Probe on subtractor128bit_1_output1a
  // Probe on subtractor128bit_1_output1a
  subtractor128bit subtractor128bit_2 (
    .input1a(subtractor128bit_1_output1a), .input1b(subtractor128bit_1_output1b),
    .input2a(cbuffer128bit_2_output1a), .input2b(cbuffer128bit_2_output1b),
    .output1a(subtractor128bit_2_output1a), .output1b(subtractor128bit_2_output1b));  // open: inborrow, borrow
  cbuffer128bit cbuffer128bit_2 (
    .buffer1(and_32_out[62]), .input1a({input2[1:0], {62{1'b0}}}), .input1b({{34{1'b0}}, input2[31:2]}),
    .output1a(cbuffer128bit_2_output1a), .output1b(cbuffer128bit_2_output1b));
  and and_2 (and_32_out[62], not_1_out, or_2_out);
  or or_2 (or_2_out, comparatoru128bit_2_greater1, comparatoru128bit_2_equal1);
  comparatoru128bit comparatoru128bit_2 (
    .input1a(subtractor128bit_1_output1a), .input1b(subtractor128bit_1_output1b),
    .input2a({input2[1:0], {62{1'b0}}}), .input2b({{34{1'b0}}, input2[31:2]}),
    .greater1(comparatoru128bit_2_greater1), .equal1(comparatoru128bit_2_equal1));  // open: less1
  // Probe on subtractor128bit_2_output1a
  // Probe on subtractor128bit_2_output1a
  subtractor128bit subtractor128bit_3 (
    .input1a(subtractor128bit_2_output1a), .input1b(subtractor128bit_2_output1b),
    .input2a(cbuffer128bit_3_output1a), .input2b(cbuffer128bit_3_output1b),
    .output1a(subtractor128bit_3_output1a), .output1b(subtractor128bit_3_output1b));  // open: inborrow, borrow
  cbuffer128bit cbuffer128bit_3 (
    .buffer1(and_32_out[61]), .input1a({input2[2:0], {61{1'b0}}}), .input1b({{35{1'b0}}, input2[31:3]}),
    .output1a(cbuffer128bit_3_output1a), .output1b(cbuffer128bit_3_output1b));
  and and_3 (and_32_out[61], not_1_out, or_3_out);
  or or_3 (or_3_out, comparatoru128bit_3_greater1, comparatoru128bit_3_equal1);
  comparatoru128bit comparatoru128bit_3 (
    .input1a(subtractor128bit_2_output1a), .input1b(subtractor128bit_2_output1b),
    .input2a({input2[2:0], {61{1'b0}}}), .input2b({{35{1'b0}}, input2[31:3]}),
    .greater1(comparatoru128bit_3_greater1), .equal1(comparatoru128bit_3_equal1));  // open: less1
  // Probe on subtractor128bit_3_output1a
  // Probe on subtractor128bit_3_output1a
  subtractor128bit subtractor128bit_4 (
    .input1a(subtractor128bit_3_output1a), .input1b(subtractor128bit_3_output1b),
    .input2a(cbuffer128bit_4_output1a), .input2b(cbuffer128bit_4_output1b),
    .output1a(subtractor128bit_4_output1a), .output1b(subtractor128bit_4_output1b));  // open: inborrow, borrow
  cbuffer128bit cbuffer128bit_4 (
    .buffer1(and_32_out[60]), .input1a({input2[3:0], {60{1'b0}}}), .input1b({{36{1'b0}}, input2[31:4]}),
    .output1a(cbuffer128bit_4_output1a), .output1b(cbuffer128bit_4_output1b));
  and and_4 (and_32_out[60], not_1_out, or_4_out);
  or or_4 (or_4_out, comparatoru128bit_4_greater1, comparatoru128bit_4_equal1);
  comparatoru128bit comparatoru128bit_4 (
    .input1a(subtractor128bit_3_output1a), .input1b(subtractor128bit_3_output1b),
    .input2a({input2[3:0], {60{1'b0}}}), .input2b({{36{1'b0}}, input2[31:4]}),
    .greater1(comparatoru128bit_4_greater1), .equal1(comparatoru128bit_4_equal1));  // open: less1
  // Probe on subtractor128bit_4_output1a
  // Probe on subtractor128bit_4_output1a
  subtractor128bit subtractor128bit_5 (
    .input1a(subtractor128bit_4_output1a), .input1b(subtractor128bit_4_output1b),
    .input2a(cbuffer128bit_5_output1a), .input2b(cbuffer128bit_5_output1b),
    .output1a(subtractor128bit_5_output1a), .output1b(subtractor128bit_5_output1b));  // open: inborrow, borrow
  cbuffer128bit cbuffer128bit_5 (
    .buffer1(and_32_out[59]), .input1a({input2[4:0], {59{1'b0}}}), .input1b({{37{1'b0}}, input2[31:5]}),
    .output1a(cbuffer128bit_5_output1a), .output1b(cbuffer128bit_5_output1b));
  and and_5 (and_32_out[59], not_1_out, or_5_out);
  or or_5 (or_5_out, comparatoru128bit_5_greater1, comparatoru128bit_5_equal1);
  comparatoru128bit comparatoru128bit_5 (
    .input1a(subtractor128bit_4_output1a), .input1b(subtractor128bit_4_output1b),
    .input2a({input2[4:0], {59{1'b0}}}), .input2b({{37{1'b0}}, input2[31:5]}),
    .greater1(comparatoru128bit_5_greater1), .equal1(comparatoru128bit_5_equal1));  // open: less1
  // Probe on subtractor128bit_5_output1a
  // Probe on subtractor128bit_5_output1a
  subtractor128bit subtractor128bit_6 (
    .input1a(subtractor128bit_5_output1a), .input1b(subtractor128bit_5_output1b),
    .input2a(cbuffer128bit_6_output1a), .input2b(cbuffer128bit_6_output1b),
    .output1a(subtractor128bit_6_output1a), .output1b(subtractor128bit_6_output1b));  // open: inborrow, borrow
  cbuffer128bit cbuffer128bit_6 (
    .buffer1(and_32_out[58]), .input1a({input2[5:0], {58{1'b0}}}), .input1b({{38{1'b0}}, input2[31:6]}),
    .output1a(cbuffer128bit_6_output1a), .output1b(cbuffer128bit_6_output1b));
  and and_6 (and_32_out[58], not_1_out, or_6_out);
  or or_6 (or_6_out, comparatoru128bit_6_greater1, comparatoru128bit_6_equal1);
  comparatoru128bit comparatoru128bit_6 (
    .input1a(subtractor128bit_5_output1a), .input1b(subtractor128bit_5_output1b),
    .input2a({input2[5:0], {58{1'b0}}}), .input2b({{38{1'b0}}, input2[31:6]}),
    .greater1(comparatoru128bit_6_greater1), .equal1(comparatoru128bit_6_equal1));  // open: less1
  // Probe on subtractor128bit_6_output1a
  // Probe on subtractor128bit_6_output1a
  subtractor128bit subtractor128bit_7 (
    .input1a(subtractor128bit_6_output1a), .input1b(subtractor128bit_6_output1b),
    .input2a(cbuffer128bit_7_output1a), .input2b(cbuffer128bit_7_output1b),
    .output1a(subtractor128bit_7_output1a), .output1b(subtractor128bit_7_output1b));  // open: inborrow, borrow
  cbuffer128bit cbuffer128bit_7 (
    .buffer1(and_32_out[57]), .input1a({input2[6:0], {57{1'b0}}}), .input1b({{39{1'b0}}, input2[31:7]}),
    .output1a(cbuffer128bit_7_output1a), .output1b(cbuffer128bit_7_output1b));
  and and_7 (and_32_out[57], not_1_out, or_7_out);
  comparatoru128bit comparatoru128bit_7 (
    .input1a(subtractor128bit_6_output1a), .input1b(subtractor128bit_6_output1b),
    .input2a({input2[6:0], {57{1'b0}}}), .input2b({{39{1'b0}}, input2[31:7]}),
    .greater1(comparatoru128bit_7_greater1), .equal1(comparatoru128bit_7_equal1));  // open: less1
  or or_7 (or_7_out, comparatoru128bit_7_greater1, comparatoru128bit_7_equal1);
  // Probe on subtractor128bit_7_output1a
  // Probe on subtractor128bit_7_output1a
  subtractor128bit subtractor128bit_8 (
    .input1a(subtractor128bit_7_output1a), .input1b(subtractor128bit_7_output1b),
    .input2a(cbuffer128bit_8_output1a), .input2b(cbuffer128bit_8_output1b),
    .output1a(subtractor128bit_8_output1a), .output1b(subtractor128bit_8_output1b));  // open: inborrow, borrow
  cbuffer128bit cbuffer128bit_8 (
    .buffer1(and_32_out[56]), .input1a({input2[7:0], {56{1'b0}}}), .input1b({{40{1'b0}}, input2[31:8]}),
    .output1a(cbuffer128bit_8_output1a), .output1b(cbuffer128bit_8_output1b));
  and and_8 (and_32_out[56], not_1_out, or_8_out);
  or or_8 (or_8_out, comparatoru128bit_8_greater1, comparatoru128bit_8_equal1);
  comparatoru128bit comparatoru128bit_8 (
    .input1a(subtractor128bit_7_output1a), .input1b(subtractor128bit_7_output1b),
    .input2a({input2[7:0], {56{1'b0}}}), .input2b({{40{1'b0}}, input2[31:8]}),
    .greater1(comparatoru128bit_8_greater1), .equal1(comparatoru128bit_8_equal1));  // open: less1
  // Probe on subtractor128bit_8_output1a
  // Probe on subtractor128bit_8_output1a
  subtractor128bit subtractor128bit_9 (
    .input1a(subtractor128bit_8_output1a), .input1b(subtractor128bit_8_output1b),
    .input2a(cbuffer128bit_9_output1a), .input2b(cbuffer128bit_9_output1b),
    .output1a(subtractor128bit_9_output1a), .output1b(subtractor128bit_9_output1b));  // open: inborrow, borrow
  cbuffer128bit cbuffer128bit_9 (
    .buffer1(and_32_out[55]), .input1a({input2[8:0], {55{1'b0}}}), .input1b({{41{1'b0}}, input2[31:9]}),
    .output1a(cbuffer128bit_9_output1a), .output1b(cbuffer128bit_9_output1b));
  and and_9 (and_32_out[55], not_1_out, or_9_out);
  or or_9 (or_9_out, comparatoru128bit_9_greater1, comparatoru128bit_9_equal1);
  comparatoru128bit comparatoru128bit_9 (
    .input1a(subtractor128bit_8_output1a), .input1b(subtractor128bit_8_output1b),
    .input2a({input2[8:0], {55{1'b0}}}), .input2b({{41{1'b0}}, input2[31:9]}),
    .greater1(comparatoru128bit_9_greater1), .equal1(comparatoru128bit_9_equal1));  // open: less1
  // Probe on subtractor128bit_9_output1a
  // Probe on subtractor128bit_9_output1a
  subtractor128bit subtractor128bit_10 (
    .input1a(subtractor128bit_9_output1a), .input1b(subtractor128bit_9_output1b),
    .input2a(cbuffer128bit_10_output1a), .input2b(cbuffer128bit_10_output1b),
    .output1a(subtractor128bit_10_output1a), .output1b(subtractor128bit_10_output1b));  // open: inborrow, borrow
  cbuffer128bit cbuffer128bit_10 (
    .buffer1(and_32_out[54]), .input1a({input2[9:0], {54{1'b0}}}), .input1b({{42{1'b0}}, input2[31:10]}),
    .output1a(cbuffer128bit_10_output1a), .output1b(cbuffer128bit_10_output1b));
  and and_10 (and_32_out[54], not_1_out, or_10_out);
  or or_10 (or_10_out, comparatoru128bit_10_greater1, comparatoru128bit_10_equal1);
  comparatoru128bit comparatoru128bit_10 (
    .input1a(subtractor128bit_9_output1a), .input1b(subtractor128bit_9_output1b),
    .input2a({input2[9:0], {54{1'b0}}}), .input2b({{42{1'b0}}, input2[31:10]}),
    .greater1(comparatoru128bit_10_greater1), .equal1(comparatoru128bit_10_equal1));  // open: less1
  // Probe on subtractor128bit_10_output1a
  // Probe on subtractor128bit_10_output1a
  subtractor128bit subtractor128bit_11 (
    .input1a(subtractor128bit_10_output1a), .input1b(subtractor128bit_10_output1b),
    .input2a(cbuffer128bit_11_output1a), .input2b(cbuffer128bit_11_output1b),
    .output1a(subtractor128bit_11_output1a), .output1b(subtractor128bit_11_output1b));  // open: inborrow, borrow
  cbuffer128bit cbuffer128bit_11 (
    .buffer1(and_32_out[53]), .input1a({input2[10:0], {53{1'b0}}}), .input1b({{43{1'b0}}, input2[31:11]}),
    .output1a(cbuffer128bit_11_output1a), .output1b(cbuffer128bit_11_output1b));
  and and_11 (and_32_out[53], not_1_out, or_11_out);
  or or_11 (or_11_out, comparatoru128bit_11_greater1, comparatoru128bit_11_equal1);
  comparatoru128bit comparatoru128bit_11 (
    .input1a(subtractor128bit_10_output1a), .input1b(subtractor128bit_10_output1b),
    .input2a({input2[10:0], {53{1'b0}}}), .input2b({{43{1'b0}}, input2[31:11]}),
    .greater1(comparatoru128bit_11_greater1), .equal1(comparatoru128bit_11_equal1));  // open: less1
  // Probe on subtractor128bit_11_output1a
  // Probe on subtractor128bit_11_output1a
  subtractor128bit subtractor128bit_12 (
    .input1a(subtractor128bit_11_output1a), .input1b(subtractor128bit_11_output1b),
    .input2a(cbuffer128bit_12_output1a), .input2b(cbuffer128bit_12_output1b),
    .output1a(subtractor128bit_12_output1a), .output1b(subtractor128bit_12_output1b));  // open: inborrow, borrow
  cbuffer128bit cbuffer128bit_12 (
    .buffer1(and_32_out[52]), .input1a({input2[11:0], {52{1'b0}}}), .input1b({{44{1'b0}}, input2[31:12]}),
    .output1a(cbuffer128bit_12_output1a), .output1b(cbuffer128bit_12_output1b));
  and and_12 (and_32_out[52], not_1_out, or_12_out);
  or or_12 (or_12_out, comparatoru128bit_12_greater1, comparatoru128bit_12_equal1);
  comparatoru128bit comparatoru128bit_12 (
    .input1a(subtractor128bit_11_output1a), .input1b(subtractor128bit_11_output1b),
    .input2a({input2[11:0], {52{1'b0}}}), .input2b({{44{1'b0}}, input2[31:12]}),
    .greater1(comparatoru128bit_12_greater1), .equal1(comparatoru128bit_12_equal1));  // open: less1
  // Probe on subtractor128bit_12_output1a
  // Probe on subtractor128bit_12_output1a
  subtractor128bit subtractor128bit_13 (
    .input1a(subtractor128bit_12_output1a), .input1b(subtractor128bit_12_output1b),
    .input2a(cbuffer128bit_13_output1a), .input2b(cbuffer128bit_13_output1b),
    .output1a(subtractor128bit_13_output1a), .output1b(subtractor128bit_13_output1b));  // open: inborrow, borrow
  cbuffer128bit cbuffer128bit_13 (
    .buffer1(and_32_out[51]), .input1a({input2[12:0], {51{1'b0}}}), .input1b({{45{1'b0}}, input2[31:13]}),
    .output1a(cbuffer128bit_13_output1a), .output1b(cbuffer128bit_13_output1b));
  and and_13 (and_32_out[51], not_1_out, or_13_out);
  or or_13 (or_13_out, comparatoru128bit_13_greater1, comparatoru128bit_13_equal1);
  comparatoru128bit comparatoru128bit_13 (
    .input1a(subtractor128bit_12_output1a), .input1b(subtractor128bit_12_output1b),
    .input2a({input2[12:0], {51{1'b0}}}), .input2b({{45{1'b0}}, input2[31:13]}),
    .greater1(comparatoru128bit_13_greater1), .equal1(comparatoru128bit_13_equal1));  // open: less1
  // Probe on subtractor128bit_13_output1a
  // Probe on subtractor128bit_13_output1a
  subtractor128bit subtractor128bit_14 (
    .input1a(subtractor128bit_13_output1a), .input1b(subtractor128bit_13_output1b),
    .input2a(cbuffer128bit_14_output1a), .input2b(cbuffer128bit_14_output1b),
    .output1a(subtractor128bit_14_output1a), .output1b(subtractor128bit_14_output1b));  // open: inborrow, borrow
  cbuffer128bit cbuffer128bit_14 (
    .buffer1(and_32_out[50]), .input1a({input2[13:0], {50{1'b0}}}), .input1b({{46{1'b0}}, input2[31:14]}),
    .output1a(cbuffer128bit_14_output1a), .output1b(cbuffer128bit_14_output1b));
  and and_14 (and_32_out[50], not_1_out, or_14_out);
  or or_14 (or_14_out, comparatoru128bit_14_greater1, comparatoru128bit_14_equal1);
  comparatoru128bit comparatoru128bit_14 (
    .input1a(subtractor128bit_13_output1a), .input1b(subtractor128bit_13_output1b),
    .input2a({input2[13:0], {50{1'b0}}}), .input2b({{46{1'b0}}, input2[31:14]}),
    .greater1(comparatoru128bit_14_greater1), .equal1(comparatoru128bit_14_equal1));  // open: less1
  // Probe on subtractor128bit_14_output1a
  // Probe on subtractor128bit_14_output1a
  subtractor128bit subtractor128bit_15 (
    .input1a(subtractor128bit_14_output1a), .input1b(subtractor128bit_14_output1b),
    .input2a(cbuffer128bit_15_output1a), .input2b(cbuffer128bit_15_output1b),
    .output1a(subtractor128bit_15_output1a), .output1b(subtractor128bit_15_output1b));  // open: inborrow, borrow
  cbuffer128bit cbuffer128bit_15 (
    .buffer1(and_32_out[49]), .input1a({input2[14:0], {49{1'b0}}}), .input1b({{47{1'b0}}, input2[31:15]}),
    .output1a(cbuffer128bit_15_output1a), .output1b(cbuffer128bit_15_output1b));
  and and_15 (and_32_out[49], not_1_out, or_15_out);
  comparatoru128bit comparatoru128bit_15 (
    .input1a(subtractor128bit_14_output1a), .input1b(subtractor128bit_14_output1b),
    .input2a({input2[14:0], {49{1'b0}}}), .input2b({{47{1'b0}}, input2[31:15]}),
    .greater1(comparatoru128bit_15_greater1), .equal1(comparatoru128bit_15_equal1));  // open: less1
  or or_15 (or_15_out, comparatoru128bit_15_greater1, comparatoru128bit_15_equal1);
  // Probe on subtractor128bit_15_output1a
  // Probe on subtractor128bit_15_output1a
  subtractor128bit subtractor128bit_16 (
    .input1a(subtractor128bit_15_output1a), .input1b(subtractor128bit_15_output1b),
    .input2a(cbuffer128bit_16_output1a), .input2b(cbuffer128bit_16_output1b),
    .output1a(subtractor128bit_16_output1a), .output1b(subtractor128bit_16_output1b));  // open: inborrow, borrow
  cbuffer128bit cbuffer128bit_16 (
    .buffer1(and_32_out[48]), .input1a({input2[15:0], {48{1'b0}}}), .input1b({{48{1'b0}}, input2[31:16]}),
    .output1a(cbuffer128bit_16_output1a), .output1b(cbuffer128bit_16_output1b));
  and and_16 (and_32_out[48], not_1_out, or_16_out);
  or or_16 (or_16_out, comparatoru128bit_16_greater1, comparatoru128bit_16_equal1);
  comparatoru128bit comparatoru128bit_16 (
    .input1a(subtractor128bit_15_output1a), .input1b(subtractor128bit_15_output1b),
    .input2a({input2[15:0], {48{1'b0}}}), .input2b({{48{1'b0}}, input2[31:16]}),
    .greater1(comparatoru128bit_16_greater1), .equal1(comparatoru128bit_16_equal1));  // open: less1
  // Probe on subtractor128bit_16_output1a
  // Probe on subtractor128bit_16_output1a
  subtractor128bit subtractor128bit_17 (
    .input1a(subtractor128bit_16_output1a), .input1b(subtractor128bit_16_output1b),
    .input2a(cbuffer128bit_17_output1a), .input2b(cbuffer128bit_17_output1b),
    .output1a(subtractor128bit_17_output1a), .output1b(subtractor128bit_17_output1b));  // open: inborrow, borrow
  cbuffer128bit cbuffer128bit_17 (
    .buffer1(and_32_out[47]), .input1a({input2[16:0], {47{1'b0}}}), .input1b({{49{1'b0}}, input2[31:17]}),
    .output1a(cbuffer128bit_17_output1a), .output1b(cbuffer128bit_17_output1b));
  and and_17 (and_32_out[47], not_1_out, or_17_out);
  or or_17 (or_17_out, comparatoru128bit_17_greater1, comparatoru128bit_17_equal1);
  comparatoru128bit comparatoru128bit_17 (
    .input1a(subtractor128bit_16_output1a), .input1b(subtractor128bit_16_output1b),
    .input2a({input2[16:0], {47{1'b0}}}), .input2b({{49{1'b0}}, input2[31:17]}),
    .greater1(comparatoru128bit_17_greater1), .equal1(comparatoru128bit_17_equal1));  // open: less1
  // Probe on subtractor128bit_17_output1a
  // Probe on subtractor128bit_17_output1a
  subtractor128bit subtractor128bit_18 (
    .input1a(subtractor128bit_17_output1a), .input1b(subtractor128bit_17_output1b),
    .input2a(cbuffer128bit_18_output1a), .input2b(cbuffer128bit_18_output1b),
    .output1a(subtractor128bit_18_output1a), .output1b(subtractor128bit_18_output1b));  // open: inborrow, borrow
  cbuffer128bit cbuffer128bit_18 (
    .buffer1(and_32_out[46]), .input1a({input2[17:0], {46{1'b0}}}), .input1b({{50{1'b0}}, input2[31:18]}),
    .output1a(cbuffer128bit_18_output1a), .output1b(cbuffer128bit_18_output1b));
  and and_18 (and_32_out[46], not_1_out, or_18_out);
  or or_18 (or_18_out, comparatoru128bit_18_greater1, comparatoru128bit_18_equal1);
  comparatoru128bit comparatoru128bit_18 (
    .input1a(subtractor128bit_17_output1a), .input1b(subtractor128bit_17_output1b),
    .input2a({input2[17:0], {46{1'b0}}}), .input2b({{50{1'b0}}, input2[31:18]}),
    .greater1(comparatoru128bit_18_greater1), .equal1(comparatoru128bit_18_equal1));  // open: less1
  // Probe on subtractor128bit_18_output1a
  // Probe on subtractor128bit_18_output1a
  subtractor128bit subtractor128bit_19 (
    .input1a(subtractor128bit_18_output1a), .input1b(subtractor128bit_18_output1b),
    .input2a(cbuffer128bit_19_output1a), .input2b(cbuffer128bit_19_output1b),
    .output1a(subtractor128bit_19_output1a), .output1b(subtractor128bit_19_output1b));  // open: inborrow, borrow
  cbuffer128bit cbuffer128bit_19 (
    .buffer1(and_32_out[45]), .input1a({input2[18:0], {45{1'b0}}}), .input1b({{51{1'b0}}, input2[31:19]}),
    .output1a(cbuffer128bit_19_output1a), .output1b(cbuffer128bit_19_output1b));
  and and_19 (and_32_out[45], not_1_out, or_19_out);
  or or_19 (or_19_out, comparatoru128bit_19_greater1, comparatoru128bit_19_equal1);
  comparatoru128bit comparatoru128bit_19 (
    .input1a(subtractor128bit_18_output1a), .input1b(subtractor128bit_18_output1b),
    .input2a({input2[18:0], {45{1'b0}}}), .input2b({{51{1'b0}}, input2[31:19]}),
    .greater1(comparatoru128bit_19_greater1), .equal1(comparatoru128bit_19_equal1));  // open: less1
  // Probe on subtractor128bit_19_output1a
  // Probe on subtractor128bit_19_output1a
  subtractor128bit subtractor128bit_20 (
    .input1a(subtractor128bit_19_output1a), .input1b(subtractor128bit_19_output1b),
    .input2a(cbuffer128bit_20_output1a), .input2b(cbuffer128bit_20_output1b),
    .output1a(subtractor128bit_20_output1a), .output1b(subtractor128bit_20_output1b));  // open: inborrow, borrow
  cbuffer128bit cbuffer128bit_20 (
    .buffer1(and_32_out[44]), .input1a({input2[19:0], {44{1'b0}}}), .input1b({{52{1'b0}}, input2[31:20]}),
    .output1a(cbuffer128bit_20_output1a), .output1b(cbuffer128bit_20_output1b));
  and and_20 (and_32_out[44], not_1_out, or_20_out);
  or or_20 (or_20_out, comparatoru128bit_20_greater1, comparatoru128bit_20_equal1);
  comparatoru128bit comparatoru128bit_20 (
    .input1a(subtractor128bit_19_output1a), .input1b(subtractor128bit_19_output1b),
    .input2a({input2[19:0], {44{1'b0}}}), .input2b({{52{1'b0}}, input2[31:20]}),
    .greater1(comparatoru128bit_20_greater1), .equal1(comparatoru128bit_20_equal1));  // open: less1
  // Probe on subtractor128bit_20_output1a
  // Probe on subtractor128bit_20_output1a
  subtractor128bit subtractor128bit_21 (
    .input1a(subtractor128bit_20_output1a), .input1b(subtractor128bit_20_output1b),
    .input2a(cbuffer128bit_21_output1a), .input2b(cbuffer128bit_21_output1b),
    .output1a(subtractor128bit_21_output1a), .output1b(subtractor128bit_21_output1b));  // open: inborrow, borrow
  cbuffer128bit cbuffer128bit_21 (
    .buffer1(and_32_out[43]), .input1a({input2[20:0], {43{1'b0}}}), .input1b({{53{1'b0}}, input2[31:21]}),
    .output1a(cbuffer128bit_21_output1a), .output1b(cbuffer128bit_21_output1b));
  and and_21 (and_32_out[43], not_1_out, or_21_out);
  or or_21 (or_21_out, comparatoru128bit_21_greater1, comparatoru128bit_21_equal1);
  comparatoru128bit comparatoru128bit_21 (
    .input1a(subtractor128bit_20_output1a), .input1b(subtractor128bit_20_output1b),
    .input2a({input2[20:0], {43{1'b0}}}), .input2b({{53{1'b0}}, input2[31:21]}),
    .greater1(comparatoru128bit_21_greater1), .equal1(comparatoru128bit_21_equal1));  // open: less1
  // Probe on subtractor128bit_21_output1a
  // Probe on subtractor128bit_21_output1a
  subtractor128bit subtractor128bit_22 (
    .input1a(subtractor128bit_21_output1a), .input1b(subtractor128bit_21_output1b),
    .input2a(cbuffer128bit_22_output1a), .input2b(cbuffer128bit_22_output1b),
    .output1a(subtractor128bit_22_output1a), .output1b(subtractor128bit_22_output1b));  // open: inborrow, borrow
  cbuffer128bit cbuffer128bit_22 (
    .buffer1(and_32_out[42]), .input1a({input2[21:0], {42{1'b0}}}), .input1b({{54{1'b0}}, input2[31:22]}),
    .output1a(cbuffer128bit_22_output1a), .output1b(cbuffer128bit_22_output1b));
  and and_22 (and_32_out[42], not_1_out, or_22_out);
  or or_22 (or_22_out, comparatoru128bit_22_greater1, comparatoru128bit_22_equal1);
  comparatoru128bit comparatoru128bit_22 (
    .input1a(subtractor128bit_21_output1a), .input1b(subtractor128bit_21_output1b),
    .input2a({input2[21:0], {42{1'b0}}}), .input2b({{54{1'b0}}, input2[31:22]}),
    .greater1(comparatoru128bit_22_greater1), .equal1(comparatoru128bit_22_equal1));  // open: less1
  // Probe on subtractor128bit_22_output1a
  // Probe on subtractor128bit_22_output1a
  subtractor128bit subtractor128bit_23 (
    .input1a(subtractor128bit_22_output1a), .input1b(subtractor128bit_22_output1b),
    .input2a(cbuffer128bit_23_output1a), .input2b(cbuffer128bit_23_output1b),
    .output1a(subtractor128bit_23_output1a), .output1b(subtractor128bit_23_output1b));  // open: inborrow, borrow
  cbuffer128bit cbuffer128bit_23 (
    .buffer1(and_32_out[41]), .input1a({input2[22:0], {41{1'b0}}}), .input1b({{55{1'b0}}, input2[31:23]}),
    .output1a(cbuffer128bit_23_output1a), .output1b(cbuffer128bit_23_output1b));
  and and_23 (and_32_out[41], not_1_out, or_23_out);
  comparatoru128bit comparatoru128bit_23 (
    .input1a(subtractor128bit_22_output1a), .input1b(subtractor128bit_22_output1b),
    .input2a({input2[22:0], {41{1'b0}}}), .input2b({{55{1'b0}}, input2[31:23]}),
    .greater1(comparatoru128bit_23_greater1), .equal1(comparatoru128bit_23_equal1));  // open: less1
  or or_23 (or_23_out, comparatoru128bit_23_greater1, comparatoru128bit_23_equal1);
  // Probe on subtractor128bit_23_output1a
  // Probe on subtractor128bit_23_output1a
  subtractor128bit subtractor128bit_24 (
    .input1a(subtractor128bit_23_output1a), .input1b(subtractor128bit_23_output1b),
    .input2a(cbuffer128bit_24_output1a), .input2b(cbuffer128bit_24_output1b),
    .output1a(subtractor128bit_24_output1a), .output1b(subtractor128bit_24_output1b));  // open: inborrow, borrow
  cbuffer128bit cbuffer128bit_24 (
    .buffer1(and_32_out[40]), .input1a({input2[23:0], {40{1'b0}}}), .input1b({{56{1'b0}}, input2[31:24]}),
    .output1a(cbuffer128bit_24_output1a), .output1b(cbuffer128bit_24_output1b));
  and and_24 (and_32_out[40], not_1_out, or_24_out);
  or or_24 (or_24_out, comparatoru128bit_24_greater1, comparatoru128bit_24_equal1);
  comparatoru128bit comparatoru128bit_24 (
    .input1a(subtractor128bit_23_output1a), .input1b(subtractor128bit_23_output1b),
    .input2a({input2[23:0], {40{1'b0}}}), .input2b({{56{1'b0}}, input2[31:24]}),
    .greater1(comparatoru128bit_24_greater1), .equal1(comparatoru128bit_24_equal1));  // open: less1
  // Probe on subtractor128bit_24_output1a
  // Probe on subtractor128bit_24_output1a
  subtractor128bit subtractor128bit_25 (
    .input1a(subtractor128bit_24_output1a), .input1b(subtractor128bit_24_output1b),
    .input2a(cbuffer128bit_25_output1a), .input2b(cbuffer128bit_25_output1b),
    .output1a(subtractor128bit_25_output1a), .output1b(subtractor128bit_25_output1b));  // open: inborrow, borrow
  cbuffer128bit cbuffer128bit_25 (
    .buffer1(and_32_out[39]), .input1a({input2[24:0], {39{1'b0}}}), .input1b({{57{1'b0}}, input2[31:25]}),
    .output1a(cbuffer128bit_25_output1a), .output1b(cbuffer128bit_25_output1b));
  and and_25 (and_32_out[39], not_1_out, or_25_out);
  or or_25 (or_25_out, comparatoru128bit_25_greater1, comparatoru128bit_25_equal1);
  comparatoru128bit comparatoru128bit_25 (
    .input1a(subtractor128bit_24_output1a), .input1b(subtractor128bit_24_output1b),
    .input2a({input2[24:0], {39{1'b0}}}), .input2b({{57{1'b0}}, input2[31:25]}),
    .greater1(comparatoru128bit_25_greater1), .equal1(comparatoru128bit_25_equal1));  // open: less1
  // Probe on subtractor128bit_25_output1a
  // Probe on subtractor128bit_25_output1a
  subtractor128bit subtractor128bit_26 (
    .input1a(subtractor128bit_25_output1a), .input1b(subtractor128bit_25_output1b),
    .input2a(cbuffer128bit_26_output1a), .input2b(cbuffer128bit_26_output1b),
    .output1a(subtractor128bit_26_output1a), .output1b(subtractor128bit_26_output1b));  // open: inborrow, borrow
  cbuffer128bit cbuffer128bit_26 (
    .buffer1(and_32_out[38]), .input1a({input2[25:0], {38{1'b0}}}), .input1b({{58{1'b0}}, input2[31:26]}),
    .output1a(cbuffer128bit_26_output1a), .output1b(cbuffer128bit_26_output1b));
  and and_26 (and_32_out[38], not_1_out, or_26_out);
  or or_26 (or_26_out, comparatoru128bit_26_greater1, comparatoru128bit_26_equal1);
  comparatoru128bit comparatoru128bit_26 (
    .input1a(subtractor128bit_25_output1a), .input1b(subtractor128bit_25_output1b),
    .input2a({input2[25:0], {38{1'b0}}}), .input2b({{58{1'b0}}, input2[31:26]}),
    .greater1(comparatoru128bit_26_greater1), .equal1(comparatoru128bit_26_equal1));  // open: less1
  // Probe on subtractor128bit_26_output1a
  // Probe on subtractor128bit_26_output1a
  subtractor128bit subtractor128bit_27 (
    .input1a(subtractor128bit_26_output1a), .input1b(subtractor128bit_26_output1b),
    .input2a(cbuffer128bit_27_output1a), .input2b(cbuffer128bit_27_output1b),
    .output1a(subtractor128bit_27_output1a), .output1b(subtractor128bit_27_output1b));  // open: inborrow, borrow
  cbuffer128bit cbuffer128bit_27 (
    .buffer1(and_32_out[37]), .input1a({input2[26:0], {37{1'b0}}}), .input1b({{59{1'b0}}, input2[31:27]}),
    .output1a(cbuffer128bit_27_output1a), .output1b(cbuffer128bit_27_output1b));
  and and_27 (and_32_out[37], not_1_out, or_27_out);
  or or_27 (or_27_out, comparatoru128bit_27_greater1, comparatoru128bit_27_equal1);
  comparatoru128bit comparatoru128bit_27 (
    .input1a(subtractor128bit_26_output1a), .input1b(subtractor128bit_26_output1b),
    .input2a({input2[26:0], {37{1'b0}}}), .input2b({{59{1'b0}}, input2[31:27]}),
    .greater1(comparatoru128bit_27_greater1), .equal1(comparatoru128bit_27_equal1));  // open: less1
  // Probe on subtractor128bit_27_output1a
  // Probe on subtractor128bit_27_output1a
  subtractor128bit subtractor128bit_28 (
    .input1a(subtractor128bit_27_output1a), .input1b(subtractor128bit_27_output1b),
    .input2a(cbuffer128bit_28_output1a), .input2b(cbuffer128bit_28_output1b),
    .output1a(subtractor128bit_28_output1a), .output1b(subtractor128bit_28_output1b));  // open: inborrow, borrow
  cbuffer128bit cbuffer128bit_28 (
    .buffer1(and_32_out[36]), .input1a({input2[27:0], {36{1'b0}}}), .input1b({{60{1'b0}}, input2[31:28]}),
    .output1a(cbuffer128bit_28_output1a), .output1b(cbuffer128bit_28_output1b));
  and and_28 (and_32_out[36], not_1_out, or_28_out);
  or or_28 (or_28_out, comparatoru128bit_28_greater1, comparatoru128bit_28_equal1);
  comparatoru128bit comparatoru128bit_28 (
    .input1a(subtractor128bit_27_output1a), .input1b(subtractor128bit_27_output1b),
    .input2a({input2[27:0], {36{1'b0}}}), .input2b({{60{1'b0}}, input2[31:28]}),
    .greater1(comparatoru128bit_28_greater1), .equal1(comparatoru128bit_28_equal1));  // open: less1
  // Probe on subtractor128bit_28_output1a
  // Probe on subtractor128bit_28_output1a
  subtractor128bit subtractor128bit_29 (
    .input1a(subtractor128bit_28_output1a), .input1b(subtractor128bit_28_output1b),
    .input2a(cbuffer128bit_29_output1a), .input2b(cbuffer128bit_29_output1b),
    .output1a(subtractor128bit_29_output1a), .output1b(subtractor128bit_29_output1b));  // open: inborrow, borrow
  cbuffer128bit cbuffer128bit_29 (
    .buffer1(and_32_out[35]), .input1a({input2[28:0], {35{1'b0}}}), .input1b({{61{1'b0}}, input2[31:29]}),
    .output1a(cbuffer128bit_29_output1a), .output1b(cbuffer128bit_29_output1b));
  and and_29 (and_32_out[35], not_1_out, or_29_out);
  or or_29 (or_29_out, comparatoru128bit_29_greater1, comparatoru128bit_29_equal1);
  comparatoru128bit comparatoru128bit_29 (
    .input1a(subtractor128bit_28_output1a), .input1b(subtractor128bit_28_output1b),
    .input2a({input2[28:0], {35{1'b0}}}), .input2b({{61{1'b0}}, input2[31:29]}),
    .greater1(comparatoru128bit_29_greater1), .equal1(comparatoru128bit_29_equal1));  // open: less1
  // Probe on subtractor128bit_29_output1a
  // Probe on subtractor128bit_29_output1a
  subtractor128bit subtractor128bit_30 (
    .input1a(subtractor128bit_29_output1a), .input1b(subtractor128bit_29_output1b),
    .input2a(cbuffer128bit_30_output1a), .input2b(cbuffer128bit_30_output1b),
    .output1a(subtractor128bit_30_output1a), .output1b(subtractor128bit_30_output1b));  // open: inborrow, borrow
  cbuffer128bit cbuffer128bit_30 (
    .buffer1(and_32_out[34]), .input1a({input2[29:0], {34{1'b0}}}), .input1b({{62{1'b0}}, input2[31:30]}),
    .output1a(cbuffer128bit_30_output1a), .output1b(cbuffer128bit_30_output1b));
  and and_30 (and_32_out[34], not_1_out, or_30_out);
  or or_30 (or_30_out, comparatoru128bit_30_greater1, comparatoru128bit_30_equal1);
  comparatoru128bit comparatoru128bit_30 (
    .input1a(subtractor128bit_29_output1a), .input1b(subtractor128bit_29_output1b),
    .input2a({input2[29:0], {34{1'b0}}}), .input2b({{62{1'b0}}, input2[31:30]}),
    .greater1(comparatoru128bit_30_greater1), .equal1(comparatoru128bit_30_equal1));  // open: less1
  // Probe on subtractor128bit_30_output1a
  // Probe on subtractor128bit_30_output1a
  subtractor128bit subtractor128bit_31 (
    .input1a(subtractor128bit_30_output1a), .input1b(subtractor128bit_30_output1b),
    .input2a(cbuffer128bit_31_output1a), .input2b(cbuffer128bit_31_output1b),
    .output1a(subtractor128bit_31_output1a), .output1b(subtractor128bit_31_output1b));  // open: inborrow, borrow
  cbuffer128bit cbuffer128bit_31 (
    .buffer1(and_32_out[33]), .input1a({input2[30:0], {33{1'b0}}}), .input1b({{63{1'b0}}, input2[31]}),
    .output1a(cbuffer128bit_31_output1a), .output1b(cbuffer128bit_31_output1b));
  and and_31 (and_32_out[33], not_1_out, or_31_out);
  comparatoru128bit comparatoru128bit_31 (
    .input1a(subtractor128bit_30_output1a), .input1b(subtractor128bit_30_output1b),
    .input2a({input2[30:0], {33{1'b0}}}), .input2b({{63{1'b0}}, input2[31]}),
    .greater1(comparatoru128bit_31_greater1), .equal1(comparatoru128bit_31_equal1));  // open: less1
  or or_31 (or_31_out, comparatoru128bit_31_greater1, comparatoru128bit_31_equal1);
  // Probe on subtractor128bit_31_output1a
  // Probe on subtractor128bit_31_output1a
  subtractor128bit subtractor128bit_32 (
    .input1a(subtractor128bit_31_output1a), .input1b(subtractor128bit_31_output1b),
    .input2a(cbuffer128bit_32_output1a), .input2b(cbuffer128bit_32_output1b),
    .output1a(subtractor128bit_32_output1a), .output1b(subtractor128bit_32_output1b));  // open: inborrow, borrow
  cbuffer128bit cbuffer128bit_32 (
    .buffer1(and_32_out[32]), .input1a({input2, {32{1'b0}}}), .input1b({64{1'b0}}),
    .output1a(cbuffer128bit_32_output1a), .output1b(cbuffer128bit_32_output1b));
  and and_32 (and_32_out[32], not_1_out, or_32_out);
  or or_32 (or_32_out, comparatoru128bit_32_greater1, comparatoru128bit_32_equal1);
  comparatoru128bit comparatoru128bit_32 (
    .input1a(subtractor128bit_31_output1a), .input1b(subtractor128bit_31_output1b),
    .input2a({input2, {32{1'b0}}}), .input2b({64{1'b0}}), .greater1(comparatoru128bit_32_greater1),
    .equal1(comparatoru128bit_32_equal1));  // open: less1
  // Probe on subtractor128bit_32_output1a
  // Probe on subtractor128bit_32_output1a
  subtractor128bit subtractor128bit_33 (
    .input1a(subtractor128bit_32_output1a), .input1b(subtractor128bit_32_output1b),
    .input2a(cbuffer128bit_33_output1a), .input2b(cbuffer128bit_33_output1b),
    .output1a(subtractor128bit_33_output1a), .output1b(subtractor128bit_33_output1b));  // open: inborrow, borrow
  cbuffer128bit cbuffer128bit_33 (
    .buffer1(output1[31]), .input1a({1'b0, input2, {31{1'b0}}}), .input1b({64{1'b0}}),
    .output1a(cbuffer128bit_33_output1a), .output1b(cbuffer128bit_33_output1b));
  and and_33 (output1[31], not_1_out, or_33_out);
  or or_33 (or_33_out, comparatoru128bit_33_greater1, comparatoru128bit_33_equal1);
  comparatoru128bit comparatoru128bit_33 (
    .input1a(subtractor128bit_32_output1a), .input1b(subtractor128bit_32_output1b),
    .input2a({1'b0, input2, {31{1'b0}}}), .input2b({64{1'b0}}), .greater1(comparatoru128bit_33_greater1),
    .equal1(comparatoru128bit_33_equal1));  // open: less1
  // Probe on subtractor128bit_33_output1a
  // Probe on subtractor128bit_33_output1a
  subtractor128bit subtractor128bit_34 (
    .input1a(subtractor128bit_33_output1a), .input1b(subtractor128bit_33_output1b),
    .input2a(cbuffer128bit_34_output1a), .input2b(cbuffer128bit_34_output1b),
    .output1a(subtractor128bit_34_output1a), .output1b(subtractor128bit_34_output1b));  // open: inborrow, borrow
  cbuffer128bit cbuffer128bit_34 (
    .buffer1(output1[30]), .input1a({2'b00, input2, {30{1'b0}}}), .input1b({64{1'b0}}),
    .output1a(cbuffer128bit_34_output1a), .output1b(cbuffer128bit_34_output1b));
  and and_34 (output1[30], not_1_out, or_34_out);
  or or_34 (or_34_out, comparatoru128bit_34_greater1, comparatoru128bit_34_equal1);
  comparatoru128bit comparatoru128bit_34 (
    .input1a(subtractor128bit_33_output1a), .input1b(subtractor128bit_33_output1b),
    .input2a({2'b00, input2, {30{1'b0}}}), .input2b({64{1'b0}}), .greater1(comparatoru128bit_34_greater1),
    .equal1(comparatoru128bit_34_equal1));  // open: less1
  // Probe on subtractor128bit_34_output1a
  // Probe on subtractor128bit_34_output1a
  subtractor128bit subtractor128bit_35 (
    .input1a(subtractor128bit_34_output1a), .input1b(subtractor128bit_34_output1b),
    .input2a(cbuffer128bit_35_output1a), .input2b(cbuffer128bit_35_output1b),
    .output1a(subtractor128bit_35_output1a), .output1b(subtractor128bit_35_output1b));  // open: inborrow, borrow
  cbuffer128bit cbuffer128bit_35 (
    .buffer1(output1[29]), .input1a({3'b000, input2, {29{1'b0}}}), .input1b({64{1'b0}}),
    .output1a(cbuffer128bit_35_output1a), .output1b(cbuffer128bit_35_output1b));
  and and_35 (output1[29], not_1_out, or_35_out);
  or or_35 (or_35_out, comparatoru128bit_35_greater1, comparatoru128bit_35_equal1);
  comparatoru128bit comparatoru128bit_35 (
    .input1a(subtractor128bit_34_output1a), .input1b(subtractor128bit_34_output1b),
    .input2a({3'b000, input2, {29{1'b0}}}), .input2b({64{1'b0}}), .greater1(comparatoru128bit_35_greater1),
    .equal1(comparatoru128bit_35_equal1));  // open: less1
  // Probe on subtractor128bit_35_output1a
  // Probe on subtractor128bit_35_output1a
  subtractor128bit subtractor128bit_36 (
    .input1a(subtractor128bit_35_output1a), .input1b(subtractor128bit_35_output1b),
    .input2a(cbuffer128bit_36_output1a), .input2b(cbuffer128bit_36_output1b),
    .output1a(subtractor128bit_36_output1a), .output1b(subtractor128bit_36_output1b));  // open: inborrow, borrow
  cbuffer128bit cbuffer128bit_36 (
    .buffer1(output1[28]), .input1a({4'b0000, input2, {28{1'b0}}}), .input1b({64{1'b0}}),
    .output1a(cbuffer128bit_36_output1a), .output1b(cbuffer128bit_36_output1b));
  and and_36 (output1[28], not_1_out, or_36_out);
  or or_36 (or_36_out, comparatoru128bit_36_greater1, comparatoru128bit_36_equal1);
  comparatoru128bit comparatoru128bit_36 (
    .input1a(subtractor128bit_35_output1a), .input1b(subtractor128bit_35_output1b),
    .input2a({4'b0000, input2, {28{1'b0}}}), .input2b({64{1'b0}}), .greater1(comparatoru128bit_36_greater1),
    .equal1(comparatoru128bit_36_equal1));  // open: less1
  // Probe on subtractor128bit_36_output1a
  // Probe on subtractor128bit_36_output1a
  subtractor128bit subtractor128bit_37 (
    .input1a(subtractor128bit_36_output1a), .input1b(subtractor128bit_36_output1b),
    .input2a(cbuffer128bit_37_output1a), .input2b(cbuffer128bit_37_output1b),
    .output1a(subtractor128bit_37_output1a), .output1b(subtractor128bit_37_output1b));  // open: inborrow, borrow
  cbuffer128bit cbuffer128bit_37 (
    .buffer1(output1[27]), .input1a({{5{1'b0}}, input2, {27{1'b0}}}), .input1b({64{1'b0}}),
    .output1a(cbuffer128bit_37_output1a), .output1b(cbuffer128bit_37_output1b));
  and and_37 (output1[27], not_1_out, or_37_out);
  or or_37 (or_37_out, comparatoru128bit_37_greater1, comparatoru128bit_37_equal1);
  comparatoru128bit comparatoru128bit_37 (
    .input1a(subtractor128bit_36_output1a), .input1b(subtractor128bit_36_output1b),
    .input2a({{5{1'b0}}, input2, {27{1'b0}}}), .input2b({64{1'b0}}),
    .greater1(comparatoru128bit_37_greater1), .equal1(comparatoru128bit_37_equal1));  // open: less1
  // Probe on subtractor128bit_37_output1a
  // Probe on subtractor128bit_37_output1a
  subtractor128bit subtractor128bit_38 (
    .input1a(subtractor128bit_37_output1a), .input1b(subtractor128bit_37_output1b),
    .input2a(cbuffer128bit_38_output1a), .input2b(cbuffer128bit_38_output1b),
    .output1a(subtractor128bit_38_output1a), .output1b(subtractor128bit_38_output1b));  // open: inborrow, borrow
  cbuffer128bit cbuffer128bit_38 (
    .buffer1(output1[26]), .input1a({{6{1'b0}}, input2, {26{1'b0}}}), .input1b({64{1'b0}}),
    .output1a(cbuffer128bit_38_output1a), .output1b(cbuffer128bit_38_output1b));
  and and_38 (output1[26], not_1_out, or_38_out);
  or or_38 (or_38_out, comparatoru128bit_38_greater1, comparatoru128bit_38_equal1);
  comparatoru128bit comparatoru128bit_38 (
    .input1a(subtractor128bit_37_output1a), .input1b(subtractor128bit_37_output1b),
    .input2a({{6{1'b0}}, input2, {26{1'b0}}}), .input2b({64{1'b0}}),
    .greater1(comparatoru128bit_38_greater1), .equal1(comparatoru128bit_38_equal1));  // open: less1
  // Probe on subtractor128bit_38_output1a
  // Probe on subtractor128bit_38_output1a
  subtractor128bit subtractor128bit_39 (
    .input1a(subtractor128bit_38_output1a), .input1b(subtractor128bit_38_output1b),
    .input2a(cbuffer128bit_39_output1a), .input2b(cbuffer128bit_39_output1b),
    .output1a(subtractor128bit_39_output1a), .output1b(subtractor128bit_39_output1b));  // open: inborrow, borrow
  cbuffer128bit cbuffer128bit_39 (
    .buffer1(output1[25]), .input1a({{7{1'b0}}, input2, {25{1'b0}}}), .input1b({64{1'b0}}),
    .output1a(cbuffer128bit_39_output1a), .output1b(cbuffer128bit_39_output1b));
  and and_39 (output1[25], not_1_out, or_39_out);
  comparatoru128bit comparatoru128bit_39 (
    .input1a(subtractor128bit_38_output1a), .input1b(subtractor128bit_38_output1b),
    .input2a({{7{1'b0}}, input2, {25{1'b0}}}), .input2b({64{1'b0}}),
    .greater1(comparatoru128bit_39_greater1), .equal1(comparatoru128bit_39_equal1));  // open: less1
  or or_39 (or_39_out, comparatoru128bit_39_greater1, comparatoru128bit_39_equal1);
  // Probe on subtractor128bit_39_output1a
  // Probe on subtractor128bit_39_output1a
  subtractor128bit subtractor128bit_40 (
    .input1a(subtractor128bit_39_output1a), .input1b(subtractor128bit_39_output1b),
    .input2a(cbuffer128bit_40_output1a), .input2b(cbuffer128bit_40_output1b),
    .output1a(subtractor128bit_40_output1a), .output1b(subtractor128bit_40_output1b));  // open: inborrow, borrow
  cbuffer128bit cbuffer128bit_40 (
    .buffer1(output1[24]), .input1a({{8{1'b0}}, input2, {24{1'b0}}}), .input1b({64{1'b0}}),
    .output1a(cbuffer128bit_40_output1a), .output1b(cbuffer128bit_40_output1b));
  and and_40 (output1[24], not_1_out, or_40_out);
  or or_40 (or_40_out, comparatoru128bit_40_greater1, comparatoru128bit_40_equal1);
  comparatoru128bit comparatoru128bit_40 (
    .input1a(subtractor128bit_39_output1a), .input1b(subtractor128bit_39_output1b),
    .input2a({{8{1'b0}}, input2, {24{1'b0}}}), .input2b({64{1'b0}}),
    .greater1(comparatoru128bit_40_greater1), .equal1(comparatoru128bit_40_equal1));  // open: less1
  // Probe on subtractor128bit_40_output1a
  // Probe on subtractor128bit_40_output1a
  subtractor128bit subtractor128bit_41 (
    .input1a(subtractor128bit_40_output1a), .input1b(subtractor128bit_40_output1b),
    .input2a(cbuffer128bit_41_output1a), .input2b(cbuffer128bit_41_output1b),
    .output1a(subtractor128bit_41_output1a), .output1b(subtractor128bit_41_output1b));  // open: inborrow, borrow
  cbuffer128bit cbuffer128bit_41 (
    .buffer1(output1[23]), .input1a({{9{1'b0}}, input2, {23{1'b0}}}), .input1b({64{1'b0}}),
    .output1a(cbuffer128bit_41_output1a), .output1b(cbuffer128bit_41_output1b));
  and and_41 (output1[23], not_1_out, or_41_out);
  or or_41 (or_41_out, comparatoru128bit_41_greater1, comparatoru128bit_41_equal1);
  comparatoru128bit comparatoru128bit_41 (
    .input1a(subtractor128bit_40_output1a), .input1b(subtractor128bit_40_output1b),
    .input2a({{9{1'b0}}, input2, {23{1'b0}}}), .input2b({64{1'b0}}),
    .greater1(comparatoru128bit_41_greater1), .equal1(comparatoru128bit_41_equal1));  // open: less1
  // Probe on subtractor128bit_41_output1a
  // Probe on subtractor128bit_41_output1a
  subtractor128bit subtractor128bit_42 (
    .input1a(subtractor128bit_41_output1a), .input1b(subtractor128bit_41_output1b),
    .input2a(cbuffer128bit_42_output1a), .input2b(cbuffer128bit_42_output1b),
    .output1a(subtractor128bit_42_output1a), .output1b(subtractor128bit_42_output1b));  // open: inborrow, borrow
  cbuffer128bit cbuffer128bit_42 (
    .buffer1(output1[22]), .input1a({{10{1'b0}}, input2, {22{1'b0}}}), .input1b({64{1'b0}}),
    .output1a(cbuffer128bit_42_output1a), .output1b(cbuffer128bit_42_output1b));
  and and_42 (output1[22], not_1_out, or_42_out);
  or or_42 (or_42_out, comparatoru128bit_42_greater1, comparatoru128bit_42_equal1);
  comparatoru128bit comparatoru128bit_42 (
    .input1a(subtractor128bit_41_output1a), .input1b(subtractor128bit_41_output1b),
    .input2a({{10{1'b0}}, input2, {22{1'b0}}}), .input2b({64{1'b0}}),
    .greater1(comparatoru128bit_42_greater1), .equal1(comparatoru128bit_42_equal1));  // open: less1
  // Probe on subtractor128bit_42_output1a
  // Probe on subtractor128bit_42_output1a
  subtractor128bit subtractor128bit_43 (
    .input1a(subtractor128bit_42_output1a), .input1b(subtractor128bit_42_output1b),
    .input2a(cbuffer128bit_43_output1a), .input2b(cbuffer128bit_43_output1b),
    .output1a(subtractor128bit_43_output1a), .output1b(subtractor128bit_43_output1b));  // open: inborrow, borrow
  cbuffer128bit cbuffer128bit_43 (
    .buffer1(output1[21]), .input1a({{11{1'b0}}, input2, {21{1'b0}}}), .input1b({64{1'b0}}),
    .output1a(cbuffer128bit_43_output1a), .output1b(cbuffer128bit_43_output1b));
  and and_43 (output1[21], not_1_out, or_43_out);
  or or_43 (or_43_out, comparatoru128bit_43_greater1, comparatoru128bit_43_equal1);
  comparatoru128bit comparatoru128bit_43 (
    .input1a(subtractor128bit_42_output1a), .input1b(subtractor128bit_42_output1b),
    .input2a({{11{1'b0}}, input2, {21{1'b0}}}), .input2b({64{1'b0}}),
    .greater1(comparatoru128bit_43_greater1), .equal1(comparatoru128bit_43_equal1));  // open: less1
  // Probe on subtractor128bit_43_output1a
  // Probe on subtractor128bit_43_output1a
  subtractor128bit subtractor128bit_44 (
    .input1a(subtractor128bit_43_output1a), .input1b(subtractor128bit_43_output1b),
    .input2a(cbuffer128bit_44_output1a), .input2b(cbuffer128bit_44_output1b),
    .output1a(subtractor128bit_44_output1a), .output1b(subtractor128bit_44_output1b));  // open: inborrow, borrow
  cbuffer128bit cbuffer128bit_44 (
    .buffer1(output1[20]), .input1a({{12{1'b0}}, input2, {20{1'b0}}}), .input1b({64{1'b0}}),
    .output1a(cbuffer128bit_44_output1a), .output1b(cbuffer128bit_44_output1b));
  and and_44 (output1[20], not_1_out, or_44_out);
  or or_44 (or_44_out, comparatoru128bit_44_greater1, comparatoru128bit_44_equal1);
  comparatoru128bit comparatoru128bit_44 (
    .input1a(subtractor128bit_43_output1a), .input1b(subtractor128bit_43_output1b),
    .input2a({{12{1'b0}}, input2, {20{1'b0}}}), .input2b({64{1'b0}}),
    .greater1(comparatoru128bit_44_greater1), .equal1(comparatoru128bit_44_equal1));  // open: less1
  // Probe on subtractor128bit_44_output1a
  // Probe on subtractor128bit_44_output1a
  subtractor128bit subtractor128bit_45 (
    .input1a(subtractor128bit_44_output1a), .input1b(subtractor128bit_44_output1b),
    .input2a(cbuffer128bit_45_output1a), .input2b(cbuffer128bit_45_output1b),
    .output1a(subtractor128bit_45_output1a), .output1b(subtractor128bit_45_output1b));  // open: inborrow, borrow
  cbuffer128bit cbuffer128bit_45 (
    .buffer1(output1[19]), .input1a({{13{1'b0}}, input2, {19{1'b0}}}), .input1b({64{1'b0}}),
    .output1a(cbuffer128bit_45_output1a), .output1b(cbuffer128bit_45_output1b));
  and and_45 (output1[19], not_1_out, or_45_out);
  or or_45 (or_45_out, comparatoru128bit_45_greater1, comparatoru128bit_45_equal1);
  comparatoru128bit comparatoru128bit_45 (
    .input1a(subtractor128bit_44_output1a), .input1b(subtractor128bit_44_output1b),
    .input2a({{13{1'b0}}, input2, {19{1'b0}}}), .input2b({64{1'b0}}),
    .greater1(comparatoru128bit_45_greater1), .equal1(comparatoru128bit_45_equal1));  // open: less1
  // Probe on subtractor128bit_45_output1a
  // Probe on subtractor128bit_45_output1a
  subtractor128bit subtractor128bit_46 (
    .input1a(subtractor128bit_45_output1a), .input1b(subtractor128bit_45_output1b),
    .input2a(cbuffer128bit_46_output1a), .input2b(cbuffer128bit_46_output1b),
    .output1a(subtractor128bit_46_output1a), .output1b(subtractor128bit_46_output1b));  // open: inborrow, borrow
  cbuffer128bit cbuffer128bit_46 (
    .buffer1(output1[18]), .input1a({{14{1'b0}}, input2, {18{1'b0}}}), .input1b({64{1'b0}}),
    .output1a(cbuffer128bit_46_output1a), .output1b(cbuffer128bit_46_output1b));
  and and_46 (output1[18], not_1_out, or_46_out);
  or or_46 (or_46_out, comparatoru128bit_46_greater1, comparatoru128bit_46_equal1);
  comparatoru128bit comparatoru128bit_46 (
    .input1a(subtractor128bit_45_output1a), .input1b(subtractor128bit_45_output1b),
    .input2a({{14{1'b0}}, input2, {18{1'b0}}}), .input2b({64{1'b0}}),
    .greater1(comparatoru128bit_46_greater1), .equal1(comparatoru128bit_46_equal1));  // open: less1
  // Probe on subtractor128bit_46_output1a
  // Probe on subtractor128bit_46_output1a
  subtractor128bit subtractor128bit_47 (
    .input1a(subtractor128bit_46_output1a), .input1b(subtractor128bit_46_output1b),
    .input2a(cbuffer128bit_47_output1a), .input2b(cbuffer128bit_47_output1b),
    .output1a(subtractor128bit_47_output1a), .output1b(subtractor128bit_47_output1b));  // open: inborrow, borrow
  cbuffer128bit cbuffer128bit_47 (
    .buffer1(output1[17]), .input1a({{15{1'b0}}, input2, {17{1'b0}}}), .input1b({64{1'b0}}),
    .output1a(cbuffer128bit_47_output1a), .output1b(cbuffer128bit_47_output1b));
  and and_47 (output1[17], not_1_out, or_47_out);
  comparatoru128bit comparatoru128bit_47 (
    .input1a(subtractor128bit_46_output1a), .input1b(subtractor128bit_46_output1b),
    .input2a({{15{1'b0}}, input2, {17{1'b0}}}), .input2b({64{1'b0}}),
    .greater1(comparatoru128bit_47_greater1), .equal1(comparatoru128bit_47_equal1));  // open: less1
  or or_47 (or_47_out, comparatoru128bit_47_greater1, comparatoru128bit_47_equal1);
  // Probe on subtractor128bit_47_output1a
  // Probe on subtractor128bit_47_output1a
  subtractor128bit subtractor128bit_48 (
    .input1a(subtractor128bit_47_output1a), .input1b(subtractor128bit_47_output1b),
    .input2a(cbuffer128bit_48_output1a), .input2b(cbuffer128bit_48_output1b),
    .output1a(subtractor128bit_48_output1a), .output1b(subtractor128bit_48_output1b));  // open: inborrow, borrow
  cbuffer128bit cbuffer128bit_48 (
    .buffer1(output1[16]), .input1a({{16{1'b0}}, input2, {16{1'b0}}}), .input1b({64{1'b0}}),
    .output1a(cbuffer128bit_48_output1a), .output1b(cbuffer128bit_48_output1b));
  and and_48 (output1[16], not_1_out, or_48_out);
  or or_48 (or_48_out, comparatoru128bit_48_greater1, comparatoru128bit_48_equal1);
  comparatoru128bit comparatoru128bit_48 (
    .input1a(subtractor128bit_47_output1a), .input1b(subtractor128bit_47_output1b),
    .input2a({{16{1'b0}}, input2, {16{1'b0}}}), .input2b({64{1'b0}}),
    .greater1(comparatoru128bit_48_greater1), .equal1(comparatoru128bit_48_equal1));  // open: less1
  // Probe on subtractor128bit_48_output1a
  // Probe on subtractor128bit_48_output1a
  subtractor128bit subtractor128bit_49 (
    .input1a(subtractor128bit_48_output1a), .input1b(subtractor128bit_48_output1b),
    .input2a(cbuffer128bit_49_output1a), .input2b(cbuffer128bit_49_output1b),
    .output1a(subtractor128bit_49_output1a), .output1b(subtractor128bit_49_output1b));  // open: inborrow, borrow
  cbuffer128bit cbuffer128bit_49 (
    .buffer1(output1[15]), .input1a({{17{1'b0}}, input2, {15{1'b0}}}), .input1b({64{1'b0}}),
    .output1a(cbuffer128bit_49_output1a), .output1b(cbuffer128bit_49_output1b));
  and and_49 (output1[15], not_1_out, or_49_out);
  or or_49 (or_49_out, comparatoru128bit_49_greater1, comparatoru128bit_49_equal1);
  comparatoru128bit comparatoru128bit_49 (
    .input1a(subtractor128bit_48_output1a), .input1b(subtractor128bit_48_output1b),
    .input2a({{17{1'b0}}, input2, {15{1'b0}}}), .input2b({64{1'b0}}),
    .greater1(comparatoru128bit_49_greater1), .equal1(comparatoru128bit_49_equal1));  // open: less1
  // Probe on subtractor128bit_49_output1a
  // Probe on subtractor128bit_49_output1a
  subtractor128bit subtractor128bit_50 (
    .input1a(subtractor128bit_49_output1a), .input1b(subtractor128bit_49_output1b),
    .input2a(cbuffer128bit_50_output1a), .input2b(cbuffer128bit_50_output1b),
    .output1a(subtractor128bit_50_output1a), .output1b(subtractor128bit_50_output1b));  // open: inborrow, borrow
  cbuffer128bit cbuffer128bit_50 (
    .buffer1(output1[14]), .input1a({{18{1'b0}}, input2, {14{1'b0}}}), .input1b({64{1'b0}}),
    .output1a(cbuffer128bit_50_output1a), .output1b(cbuffer128bit_50_output1b));
  and and_50 (output1[14], not_1_out, or_50_out);
  or or_50 (or_50_out, comparatoru128bit_50_greater1, comparatoru128bit_50_equal1);
  comparatoru128bit comparatoru128bit_50 (
    .input1a(subtractor128bit_49_output1a), .input1b(subtractor128bit_49_output1b),
    .input2a({{18{1'b0}}, input2, {14{1'b0}}}), .input2b({64{1'b0}}),
    .greater1(comparatoru128bit_50_greater1), .equal1(comparatoru128bit_50_equal1));  // open: less1
  // Probe on subtractor128bit_50_output1a
  // Probe on subtractor128bit_50_output1a
  subtractor128bit subtractor128bit_51 (
    .input1a(subtractor128bit_50_output1a), .input1b(subtractor128bit_50_output1b),
    .input2a(cbuffer128bit_51_output1a), .input2b(cbuffer128bit_51_output1b),
    .output1a(subtractor128bit_51_output1a), .output1b(subtractor128bit_51_output1b));  // open: inborrow, borrow
  cbuffer128bit cbuffer128bit_51 (
    .buffer1(output1[13]), .input1a({{19{1'b0}}, input2, {13{1'b0}}}), .input1b({64{1'b0}}),
    .output1a(cbuffer128bit_51_output1a), .output1b(cbuffer128bit_51_output1b));
  and and_51 (output1[13], not_1_out, or_51_out);
  or or_51 (or_51_out, comparatoru128bit_51_greater1, comparatoru128bit_51_equal1);
  comparatoru128bit comparatoru128bit_51 (
    .input1a(subtractor128bit_50_output1a), .input1b(subtractor128bit_50_output1b),
    .input2a({{19{1'b0}}, input2, {13{1'b0}}}), .input2b({64{1'b0}}),
    .greater1(comparatoru128bit_51_greater1), .equal1(comparatoru128bit_51_equal1));  // open: less1
  // Probe on subtractor128bit_51_output1a
  // Probe on subtractor128bit_51_output1a
  subtractor128bit subtractor128bit_52 (
    .input1a(subtractor128bit_51_output1a), .input1b(subtractor128bit_51_output1b),
    .input2a(cbuffer128bit_52_output1a), .input2b(cbuffer128bit_52_output1b),
    .output1a(subtractor128bit_52_output1a), .output1b(subtractor128bit_52_output1b));  // open: inborrow, borrow
  cbuffer128bit cbuffer128bit_52 (
    .buffer1(output1[12]), .input1a({{20{1'b0}}, input2, {12{1'b0}}}), .input1b({64{1'b0}}),
    .output1a(cbuffer128bit_52_output1a), .output1b(cbuffer128bit_52_output1b));
  and and_52 (output1[12], not_1_out, or_52_out);
  or or_52 (or_52_out, comparatoru128bit_52_greater1, comparatoru128bit_52_equal1);
  comparatoru128bit comparatoru128bit_52 (
    .input1a(subtractor128bit_51_output1a), .input1b(subtractor128bit_51_output1b),
    .input2a({{20{1'b0}}, input2, {12{1'b0}}}), .input2b({64{1'b0}}),
    .greater1(comparatoru128bit_52_greater1), .equal1(comparatoru128bit_52_equal1));  // open: less1
  // Probe on subtractor128bit_52_output1a
  // Probe on subtractor128bit_52_output1a
  subtractor128bit subtractor128bit_53 (
    .input1a(subtractor128bit_52_output1a), .input1b(subtractor128bit_52_output1b),
    .input2a(cbuffer128bit_53_output1a), .input2b(cbuffer128bit_53_output1b),
    .output1a(subtractor128bit_53_output1a), .output1b(subtractor128bit_53_output1b));  // open: inborrow, borrow
  cbuffer128bit cbuffer128bit_53 (
    .buffer1(output1[11]), .input1a({{21{1'b0}}, input2, {11{1'b0}}}), .input1b({64{1'b0}}),
    .output1a(cbuffer128bit_53_output1a), .output1b(cbuffer128bit_53_output1b));
  and and_53 (output1[11], not_1_out, or_53_out);
  or or_53 (or_53_out, comparatoru128bit_53_greater1, comparatoru128bit_53_equal1);
  comparatoru128bit comparatoru128bit_53 (
    .input1a(subtractor128bit_52_output1a), .input1b(subtractor128bit_52_output1b),
    .input2a({{21{1'b0}}, input2, {11{1'b0}}}), .input2b({64{1'b0}}),
    .greater1(comparatoru128bit_53_greater1), .equal1(comparatoru128bit_53_equal1));  // open: less1
  // Probe on subtractor128bit_53_output1a
  // Probe on subtractor128bit_53_output1a
  subtractor128bit subtractor128bit_54 (
    .input1a(subtractor128bit_53_output1a), .input1b(subtractor128bit_53_output1b),
    .input2a(cbuffer128bit_54_output1a), .input2b(cbuffer128bit_54_output1b),
    .output1a(subtractor128bit_54_output1a), .output1b(subtractor128bit_54_output1b));  // open: inborrow, borrow
  cbuffer128bit cbuffer128bit_54 (
    .buffer1(output1[10]), .input1a({{22{1'b0}}, input2, {10{1'b0}}}), .input1b({64{1'b0}}),
    .output1a(cbuffer128bit_54_output1a), .output1b(cbuffer128bit_54_output1b));
  and and_54 (output1[10], not_1_out, or_54_out);
  or or_54 (or_54_out, comparatoru128bit_54_greater1, comparatoru128bit_54_equal1);
  comparatoru128bit comparatoru128bit_54 (
    .input1a(subtractor128bit_53_output1a), .input1b(subtractor128bit_53_output1b),
    .input2a({{22{1'b0}}, input2, {10{1'b0}}}), .input2b({64{1'b0}}),
    .greater1(comparatoru128bit_54_greater1), .equal1(comparatoru128bit_54_equal1));  // open: less1
  // Probe on subtractor128bit_54_output1a
  // Probe on subtractor128bit_54_output1a
  subtractor128bit subtractor128bit_55 (
    .input1a(subtractor128bit_54_output1a), .input1b(subtractor128bit_54_output1b),
    .input2a(cbuffer128bit_55_output1a), .input2b(cbuffer128bit_55_output1b),
    .output1a(subtractor128bit_55_output1a), .output1b(subtractor128bit_55_output1b));  // open: inborrow, borrow
  cbuffer128bit cbuffer128bit_55 (
    .buffer1(output1[9]), .input1a({{23{1'b0}}, input2, {9{1'b0}}}), .input1b({64{1'b0}}),
    .output1a(cbuffer128bit_55_output1a), .output1b(cbuffer128bit_55_output1b));
  and and_55 (output1[9], not_1_out, or_55_out);
  comparatoru128bit comparatoru128bit_55 (
    .input1a(subtractor128bit_54_output1a), .input1b(subtractor128bit_54_output1b),
    .input2a({{23{1'b0}}, input2, {9{1'b0}}}), .input2b({64{1'b0}}),
    .greater1(comparatoru128bit_55_greater1), .equal1(comparatoru128bit_55_equal1));  // open: less1
  or or_55 (or_55_out, comparatoru128bit_55_greater1, comparatoru128bit_55_equal1);
  // Probe on subtractor128bit_55_output1a
  // Probe on subtractor128bit_55_output1a
  subtractor128bit subtractor128bit_56 (
    .input1a(subtractor128bit_55_output1a), .input1b(subtractor128bit_55_output1b),
    .input2a(cbuffer128bit_56_output1a), .input2b(cbuffer128bit_56_output1b),
    .output1a(subtractor128bit_56_output1a), .output1b(subtractor128bit_56_output1b));  // open: inborrow, borrow
  cbuffer128bit cbuffer128bit_56 (
    .buffer1(output1[8]), .input1a({{24{1'b0}}, input2, {8{1'b0}}}), .input1b({64{1'b0}}),
    .output1a(cbuffer128bit_56_output1a), .output1b(cbuffer128bit_56_output1b));
  and and_56 (output1[8], not_1_out, or_56_out);
  or or_56 (or_56_out, comparatoru128bit_56_greater1, comparatoru128bit_56_equal1);
  comparatoru128bit comparatoru128bit_56 (
    .input1a(subtractor128bit_55_output1a), .input1b(subtractor128bit_55_output1b),
    .input2a({{24{1'b0}}, input2, {8{1'b0}}}), .input2b({64{1'b0}}),
    .greater1(comparatoru128bit_56_greater1), .equal1(comparatoru128bit_56_equal1));  // open: less1
  // Probe on subtractor128bit_56_output1a
  // Probe on subtractor128bit_56_output1a
  subtractor128bit subtractor128bit_57 (
    .input1a(subtractor128bit_56_output1a), .input1b(subtractor128bit_56_output1b),
    .input2a(cbuffer128bit_57_output1a), .input2b(cbuffer128bit_57_output1b),
    .output1a(subtractor128bit_57_output1a), .output1b(subtractor128bit_57_output1b));  // open: inborrow, borrow
  cbuffer128bit cbuffer128bit_57 (
    .buffer1(output1[7]), .input1a({{25{1'b0}}, input2, {7{1'b0}}}), .input1b({64{1'b0}}),
    .output1a(cbuffer128bit_57_output1a), .output1b(cbuffer128bit_57_output1b));
  and and_57 (output1[7], not_1_out, or_57_out);
  or or_57 (or_57_out, comparatoru128bit_57_greater1, comparatoru128bit_57_equal1);
  comparatoru128bit comparatoru128bit_57 (
    .input1a(subtractor128bit_56_output1a), .input1b(subtractor128bit_56_output1b),
    .input2a({{25{1'b0}}, input2, {7{1'b0}}}), .input2b({64{1'b0}}),
    .greater1(comparatoru128bit_57_greater1), .equal1(comparatoru128bit_57_equal1));  // open: less1
  // Probe on subtractor128bit_57_output1a
  // Probe on subtractor128bit_57_output1a
  subtractor128bit subtractor128bit_58 (
    .input1a(subtractor128bit_57_output1a), .input1b(subtractor128bit_57_output1b),
    .input2a(cbuffer128bit_58_output1a), .input2b(cbuffer128bit_58_output1b),
    .output1a(subtractor128bit_58_output1a), .output1b(subtractor128bit_58_output1b));  // open: inborrow, borrow
  cbuffer128bit cbuffer128bit_58 (
    .buffer1(output1[6]), .input1a({{26{1'b0}}, input2, {6{1'b0}}}), .input1b({64{1'b0}}),
    .output1a(cbuffer128bit_58_output1a), .output1b(cbuffer128bit_58_output1b));
  and and_58 (output1[6], not_1_out, or_58_out);
  or or_58 (or_58_out, comparatoru128bit_58_greater1, comparatoru128bit_58_equal1);
  comparatoru128bit comparatoru128bit_58 (
    .input1a(subtractor128bit_57_output1a), .input1b(subtractor128bit_57_output1b),
    .input2a({{26{1'b0}}, input2, {6{1'b0}}}), .input2b({64{1'b0}}),
    .greater1(comparatoru128bit_58_greater1), .equal1(comparatoru128bit_58_equal1));  // open: less1
  // Probe on subtractor128bit_58_output1a
  // Probe on subtractor128bit_58_output1a
  subtractor128bit subtractor128bit_59 (
    .input1a(subtractor128bit_58_output1a), .input1b(subtractor128bit_58_output1b),
    .input2a(cbuffer128bit_59_output1a), .input2b(cbuffer128bit_59_output1b),
    .output1a(subtractor128bit_59_output1a), .output1b(subtractor128bit_59_output1b));  // open: inborrow, borrow
  cbuffer128bit cbuffer128bit_59 (
    .buffer1(output1[5]), .input1a({{27{1'b0}}, input2, {5{1'b0}}}), .input1b({64{1'b0}}),
    .output1a(cbuffer128bit_59_output1a), .output1b(cbuffer128bit_59_output1b));
  and and_59 (output1[5], not_1_out, or_59_out);
  or or_59 (or_59_out, comparatoru128bit_59_greater1, comparatoru128bit_59_equal1);
  comparatoru128bit comparatoru128bit_59 (
    .input1a(subtractor128bit_58_output1a), .input1b(subtractor128bit_58_output1b),
    .input2a({{27{1'b0}}, input2, {5{1'b0}}}), .input2b({64{1'b0}}),
    .greater1(comparatoru128bit_59_greater1), .equal1(comparatoru128bit_59_equal1));  // open: less1
  // Probe on subtractor128bit_59_output1a
  // Probe on subtractor128bit_59_output1a
  subtractor128bit subtractor128bit_60 (
    .input1a(subtractor128bit_59_output1a), .input1b(subtractor128bit_59_output1b),
    .input2a(cbuffer128bit_60_output1a), .input2b(cbuffer128bit_60_output1b),
    .output1a(subtractor128bit_60_output1a), .output1b(subtractor128bit_60_output1b));  // open: inborrow, borrow
  cbuffer128bit cbuffer128bit_60 (
    .buffer1(output1[4]), .input1a({{28{1'b0}}, input2, 4'b0000}), .input1b({64{1'b0}}),
    .output1a(cbuffer128bit_60_output1a), .output1b(cbuffer128bit_60_output1b));
  and and_60 (output1[4], not_1_out, or_60_out);
  or or_60 (or_60_out, comparatoru128bit_60_greater1, comparatoru128bit_60_equal1);
  comparatoru128bit comparatoru128bit_60 (
    .input1a(subtractor128bit_59_output1a), .input1b(subtractor128bit_59_output1b),
    .input2a({{28{1'b0}}, input2, 4'b0000}), .input2b({64{1'b0}}), .greater1(comparatoru128bit_60_greater1),
    .equal1(comparatoru128bit_60_equal1));  // open: less1
  // Probe on subtractor128bit_60_output1a
  // Probe on subtractor128bit_60_output1a
  subtractor128bit subtractor128bit_61 (
    .input1a(subtractor128bit_60_output1a), .input1b(subtractor128bit_60_output1b),
    .input2a(cbuffer128bit_61_output1a), .input2b(cbuffer128bit_61_output1b),
    .output1a(subtractor128bit_61_output1a), .output1b(subtractor128bit_61_output1b));  // open: inborrow, borrow
  cbuffer128bit cbuffer128bit_61 (
    .buffer1(output1[3]), .input1a({{29{1'b0}}, input2, 3'b000}), .input1b({64{1'b0}}),
    .output1a(cbuffer128bit_61_output1a), .output1b(cbuffer128bit_61_output1b));
  and and_61 (output1[3], not_1_out, or_61_out);
  or or_61 (or_61_out, comparatoru128bit_61_greater1, comparatoru128bit_61_equal1);
  comparatoru128bit comparatoru128bit_61 (
    .input1a(subtractor128bit_60_output1a), .input1b(subtractor128bit_60_output1b),
    .input2a({{29{1'b0}}, input2, 3'b000}), .input2b({64{1'b0}}), .greater1(comparatoru128bit_61_greater1),
    .equal1(comparatoru128bit_61_equal1));  // open: less1
  // Probe on subtractor128bit_61_output1a
  // Probe on subtractor128bit_61_output1a
  subtractor128bit subtractor128bit_62 (
    .input1a(subtractor128bit_61_output1a), .input1b(subtractor128bit_61_output1b),
    .input2a(cbuffer128bit_62_output1a), .input2b(cbuffer128bit_62_output1b),
    .output1a(subtractor128bit_62_output1a), .output1b(subtractor128bit_62_output1b));  // open: inborrow, borrow
  cbuffer128bit cbuffer128bit_62 (
    .buffer1(output1[2]), .input1a({{30{1'b0}}, input2, 2'b00}), .input1b({64{1'b0}}),
    .output1a(cbuffer128bit_62_output1a), .output1b(cbuffer128bit_62_output1b));
  and and_62 (output1[2], not_1_out, or_62_out);
  or or_62 (or_62_out, comparatoru128bit_62_greater1, comparatoru128bit_62_equal1);
  comparatoru128bit comparatoru128bit_62 (
    .input1a(subtractor128bit_61_output1a), .input1b(subtractor128bit_61_output1b),
    .input2a({{30{1'b0}}, input2, 2'b00}), .input2b({64{1'b0}}), .greater1(comparatoru128bit_62_greater1),
    .equal1(comparatoru128bit_62_equal1));  // open: less1
  // Probe on subtractor128bit_62_output1a
  // Probe on subtractor128bit_62_output1a
  subtractor128bit subtractor128bit_63 (
    .input1a(subtractor128bit_62_output1a), .input1b(subtractor128bit_62_output1b),
    .input2a(cbuffer128bit_63_output1a), .input2b(cbuffer128bit_63_output1b),
    .output1a(subtractor128bit_63_output1a), .output1b(subtractor128bit_63_output1b));  // open: inborrow, borrow
  cbuffer128bit cbuffer128bit_63 (
    .buffer1(output1[1]), .input1a({{31{1'b0}}, input2, 1'b0}), .input1b({64{1'b0}}),
    .output1a(cbuffer128bit_63_output1a), .output1b(cbuffer128bit_63_output1b));
  and and_63 (output1[1], not_1_out, or_63_out);
  comparatoru128bit comparatoru128bit_63 (
    .input1a(subtractor128bit_62_output1a), .input1b(subtractor128bit_62_output1b),
    .input2a({{31{1'b0}}, input2, 1'b0}), .input2b({64{1'b0}}), .greater1(comparatoru128bit_63_greater1),
    .equal1(comparatoru128bit_63_equal1));  // open: less1
  or or_63 (or_63_out, comparatoru128bit_63_greater1, comparatoru128bit_63_equal1);
  // Probe on subtractor128bit_63_output1a
  // Probe on subtractor128bit_63_output1a
  subtractor128bit subtractor128bit_64 (
    .input1a(subtractor128bit_63_output1a), .input1b(subtractor128bit_63_output1b),
    .input2a(cbuffer128bit_64_output1a), .input2b(cbuffer128bit_64_output1b),
    .output1a({subtractor128bit_64_output1a, remainder}), .output1b(subtractor128bit_64_output1b));  // open: inborrow, borrow
  cbuffer128bit cbuffer128bit_64 (
    .buffer1(output1[0]), .input1a({{32{1'b0}}, input2}), .input1b({64{1'b0}}),
    .output1a(cbuffer128bit_64_output1a), .output1b(cbuffer128bit_64_output1b));
  and and_64 (output1[0], not_1_out, or_64_out);
  or or_64 (or_64_out, comparatoru128bit_64_greater1, comparatoru128bit_64_equal1);
  comparatoru128bit comparatoru128bit_64 (
    .input1a(subtractor128bit_63_output1a), .input1b(subtractor128bit_63_output1b),
    .input2a({{32{1'b0}}, input2}), .input2b({64{1'b0}}), .greater1(comparatoru128bit_64_greater1),
    .equal1(comparatoru128bit_64_equal1));  // open: less1
  // Probe on {subtractor128bit_64_output1a, remainder}
  // Probe on {subtractor128bit_64_output1a, remainder}
  // Probe on {and_32_out, output1}
  // Probe on {and_32_out, output1}
  // Probe on remainder
  // Probe on remainder
  // Probe on output1
  // Probe on output1

  // Notes on the sheet:
  //   inupper: initial=0x3b5afedc
  //   input2: initial=0x14b7a
  //   input1: initial=0x26ebfa3d
endmodule

module comparatoru1bit (
  input  input1,
  input  input2,
  output greater1,
  output equal1,
  output less1
);

  wire not_1_out, not_2_out;

  and and_1 (greater1, input1, not_1_out);
  not not_1 (not_1_out, input2);
  xnor xnor_1 (equal1, input1, input2);
  not not_2 (not_2_out, input1);
  and and_2 (less1, not_2_out, input2);
endmodule

module comparatoru2bit (
  input  [1:0] input1,
  input  [1:0] input2,
  output greater1,
  output equal1,
  output less1
);

  wire and_2_out, and_3_out, comparatoru1bit_1_equal1, comparatoru1bit_1_greater1, comparatoru1bit_1_less1,
       comparatoru1bit_2_equal1, comparatoru1bit_2_greater1, comparatoru1bit_2_less1;

  comparatoru1bit comparatoru1bit_1 (
    .input1(input1[1]), .input2(input2[1]), .greater1(comparatoru1bit_1_greater1),
    .equal1(comparatoru1bit_1_equal1), .less1(comparatoru1bit_1_less1));
  and and_1 (equal1, comparatoru1bit_1_equal1, comparatoru1bit_2_equal1);
  or or_1 (greater1, comparatoru1bit_1_greater1, and_2_out);
  and and_2 (and_2_out, comparatoru1bit_1_equal1, comparatoru1bit_2_greater1);
  or or_2 (less1, comparatoru1bit_1_less1, and_3_out);
  and and_3 (and_3_out, comparatoru1bit_1_equal1, comparatoru1bit_2_less1);
  comparatoru1bit comparatoru1bit_2 (
    .input1(input1[0]), .input2(input2[0]), .greater1(comparatoru1bit_2_greater1),
    .equal1(comparatoru1bit_2_equal1), .less1(comparatoru1bit_2_less1));

  // Notes on the sheet:
  //   input1: initial=0x2
  //   input2: initial=0x3
endmodule

module comparatoru4bit (
  input  [3:0] input1,
  input  [3:0] input2,
  output greater1,
  output equal1,
  output less1
);

  wire and_2_out, and_3_out, comparatoru2bit_1_equal1, comparatoru2bit_1_greater1, comparatoru2bit_1_less1,
       comparatoru2bit_2_equal1, comparatoru2bit_2_greater1, comparatoru2bit_2_less1;

  comparatoru2bit comparatoru2bit_1 (
    .input1(input1[3:2]), .input2(input2[3:2]), .greater1(comparatoru2bit_1_greater1),
    .equal1(comparatoru2bit_1_equal1), .less1(comparatoru2bit_1_less1));
  and and_1 (equal1, comparatoru2bit_1_equal1, comparatoru2bit_2_equal1);
  or or_1 (greater1, comparatoru2bit_1_greater1, and_2_out);
  and and_2 (and_2_out, comparatoru2bit_1_equal1, comparatoru2bit_2_greater1);
  or or_2 (less1, comparatoru2bit_1_less1, and_3_out);
  and and_3 (and_3_out, comparatoru2bit_1_equal1, comparatoru2bit_2_less1);
  comparatoru2bit comparatoru2bit_2 (
    .input1(input1[1:0]), .input2(input2[1:0]), .greater1(comparatoru2bit_2_greater1),
    .equal1(comparatoru2bit_2_equal1), .less1(comparatoru2bit_2_less1));

  // Notes on the sheet:
  //   input1: initial=0x2
  //   input2: initial=0x3
endmodule

module comparatoru8bit (
  input  [7:0] input1,
  input  [7:0] input2,
  output greater1,
  output equal1,
  output less1
);

  wire and_2_out, and_3_out, comparatoru4bit_1_equal1, comparatoru4bit_1_greater1, comparatoru4bit_1_less1,
       comparatoru4bit_2_equal1, comparatoru4bit_2_greater1, comparatoru4bit_2_less1;

  comparatoru4bit comparatoru4bit_1 (
    .input1(input1[7:4]), .input2(input2[7:4]), .greater1(comparatoru4bit_1_greater1),
    .equal1(comparatoru4bit_1_equal1), .less1(comparatoru4bit_1_less1));
  and and_1 (equal1, comparatoru4bit_1_equal1, comparatoru4bit_2_equal1);
  or or_1 (greater1, comparatoru4bit_1_greater1, and_2_out);
  and and_2 (and_2_out, comparatoru4bit_1_equal1, comparatoru4bit_2_greater1);
  or or_2 (less1, comparatoru4bit_1_less1, and_3_out);
  and and_3 (and_3_out, comparatoru4bit_1_equal1, comparatoru4bit_2_less1);
  comparatoru4bit comparatoru4bit_2 (
    .input1(input1[3:0]), .input2(input2[3:0]), .greater1(comparatoru4bit_2_greater1),
    .equal1(comparatoru4bit_2_equal1), .less1(comparatoru4bit_2_less1));

  // Notes on the sheet:
  //   input1: initial=0x2
  //   input2: initial=0x3
endmodule

module comparatoru16bit (
  input  [15:0] input1,
  input  [15:0] input2,
  output greater1,
  output equal1,
  output less1
);

  wire and_2_out, and_3_out, comparatoru8bit_1_equal1, comparatoru8bit_1_greater1, comparatoru8bit_1_less1,
       comparatoru8bit_2_equal1, comparatoru8bit_2_greater1, comparatoru8bit_2_less1;

  comparatoru8bit comparatoru8bit_1 (
    .input1(input1[15:8]), .input2(input2[15:8]), .greater1(comparatoru8bit_1_greater1),
    .equal1(comparatoru8bit_1_equal1), .less1(comparatoru8bit_1_less1));
  and and_1 (equal1, comparatoru8bit_1_equal1, comparatoru8bit_2_equal1);
  or or_1 (greater1, comparatoru8bit_1_greater1, and_2_out);
  and and_2 (and_2_out, comparatoru8bit_1_equal1, comparatoru8bit_2_greater1);
  or or_2 (less1, comparatoru8bit_1_less1, and_3_out);
  and and_3 (and_3_out, comparatoru8bit_1_equal1, comparatoru8bit_2_less1);
  comparatoru8bit comparatoru8bit_2 (
    .input1(input1[7:0]), .input2(input2[7:0]), .greater1(comparatoru8bit_2_greater1),
    .equal1(comparatoru8bit_2_equal1), .less1(comparatoru8bit_2_less1));

  // Notes on the sheet:
  //   input1: initial=0x2
  //   input2: initial=0x3
endmodule

module comparatoru32bit (
  input  [31:0] input1,
  input  [31:0] input2,
  output greater1,
  output equal1,
  output less1
);

  wire and_2_out, and_3_out, comparatoru16bit_1_equal1, comparatoru16bit_1_greater1,
       comparatoru16bit_1_less1, comparatoru16bit_2_equal1, comparatoru16bit_2_greater1,
       comparatoru16bit_2_less1;

  comparatoru16bit comparatoru16bit_1 (
    .input1(input1[31:16]), .input2(input2[31:16]), .greater1(comparatoru16bit_1_greater1),
    .equal1(comparatoru16bit_1_equal1), .less1(comparatoru16bit_1_less1));
  and and_1 (equal1, comparatoru16bit_1_equal1, comparatoru16bit_2_equal1);
  or or_1 (greater1, comparatoru16bit_1_greater1, and_2_out);
  and and_2 (and_2_out, comparatoru16bit_1_equal1, comparatoru16bit_2_greater1);
  or or_2 (less1, comparatoru16bit_1_less1, and_3_out);
  and and_3 (and_3_out, comparatoru16bit_1_equal1, comparatoru16bit_2_less1);
  comparatoru16bit comparatoru16bit_2 (
    .input1(input1[15:0]), .input2(input2[15:0]), .greater1(comparatoru16bit_2_greater1),
    .equal1(comparatoru16bit_2_equal1), .less1(comparatoru16bit_2_less1));

  // Notes on the sheet:
  //   input1: initial=0x2
  //   input2: initial=0x3
endmodule

module comparatoru64bit (
  input  [63:0] input1,
  input  [63:0] input2,
  output greater1,
  output equal1,
  output less1
);

  wire and_2_out, and_3_out, comparatoru32bit_1_equal1, comparatoru32bit_1_greater1,
       comparatoru32bit_1_less1, comparatoru32bit_2_equal1, comparatoru32bit_2_greater1,
       comparatoru32bit_2_less1;

  comparatoru32bit comparatoru32bit_1 (
    .input1(input1[63:32]), .input2(input2[63:32]), .greater1(comparatoru32bit_1_greater1),
    .equal1(comparatoru32bit_1_equal1), .less1(comparatoru32bit_1_less1));
  and and_1 (equal1, comparatoru32bit_1_equal1, comparatoru32bit_2_equal1);
  or or_1 (greater1, comparatoru32bit_1_greater1, and_2_out);
  and and_2 (and_2_out, comparatoru32bit_1_equal1, comparatoru32bit_2_greater1);
  or or_2 (less1, comparatoru32bit_1_less1, and_3_out);
  and and_3 (and_3_out, comparatoru32bit_1_equal1, comparatoru32bit_2_less1);
  comparatoru32bit comparatoru32bit_2 (
    .input1(input1[31:0]), .input2(input2[31:0]), .greater1(comparatoru32bit_2_greater1),
    .equal1(comparatoru32bit_2_equal1), .less1(comparatoru32bit_2_less1));

  // Notes on the sheet:
  //   input1: initial=0x2
  //   input2: initial=0x3
endmodule

module comparatoru128bit (
  input  [63:0] input1a,
  input  [63:0] input1b,
  input  [63:0] input2a,
  input  [63:0] input2b,
  output greater1,
  output equal1,
  output less1
);

  wire and_2_out, and_3_out, comparatoru64bit_1_equal1, comparatoru64bit_1_greater1,
       comparatoru64bit_1_less1, comparatoru64bit_2_equal1, comparatoru64bit_2_greater1,
       comparatoru64bit_2_less1;

  comparatoru64bit comparatoru64bit_1 (
    .input1(input1b), .input2(input2b), .greater1(comparatoru64bit_1_greater1),
    .equal1(comparatoru64bit_1_equal1), .less1(comparatoru64bit_1_less1));
  and and_1 (equal1, comparatoru64bit_1_equal1, comparatoru64bit_2_equal1);
  or or_1 (greater1, comparatoru64bit_1_greater1, and_2_out);
  and and_2 (and_2_out, comparatoru64bit_1_equal1, comparatoru64bit_2_greater1);
  or or_2 (less1, comparatoru64bit_1_less1, and_3_out);
  and and_3 (and_3_out, comparatoru64bit_1_equal1, comparatoru64bit_2_less1);
  comparatoru64bit comparatoru64bit_2 (
    .input1(input1a), .input2(input2a), .greater1(comparatoru64bit_2_greater1),
    .equal1(comparatoru64bit_2_equal1), .less1(comparatoru64bit_2_less1));

  // Notes on the sheet:
  //   input1b: initial=0x2
  //   input2b: initial=0x3
endmodule

module comparatoru256bit (
  input  [63:0] input1a,
  input  [63:0] input1b,
  input  [63:0] input1c,
  input  [63:0] input1d,
  input  [63:0] input2a,
  input  [63:0] input2b,
  input  [63:0] input2c,
  input  [63:0] input2d,
  output greater1,
  output equal1,
  output less1
);

  wire and_2_out, and_3_out, comparatoru128bit_1_equal1, comparatoru128bit_1_greater1,
       comparatoru128bit_1_less1, comparatoru128bit_2_equal1, comparatoru128bit_2_greater1,
       comparatoru128bit_2_less1;

  comparatoru128bit comparatoru128bit_1 (
    .input1a(input1c), .input1b(input1d), .input2a(input2c), .input2b(input2d),
    .greater1(comparatoru128bit_1_greater1), .equal1(comparatoru128bit_1_equal1),
    .less1(comparatoru128bit_1_less1));
  and and_1 (equal1, comparatoru128bit_1_equal1, comparatoru128bit_2_equal1);
  or or_1 (greater1, comparatoru128bit_1_greater1, and_2_out);
  and and_2 (and_2_out, comparatoru128bit_1_equal1, comparatoru128bit_2_greater1);
  or or_2 (less1, comparatoru128bit_1_less1, and_3_out);
  and and_3 (and_3_out, comparatoru128bit_1_equal1, comparatoru128bit_2_less1);
  comparatoru128bit comparatoru128bit_2 (
    .input1a(input1a), .input1b(input1b), .input2a(input2a), .input2b(input2b),
    .greater1(comparatoru128bit_2_greater1), .equal1(comparatoru128bit_2_equal1),
    .less1(comparatoru128bit_2_less1));
endmodule
module divideru64bit (
  input  [63:0] inupper,
  input  [63:0] input1,
  input  [63:0] input2,
  output [63:0] remainder,
  output [63:0] output1
);

  wire comparatoru64bit_1_equal1, comparatoru256bit_1_equal1, comparatoru256bit_1_greater1,
       comparatoru256bit_2_equal1, comparatoru256bit_2_greater1, comparatoru256bit_3_equal1,
       comparatoru256bit_3_greater1, comparatoru256bit_4_equal1, comparatoru256bit_4_greater1,
       comparatoru256bit_5_equal1, comparatoru256bit_5_greater1, comparatoru256bit_6_equal1,
       comparatoru256bit_6_greater1, comparatoru256bit_7_equal1, comparatoru256bit_7_greater1,
       comparatoru256bit_8_equal1, comparatoru256bit_8_greater1, comparatoru256bit_9_equal1,
       comparatoru256bit_9_greater1, comparatoru256bit_10_equal1, comparatoru256bit_10_greater1,
       comparatoru256bit_11_equal1, comparatoru256bit_11_greater1, comparatoru256bit_12_equal1,
       comparatoru256bit_12_greater1, comparatoru256bit_13_equal1, comparatoru256bit_13_greater1,
       comparatoru256bit_14_equal1, comparatoru256bit_14_greater1, comparatoru256bit_15_equal1,
       comparatoru256bit_15_greater1, comparatoru256bit_16_equal1, comparatoru256bit_16_greater1,
       comparatoru256bit_17_equal1, comparatoru256bit_17_greater1, comparatoru256bit_18_equal1,
       comparatoru256bit_18_greater1, comparatoru256bit_19_equal1, comparatoru256bit_19_greater1,
       comparatoru256bit_20_equal1, comparatoru256bit_20_greater1, comparatoru256bit_21_equal1,
       comparatoru256bit_21_greater1, comparatoru256bit_22_equal1, comparatoru256bit_22_greater1,
       comparatoru256bit_23_equal1, comparatoru256bit_23_greater1, comparatoru256bit_24_equal1,
       comparatoru256bit_24_greater1, comparatoru256bit_25_equal1, comparatoru256bit_25_greater1,
       comparatoru256bit_26_equal1, comparatoru256bit_26_greater1, comparatoru256bit_27_equal1,
       comparatoru256bit_27_greater1, comparatoru256bit_28_equal1, comparatoru256bit_28_greater1,
       comparatoru256bit_29_equal1, comparatoru256bit_29_greater1, comparatoru256bit_30_equal1,
       comparatoru256bit_30_greater1, comparatoru256bit_31_equal1, comparatoru256bit_31_greater1,
       comparatoru256bit_32_equal1, comparatoru256bit_32_greater1, comparatoru256bit_33_equal1,
       comparatoru256bit_33_greater1, comparatoru256bit_34_equal1, comparatoru256bit_34_greater1,
       comparatoru256bit_35_equal1, comparatoru256bit_35_greater1, comparatoru256bit_36_equal1,
       comparatoru256bit_36_greater1, comparatoru256bit_37_equal1, comparatoru256bit_37_greater1,
       comparatoru256bit_38_equal1, comparatoru256bit_38_greater1, comparatoru256bit_39_equal1,
       comparatoru256bit_39_greater1, comparatoru256bit_40_equal1, comparatoru256bit_40_greater1,
       comparatoru256bit_41_equal1, comparatoru256bit_41_greater1, comparatoru256bit_42_equal1,
       comparatoru256bit_42_greater1, comparatoru256bit_43_equal1, comparatoru256bit_43_greater1,
       comparatoru256bit_44_equal1, comparatoru256bit_44_greater1, comparatoru256bit_45_equal1,
       comparatoru256bit_45_greater1, comparatoru256bit_46_equal1, comparatoru256bit_46_greater1,
       comparatoru256bit_47_equal1, comparatoru256bit_47_greater1, comparatoru256bit_48_equal1,
       comparatoru256bit_48_greater1, comparatoru256bit_49_equal1, comparatoru256bit_49_greater1,
       comparatoru256bit_50_equal1, comparatoru256bit_50_greater1, comparatoru256bit_51_equal1,
       comparatoru256bit_51_greater1, comparatoru256bit_52_equal1, comparatoru256bit_52_greater1,
       comparatoru256bit_53_equal1, comparatoru256bit_53_greater1, comparatoru256bit_54_equal1,
       comparatoru256bit_54_greater1, comparatoru256bit_55_equal1, comparatoru256bit_55_greater1,
       comparatoru256bit_56_equal1, comparatoru256bit_56_greater1, comparatoru256bit_57_equal1,
       comparatoru256bit_57_greater1, comparatoru256bit_58_equal1, comparatoru256bit_58_greater1,
       comparatoru256bit_59_equal1, comparatoru256bit_59_greater1, comparatoru256bit_60_equal1,
       comparatoru256bit_60_greater1, comparatoru256bit_61_equal1, comparatoru256bit_61_greater1,
       comparatoru256bit_62_equal1, comparatoru256bit_62_greater1, comparatoru256bit_63_equal1,
       comparatoru256bit_63_greater1, comparatoru256bit_64_equal1, comparatoru256bit_64_greater1, not_1_out,
       or_1_out, or_2_out, or_3_out, or_4_out, or_5_out, or_6_out, or_7_out, or_8_out, or_9_out, or_10_out,
       or_11_out, or_12_out, or_13_out, or_14_out, or_15_out, or_16_out, or_17_out, or_18_out, or_19_out,
       or_20_out, or_21_out, or_22_out, or_23_out, or_24_out, or_25_out, or_26_out, or_27_out, or_28_out,
       or_29_out, or_30_out, or_31_out, or_32_out, or_33_out, or_34_out, or_35_out, or_36_out, or_37_out,
       or_38_out, or_39_out, or_40_out, or_41_out, or_42_out, or_43_out, or_44_out, or_45_out, or_46_out,
       or_47_out, or_48_out, or_49_out, or_50_out, or_51_out, or_52_out, or_53_out, or_54_out, or_55_out,
       or_56_out, or_57_out, or_58_out, or_59_out, or_60_out, or_61_out, or_62_out, or_63_out, or_64_out;
  wire [63:0] cbuffer256bit_1_output1a, cbuffer256bit_1_output1b, cbuffer256bit_1_output1c,
       cbuffer256bit_1_output1d, cbuffer256bit_2_output1a, cbuffer256bit_2_output1b,
       cbuffer256bit_2_output1c, cbuffer256bit_2_output1d, cbuffer256bit_3_output1a,
       cbuffer256bit_3_output1b, cbuffer256bit_3_output1c, cbuffer256bit_3_output1d,
       cbuffer256bit_4_output1a, cbuffer256bit_4_output1b, cbuffer256bit_4_output1c,
       cbuffer256bit_4_output1d, cbuffer256bit_5_output1a, cbuffer256bit_5_output1b,
       cbuffer256bit_5_output1c, cbuffer256bit_5_output1d, cbuffer256bit_6_output1a,
       cbuffer256bit_6_output1b, cbuffer256bit_6_output1c, cbuffer256bit_6_output1d,
       cbuffer256bit_7_output1a, cbuffer256bit_7_output1b, cbuffer256bit_7_output1c,
       cbuffer256bit_7_output1d, cbuffer256bit_8_output1a, cbuffer256bit_8_output1b,
       cbuffer256bit_8_output1c, cbuffer256bit_8_output1d, cbuffer256bit_9_output1a,
       cbuffer256bit_9_output1b, cbuffer256bit_9_output1c, cbuffer256bit_9_output1d,
       cbuffer256bit_10_output1a, cbuffer256bit_10_output1b, cbuffer256bit_10_output1c,
       cbuffer256bit_10_output1d, cbuffer256bit_11_output1a, cbuffer256bit_11_output1b,
       cbuffer256bit_11_output1c, cbuffer256bit_11_output1d, cbuffer256bit_12_output1a,
       cbuffer256bit_12_output1b, cbuffer256bit_12_output1c, cbuffer256bit_12_output1d,
       cbuffer256bit_13_output1a, cbuffer256bit_13_output1b, cbuffer256bit_13_output1c,
       cbuffer256bit_13_output1d, cbuffer256bit_14_output1a, cbuffer256bit_14_output1b,
       cbuffer256bit_14_output1c, cbuffer256bit_14_output1d, cbuffer256bit_15_output1a,
       cbuffer256bit_15_output1b, cbuffer256bit_15_output1c, cbuffer256bit_15_output1d,
       cbuffer256bit_16_output1a, cbuffer256bit_16_output1b, cbuffer256bit_16_output1c,
       cbuffer256bit_16_output1d, cbuffer256bit_17_output1a, cbuffer256bit_17_output1b,
       cbuffer256bit_17_output1c, cbuffer256bit_17_output1d, cbuffer256bit_18_output1a,
       cbuffer256bit_18_output1b, cbuffer256bit_18_output1c, cbuffer256bit_18_output1d,
       cbuffer256bit_19_output1a, cbuffer256bit_19_output1b, cbuffer256bit_19_output1c,
       cbuffer256bit_19_output1d, cbuffer256bit_20_output1a, cbuffer256bit_20_output1b,
       cbuffer256bit_20_output1c, cbuffer256bit_20_output1d, cbuffer256bit_21_output1a,
       cbuffer256bit_21_output1b, cbuffer256bit_21_output1c, cbuffer256bit_21_output1d,
       cbuffer256bit_22_output1a, cbuffer256bit_22_output1b, cbuffer256bit_22_output1c,
       cbuffer256bit_22_output1d, cbuffer256bit_23_output1a, cbuffer256bit_23_output1b,
       cbuffer256bit_23_output1c, cbuffer256bit_23_output1d, cbuffer256bit_24_output1a,
       cbuffer256bit_24_output1b, cbuffer256bit_24_output1c, cbuffer256bit_24_output1d,
       cbuffer256bit_25_output1a, cbuffer256bit_25_output1b, cbuffer256bit_25_output1c,
       cbuffer256bit_25_output1d, cbuffer256bit_26_output1a, cbuffer256bit_26_output1b,
       cbuffer256bit_26_output1c, cbuffer256bit_26_output1d, cbuffer256bit_27_output1a,
       cbuffer256bit_27_output1b, cbuffer256bit_27_output1c, cbuffer256bit_27_output1d,
       cbuffer256bit_28_output1a, cbuffer256bit_28_output1b, cbuffer256bit_28_output1c,
       cbuffer256bit_28_output1d, cbuffer256bit_29_output1a, cbuffer256bit_29_output1b,
       cbuffer256bit_29_output1c, cbuffer256bit_29_output1d, cbuffer256bit_30_output1a,
       cbuffer256bit_30_output1b, cbuffer256bit_30_output1c, cbuffer256bit_30_output1d,
       cbuffer256bit_31_output1a, cbuffer256bit_31_output1b, cbuffer256bit_31_output1c,
       cbuffer256bit_31_output1d, cbuffer256bit_32_output1a, cbuffer256bit_32_output1b,
       cbuffer256bit_32_output1c, cbuffer256bit_32_output1d, cbuffer256bit_33_output1a,
       cbuffer256bit_33_output1b, cbuffer256bit_33_output1c, cbuffer256bit_33_output1d,
       cbuffer256bit_34_output1a, cbuffer256bit_34_output1b, cbuffer256bit_34_output1c,
       cbuffer256bit_34_output1d, cbuffer256bit_35_output1a, cbuffer256bit_35_output1b,
       cbuffer256bit_35_output1c, cbuffer256bit_35_output1d, cbuffer256bit_36_output1a,
       cbuffer256bit_36_output1b, cbuffer256bit_36_output1c, cbuffer256bit_36_output1d,
       cbuffer256bit_37_output1a, cbuffer256bit_37_output1b, cbuffer256bit_37_output1c,
       cbuffer256bit_37_output1d, cbuffer256bit_38_output1a, cbuffer256bit_38_output1b,
       cbuffer256bit_38_output1c, cbuffer256bit_38_output1d, cbuffer256bit_39_output1a,
       cbuffer256bit_39_output1b, cbuffer256bit_39_output1c, cbuffer256bit_39_output1d,
       cbuffer256bit_40_output1a, cbuffer256bit_40_output1b, cbuffer256bit_40_output1c,
       cbuffer256bit_40_output1d, cbuffer256bit_41_output1a, cbuffer256bit_41_output1b,
       cbuffer256bit_41_output1c, cbuffer256bit_41_output1d, cbuffer256bit_42_output1a,
       cbuffer256bit_42_output1b, cbuffer256bit_42_output1c, cbuffer256bit_42_output1d,
       cbuffer256bit_43_output1a, cbuffer256bit_43_output1b, cbuffer256bit_43_output1c,
       cbuffer256bit_43_output1d, cbuffer256bit_44_output1a, cbuffer256bit_44_output1b,
       cbuffer256bit_44_output1c, cbuffer256bit_44_output1d, cbuffer256bit_45_output1a,
       cbuffer256bit_45_output1b, cbuffer256bit_45_output1c, cbuffer256bit_45_output1d,
       cbuffer256bit_46_output1a, cbuffer256bit_46_output1b, cbuffer256bit_46_output1c,
       cbuffer256bit_46_output1d, cbuffer256bit_47_output1a, cbuffer256bit_47_output1b,
       cbuffer256bit_47_output1c, cbuffer256bit_47_output1d, cbuffer256bit_48_output1a,
       cbuffer256bit_48_output1b, cbuffer256bit_48_output1c, cbuffer256bit_48_output1d,
       cbuffer256bit_49_output1a, cbuffer256bit_49_output1b, cbuffer256bit_49_output1c,
       cbuffer256bit_49_output1d, cbuffer256bit_50_output1a, cbuffer256bit_50_output1b,
       cbuffer256bit_50_output1c, cbuffer256bit_50_output1d, cbuffer256bit_51_output1a,
       cbuffer256bit_51_output1b, cbuffer256bit_51_output1c, cbuffer256bit_51_output1d,
       cbuffer256bit_52_output1a, cbuffer256bit_52_output1b, cbuffer256bit_52_output1c,
       cbuffer256bit_52_output1d, cbuffer256bit_53_output1a, cbuffer256bit_53_output1b,
       cbuffer256bit_53_output1c, cbuffer256bit_53_output1d, cbuffer256bit_54_output1a,
       cbuffer256bit_54_output1b, cbuffer256bit_54_output1c, cbuffer256bit_54_output1d,
       cbuffer256bit_55_output1a, cbuffer256bit_55_output1b, cbuffer256bit_55_output1c,
       cbuffer256bit_55_output1d, cbuffer256bit_56_output1a, cbuffer256bit_56_output1b,
       cbuffer256bit_56_output1c, cbuffer256bit_56_output1d, cbuffer256bit_57_output1a,
       cbuffer256bit_57_output1b, cbuffer256bit_57_output1c, cbuffer256bit_57_output1d,
       cbuffer256bit_58_output1a, cbuffer256bit_58_output1b, cbuffer256bit_58_output1c,
       cbuffer256bit_58_output1d, cbuffer256bit_59_output1a, cbuffer256bit_59_output1b,
       cbuffer256bit_59_output1c, cbuffer256bit_59_output1d, cbuffer256bit_60_output1a,
       cbuffer256bit_60_output1b, cbuffer256bit_60_output1c, cbuffer256bit_60_output1d,
       cbuffer256bit_61_output1a, cbuffer256bit_61_output1b, cbuffer256bit_61_output1c,
       cbuffer256bit_61_output1d, cbuffer256bit_62_output1a, cbuffer256bit_62_output1b,
       cbuffer256bit_62_output1c, cbuffer256bit_62_output1d, cbuffer256bit_63_output1a,
       cbuffer256bit_63_output1b, cbuffer256bit_63_output1c, cbuffer256bit_63_output1d,
       cbuffer256bit_64_output1a, cbuffer256bit_64_output1b, cbuffer256bit_64_output1c,
       cbuffer256bit_64_output1d, divider_1_out, divider_1_rem, subtractor256bit_1_output1a,
       subtractor256bit_1_output1b, subtractor256bit_1_output1c, subtractor256bit_1_output1d,
       subtractor256bit_2_output1a, subtractor256bit_2_output1b, subtractor256bit_2_output1c,
       subtractor256bit_2_output1d, subtractor256bit_3_output1a, subtractor256bit_3_output1b,
       subtractor256bit_3_output1c, subtractor256bit_3_output1d, subtractor256bit_4_output1a,
       subtractor256bit_4_output1b, subtractor256bit_4_output1c, subtractor256bit_4_output1d,
       subtractor256bit_5_output1a, subtractor256bit_5_output1b, subtractor256bit_5_output1c,
       subtractor256bit_5_output1d, subtractor256bit_6_output1a, subtractor256bit_6_output1b,
       subtractor256bit_6_output1c, subtractor256bit_6_output1d, subtractor256bit_7_output1a,
       subtractor256bit_7_output1b, subtractor256bit_7_output1c, subtractor256bit_7_output1d,
       subtractor256bit_8_output1a, subtractor256bit_8_output1b, subtractor256bit_8_output1c,
       subtractor256bit_8_output1d, subtractor256bit_9_output1a, subtractor256bit_9_output1b,
       subtractor256bit_9_output1c, subtractor256bit_9_output1d, subtractor256bit_10_output1a,
       subtractor256bit_10_output1b, subtractor256bit_10_output1c, subtractor256bit_10_output1d,
       subtractor256bit_11_output1a, subtractor256bit_11_output1b, subtractor256bit_11_output1c,
       subtractor256bit_11_output1d, subtractor256bit_12_output1a, subtractor256bit_12_output1b,
       subtractor256bit_12_output1c, subtractor256bit_12_output1d, subtractor256bit_13_output1a,
       subtractor256bit_13_output1b, subtractor256bit_13_output1c, subtractor256bit_13_output1d,
       subtractor256bit_14_output1a, subtractor256bit_14_output1b, subtractor256bit_14_output1c,
       subtractor256bit_14_output1d, subtractor256bit_15_output1a, subtractor256bit_15_output1b,
       subtractor256bit_15_output1c, subtractor256bit_15_output1d, subtractor256bit_16_output1a,
       subtractor256bit_16_output1b, subtractor256bit_16_output1c, subtractor256bit_16_output1d,
       subtractor256bit_17_output1a, subtractor256bit_17_output1b, subtractor256bit_17_output1c,
       subtractor256bit_17_output1d, subtractor256bit_18_output1a, subtractor256bit_18_output1b,
       subtractor256bit_18_output1c, subtractor256bit_18_output1d, subtractor256bit_19_output1a,
       subtractor256bit_19_output1b, subtractor256bit_19_output1c, subtractor256bit_19_output1d,
       subtractor256bit_20_output1a, subtractor256bit_20_output1b, subtractor256bit_20_output1c,
       subtractor256bit_20_output1d, subtractor256bit_21_output1a, subtractor256bit_21_output1b,
       subtractor256bit_21_output1c, subtractor256bit_21_output1d, subtractor256bit_22_output1a,
       subtractor256bit_22_output1b, subtractor256bit_22_output1c, subtractor256bit_22_output1d,
       subtractor256bit_23_output1a, subtractor256bit_23_output1b, subtractor256bit_23_output1c,
       subtractor256bit_23_output1d, subtractor256bit_24_output1a, subtractor256bit_24_output1b,
       subtractor256bit_24_output1c, subtractor256bit_24_output1d, subtractor256bit_25_output1a,
       subtractor256bit_25_output1b, subtractor256bit_25_output1c, subtractor256bit_25_output1d,
       subtractor256bit_26_output1a, subtractor256bit_26_output1b, subtractor256bit_26_output1c,
       subtractor256bit_26_output1d, subtractor256bit_27_output1a, subtractor256bit_27_output1b,
       subtractor256bit_27_output1c, subtractor256bit_27_output1d, subtractor256bit_28_output1a,
       subtractor256bit_28_output1b, subtractor256bit_28_output1c, subtractor256bit_28_output1d,
       subtractor256bit_29_output1a, subtractor256bit_29_output1b, subtractor256bit_29_output1c,
       subtractor256bit_29_output1d, subtractor256bit_30_output1a, subtractor256bit_30_output1b,
       subtractor256bit_30_output1c, subtractor256bit_30_output1d, subtractor256bit_31_output1a,
       subtractor256bit_31_output1b, subtractor256bit_31_output1c, subtractor256bit_31_output1d,
       subtractor256bit_32_output1a, subtractor256bit_32_output1b, subtractor256bit_32_output1c,
       subtractor256bit_32_output1d, subtractor256bit_33_output1a, subtractor256bit_33_output1b,
       subtractor256bit_33_output1c, subtractor256bit_33_output1d, subtractor256bit_34_output1a,
       subtractor256bit_34_output1b, subtractor256bit_34_output1c, subtractor256bit_34_output1d,
       subtractor256bit_35_output1a, subtractor256bit_35_output1b, subtractor256bit_35_output1c,
       subtractor256bit_35_output1d, subtractor256bit_36_output1a, subtractor256bit_36_output1b,
       subtractor256bit_36_output1c, subtractor256bit_36_output1d, subtractor256bit_37_output1a,
       subtractor256bit_37_output1b, subtractor256bit_37_output1c, subtractor256bit_37_output1d,
       subtractor256bit_38_output1a, subtractor256bit_38_output1b, subtractor256bit_38_output1c,
       subtractor256bit_38_output1d, subtractor256bit_39_output1a, subtractor256bit_39_output1b,
       subtractor256bit_39_output1c, subtractor256bit_39_output1d, subtractor256bit_40_output1a,
       subtractor256bit_40_output1b, subtractor256bit_40_output1c, subtractor256bit_40_output1d,
       subtractor256bit_41_output1a, subtractor256bit_41_output1b, subtractor256bit_41_output1c,
       subtractor256bit_41_output1d, subtractor256bit_42_output1a, subtractor256bit_42_output1b,
       subtractor256bit_42_output1c, subtractor256bit_42_output1d, subtractor256bit_43_output1a,
       subtractor256bit_43_output1b, subtractor256bit_43_output1c, subtractor256bit_43_output1d,
       subtractor256bit_44_output1a, subtractor256bit_44_output1b, subtractor256bit_44_output1c,
       subtractor256bit_44_output1d, subtractor256bit_45_output1a, subtractor256bit_45_output1b,
       subtractor256bit_45_output1c, subtractor256bit_45_output1d, subtractor256bit_46_output1a,
       subtractor256bit_46_output1b, subtractor256bit_46_output1c, subtractor256bit_46_output1d,
       subtractor256bit_47_output1a, subtractor256bit_47_output1b, subtractor256bit_47_output1c,
       subtractor256bit_47_output1d, subtractor256bit_48_output1a, subtractor256bit_48_output1b,
       subtractor256bit_48_output1c, subtractor256bit_48_output1d, subtractor256bit_49_output1a,
       subtractor256bit_49_output1b, subtractor256bit_49_output1c, subtractor256bit_49_output1d,
       subtractor256bit_50_output1a, subtractor256bit_50_output1b, subtractor256bit_50_output1c,
       subtractor256bit_50_output1d, subtractor256bit_51_output1a, subtractor256bit_51_output1b,
       subtractor256bit_51_output1c, subtractor256bit_51_output1d, subtractor256bit_52_output1a,
       subtractor256bit_52_output1b, subtractor256bit_52_output1c, subtractor256bit_52_output1d,
       subtractor256bit_53_output1a, subtractor256bit_53_output1b, subtractor256bit_53_output1c,
       subtractor256bit_53_output1d, subtractor256bit_54_output1a, subtractor256bit_54_output1b,
       subtractor256bit_54_output1c, subtractor256bit_54_output1d, subtractor256bit_55_output1a,
       subtractor256bit_55_output1b, subtractor256bit_55_output1c, subtractor256bit_55_output1d,
       subtractor256bit_56_output1a, subtractor256bit_56_output1b, subtractor256bit_56_output1c,
       subtractor256bit_56_output1d, subtractor256bit_57_output1a, subtractor256bit_57_output1b,
       subtractor256bit_57_output1c, subtractor256bit_57_output1d, subtractor256bit_58_output1a,
       subtractor256bit_58_output1b, subtractor256bit_58_output1c, subtractor256bit_58_output1d,
       subtractor256bit_59_output1a, subtractor256bit_59_output1b, subtractor256bit_59_output1c,
       subtractor256bit_59_output1d, subtractor256bit_60_output1a, subtractor256bit_60_output1b,
       subtractor256bit_60_output1c, subtractor256bit_60_output1d, subtractor256bit_61_output1a,
       subtractor256bit_61_output1b, subtractor256bit_61_output1c, subtractor256bit_61_output1d,
       subtractor256bit_62_output1a, subtractor256bit_62_output1b, subtractor256bit_62_output1c,
       subtractor256bit_62_output1d, subtractor256bit_63_output1a, subtractor256bit_63_output1b,
       subtractor256bit_63_output1c, subtractor256bit_63_output1d, subtractor256bit_64_output1b,
       subtractor256bit_64_output1c, subtractor256bit_64_output1d;

  // Probe on divider_1_out
  // Probe on divider_1_out
  Divider #(.width(64)) divider_1 (.a(input1), .b(input2), .out(divider_1_out), .upper(inupper), .rem(divider_1_rem));
  // Probe on divider_1_rem
  // Probe on divider_1_rem
  // Probe on inupper
  // Probe on inupper
  // Probe on input1
  // Probe on input1
  not not_1 (not_1_out, comparatoru64bit_1_equal1);
  comparatoru64bit comparatoru64bit_1 (
    .input1(input2), .input2({64{1'b0}}), .equal1(comparatoru64bit_1_equal1));  // open: greater1, less1
  // Probe on input2
  // Probe on input2
  subtractor256bit subtractor256bit_1 (
    .input1a(input1), .input1b(inupper), .input1c({64{1'b0}}), .input1d({64{1'b0}}),
    .input2a(cbuffer256bit_1_output1a), .input2b(cbuffer256bit_1_output1b),
    .input2c(cbuffer256bit_1_output1c), .input2d(cbuffer256bit_1_output1d),
    .output1a(subtractor256bit_1_output1a), .output1b(subtractor256bit_1_output1b),
    .output1c(subtractor256bit_1_output1c), .output1d(subtractor256bit_1_output1d));  // open: inborrow, borrow
  cbuffer256bit cbuffer256bit_1 (
    .buffer1(output1[63]), .input1a({64{1'b0}}), .input1b({input2[0], {63{1'b0}}}),
    .input1c({1'b0, input2[63:1]}), .input1d({64{1'b0}}), .output1a(cbuffer256bit_1_output1a),
    .output1b(cbuffer256bit_1_output1b), .output1c(cbuffer256bit_1_output1c),
    .output1d(cbuffer256bit_1_output1d));
  and and_1 (output1[63], not_1_out, or_1_out);
  or or_1 (or_1_out, comparatoru256bit_1_greater1, comparatoru256bit_1_equal1);
  comparatoru256bit comparatoru256bit_1 (
    .input1a(input1), .input1b(inupper), .input1c({64{1'b0}}), .input1d({64{1'b0}}), .input2a({64{1'b0}}),
    .input2b({input2[0], {63{1'b0}}}), .input2c({1'b0, input2[63:1]}), .input2d({64{1'b0}}),
    .greater1(comparatoru256bit_1_greater1), .equal1(comparatoru256bit_1_equal1));  // open: less1
  subtractor256bit subtractor256bit_2 (
    .input1a(subtractor256bit_1_output1a), .input1b(subtractor256bit_1_output1b),
    .input1c(subtractor256bit_1_output1c), .input1d(subtractor256bit_1_output1d),
    .input2a(cbuffer256bit_2_output1a), .input2b(cbuffer256bit_2_output1b),
    .input2c(cbuffer256bit_2_output1c), .input2d(cbuffer256bit_2_output1d),
    .output1a(subtractor256bit_2_output1a), .output1b(subtractor256bit_2_output1b),
    .output1c(subtractor256bit_2_output1c), .output1d(subtractor256bit_2_output1d));  // open: inborrow, borrow
  cbuffer256bit cbuffer256bit_2 (
    .buffer1(output1[62]), .input1a({64{1'b0}}), .input1b({input2[1:0], {62{1'b0}}}),
    .input1c({2'b00, input2[63:2]}), .input1d({64{1'b0}}), .output1a(cbuffer256bit_2_output1a),
    .output1b(cbuffer256bit_2_output1b), .output1c(cbuffer256bit_2_output1c),
    .output1d(cbuffer256bit_2_output1d));
  and and_2 (output1[62], not_1_out, or_2_out);
  or or_2 (or_2_out, comparatoru256bit_2_greater1, comparatoru256bit_2_equal1);
  comparatoru256bit comparatoru256bit_2 (
    .input1a(subtractor256bit_1_output1a), .input1b(subtractor256bit_1_output1b),
    .input1c(subtractor256bit_1_output1c), .input1d(subtractor256bit_1_output1d), .input2a({64{1'b0}}),
    .input2b({input2[1:0], {62{1'b0}}}), .input2c({2'b00, input2[63:2]}), .input2d({64{1'b0}}),
    .greater1(comparatoru256bit_2_greater1), .equal1(comparatoru256bit_2_equal1));  // open: less1
  subtractor256bit subtractor256bit_3 (
    .input1a(subtractor256bit_2_output1a), .input1b(subtractor256bit_2_output1b),
    .input1c(subtractor256bit_2_output1c), .input1d(subtractor256bit_2_output1d),
    .input2a(cbuffer256bit_3_output1a), .input2b(cbuffer256bit_3_output1b),
    .input2c(cbuffer256bit_3_output1c), .input2d(cbuffer256bit_3_output1d),
    .output1a(subtractor256bit_3_output1a), .output1b(subtractor256bit_3_output1b),
    .output1c(subtractor256bit_3_output1c), .output1d(subtractor256bit_3_output1d));  // open: inborrow, borrow
  cbuffer256bit cbuffer256bit_3 (
    .buffer1(output1[61]), .input1a({64{1'b0}}), .input1b({input2[2:0], {61{1'b0}}}),
    .input1c({3'b000, input2[63:3]}), .input1d({64{1'b0}}), .output1a(cbuffer256bit_3_output1a),
    .output1b(cbuffer256bit_3_output1b), .output1c(cbuffer256bit_3_output1c),
    .output1d(cbuffer256bit_3_output1d));
  and and_3 (output1[61], not_1_out, or_3_out);
  or or_3 (or_3_out, comparatoru256bit_3_greater1, comparatoru256bit_3_equal1);
  comparatoru256bit comparatoru256bit_3 (
    .input1a(subtractor256bit_2_output1a), .input1b(subtractor256bit_2_output1b),
    .input1c(subtractor256bit_2_output1c), .input1d(subtractor256bit_2_output1d), .input2a({64{1'b0}}),
    .input2b({input2[2:0], {61{1'b0}}}), .input2c({3'b000, input2[63:3]}), .input2d({64{1'b0}}),
    .greater1(comparatoru256bit_3_greater1), .equal1(comparatoru256bit_3_equal1));  // open: less1
  subtractor256bit subtractor256bit_4 (
    .input1a(subtractor256bit_3_output1a), .input1b(subtractor256bit_3_output1b),
    .input1c(subtractor256bit_3_output1c), .input1d(subtractor256bit_3_output1d),
    .input2a(cbuffer256bit_4_output1a), .input2b(cbuffer256bit_4_output1b),
    .input2c(cbuffer256bit_4_output1c), .input2d(cbuffer256bit_4_output1d),
    .output1a(subtractor256bit_4_output1a), .output1b(subtractor256bit_4_output1b),
    .output1c(subtractor256bit_4_output1c), .output1d(subtractor256bit_4_output1d));  // open: inborrow, borrow
  cbuffer256bit cbuffer256bit_4 (
    .buffer1(output1[60]), .input1a({64{1'b0}}), .input1b({input2[3:0], {60{1'b0}}}),
    .input1c({4'b0000, input2[63:4]}), .input1d({64{1'b0}}), .output1a(cbuffer256bit_4_output1a),
    .output1b(cbuffer256bit_4_output1b), .output1c(cbuffer256bit_4_output1c),
    .output1d(cbuffer256bit_4_output1d));
  and and_4 (output1[60], not_1_out, or_4_out);
  or or_4 (or_4_out, comparatoru256bit_4_greater1, comparatoru256bit_4_equal1);
  comparatoru256bit comparatoru256bit_4 (
    .input1a(subtractor256bit_3_output1a), .input1b(subtractor256bit_3_output1b),
    .input1c(subtractor256bit_3_output1c), .input1d(subtractor256bit_3_output1d), .input2a({64{1'b0}}),
    .input2b({input2[3:0], {60{1'b0}}}), .input2c({4'b0000, input2[63:4]}), .input2d({64{1'b0}}),
    .greater1(comparatoru256bit_4_greater1), .equal1(comparatoru256bit_4_equal1));  // open: less1
  subtractor256bit subtractor256bit_5 (
    .input1a(subtractor256bit_4_output1a), .input1b(subtractor256bit_4_output1b),
    .input1c(subtractor256bit_4_output1c), .input1d(subtractor256bit_4_output1d),
    .input2a(cbuffer256bit_5_output1a), .input2b(cbuffer256bit_5_output1b),
    .input2c(cbuffer256bit_5_output1c), .input2d(cbuffer256bit_5_output1d),
    .output1a(subtractor256bit_5_output1a), .output1b(subtractor256bit_5_output1b),
    .output1c(subtractor256bit_5_output1c), .output1d(subtractor256bit_5_output1d));  // open: inborrow, borrow
  cbuffer256bit cbuffer256bit_5 (
    .buffer1(output1[59]), .input1a({64{1'b0}}), .input1b({input2[4:0], {59{1'b0}}}),
    .input1c({{5{1'b0}}, input2[63:5]}), .input1d({64{1'b0}}), .output1a(cbuffer256bit_5_output1a),
    .output1b(cbuffer256bit_5_output1b), .output1c(cbuffer256bit_5_output1c),
    .output1d(cbuffer256bit_5_output1d));
  and and_5 (output1[59], not_1_out, or_5_out);
  or or_5 (or_5_out, comparatoru256bit_5_greater1, comparatoru256bit_5_equal1);
  comparatoru256bit comparatoru256bit_5 (
    .input1a(subtractor256bit_4_output1a), .input1b(subtractor256bit_4_output1b),
    .input1c(subtractor256bit_4_output1c), .input1d(subtractor256bit_4_output1d), .input2a({64{1'b0}}),
    .input2b({input2[4:0], {59{1'b0}}}), .input2c({{5{1'b0}}, input2[63:5]}), .input2d({64{1'b0}}),
    .greater1(comparatoru256bit_5_greater1), .equal1(comparatoru256bit_5_equal1));  // open: less1
  subtractor256bit subtractor256bit_6 (
    .input1a(subtractor256bit_5_output1a), .input1b(subtractor256bit_5_output1b),
    .input1c(subtractor256bit_5_output1c), .input1d(subtractor256bit_5_output1d),
    .input2a(cbuffer256bit_6_output1a), .input2b(cbuffer256bit_6_output1b),
    .input2c(cbuffer256bit_6_output1c), .input2d(cbuffer256bit_6_output1d),
    .output1a(subtractor256bit_6_output1a), .output1b(subtractor256bit_6_output1b),
    .output1c(subtractor256bit_6_output1c), .output1d(subtractor256bit_6_output1d));  // open: inborrow, borrow
  cbuffer256bit cbuffer256bit_6 (
    .buffer1(output1[58]), .input1a({64{1'b0}}), .input1b({input2[5:0], {58{1'b0}}}),
    .input1c({{6{1'b0}}, input2[63:6]}), .input1d({64{1'b0}}), .output1a(cbuffer256bit_6_output1a),
    .output1b(cbuffer256bit_6_output1b), .output1c(cbuffer256bit_6_output1c),
    .output1d(cbuffer256bit_6_output1d));
  and and_6 (output1[58], not_1_out, or_6_out);
  or or_6 (or_6_out, comparatoru256bit_6_greater1, comparatoru256bit_6_equal1);
  comparatoru256bit comparatoru256bit_6 (
    .input1a(subtractor256bit_5_output1a), .input1b(subtractor256bit_5_output1b),
    .input1c(subtractor256bit_5_output1c), .input1d(subtractor256bit_5_output1d), .input2a({64{1'b0}}),
    .input2b({input2[5:0], {58{1'b0}}}), .input2c({{6{1'b0}}, input2[63:6]}), .input2d({64{1'b0}}),
    .greater1(comparatoru256bit_6_greater1), .equal1(comparatoru256bit_6_equal1));  // open: less1
  subtractor256bit subtractor256bit_7 (
    .input1a(subtractor256bit_6_output1a), .input1b(subtractor256bit_6_output1b),
    .input1c(subtractor256bit_6_output1c), .input1d(subtractor256bit_6_output1d),
    .input2a(cbuffer256bit_7_output1a), .input2b(cbuffer256bit_7_output1b),
    .input2c(cbuffer256bit_7_output1c), .input2d(cbuffer256bit_7_output1d),
    .output1a(subtractor256bit_7_output1a), .output1b(subtractor256bit_7_output1b),
    .output1c(subtractor256bit_7_output1c), .output1d(subtractor256bit_7_output1d));  // open: inborrow, borrow
  cbuffer256bit cbuffer256bit_7 (
    .buffer1(output1[57]), .input1a({64{1'b0}}), .input1b({input2[6:0], {57{1'b0}}}),
    .input1c({{7{1'b0}}, input2[63:7]}), .input1d({64{1'b0}}), .output1a(cbuffer256bit_7_output1a),
    .output1b(cbuffer256bit_7_output1b), .output1c(cbuffer256bit_7_output1c),
    .output1d(cbuffer256bit_7_output1d));
  and and_7 (output1[57], not_1_out, or_7_out);
  comparatoru256bit comparatoru256bit_7 (
    .input1a(subtractor256bit_6_output1a), .input1b(subtractor256bit_6_output1b),
    .input1c(subtractor256bit_6_output1c), .input1d(subtractor256bit_6_output1d), .input2a({64{1'b0}}),
    .input2b({input2[6:0], {57{1'b0}}}), .input2c({{7{1'b0}}, input2[63:7]}), .input2d({64{1'b0}}),
    .greater1(comparatoru256bit_7_greater1), .equal1(comparatoru256bit_7_equal1));  // open: less1
  or or_7 (or_7_out, comparatoru256bit_7_greater1, comparatoru256bit_7_equal1);
  subtractor256bit subtractor256bit_8 (
    .input1a(subtractor256bit_7_output1a), .input1b(subtractor256bit_7_output1b),
    .input1c(subtractor256bit_7_output1c), .input1d(subtractor256bit_7_output1d),
    .input2a(cbuffer256bit_8_output1a), .input2b(cbuffer256bit_8_output1b),
    .input2c(cbuffer256bit_8_output1c), .input2d(cbuffer256bit_8_output1d),
    .output1a(subtractor256bit_8_output1a), .output1b(subtractor256bit_8_output1b),
    .output1c(subtractor256bit_8_output1c), .output1d(subtractor256bit_8_output1d));  // open: inborrow, borrow
  cbuffer256bit cbuffer256bit_8 (
    .buffer1(output1[56]), .input1a({64{1'b0}}), .input1b({input2[7:0], {56{1'b0}}}),
    .input1c({{8{1'b0}}, input2[63:8]}), .input1d({64{1'b0}}), .output1a(cbuffer256bit_8_output1a),
    .output1b(cbuffer256bit_8_output1b), .output1c(cbuffer256bit_8_output1c),
    .output1d(cbuffer256bit_8_output1d));
  and and_8 (output1[56], not_1_out, or_8_out);
  or or_8 (or_8_out, comparatoru256bit_8_greater1, comparatoru256bit_8_equal1);
  comparatoru256bit comparatoru256bit_8 (
    .input1a(subtractor256bit_7_output1a), .input1b(subtractor256bit_7_output1b),
    .input1c(subtractor256bit_7_output1c), .input1d(subtractor256bit_7_output1d), .input2a({64{1'b0}}),
    .input2b({input2[7:0], {56{1'b0}}}), .input2c({{8{1'b0}}, input2[63:8]}), .input2d({64{1'b0}}),
    .greater1(comparatoru256bit_8_greater1), .equal1(comparatoru256bit_8_equal1));  // open: less1
  subtractor256bit subtractor256bit_9 (
    .input1a(subtractor256bit_8_output1a), .input1b(subtractor256bit_8_output1b),
    .input1c(subtractor256bit_8_output1c), .input1d(subtractor256bit_8_output1d),
    .input2a(cbuffer256bit_9_output1a), .input2b(cbuffer256bit_9_output1b),
    .input2c(cbuffer256bit_9_output1c), .input2d(cbuffer256bit_9_output1d),
    .output1a(subtractor256bit_9_output1a), .output1b(subtractor256bit_9_output1b),
    .output1c(subtractor256bit_9_output1c), .output1d(subtractor256bit_9_output1d));  // open: inborrow, borrow
  cbuffer256bit cbuffer256bit_9 (
    .buffer1(output1[55]), .input1a({64{1'b0}}), .input1b({input2[8:0], {55{1'b0}}}),
    .input1c({{9{1'b0}}, input2[63:9]}), .input1d({64{1'b0}}), .output1a(cbuffer256bit_9_output1a),
    .output1b(cbuffer256bit_9_output1b), .output1c(cbuffer256bit_9_output1c),
    .output1d(cbuffer256bit_9_output1d));
  and and_9 (output1[55], not_1_out, or_9_out);
  or or_9 (or_9_out, comparatoru256bit_9_greater1, comparatoru256bit_9_equal1);
  comparatoru256bit comparatoru256bit_9 (
    .input1a(subtractor256bit_8_output1a), .input1b(subtractor256bit_8_output1b),
    .input1c(subtractor256bit_8_output1c), .input1d(subtractor256bit_8_output1d), .input2a({64{1'b0}}),
    .input2b({input2[8:0], {55{1'b0}}}), .input2c({{9{1'b0}}, input2[63:9]}), .input2d({64{1'b0}}),
    .greater1(comparatoru256bit_9_greater1), .equal1(comparatoru256bit_9_equal1));  // open: less1
  subtractor256bit subtractor256bit_10 (
    .input1a(subtractor256bit_9_output1a), .input1b(subtractor256bit_9_output1b),
    .input1c(subtractor256bit_9_output1c), .input1d(subtractor256bit_9_output1d),
    .input2a(cbuffer256bit_10_output1a), .input2b(cbuffer256bit_10_output1b),
    .input2c(cbuffer256bit_10_output1c), .input2d(cbuffer256bit_10_output1d),
    .output1a(subtractor256bit_10_output1a), .output1b(subtractor256bit_10_output1b),
    .output1c(subtractor256bit_10_output1c), .output1d(subtractor256bit_10_output1d));  // open: inborrow, borrow
  cbuffer256bit cbuffer256bit_10 (
    .buffer1(output1[54]), .input1a({64{1'b0}}), .input1b({input2[9:0], {54{1'b0}}}),
    .input1c({{10{1'b0}}, input2[63:10]}), .input1d({64{1'b0}}), .output1a(cbuffer256bit_10_output1a),
    .output1b(cbuffer256bit_10_output1b), .output1c(cbuffer256bit_10_output1c),
    .output1d(cbuffer256bit_10_output1d));
  and and_10 (output1[54], not_1_out, or_10_out);
  or or_10 (or_10_out, comparatoru256bit_10_greater1, comparatoru256bit_10_equal1);
  comparatoru256bit comparatoru256bit_10 (
    .input1a(subtractor256bit_9_output1a), .input1b(subtractor256bit_9_output1b),
    .input1c(subtractor256bit_9_output1c), .input1d(subtractor256bit_9_output1d), .input2a({64{1'b0}}),
    .input2b({input2[9:0], {54{1'b0}}}), .input2c({{10{1'b0}}, input2[63:10]}), .input2d({64{1'b0}}),
    .greater1(comparatoru256bit_10_greater1), .equal1(comparatoru256bit_10_equal1));  // open: less1
  subtractor256bit subtractor256bit_11 (
    .input1a(subtractor256bit_10_output1a), .input1b(subtractor256bit_10_output1b),
    .input1c(subtractor256bit_10_output1c), .input1d(subtractor256bit_10_output1d),
    .input2a(cbuffer256bit_11_output1a), .input2b(cbuffer256bit_11_output1b),
    .input2c(cbuffer256bit_11_output1c), .input2d(cbuffer256bit_11_output1d),
    .output1a(subtractor256bit_11_output1a), .output1b(subtractor256bit_11_output1b),
    .output1c(subtractor256bit_11_output1c), .output1d(subtractor256bit_11_output1d));  // open: inborrow, borrow
  cbuffer256bit cbuffer256bit_11 (
    .buffer1(output1[53]), .input1a({64{1'b0}}), .input1b({input2[10:0], {53{1'b0}}}),
    .input1c({{11{1'b0}}, input2[63:11]}), .input1d({64{1'b0}}), .output1a(cbuffer256bit_11_output1a),
    .output1b(cbuffer256bit_11_output1b), .output1c(cbuffer256bit_11_output1c),
    .output1d(cbuffer256bit_11_output1d));
  and and_11 (output1[53], not_1_out, or_11_out);
  or or_11 (or_11_out, comparatoru256bit_11_greater1, comparatoru256bit_11_equal1);
  comparatoru256bit comparatoru256bit_11 (
    .input1a(subtractor256bit_10_output1a), .input1b(subtractor256bit_10_output1b),
    .input1c(subtractor256bit_10_output1c), .input1d(subtractor256bit_10_output1d), .input2a({64{1'b0}}),
    .input2b({input2[10:0], {53{1'b0}}}), .input2c({{11{1'b0}}, input2[63:11]}), .input2d({64{1'b0}}),
    .greater1(comparatoru256bit_11_greater1), .equal1(comparatoru256bit_11_equal1));  // open: less1
  subtractor256bit subtractor256bit_12 (
    .input1a(subtractor256bit_11_output1a), .input1b(subtractor256bit_11_output1b),
    .input1c(subtractor256bit_11_output1c), .input1d(subtractor256bit_11_output1d),
    .input2a(cbuffer256bit_12_output1a), .input2b(cbuffer256bit_12_output1b),
    .input2c(cbuffer256bit_12_output1c), .input2d(cbuffer256bit_12_output1d),
    .output1a(subtractor256bit_12_output1a), .output1b(subtractor256bit_12_output1b),
    .output1c(subtractor256bit_12_output1c), .output1d(subtractor256bit_12_output1d));  // open: inborrow, borrow
  cbuffer256bit cbuffer256bit_12 (
    .buffer1(output1[52]), .input1a({64{1'b0}}), .input1b({input2[11:0], {52{1'b0}}}),
    .input1c({{12{1'b0}}, input2[63:12]}), .input1d({64{1'b0}}), .output1a(cbuffer256bit_12_output1a),
    .output1b(cbuffer256bit_12_output1b), .output1c(cbuffer256bit_12_output1c),
    .output1d(cbuffer256bit_12_output1d));
  and and_12 (output1[52], not_1_out, or_12_out);
  or or_12 (or_12_out, comparatoru256bit_12_greater1, comparatoru256bit_12_equal1);
  comparatoru256bit comparatoru256bit_12 (
    .input1a(subtractor256bit_11_output1a), .input1b(subtractor256bit_11_output1b),
    .input1c(subtractor256bit_11_output1c), .input1d(subtractor256bit_11_output1d), .input2a({64{1'b0}}),
    .input2b({input2[11:0], {52{1'b0}}}), .input2c({{12{1'b0}}, input2[63:12]}), .input2d({64{1'b0}}),
    .greater1(comparatoru256bit_12_greater1), .equal1(comparatoru256bit_12_equal1));  // open: less1
  subtractor256bit subtractor256bit_13 (
    .input1a(subtractor256bit_12_output1a), .input1b(subtractor256bit_12_output1b),
    .input1c(subtractor256bit_12_output1c), .input1d(subtractor256bit_12_output1d),
    .input2a(cbuffer256bit_13_output1a), .input2b(cbuffer256bit_13_output1b),
    .input2c(cbuffer256bit_13_output1c), .input2d(cbuffer256bit_13_output1d),
    .output1a(subtractor256bit_13_output1a), .output1b(subtractor256bit_13_output1b),
    .output1c(subtractor256bit_13_output1c), .output1d(subtractor256bit_13_output1d));  // open: inborrow, borrow
  cbuffer256bit cbuffer256bit_13 (
    .buffer1(output1[51]), .input1a({64{1'b0}}), .input1b({input2[12:0], {51{1'b0}}}),
    .input1c({{13{1'b0}}, input2[63:13]}), .input1d({64{1'b0}}), .output1a(cbuffer256bit_13_output1a),
    .output1b(cbuffer256bit_13_output1b), .output1c(cbuffer256bit_13_output1c),
    .output1d(cbuffer256bit_13_output1d));
  and and_13 (output1[51], not_1_out, or_13_out);
  or or_13 (or_13_out, comparatoru256bit_13_greater1, comparatoru256bit_13_equal1);
  comparatoru256bit comparatoru256bit_13 (
    .input1a(subtractor256bit_12_output1a), .input1b(subtractor256bit_12_output1b),
    .input1c(subtractor256bit_12_output1c), .input1d(subtractor256bit_12_output1d), .input2a({64{1'b0}}),
    .input2b({input2[12:0], {51{1'b0}}}), .input2c({{13{1'b0}}, input2[63:13]}), .input2d({64{1'b0}}),
    .greater1(comparatoru256bit_13_greater1), .equal1(comparatoru256bit_13_equal1));  // open: less1
  subtractor256bit subtractor256bit_14 (
    .input1a(subtractor256bit_13_output1a), .input1b(subtractor256bit_13_output1b),
    .input1c(subtractor256bit_13_output1c), .input1d(subtractor256bit_13_output1d),
    .input2a(cbuffer256bit_14_output1a), .input2b(cbuffer256bit_14_output1b),
    .input2c(cbuffer256bit_14_output1c), .input2d(cbuffer256bit_14_output1d),
    .output1a(subtractor256bit_14_output1a), .output1b(subtractor256bit_14_output1b),
    .output1c(subtractor256bit_14_output1c), .output1d(subtractor256bit_14_output1d));  // open: inborrow, borrow
  cbuffer256bit cbuffer256bit_14 (
    .buffer1(output1[50]), .input1a({64{1'b0}}), .input1b({input2[13:0], {50{1'b0}}}),
    .input1c({{14{1'b0}}, input2[63:14]}), .input1d({64{1'b0}}), .output1a(cbuffer256bit_14_output1a),
    .output1b(cbuffer256bit_14_output1b), .output1c(cbuffer256bit_14_output1c),
    .output1d(cbuffer256bit_14_output1d));
  and and_14 (output1[50], not_1_out, or_14_out);
  or or_14 (or_14_out, comparatoru256bit_14_greater1, comparatoru256bit_14_equal1);
  comparatoru256bit comparatoru256bit_14 (
    .input1a(subtractor256bit_13_output1a), .input1b(subtractor256bit_13_output1b),
    .input1c(subtractor256bit_13_output1c), .input1d(subtractor256bit_13_output1d), .input2a({64{1'b0}}),
    .input2b({input2[13:0], {50{1'b0}}}), .input2c({{14{1'b0}}, input2[63:14]}), .input2d({64{1'b0}}),
    .greater1(comparatoru256bit_14_greater1), .equal1(comparatoru256bit_14_equal1));  // open: less1
  subtractor256bit subtractor256bit_15 (
    .input1a(subtractor256bit_14_output1a), .input1b(subtractor256bit_14_output1b),
    .input1c(subtractor256bit_14_output1c), .input1d(subtractor256bit_14_output1d),
    .input2a(cbuffer256bit_15_output1a), .input2b(cbuffer256bit_15_output1b),
    .input2c(cbuffer256bit_15_output1c), .input2d(cbuffer256bit_15_output1d),
    .output1a(subtractor256bit_15_output1a), .output1b(subtractor256bit_15_output1b),
    .output1c(subtractor256bit_15_output1c), .output1d(subtractor256bit_15_output1d));  // open: inborrow, borrow
  cbuffer256bit cbuffer256bit_15 (
    .buffer1(output1[49]), .input1a({64{1'b0}}), .input1b({input2[14:0], {49{1'b0}}}),
    .input1c({{15{1'b0}}, input2[63:15]}), .input1d({64{1'b0}}), .output1a(cbuffer256bit_15_output1a),
    .output1b(cbuffer256bit_15_output1b), .output1c(cbuffer256bit_15_output1c),
    .output1d(cbuffer256bit_15_output1d));
  and and_15 (output1[49], not_1_out, or_15_out);
  comparatoru256bit comparatoru256bit_15 (
    .input1a(subtractor256bit_14_output1a), .input1b(subtractor256bit_14_output1b),
    .input1c(subtractor256bit_14_output1c), .input1d(subtractor256bit_14_output1d), .input2a({64{1'b0}}),
    .input2b({input2[14:0], {49{1'b0}}}), .input2c({{15{1'b0}}, input2[63:15]}), .input2d({64{1'b0}}),
    .greater1(comparatoru256bit_15_greater1), .equal1(comparatoru256bit_15_equal1));  // open: less1
  or or_15 (or_15_out, comparatoru256bit_15_greater1, comparatoru256bit_15_equal1);
  subtractor256bit subtractor256bit_16 (
    .input1a(subtractor256bit_15_output1a), .input1b(subtractor256bit_15_output1b),
    .input1c(subtractor256bit_15_output1c), .input1d(subtractor256bit_15_output1d),
    .input2a(cbuffer256bit_16_output1a), .input2b(cbuffer256bit_16_output1b),
    .input2c(cbuffer256bit_16_output1c), .input2d(cbuffer256bit_16_output1d),
    .output1a(subtractor256bit_16_output1a), .output1b(subtractor256bit_16_output1b),
    .output1c(subtractor256bit_16_output1c), .output1d(subtractor256bit_16_output1d));  // open: inborrow, borrow
  cbuffer256bit cbuffer256bit_16 (
    .buffer1(output1[48]), .input1a({64{1'b0}}), .input1b({input2[15:0], {48{1'b0}}}),
    .input1c({{16{1'b0}}, input2[63:16]}), .input1d({64{1'b0}}), .output1a(cbuffer256bit_16_output1a),
    .output1b(cbuffer256bit_16_output1b), .output1c(cbuffer256bit_16_output1c),
    .output1d(cbuffer256bit_16_output1d));
  and and_16 (output1[48], not_1_out, or_16_out);
  or or_16 (or_16_out, comparatoru256bit_16_greater1, comparatoru256bit_16_equal1);
  comparatoru256bit comparatoru256bit_16 (
    .input1a(subtractor256bit_15_output1a), .input1b(subtractor256bit_15_output1b),
    .input1c(subtractor256bit_15_output1c), .input1d(subtractor256bit_15_output1d), .input2a({64{1'b0}}),
    .input2b({input2[15:0], {48{1'b0}}}), .input2c({{16{1'b0}}, input2[63:16]}), .input2d({64{1'b0}}),
    .greater1(comparatoru256bit_16_greater1), .equal1(comparatoru256bit_16_equal1));  // open: less1
  subtractor256bit subtractor256bit_17 (
    .input1a(subtractor256bit_16_output1a), .input1b(subtractor256bit_16_output1b),
    .input1c(subtractor256bit_16_output1c), .input1d(subtractor256bit_16_output1d),
    .input2a(cbuffer256bit_17_output1a), .input2b(cbuffer256bit_17_output1b),
    .input2c(cbuffer256bit_17_output1c), .input2d(cbuffer256bit_17_output1d),
    .output1a(subtractor256bit_17_output1a), .output1b(subtractor256bit_17_output1b),
    .output1c(subtractor256bit_17_output1c), .output1d(subtractor256bit_17_output1d));  // open: inborrow, borrow
  cbuffer256bit cbuffer256bit_17 (
    .buffer1(output1[47]), .input1a({64{1'b0}}), .input1b({input2[16:0], {47{1'b0}}}),
    .input1c({{17{1'b0}}, input2[63:17]}), .input1d({64{1'b0}}), .output1a(cbuffer256bit_17_output1a),
    .output1b(cbuffer256bit_17_output1b), .output1c(cbuffer256bit_17_output1c),
    .output1d(cbuffer256bit_17_output1d));
  and and_17 (output1[47], not_1_out, or_17_out);
  or or_17 (or_17_out, comparatoru256bit_17_greater1, comparatoru256bit_17_equal1);
  comparatoru256bit comparatoru256bit_17 (
    .input1a(subtractor256bit_16_output1a), .input1b(subtractor256bit_16_output1b),
    .input1c(subtractor256bit_16_output1c), .input1d(subtractor256bit_16_output1d), .input2a({64{1'b0}}),
    .input2b({input2[16:0], {47{1'b0}}}), .input2c({{17{1'b0}}, input2[63:17]}), .input2d({64{1'b0}}),
    .greater1(comparatoru256bit_17_greater1), .equal1(comparatoru256bit_17_equal1));  // open: less1
  subtractor256bit subtractor256bit_18 (
    .input1a(subtractor256bit_17_output1a), .input1b(subtractor256bit_17_output1b),
    .input1c(subtractor256bit_17_output1c), .input1d(subtractor256bit_17_output1d),
    .input2a(cbuffer256bit_18_output1a), .input2b(cbuffer256bit_18_output1b),
    .input2c(cbuffer256bit_18_output1c), .input2d(cbuffer256bit_18_output1d),
    .output1a(subtractor256bit_18_output1a), .output1b(subtractor256bit_18_output1b),
    .output1c(subtractor256bit_18_output1c), .output1d(subtractor256bit_18_output1d));  // open: inborrow, borrow
  cbuffer256bit cbuffer256bit_18 (
    .buffer1(output1[46]), .input1a({64{1'b0}}), .input1b({input2[17:0], {46{1'b0}}}),
    .input1c({{18{1'b0}}, input2[63:18]}), .input1d({64{1'b0}}), .output1a(cbuffer256bit_18_output1a),
    .output1b(cbuffer256bit_18_output1b), .output1c(cbuffer256bit_18_output1c),
    .output1d(cbuffer256bit_18_output1d));
  and and_18 (output1[46], not_1_out, or_18_out);
  or or_18 (or_18_out, comparatoru256bit_18_greater1, comparatoru256bit_18_equal1);
  comparatoru256bit comparatoru256bit_18 (
    .input1a(subtractor256bit_17_output1a), .input1b(subtractor256bit_17_output1b),
    .input1c(subtractor256bit_17_output1c), .input1d(subtractor256bit_17_output1d), .input2a({64{1'b0}}),
    .input2b({input2[17:0], {46{1'b0}}}), .input2c({{18{1'b0}}, input2[63:18]}), .input2d({64{1'b0}}),
    .greater1(comparatoru256bit_18_greater1), .equal1(comparatoru256bit_18_equal1));  // open: less1
  subtractor256bit subtractor256bit_19 (
    .input1a(subtractor256bit_18_output1a), .input1b(subtractor256bit_18_output1b),
    .input1c(subtractor256bit_18_output1c), .input1d(subtractor256bit_18_output1d),
    .input2a(cbuffer256bit_19_output1a), .input2b(cbuffer256bit_19_output1b),
    .input2c(cbuffer256bit_19_output1c), .input2d(cbuffer256bit_19_output1d),
    .output1a(subtractor256bit_19_output1a), .output1b(subtractor256bit_19_output1b),
    .output1c(subtractor256bit_19_output1c), .output1d(subtractor256bit_19_output1d));  // open: inborrow, borrow
  cbuffer256bit cbuffer256bit_19 (
    .buffer1(output1[45]), .input1a({64{1'b0}}), .input1b({input2[18:0], {45{1'b0}}}),
    .input1c({{19{1'b0}}, input2[63:19]}), .input1d({64{1'b0}}), .output1a(cbuffer256bit_19_output1a),
    .output1b(cbuffer256bit_19_output1b), .output1c(cbuffer256bit_19_output1c),
    .output1d(cbuffer256bit_19_output1d));
  and and_19 (output1[45], not_1_out, or_19_out);
  or or_19 (or_19_out, comparatoru256bit_19_greater1, comparatoru256bit_19_equal1);
  comparatoru256bit comparatoru256bit_19 (
    .input1a(subtractor256bit_18_output1a), .input1b(subtractor256bit_18_output1b),
    .input1c(subtractor256bit_18_output1c), .input1d(subtractor256bit_18_output1d), .input2a({64{1'b0}}),
    .input2b({input2[18:0], {45{1'b0}}}), .input2c({{19{1'b0}}, input2[63:19]}), .input2d({64{1'b0}}),
    .greater1(comparatoru256bit_19_greater1), .equal1(comparatoru256bit_19_equal1));  // open: less1
  subtractor256bit subtractor256bit_20 (
    .input1a(subtractor256bit_19_output1a), .input1b(subtractor256bit_19_output1b),
    .input1c(subtractor256bit_19_output1c), .input1d(subtractor256bit_19_output1d),
    .input2a(cbuffer256bit_20_output1a), .input2b(cbuffer256bit_20_output1b),
    .input2c(cbuffer256bit_20_output1c), .input2d(cbuffer256bit_20_output1d),
    .output1a(subtractor256bit_20_output1a), .output1b(subtractor256bit_20_output1b),
    .output1c(subtractor256bit_20_output1c), .output1d(subtractor256bit_20_output1d));  // open: inborrow, borrow
  cbuffer256bit cbuffer256bit_20 (
    .buffer1(output1[44]), .input1a({64{1'b0}}), .input1b({input2[19:0], {44{1'b0}}}),
    .input1c({{20{1'b0}}, input2[63:20]}), .input1d({64{1'b0}}), .output1a(cbuffer256bit_20_output1a),
    .output1b(cbuffer256bit_20_output1b), .output1c(cbuffer256bit_20_output1c),
    .output1d(cbuffer256bit_20_output1d));
  and and_20 (output1[44], not_1_out, or_20_out);
  or or_20 (or_20_out, comparatoru256bit_20_greater1, comparatoru256bit_20_equal1);
  comparatoru256bit comparatoru256bit_20 (
    .input1a(subtractor256bit_19_output1a), .input1b(subtractor256bit_19_output1b),
    .input1c(subtractor256bit_19_output1c), .input1d(subtractor256bit_19_output1d), .input2a({64{1'b0}}),
    .input2b({input2[19:0], {44{1'b0}}}), .input2c({{20{1'b0}}, input2[63:20]}), .input2d({64{1'b0}}),
    .greater1(comparatoru256bit_20_greater1), .equal1(comparatoru256bit_20_equal1));  // open: less1
  subtractor256bit subtractor256bit_21 (
    .input1a(subtractor256bit_20_output1a), .input1b(subtractor256bit_20_output1b),
    .input1c(subtractor256bit_20_output1c), .input1d(subtractor256bit_20_output1d),
    .input2a(cbuffer256bit_21_output1a), .input2b(cbuffer256bit_21_output1b),
    .input2c(cbuffer256bit_21_output1c), .input2d(cbuffer256bit_21_output1d),
    .output1a(subtractor256bit_21_output1a), .output1b(subtractor256bit_21_output1b),
    .output1c(subtractor256bit_21_output1c), .output1d(subtractor256bit_21_output1d));  // open: inborrow, borrow
  cbuffer256bit cbuffer256bit_21 (
    .buffer1(output1[43]), .input1a({64{1'b0}}), .input1b({input2[20:0], {43{1'b0}}}),
    .input1c({{21{1'b0}}, input2[63:21]}), .input1d({64{1'b0}}), .output1a(cbuffer256bit_21_output1a),
    .output1b(cbuffer256bit_21_output1b), .output1c(cbuffer256bit_21_output1c),
    .output1d(cbuffer256bit_21_output1d));
  and and_21 (output1[43], not_1_out, or_21_out);
  or or_21 (or_21_out, comparatoru256bit_21_greater1, comparatoru256bit_21_equal1);
  comparatoru256bit comparatoru256bit_21 (
    .input1a(subtractor256bit_20_output1a), .input1b(subtractor256bit_20_output1b),
    .input1c(subtractor256bit_20_output1c), .input1d(subtractor256bit_20_output1d), .input2a({64{1'b0}}),
    .input2b({input2[20:0], {43{1'b0}}}), .input2c({{21{1'b0}}, input2[63:21]}), .input2d({64{1'b0}}),
    .greater1(comparatoru256bit_21_greater1), .equal1(comparatoru256bit_21_equal1));  // open: less1
  subtractor256bit subtractor256bit_22 (
    .input1a(subtractor256bit_21_output1a), .input1b(subtractor256bit_21_output1b),
    .input1c(subtractor256bit_21_output1c), .input1d(subtractor256bit_21_output1d),
    .input2a(cbuffer256bit_22_output1a), .input2b(cbuffer256bit_22_output1b),
    .input2c(cbuffer256bit_22_output1c), .input2d(cbuffer256bit_22_output1d),
    .output1a(subtractor256bit_22_output1a), .output1b(subtractor256bit_22_output1b),
    .output1c(subtractor256bit_22_output1c), .output1d(subtractor256bit_22_output1d));  // open: inborrow, borrow
  cbuffer256bit cbuffer256bit_22 (
    .buffer1(output1[42]), .input1a({64{1'b0}}), .input1b({input2[21:0], {42{1'b0}}}),
    .input1c({{22{1'b0}}, input2[63:22]}), .input1d({64{1'b0}}), .output1a(cbuffer256bit_22_output1a),
    .output1b(cbuffer256bit_22_output1b), .output1c(cbuffer256bit_22_output1c),
    .output1d(cbuffer256bit_22_output1d));
  and and_22 (output1[42], not_1_out, or_22_out);
  or or_22 (or_22_out, comparatoru256bit_22_greater1, comparatoru256bit_22_equal1);
  comparatoru256bit comparatoru256bit_22 (
    .input1a(subtractor256bit_21_output1a), .input1b(subtractor256bit_21_output1b),
    .input1c(subtractor256bit_21_output1c), .input1d(subtractor256bit_21_output1d), .input2a({64{1'b0}}),
    .input2b({input2[21:0], {42{1'b0}}}), .input2c({{22{1'b0}}, input2[63:22]}), .input2d({64{1'b0}}),
    .greater1(comparatoru256bit_22_greater1), .equal1(comparatoru256bit_22_equal1));  // open: less1
  subtractor256bit subtractor256bit_23 (
    .input1a(subtractor256bit_22_output1a), .input1b(subtractor256bit_22_output1b),
    .input1c(subtractor256bit_22_output1c), .input1d(subtractor256bit_22_output1d),
    .input2a(cbuffer256bit_23_output1a), .input2b(cbuffer256bit_23_output1b),
    .input2c(cbuffer256bit_23_output1c), .input2d(cbuffer256bit_23_output1d),
    .output1a(subtractor256bit_23_output1a), .output1b(subtractor256bit_23_output1b),
    .output1c(subtractor256bit_23_output1c), .output1d(subtractor256bit_23_output1d));  // open: inborrow, borrow
  cbuffer256bit cbuffer256bit_23 (
    .buffer1(output1[41]), .input1a({64{1'b0}}), .input1b({input2[22:0], {41{1'b0}}}),
    .input1c({{23{1'b0}}, input2[63:23]}), .input1d({64{1'b0}}), .output1a(cbuffer256bit_23_output1a),
    .output1b(cbuffer256bit_23_output1b), .output1c(cbuffer256bit_23_output1c),
    .output1d(cbuffer256bit_23_output1d));
  and and_23 (output1[41], not_1_out, or_23_out);
  comparatoru256bit comparatoru256bit_23 (
    .input1a(subtractor256bit_22_output1a), .input1b(subtractor256bit_22_output1b),
    .input1c(subtractor256bit_22_output1c), .input1d(subtractor256bit_22_output1d), .input2a({64{1'b0}}),
    .input2b({input2[22:0], {41{1'b0}}}), .input2c({{23{1'b0}}, input2[63:23]}), .input2d({64{1'b0}}),
    .greater1(comparatoru256bit_23_greater1), .equal1(comparatoru256bit_23_equal1));  // open: less1
  or or_23 (or_23_out, comparatoru256bit_23_greater1, comparatoru256bit_23_equal1);
  subtractor256bit subtractor256bit_24 (
    .input1a(subtractor256bit_23_output1a), .input1b(subtractor256bit_23_output1b),
    .input1c(subtractor256bit_23_output1c), .input1d(subtractor256bit_23_output1d),
    .input2a(cbuffer256bit_24_output1a), .input2b(cbuffer256bit_24_output1b),
    .input2c(cbuffer256bit_24_output1c), .input2d(cbuffer256bit_24_output1d),
    .output1a(subtractor256bit_24_output1a), .output1b(subtractor256bit_24_output1b),
    .output1c(subtractor256bit_24_output1c), .output1d(subtractor256bit_24_output1d));  // open: inborrow, borrow
  cbuffer256bit cbuffer256bit_24 (
    .buffer1(output1[40]), .input1a({64{1'b0}}), .input1b({input2[23:0], {40{1'b0}}}),
    .input1c({{24{1'b0}}, input2[63:24]}), .input1d({64{1'b0}}), .output1a(cbuffer256bit_24_output1a),
    .output1b(cbuffer256bit_24_output1b), .output1c(cbuffer256bit_24_output1c),
    .output1d(cbuffer256bit_24_output1d));
  and and_24 (output1[40], not_1_out, or_24_out);
  or or_24 (or_24_out, comparatoru256bit_24_greater1, comparatoru256bit_24_equal1);
  comparatoru256bit comparatoru256bit_24 (
    .input1a(subtractor256bit_23_output1a), .input1b(subtractor256bit_23_output1b),
    .input1c(subtractor256bit_23_output1c), .input1d(subtractor256bit_23_output1d), .input2a({64{1'b0}}),
    .input2b({input2[23:0], {40{1'b0}}}), .input2c({{24{1'b0}}, input2[63:24]}), .input2d({64{1'b0}}),
    .greater1(comparatoru256bit_24_greater1), .equal1(comparatoru256bit_24_equal1));  // open: less1
  subtractor256bit subtractor256bit_25 (
    .input1a(subtractor256bit_24_output1a), .input1b(subtractor256bit_24_output1b),
    .input1c(subtractor256bit_24_output1c), .input1d(subtractor256bit_24_output1d),
    .input2a(cbuffer256bit_25_output1a), .input2b(cbuffer256bit_25_output1b),
    .input2c(cbuffer256bit_25_output1c), .input2d(cbuffer256bit_25_output1d),
    .output1a(subtractor256bit_25_output1a), .output1b(subtractor256bit_25_output1b),
    .output1c(subtractor256bit_25_output1c), .output1d(subtractor256bit_25_output1d));  // open: inborrow, borrow
  cbuffer256bit cbuffer256bit_25 (
    .buffer1(output1[39]), .input1a({64{1'b0}}), .input1b({input2[24:0], {39{1'b0}}}),
    .input1c({{25{1'b0}}, input2[63:25]}), .input1d({64{1'b0}}), .output1a(cbuffer256bit_25_output1a),
    .output1b(cbuffer256bit_25_output1b), .output1c(cbuffer256bit_25_output1c),
    .output1d(cbuffer256bit_25_output1d));
  and and_25 (output1[39], not_1_out, or_25_out);
  or or_25 (or_25_out, comparatoru256bit_25_greater1, comparatoru256bit_25_equal1);
  comparatoru256bit comparatoru256bit_25 (
    .input1a(subtractor256bit_24_output1a), .input1b(subtractor256bit_24_output1b),
    .input1c(subtractor256bit_24_output1c), .input1d(subtractor256bit_24_output1d), .input2a({64{1'b0}}),
    .input2b({input2[24:0], {39{1'b0}}}), .input2c({{25{1'b0}}, input2[63:25]}), .input2d({64{1'b0}}),
    .greater1(comparatoru256bit_25_greater1), .equal1(comparatoru256bit_25_equal1));  // open: less1
  subtractor256bit subtractor256bit_26 (
    .input1a(subtractor256bit_25_output1a), .input1b(subtractor256bit_25_output1b),
    .input1c(subtractor256bit_25_output1c), .input1d(subtractor256bit_25_output1d),
    .input2a(cbuffer256bit_26_output1a), .input2b(cbuffer256bit_26_output1b),
    .input2c(cbuffer256bit_26_output1c), .input2d(cbuffer256bit_26_output1d),
    .output1a(subtractor256bit_26_output1a), .output1b(subtractor256bit_26_output1b),
    .output1c(subtractor256bit_26_output1c), .output1d(subtractor256bit_26_output1d));  // open: inborrow, borrow
  cbuffer256bit cbuffer256bit_26 (
    .buffer1(output1[38]), .input1a({64{1'b0}}), .input1b({input2[25:0], {38{1'b0}}}),
    .input1c({{26{1'b0}}, input2[63:26]}), .input1d({64{1'b0}}), .output1a(cbuffer256bit_26_output1a),
    .output1b(cbuffer256bit_26_output1b), .output1c(cbuffer256bit_26_output1c),
    .output1d(cbuffer256bit_26_output1d));
  and and_26 (output1[38], not_1_out, or_26_out);
  or or_26 (or_26_out, comparatoru256bit_26_greater1, comparatoru256bit_26_equal1);
  comparatoru256bit comparatoru256bit_26 (
    .input1a(subtractor256bit_25_output1a), .input1b(subtractor256bit_25_output1b),
    .input1c(subtractor256bit_25_output1c), .input1d(subtractor256bit_25_output1d), .input2a({64{1'b0}}),
    .input2b({input2[25:0], {38{1'b0}}}), .input2c({{26{1'b0}}, input2[63:26]}), .input2d({64{1'b0}}),
    .greater1(comparatoru256bit_26_greater1), .equal1(comparatoru256bit_26_equal1));  // open: less1
  subtractor256bit subtractor256bit_27 (
    .input1a(subtractor256bit_26_output1a), .input1b(subtractor256bit_26_output1b),
    .input1c(subtractor256bit_26_output1c), .input1d(subtractor256bit_26_output1d),
    .input2a(cbuffer256bit_27_output1a), .input2b(cbuffer256bit_27_output1b),
    .input2c(cbuffer256bit_27_output1c), .input2d(cbuffer256bit_27_output1d),
    .output1a(subtractor256bit_27_output1a), .output1b(subtractor256bit_27_output1b),
    .output1c(subtractor256bit_27_output1c), .output1d(subtractor256bit_27_output1d));  // open: inborrow, borrow
  cbuffer256bit cbuffer256bit_27 (
    .buffer1(output1[37]), .input1a({64{1'b0}}), .input1b({input2[26:0], {37{1'b0}}}),
    .input1c({{27{1'b0}}, input2[63:27]}), .input1d({64{1'b0}}), .output1a(cbuffer256bit_27_output1a),
    .output1b(cbuffer256bit_27_output1b), .output1c(cbuffer256bit_27_output1c),
    .output1d(cbuffer256bit_27_output1d));
  and and_27 (output1[37], not_1_out, or_27_out);
  or or_27 (or_27_out, comparatoru256bit_27_greater1, comparatoru256bit_27_equal1);
  comparatoru256bit comparatoru256bit_27 (
    .input1a(subtractor256bit_26_output1a), .input1b(subtractor256bit_26_output1b),
    .input1c(subtractor256bit_26_output1c), .input1d(subtractor256bit_26_output1d), .input2a({64{1'b0}}),
    .input2b({input2[26:0], {37{1'b0}}}), .input2c({{27{1'b0}}, input2[63:27]}), .input2d({64{1'b0}}),
    .greater1(comparatoru256bit_27_greater1), .equal1(comparatoru256bit_27_equal1));  // open: less1
  subtractor256bit subtractor256bit_28 (
    .input1a(subtractor256bit_27_output1a), .input1b(subtractor256bit_27_output1b),
    .input1c(subtractor256bit_27_output1c), .input1d(subtractor256bit_27_output1d),
    .input2a(cbuffer256bit_28_output1a), .input2b(cbuffer256bit_28_output1b),
    .input2c(cbuffer256bit_28_output1c), .input2d(cbuffer256bit_28_output1d),
    .output1a(subtractor256bit_28_output1a), .output1b(subtractor256bit_28_output1b),
    .output1c(subtractor256bit_28_output1c), .output1d(subtractor256bit_28_output1d));  // open: inborrow, borrow
  cbuffer256bit cbuffer256bit_28 (
    .buffer1(output1[36]), .input1a({64{1'b0}}), .input1b({input2[27:0], {36{1'b0}}}),
    .input1c({{28{1'b0}}, input2[63:28]}), .input1d({64{1'b0}}), .output1a(cbuffer256bit_28_output1a),
    .output1b(cbuffer256bit_28_output1b), .output1c(cbuffer256bit_28_output1c),
    .output1d(cbuffer256bit_28_output1d));
  and and_28 (output1[36], not_1_out, or_28_out);
  or or_28 (or_28_out, comparatoru256bit_28_greater1, comparatoru256bit_28_equal1);
  comparatoru256bit comparatoru256bit_28 (
    .input1a(subtractor256bit_27_output1a), .input1b(subtractor256bit_27_output1b),
    .input1c(subtractor256bit_27_output1c), .input1d(subtractor256bit_27_output1d), .input2a({64{1'b0}}),
    .input2b({input2[27:0], {36{1'b0}}}), .input2c({{28{1'b0}}, input2[63:28]}), .input2d({64{1'b0}}),
    .greater1(comparatoru256bit_28_greater1), .equal1(comparatoru256bit_28_equal1));  // open: less1
  subtractor256bit subtractor256bit_29 (
    .input1a(subtractor256bit_28_output1a), .input1b(subtractor256bit_28_output1b),
    .input1c(subtractor256bit_28_output1c), .input1d(subtractor256bit_28_output1d),
    .input2a(cbuffer256bit_29_output1a), .input2b(cbuffer256bit_29_output1b),
    .input2c(cbuffer256bit_29_output1c), .input2d(cbuffer256bit_29_output1d),
    .output1a(subtractor256bit_29_output1a), .output1b(subtractor256bit_29_output1b),
    .output1c(subtractor256bit_29_output1c), .output1d(subtractor256bit_29_output1d));  // open: inborrow, borrow
  cbuffer256bit cbuffer256bit_29 (
    .buffer1(output1[35]), .input1a({64{1'b0}}), .input1b({input2[28:0], {35{1'b0}}}),
    .input1c({{29{1'b0}}, input2[63:29]}), .input1d({64{1'b0}}), .output1a(cbuffer256bit_29_output1a),
    .output1b(cbuffer256bit_29_output1b), .output1c(cbuffer256bit_29_output1c),
    .output1d(cbuffer256bit_29_output1d));
  and and_29 (output1[35], not_1_out, or_29_out);
  or or_29 (or_29_out, comparatoru256bit_29_greater1, comparatoru256bit_29_equal1);
  comparatoru256bit comparatoru256bit_29 (
    .input1a(subtractor256bit_28_output1a), .input1b(subtractor256bit_28_output1b),
    .input1c(subtractor256bit_28_output1c), .input1d(subtractor256bit_28_output1d), .input2a({64{1'b0}}),
    .input2b({input2[28:0], {35{1'b0}}}), .input2c({{29{1'b0}}, input2[63:29]}), .input2d({64{1'b0}}),
    .greater1(comparatoru256bit_29_greater1), .equal1(comparatoru256bit_29_equal1));  // open: less1
  subtractor256bit subtractor256bit_30 (
    .input1a(subtractor256bit_29_output1a), .input1b(subtractor256bit_29_output1b),
    .input1c(subtractor256bit_29_output1c), .input1d(subtractor256bit_29_output1d),
    .input2a(cbuffer256bit_30_output1a), .input2b(cbuffer256bit_30_output1b),
    .input2c(cbuffer256bit_30_output1c), .input2d(cbuffer256bit_30_output1d),
    .output1a(subtractor256bit_30_output1a), .output1b(subtractor256bit_30_output1b),
    .output1c(subtractor256bit_30_output1c), .output1d(subtractor256bit_30_output1d));  // open: inborrow, borrow
  cbuffer256bit cbuffer256bit_30 (
    .buffer1(output1[34]), .input1a({64{1'b0}}), .input1b({input2[29:0], {34{1'b0}}}),
    .input1c({{30{1'b0}}, input2[63:30]}), .input1d({64{1'b0}}), .output1a(cbuffer256bit_30_output1a),
    .output1b(cbuffer256bit_30_output1b), .output1c(cbuffer256bit_30_output1c),
    .output1d(cbuffer256bit_30_output1d));
  and and_30 (output1[34], not_1_out, or_30_out);
  or or_30 (or_30_out, comparatoru256bit_30_greater1, comparatoru256bit_30_equal1);
  comparatoru256bit comparatoru256bit_30 (
    .input1a(subtractor256bit_29_output1a), .input1b(subtractor256bit_29_output1b),
    .input1c(subtractor256bit_29_output1c), .input1d(subtractor256bit_29_output1d), .input2a({64{1'b0}}),
    .input2b({input2[29:0], {34{1'b0}}}), .input2c({{30{1'b0}}, input2[63:30]}), .input2d({64{1'b0}}),
    .greater1(comparatoru256bit_30_greater1), .equal1(comparatoru256bit_30_equal1));  // open: less1
  subtractor256bit subtractor256bit_31 (
    .input1a(subtractor256bit_30_output1a), .input1b(subtractor256bit_30_output1b),
    .input1c(subtractor256bit_30_output1c), .input1d(subtractor256bit_30_output1d),
    .input2a(cbuffer256bit_31_output1a), .input2b(cbuffer256bit_31_output1b),
    .input2c(cbuffer256bit_31_output1c), .input2d(cbuffer256bit_31_output1d),
    .output1a(subtractor256bit_31_output1a), .output1b(subtractor256bit_31_output1b),
    .output1c(subtractor256bit_31_output1c), .output1d(subtractor256bit_31_output1d));  // open: inborrow, borrow
  cbuffer256bit cbuffer256bit_31 (
    .buffer1(output1[33]), .input1a({64{1'b0}}), .input1b({input2[30:0], {33{1'b0}}}),
    .input1c({{31{1'b0}}, input2[63:31]}), .input1d({64{1'b0}}), .output1a(cbuffer256bit_31_output1a),
    .output1b(cbuffer256bit_31_output1b), .output1c(cbuffer256bit_31_output1c),
    .output1d(cbuffer256bit_31_output1d));
  and and_31 (output1[33], not_1_out, or_31_out);
  comparatoru256bit comparatoru256bit_31 (
    .input1a(subtractor256bit_30_output1a), .input1b(subtractor256bit_30_output1b),
    .input1c(subtractor256bit_30_output1c), .input1d(subtractor256bit_30_output1d), .input2a({64{1'b0}}),
    .input2b({input2[30:0], {33{1'b0}}}), .input2c({{31{1'b0}}, input2[63:31]}), .input2d({64{1'b0}}),
    .greater1(comparatoru256bit_31_greater1), .equal1(comparatoru256bit_31_equal1));  // open: less1
  or or_31 (or_31_out, comparatoru256bit_31_greater1, comparatoru256bit_31_equal1);
  subtractor256bit subtractor256bit_32 (
    .input1a(subtractor256bit_31_output1a), .input1b(subtractor256bit_31_output1b),
    .input1c(subtractor256bit_31_output1c), .input1d(subtractor256bit_31_output1d),
    .input2a(cbuffer256bit_32_output1a), .input2b(cbuffer256bit_32_output1b),
    .input2c(cbuffer256bit_32_output1c), .input2d(cbuffer256bit_32_output1d),
    .output1a(subtractor256bit_32_output1a), .output1b(subtractor256bit_32_output1b),
    .output1c(subtractor256bit_32_output1c), .output1d(subtractor256bit_32_output1d));  // open: inborrow, borrow
  cbuffer256bit cbuffer256bit_32 (
    .buffer1(output1[32]), .input1a({64{1'b0}}), .input1b({input2[31:0], {32{1'b0}}}),
    .input1c({{32{1'b0}}, input2[63:32]}), .input1d({64{1'b0}}), .output1a(cbuffer256bit_32_output1a),
    .output1b(cbuffer256bit_32_output1b), .output1c(cbuffer256bit_32_output1c),
    .output1d(cbuffer256bit_32_output1d));
  and and_32 (output1[32], not_1_out, or_32_out);
  or or_32 (or_32_out, comparatoru256bit_32_greater1, comparatoru256bit_32_equal1);
  comparatoru256bit comparatoru256bit_32 (
    .input1a(subtractor256bit_31_output1a), .input1b(subtractor256bit_31_output1b),
    .input1c(subtractor256bit_31_output1c), .input1d(subtractor256bit_31_output1d), .input2a({64{1'b0}}),
    .input2b({input2[31:0], {32{1'b0}}}), .input2c({{32{1'b0}}, input2[63:32]}), .input2d({64{1'b0}}),
    .greater1(comparatoru256bit_32_greater1), .equal1(comparatoru256bit_32_equal1));  // open: less1
  subtractor256bit subtractor256bit_33 (
    .input1a(subtractor256bit_32_output1a), .input1b(subtractor256bit_32_output1b),
    .input1c(subtractor256bit_32_output1c), .input1d(subtractor256bit_32_output1d),
    .input2a(cbuffer256bit_33_output1a), .input2b(cbuffer256bit_33_output1b),
    .input2c(cbuffer256bit_33_output1c), .input2d(cbuffer256bit_33_output1d),
    .output1a(subtractor256bit_33_output1a), .output1b(subtractor256bit_33_output1b),
    .output1c(subtractor256bit_33_output1c), .output1d(subtractor256bit_33_output1d));  // open: inborrow, borrow
  cbuffer256bit cbuffer256bit_33 (
    .buffer1(output1[31]), .input1a({64{1'b0}}), .input1b({input2[32:0], {31{1'b0}}}),
    .input1c({{33{1'b0}}, input2[63:33]}), .input1d({64{1'b0}}), .output1a(cbuffer256bit_33_output1a),
    .output1b(cbuffer256bit_33_output1b), .output1c(cbuffer256bit_33_output1c),
    .output1d(cbuffer256bit_33_output1d));
  and and_33 (output1[31], not_1_out, or_33_out);
  or or_33 (or_33_out, comparatoru256bit_33_greater1, comparatoru256bit_33_equal1);
  comparatoru256bit comparatoru256bit_33 (
    .input1a(subtractor256bit_32_output1a), .input1b(subtractor256bit_32_output1b),
    .input1c(subtractor256bit_32_output1c), .input1d(subtractor256bit_32_output1d), .input2a({64{1'b0}}),
    .input2b({input2[32:0], {31{1'b0}}}), .input2c({{33{1'b0}}, input2[63:33]}), .input2d({64{1'b0}}),
    .greater1(comparatoru256bit_33_greater1), .equal1(comparatoru256bit_33_equal1));  // open: less1
  subtractor256bit subtractor256bit_34 (
    .input1a(subtractor256bit_33_output1a), .input1b(subtractor256bit_33_output1b),
    .input1c(subtractor256bit_33_output1c), .input1d(subtractor256bit_33_output1d),
    .input2a(cbuffer256bit_34_output1a), .input2b(cbuffer256bit_34_output1b),
    .input2c(cbuffer256bit_34_output1c), .input2d(cbuffer256bit_34_output1d),
    .output1a(subtractor256bit_34_output1a), .output1b(subtractor256bit_34_output1b),
    .output1c(subtractor256bit_34_output1c), .output1d(subtractor256bit_34_output1d));  // open: inborrow, borrow
  cbuffer256bit cbuffer256bit_34 (
    .buffer1(output1[30]), .input1a({64{1'b0}}), .input1b({input2[33:0], {30{1'b0}}}),
    .input1c({{34{1'b0}}, input2[63:34]}), .input1d({64{1'b0}}), .output1a(cbuffer256bit_34_output1a),
    .output1b(cbuffer256bit_34_output1b), .output1c(cbuffer256bit_34_output1c),
    .output1d(cbuffer256bit_34_output1d));
  and and_34 (output1[30], not_1_out, or_34_out);
  or or_34 (or_34_out, comparatoru256bit_34_greater1, comparatoru256bit_34_equal1);
  comparatoru256bit comparatoru256bit_34 (
    .input1a(subtractor256bit_33_output1a), .input1b(subtractor256bit_33_output1b),
    .input1c(subtractor256bit_33_output1c), .input1d(subtractor256bit_33_output1d), .input2a({64{1'b0}}),
    .input2b({input2[33:0], {30{1'b0}}}), .input2c({{34{1'b0}}, input2[63:34]}), .input2d({64{1'b0}}),
    .greater1(comparatoru256bit_34_greater1), .equal1(comparatoru256bit_34_equal1));  // open: less1
  subtractor256bit subtractor256bit_35 (
    .input1a(subtractor256bit_34_output1a), .input1b(subtractor256bit_34_output1b),
    .input1c(subtractor256bit_34_output1c), .input1d(subtractor256bit_34_output1d),
    .input2a(cbuffer256bit_35_output1a), .input2b(cbuffer256bit_35_output1b),
    .input2c(cbuffer256bit_35_output1c), .input2d(cbuffer256bit_35_output1d),
    .output1a(subtractor256bit_35_output1a), .output1b(subtractor256bit_35_output1b),
    .output1c(subtractor256bit_35_output1c), .output1d(subtractor256bit_35_output1d));  // open: inborrow, borrow
  cbuffer256bit cbuffer256bit_35 (
    .buffer1(output1[29]), .input1a({64{1'b0}}), .input1b({input2[34:0], {29{1'b0}}}),
    .input1c({{35{1'b0}}, input2[63:35]}), .input1d({64{1'b0}}), .output1a(cbuffer256bit_35_output1a),
    .output1b(cbuffer256bit_35_output1b), .output1c(cbuffer256bit_35_output1c),
    .output1d(cbuffer256bit_35_output1d));
  and and_35 (output1[29], not_1_out, or_35_out);
  or or_35 (or_35_out, comparatoru256bit_35_greater1, comparatoru256bit_35_equal1);
  comparatoru256bit comparatoru256bit_35 (
    .input1a(subtractor256bit_34_output1a), .input1b(subtractor256bit_34_output1b),
    .input1c(subtractor256bit_34_output1c), .input1d(subtractor256bit_34_output1d), .input2a({64{1'b0}}),
    .input2b({input2[34:0], {29{1'b0}}}), .input2c({{35{1'b0}}, input2[63:35]}), .input2d({64{1'b0}}),
    .greater1(comparatoru256bit_35_greater1), .equal1(comparatoru256bit_35_equal1));  // open: less1
  subtractor256bit subtractor256bit_36 (
    .input1a(subtractor256bit_35_output1a), .input1b(subtractor256bit_35_output1b),
    .input1c(subtractor256bit_35_output1c), .input1d(subtractor256bit_35_output1d),
    .input2a(cbuffer256bit_36_output1a), .input2b(cbuffer256bit_36_output1b),
    .input2c(cbuffer256bit_36_output1c), .input2d(cbuffer256bit_36_output1d),
    .output1a(subtractor256bit_36_output1a), .output1b(subtractor256bit_36_output1b),
    .output1c(subtractor256bit_36_output1c), .output1d(subtractor256bit_36_output1d));  // open: inborrow, borrow
  cbuffer256bit cbuffer256bit_36 (
    .buffer1(output1[28]), .input1a({64{1'b0}}), .input1b({input2[35:0], {28{1'b0}}}),
    .input1c({{36{1'b0}}, input2[63:36]}), .input1d({64{1'b0}}), .output1a(cbuffer256bit_36_output1a),
    .output1b(cbuffer256bit_36_output1b), .output1c(cbuffer256bit_36_output1c),
    .output1d(cbuffer256bit_36_output1d));
  and and_36 (output1[28], not_1_out, or_36_out);
  or or_36 (or_36_out, comparatoru256bit_36_greater1, comparatoru256bit_36_equal1);
  comparatoru256bit comparatoru256bit_36 (
    .input1a(subtractor256bit_35_output1a), .input1b(subtractor256bit_35_output1b),
    .input1c(subtractor256bit_35_output1c), .input1d(subtractor256bit_35_output1d), .input2a({64{1'b0}}),
    .input2b({input2[35:0], {28{1'b0}}}), .input2c({{36{1'b0}}, input2[63:36]}), .input2d({64{1'b0}}),
    .greater1(comparatoru256bit_36_greater1), .equal1(comparatoru256bit_36_equal1));  // open: less1
  subtractor256bit subtractor256bit_37 (
    .input1a(subtractor256bit_36_output1a), .input1b(subtractor256bit_36_output1b),
    .input1c(subtractor256bit_36_output1c), .input1d(subtractor256bit_36_output1d),
    .input2a(cbuffer256bit_37_output1a), .input2b(cbuffer256bit_37_output1b),
    .input2c(cbuffer256bit_37_output1c), .input2d(cbuffer256bit_37_output1d),
    .output1a(subtractor256bit_37_output1a), .output1b(subtractor256bit_37_output1b),
    .output1c(subtractor256bit_37_output1c), .output1d(subtractor256bit_37_output1d));  // open: inborrow, borrow
  cbuffer256bit cbuffer256bit_37 (
    .buffer1(output1[27]), .input1a({64{1'b0}}), .input1b({input2[36:0], {27{1'b0}}}),
    .input1c({{37{1'b0}}, input2[63:37]}), .input1d({64{1'b0}}), .output1a(cbuffer256bit_37_output1a),
    .output1b(cbuffer256bit_37_output1b), .output1c(cbuffer256bit_37_output1c),
    .output1d(cbuffer256bit_37_output1d));
  and and_37 (output1[27], not_1_out, or_37_out);
  or or_37 (or_37_out, comparatoru256bit_37_greater1, comparatoru256bit_37_equal1);
  comparatoru256bit comparatoru256bit_37 (
    .input1a(subtractor256bit_36_output1a), .input1b(subtractor256bit_36_output1b),
    .input1c(subtractor256bit_36_output1c), .input1d(subtractor256bit_36_output1d), .input2a({64{1'b0}}),
    .input2b({input2[36:0], {27{1'b0}}}), .input2c({{37{1'b0}}, input2[63:37]}), .input2d({64{1'b0}}),
    .greater1(comparatoru256bit_37_greater1), .equal1(comparatoru256bit_37_equal1));  // open: less1
  subtractor256bit subtractor256bit_38 (
    .input1a(subtractor256bit_37_output1a), .input1b(subtractor256bit_37_output1b),
    .input1c(subtractor256bit_37_output1c), .input1d(subtractor256bit_37_output1d),
    .input2a(cbuffer256bit_38_output1a), .input2b(cbuffer256bit_38_output1b),
    .input2c(cbuffer256bit_38_output1c), .input2d(cbuffer256bit_38_output1d),
    .output1a(subtractor256bit_38_output1a), .output1b(subtractor256bit_38_output1b),
    .output1c(subtractor256bit_38_output1c), .output1d(subtractor256bit_38_output1d));  // open: inborrow, borrow
  cbuffer256bit cbuffer256bit_38 (
    .buffer1(output1[26]), .input1a({64{1'b0}}), .input1b({input2[37:0], {26{1'b0}}}),
    .input1c({{38{1'b0}}, input2[63:38]}), .input1d({64{1'b0}}), .output1a(cbuffer256bit_38_output1a),
    .output1b(cbuffer256bit_38_output1b), .output1c(cbuffer256bit_38_output1c),
    .output1d(cbuffer256bit_38_output1d));
  and and_38 (output1[26], not_1_out, or_38_out);
  or or_38 (or_38_out, comparatoru256bit_38_greater1, comparatoru256bit_38_equal1);
  comparatoru256bit comparatoru256bit_38 (
    .input1a(subtractor256bit_37_output1a), .input1b(subtractor256bit_37_output1b),
    .input1c(subtractor256bit_37_output1c), .input1d(subtractor256bit_37_output1d), .input2a({64{1'b0}}),
    .input2b({input2[37:0], {26{1'b0}}}), .input2c({{38{1'b0}}, input2[63:38]}), .input2d({64{1'b0}}),
    .greater1(comparatoru256bit_38_greater1), .equal1(comparatoru256bit_38_equal1));  // open: less1
  subtractor256bit subtractor256bit_39 (
    .input1a(subtractor256bit_38_output1a), .input1b(subtractor256bit_38_output1b),
    .input1c(subtractor256bit_38_output1c), .input1d(subtractor256bit_38_output1d),
    .input2a(cbuffer256bit_39_output1a), .input2b(cbuffer256bit_39_output1b),
    .input2c(cbuffer256bit_39_output1c), .input2d(cbuffer256bit_39_output1d),
    .output1a(subtractor256bit_39_output1a), .output1b(subtractor256bit_39_output1b),
    .output1c(subtractor256bit_39_output1c), .output1d(subtractor256bit_39_output1d));  // open: inborrow, borrow
  cbuffer256bit cbuffer256bit_39 (
    .buffer1(output1[25]), .input1a({64{1'b0}}), .input1b({input2[38:0], {25{1'b0}}}),
    .input1c({{39{1'b0}}, input2[63:39]}), .input1d({64{1'b0}}), .output1a(cbuffer256bit_39_output1a),
    .output1b(cbuffer256bit_39_output1b), .output1c(cbuffer256bit_39_output1c),
    .output1d(cbuffer256bit_39_output1d));
  and and_39 (output1[25], not_1_out, or_39_out);
  comparatoru256bit comparatoru256bit_39 (
    .input1a(subtractor256bit_38_output1a), .input1b(subtractor256bit_38_output1b),
    .input1c(subtractor256bit_38_output1c), .input1d(subtractor256bit_38_output1d), .input2a({64{1'b0}}),
    .input2b({input2[38:0], {25{1'b0}}}), .input2c({{39{1'b0}}, input2[63:39]}), .input2d({64{1'b0}}),
    .greater1(comparatoru256bit_39_greater1), .equal1(comparatoru256bit_39_equal1));  // open: less1
  or or_39 (or_39_out, comparatoru256bit_39_greater1, comparatoru256bit_39_equal1);
  subtractor256bit subtractor256bit_40 (
    .input1a(subtractor256bit_39_output1a), .input1b(subtractor256bit_39_output1b),
    .input1c(subtractor256bit_39_output1c), .input1d(subtractor256bit_39_output1d),
    .input2a(cbuffer256bit_40_output1a), .input2b(cbuffer256bit_40_output1b),
    .input2c(cbuffer256bit_40_output1c), .input2d(cbuffer256bit_40_output1d),
    .output1a(subtractor256bit_40_output1a), .output1b(subtractor256bit_40_output1b),
    .output1c(subtractor256bit_40_output1c), .output1d(subtractor256bit_40_output1d));  // open: inborrow, borrow
  cbuffer256bit cbuffer256bit_40 (
    .buffer1(output1[24]), .input1a({64{1'b0}}), .input1b({input2[39:0], {24{1'b0}}}),
    .input1c({{40{1'b0}}, input2[63:40]}), .input1d({64{1'b0}}), .output1a(cbuffer256bit_40_output1a),
    .output1b(cbuffer256bit_40_output1b), .output1c(cbuffer256bit_40_output1c),
    .output1d(cbuffer256bit_40_output1d));
  and and_40 (output1[24], not_1_out, or_40_out);
  or or_40 (or_40_out, comparatoru256bit_40_greater1, comparatoru256bit_40_equal1);
  comparatoru256bit comparatoru256bit_40 (
    .input1a(subtractor256bit_39_output1a), .input1b(subtractor256bit_39_output1b),
    .input1c(subtractor256bit_39_output1c), .input1d(subtractor256bit_39_output1d), .input2a({64{1'b0}}),
    .input2b({input2[39:0], {24{1'b0}}}), .input2c({{40{1'b0}}, input2[63:40]}), .input2d({64{1'b0}}),
    .greater1(comparatoru256bit_40_greater1), .equal1(comparatoru256bit_40_equal1));  // open: less1
  subtractor256bit subtractor256bit_41 (
    .input1a(subtractor256bit_40_output1a), .input1b(subtractor256bit_40_output1b),
    .input1c(subtractor256bit_40_output1c), .input1d(subtractor256bit_40_output1d),
    .input2a(cbuffer256bit_41_output1a), .input2b(cbuffer256bit_41_output1b),
    .input2c(cbuffer256bit_41_output1c), .input2d(cbuffer256bit_41_output1d),
    .output1a(subtractor256bit_41_output1a), .output1b(subtractor256bit_41_output1b),
    .output1c(subtractor256bit_41_output1c), .output1d(subtractor256bit_41_output1d));  // open: inborrow, borrow
  cbuffer256bit cbuffer256bit_41 (
    .buffer1(output1[23]), .input1a({64{1'b0}}), .input1b({input2[40:0], {23{1'b0}}}),
    .input1c({{41{1'b0}}, input2[63:41]}), .input1d({64{1'b0}}), .output1a(cbuffer256bit_41_output1a),
    .output1b(cbuffer256bit_41_output1b), .output1c(cbuffer256bit_41_output1c),
    .output1d(cbuffer256bit_41_output1d));
  and and_41 (output1[23], not_1_out, or_41_out);
  or or_41 (or_41_out, comparatoru256bit_41_greater1, comparatoru256bit_41_equal1);
  comparatoru256bit comparatoru256bit_41 (
    .input1a(subtractor256bit_40_output1a), .input1b(subtractor256bit_40_output1b),
    .input1c(subtractor256bit_40_output1c), .input1d(subtractor256bit_40_output1d), .input2a({64{1'b0}}),
    .input2b({input2[40:0], {23{1'b0}}}), .input2c({{41{1'b0}}, input2[63:41]}), .input2d({64{1'b0}}),
    .greater1(comparatoru256bit_41_greater1), .equal1(comparatoru256bit_41_equal1));  // open: less1
  subtractor256bit subtractor256bit_42 (
    .input1a(subtractor256bit_41_output1a), .input1b(subtractor256bit_41_output1b),
    .input1c(subtractor256bit_41_output1c), .input1d(subtractor256bit_41_output1d),
    .input2a(cbuffer256bit_42_output1a), .input2b(cbuffer256bit_42_output1b),
    .input2c(cbuffer256bit_42_output1c), .input2d(cbuffer256bit_42_output1d),
    .output1a(subtractor256bit_42_output1a), .output1b(subtractor256bit_42_output1b),
    .output1c(subtractor256bit_42_output1c), .output1d(subtractor256bit_42_output1d));  // open: inborrow, borrow
  cbuffer256bit cbuffer256bit_42 (
    .buffer1(output1[22]), .input1a({64{1'b0}}), .input1b({input2[41:0], {22{1'b0}}}),
    .input1c({{42{1'b0}}, input2[63:42]}), .input1d({64{1'b0}}), .output1a(cbuffer256bit_42_output1a),
    .output1b(cbuffer256bit_42_output1b), .output1c(cbuffer256bit_42_output1c),
    .output1d(cbuffer256bit_42_output1d));
  and and_42 (output1[22], not_1_out, or_42_out);
  or or_42 (or_42_out, comparatoru256bit_42_greater1, comparatoru256bit_42_equal1);
  comparatoru256bit comparatoru256bit_42 (
    .input1a(subtractor256bit_41_output1a), .input1b(subtractor256bit_41_output1b),
    .input1c(subtractor256bit_41_output1c), .input1d(subtractor256bit_41_output1d), .input2a({64{1'b0}}),
    .input2b({input2[41:0], {22{1'b0}}}), .input2c({{42{1'b0}}, input2[63:42]}), .input2d({64{1'b0}}),
    .greater1(comparatoru256bit_42_greater1), .equal1(comparatoru256bit_42_equal1));  // open: less1
  subtractor256bit subtractor256bit_43 (
    .input1a(subtractor256bit_42_output1a), .input1b(subtractor256bit_42_output1b),
    .input1c(subtractor256bit_42_output1c), .input1d(subtractor256bit_42_output1d),
    .input2a(cbuffer256bit_43_output1a), .input2b(cbuffer256bit_43_output1b),
    .input2c(cbuffer256bit_43_output1c), .input2d(cbuffer256bit_43_output1d),
    .output1a(subtractor256bit_43_output1a), .output1b(subtractor256bit_43_output1b),
    .output1c(subtractor256bit_43_output1c), .output1d(subtractor256bit_43_output1d));  // open: inborrow, borrow
  cbuffer256bit cbuffer256bit_43 (
    .buffer1(output1[21]), .input1a({64{1'b0}}), .input1b({input2[42:0], {21{1'b0}}}),
    .input1c({{43{1'b0}}, input2[63:43]}), .input1d({64{1'b0}}), .output1a(cbuffer256bit_43_output1a),
    .output1b(cbuffer256bit_43_output1b), .output1c(cbuffer256bit_43_output1c),
    .output1d(cbuffer256bit_43_output1d));
  and and_43 (output1[21], not_1_out, or_43_out);
  or or_43 (or_43_out, comparatoru256bit_43_greater1, comparatoru256bit_43_equal1);
  comparatoru256bit comparatoru256bit_43 (
    .input1a(subtractor256bit_42_output1a), .input1b(subtractor256bit_42_output1b),
    .input1c(subtractor256bit_42_output1c), .input1d(subtractor256bit_42_output1d), .input2a({64{1'b0}}),
    .input2b({input2[42:0], {21{1'b0}}}), .input2c({{43{1'b0}}, input2[63:43]}), .input2d({64{1'b0}}),
    .greater1(comparatoru256bit_43_greater1), .equal1(comparatoru256bit_43_equal1));  // open: less1
  subtractor256bit subtractor256bit_44 (
    .input1a(subtractor256bit_43_output1a), .input1b(subtractor256bit_43_output1b),
    .input1c(subtractor256bit_43_output1c), .input1d(subtractor256bit_43_output1d),
    .input2a(cbuffer256bit_44_output1a), .input2b(cbuffer256bit_44_output1b),
    .input2c(cbuffer256bit_44_output1c), .input2d(cbuffer256bit_44_output1d),
    .output1a(subtractor256bit_44_output1a), .output1b(subtractor256bit_44_output1b),
    .output1c(subtractor256bit_44_output1c), .output1d(subtractor256bit_44_output1d));  // open: inborrow, borrow
  cbuffer256bit cbuffer256bit_44 (
    .buffer1(output1[20]), .input1a({64{1'b0}}), .input1b({input2[43:0], {20{1'b0}}}),
    .input1c({{44{1'b0}}, input2[63:44]}), .input1d({64{1'b0}}), .output1a(cbuffer256bit_44_output1a),
    .output1b(cbuffer256bit_44_output1b), .output1c(cbuffer256bit_44_output1c),
    .output1d(cbuffer256bit_44_output1d));
  and and_44 (output1[20], not_1_out, or_44_out);
  or or_44 (or_44_out, comparatoru256bit_44_greater1, comparatoru256bit_44_equal1);
  comparatoru256bit comparatoru256bit_44 (
    .input1a(subtractor256bit_43_output1a), .input1b(subtractor256bit_43_output1b),
    .input1c(subtractor256bit_43_output1c), .input1d(subtractor256bit_43_output1d), .input2a({64{1'b0}}),
    .input2b({input2[43:0], {20{1'b0}}}), .input2c({{44{1'b0}}, input2[63:44]}), .input2d({64{1'b0}}),
    .greater1(comparatoru256bit_44_greater1), .equal1(comparatoru256bit_44_equal1));  // open: less1
  subtractor256bit subtractor256bit_45 (
    .input1a(subtractor256bit_44_output1a), .input1b(subtractor256bit_44_output1b),
    .input1c(subtractor256bit_44_output1c), .input1d(subtractor256bit_44_output1d),
    .input2a(cbuffer256bit_45_output1a), .input2b(cbuffer256bit_45_output1b),
    .input2c(cbuffer256bit_45_output1c), .input2d(cbuffer256bit_45_output1d),
    .output1a(subtractor256bit_45_output1a), .output1b(subtractor256bit_45_output1b),
    .output1c(subtractor256bit_45_output1c), .output1d(subtractor256bit_45_output1d));  // open: inborrow, borrow
  cbuffer256bit cbuffer256bit_45 (
    .buffer1(output1[19]), .input1a({64{1'b0}}), .input1b({input2[44:0], {19{1'b0}}}),
    .input1c({{45{1'b0}}, input2[63:45]}), .input1d({64{1'b0}}), .output1a(cbuffer256bit_45_output1a),
    .output1b(cbuffer256bit_45_output1b), .output1c(cbuffer256bit_45_output1c),
    .output1d(cbuffer256bit_45_output1d));
  and and_45 (output1[19], not_1_out, or_45_out);
  or or_45 (or_45_out, comparatoru256bit_45_greater1, comparatoru256bit_45_equal1);
  comparatoru256bit comparatoru256bit_45 (
    .input1a(subtractor256bit_44_output1a), .input1b(subtractor256bit_44_output1b),
    .input1c(subtractor256bit_44_output1c), .input1d(subtractor256bit_44_output1d), .input2a({64{1'b0}}),
    .input2b({input2[44:0], {19{1'b0}}}), .input2c({{45{1'b0}}, input2[63:45]}), .input2d({64{1'b0}}),
    .greater1(comparatoru256bit_45_greater1), .equal1(comparatoru256bit_45_equal1));  // open: less1
  subtractor256bit subtractor256bit_46 (
    .input1a(subtractor256bit_45_output1a), .input1b(subtractor256bit_45_output1b),
    .input1c(subtractor256bit_45_output1c), .input1d(subtractor256bit_45_output1d),
    .input2a(cbuffer256bit_46_output1a), .input2b(cbuffer256bit_46_output1b),
    .input2c(cbuffer256bit_46_output1c), .input2d(cbuffer256bit_46_output1d),
    .output1a(subtractor256bit_46_output1a), .output1b(subtractor256bit_46_output1b),
    .output1c(subtractor256bit_46_output1c), .output1d(subtractor256bit_46_output1d));  // open: inborrow, borrow
  cbuffer256bit cbuffer256bit_46 (
    .buffer1(output1[18]), .input1a({64{1'b0}}), .input1b({input2[45:0], {18{1'b0}}}),
    .input1c({{46{1'b0}}, input2[63:46]}), .input1d({64{1'b0}}), .output1a(cbuffer256bit_46_output1a),
    .output1b(cbuffer256bit_46_output1b), .output1c(cbuffer256bit_46_output1c),
    .output1d(cbuffer256bit_46_output1d));
  and and_46 (output1[18], not_1_out, or_46_out);
  or or_46 (or_46_out, comparatoru256bit_46_greater1, comparatoru256bit_46_equal1);
  comparatoru256bit comparatoru256bit_46 (
    .input1a(subtractor256bit_45_output1a), .input1b(subtractor256bit_45_output1b),
    .input1c(subtractor256bit_45_output1c), .input1d(subtractor256bit_45_output1d), .input2a({64{1'b0}}),
    .input2b({input2[45:0], {18{1'b0}}}), .input2c({{46{1'b0}}, input2[63:46]}), .input2d({64{1'b0}}),
    .greater1(comparatoru256bit_46_greater1), .equal1(comparatoru256bit_46_equal1));  // open: less1
  subtractor256bit subtractor256bit_47 (
    .input1a(subtractor256bit_46_output1a), .input1b(subtractor256bit_46_output1b),
    .input1c(subtractor256bit_46_output1c), .input1d(subtractor256bit_46_output1d),
    .input2a(cbuffer256bit_47_output1a), .input2b(cbuffer256bit_47_output1b),
    .input2c(cbuffer256bit_47_output1c), .input2d(cbuffer256bit_47_output1d),
    .output1a(subtractor256bit_47_output1a), .output1b(subtractor256bit_47_output1b),
    .output1c(subtractor256bit_47_output1c), .output1d(subtractor256bit_47_output1d));  // open: inborrow, borrow
  cbuffer256bit cbuffer256bit_47 (
    .buffer1(output1[17]), .input1a({64{1'b0}}), .input1b({input2[46:0], {17{1'b0}}}),
    .input1c({{47{1'b0}}, input2[63:47]}), .input1d({64{1'b0}}), .output1a(cbuffer256bit_47_output1a),
    .output1b(cbuffer256bit_47_output1b), .output1c(cbuffer256bit_47_output1c),
    .output1d(cbuffer256bit_47_output1d));
  and and_47 (output1[17], not_1_out, or_47_out);
  comparatoru256bit comparatoru256bit_47 (
    .input1a(subtractor256bit_46_output1a), .input1b(subtractor256bit_46_output1b),
    .input1c(subtractor256bit_46_output1c), .input1d(subtractor256bit_46_output1d), .input2a({64{1'b0}}),
    .input2b({input2[46:0], {17{1'b0}}}), .input2c({{47{1'b0}}, input2[63:47]}), .input2d({64{1'b0}}),
    .greater1(comparatoru256bit_47_greater1), .equal1(comparatoru256bit_47_equal1));  // open: less1
  or or_47 (or_47_out, comparatoru256bit_47_greater1, comparatoru256bit_47_equal1);
  subtractor256bit subtractor256bit_48 (
    .input1a(subtractor256bit_47_output1a), .input1b(subtractor256bit_47_output1b),
    .input1c(subtractor256bit_47_output1c), .input1d(subtractor256bit_47_output1d),
    .input2a(cbuffer256bit_48_output1a), .input2b(cbuffer256bit_48_output1b),
    .input2c(cbuffer256bit_48_output1c), .input2d(cbuffer256bit_48_output1d),
    .output1a(subtractor256bit_48_output1a), .output1b(subtractor256bit_48_output1b),
    .output1c(subtractor256bit_48_output1c), .output1d(subtractor256bit_48_output1d));  // open: inborrow, borrow
  cbuffer256bit cbuffer256bit_48 (
    .buffer1(output1[16]), .input1a({64{1'b0}}), .input1b({input2[47:0], {16{1'b0}}}),
    .input1c({{48{1'b0}}, input2[63:48]}), .input1d({64{1'b0}}), .output1a(cbuffer256bit_48_output1a),
    .output1b(cbuffer256bit_48_output1b), .output1c(cbuffer256bit_48_output1c),
    .output1d(cbuffer256bit_48_output1d));
  and and_48 (output1[16], not_1_out, or_48_out);
  or or_48 (or_48_out, comparatoru256bit_48_greater1, comparatoru256bit_48_equal1);
  comparatoru256bit comparatoru256bit_48 (
    .input1a(subtractor256bit_47_output1a), .input1b(subtractor256bit_47_output1b),
    .input1c(subtractor256bit_47_output1c), .input1d(subtractor256bit_47_output1d), .input2a({64{1'b0}}),
    .input2b({input2[47:0], {16{1'b0}}}), .input2c({{48{1'b0}}, input2[63:48]}), .input2d({64{1'b0}}),
    .greater1(comparatoru256bit_48_greater1), .equal1(comparatoru256bit_48_equal1));  // open: less1
  subtractor256bit subtractor256bit_49 (
    .input1a(subtractor256bit_48_output1a), .input1b(subtractor256bit_48_output1b),
    .input1c(subtractor256bit_48_output1c), .input1d(subtractor256bit_48_output1d),
    .input2a(cbuffer256bit_49_output1a), .input2b(cbuffer256bit_49_output1b),
    .input2c(cbuffer256bit_49_output1c), .input2d(cbuffer256bit_49_output1d),
    .output1a(subtractor256bit_49_output1a), .output1b(subtractor256bit_49_output1b),
    .output1c(subtractor256bit_49_output1c), .output1d(subtractor256bit_49_output1d));  // open: inborrow, borrow
  cbuffer256bit cbuffer256bit_49 (
    .buffer1(output1[15]), .input1a({64{1'b0}}), .input1b({input2[48:0], {15{1'b0}}}),
    .input1c({{49{1'b0}}, input2[63:49]}), .input1d({64{1'b0}}), .output1a(cbuffer256bit_49_output1a),
    .output1b(cbuffer256bit_49_output1b), .output1c(cbuffer256bit_49_output1c),
    .output1d(cbuffer256bit_49_output1d));
  and and_49 (output1[15], not_1_out, or_49_out);
  or or_49 (or_49_out, comparatoru256bit_49_greater1, comparatoru256bit_49_equal1);
  comparatoru256bit comparatoru256bit_49 (
    .input1a(subtractor256bit_48_output1a), .input1b(subtractor256bit_48_output1b),
    .input1c(subtractor256bit_48_output1c), .input1d(subtractor256bit_48_output1d), .input2a({64{1'b0}}),
    .input2b({input2[48:0], {15{1'b0}}}), .input2c({{49{1'b0}}, input2[63:49]}), .input2d({64{1'b0}}),
    .greater1(comparatoru256bit_49_greater1), .equal1(comparatoru256bit_49_equal1));  // open: less1
  subtractor256bit subtractor256bit_50 (
    .input1a(subtractor256bit_49_output1a), .input1b(subtractor256bit_49_output1b),
    .input1c(subtractor256bit_49_output1c), .input1d(subtractor256bit_49_output1d),
    .input2a(cbuffer256bit_50_output1a), .input2b(cbuffer256bit_50_output1b),
    .input2c(cbuffer256bit_50_output1c), .input2d(cbuffer256bit_50_output1d),
    .output1a(subtractor256bit_50_output1a), .output1b(subtractor256bit_50_output1b),
    .output1c(subtractor256bit_50_output1c), .output1d(subtractor256bit_50_output1d));  // open: inborrow, borrow
  cbuffer256bit cbuffer256bit_50 (
    .buffer1(output1[14]), .input1a({64{1'b0}}), .input1b({input2[49:0], {14{1'b0}}}),
    .input1c({{50{1'b0}}, input2[63:50]}), .input1d({64{1'b0}}), .output1a(cbuffer256bit_50_output1a),
    .output1b(cbuffer256bit_50_output1b), .output1c(cbuffer256bit_50_output1c),
    .output1d(cbuffer256bit_50_output1d));
  and and_50 (output1[14], not_1_out, or_50_out);
  or or_50 (or_50_out, comparatoru256bit_50_greater1, comparatoru256bit_50_equal1);
  comparatoru256bit comparatoru256bit_50 (
    .input1a(subtractor256bit_49_output1a), .input1b(subtractor256bit_49_output1b),
    .input1c(subtractor256bit_49_output1c), .input1d(subtractor256bit_49_output1d), .input2a({64{1'b0}}),
    .input2b({input2[49:0], {14{1'b0}}}), .input2c({{50{1'b0}}, input2[63:50]}), .input2d({64{1'b0}}),
    .greater1(comparatoru256bit_50_greater1), .equal1(comparatoru256bit_50_equal1));  // open: less1
  subtractor256bit subtractor256bit_51 (
    .input1a(subtractor256bit_50_output1a), .input1b(subtractor256bit_50_output1b),
    .input1c(subtractor256bit_50_output1c), .input1d(subtractor256bit_50_output1d),
    .input2a(cbuffer256bit_51_output1a), .input2b(cbuffer256bit_51_output1b),
    .input2c(cbuffer256bit_51_output1c), .input2d(cbuffer256bit_51_output1d),
    .output1a(subtractor256bit_51_output1a), .output1b(subtractor256bit_51_output1b),
    .output1c(subtractor256bit_51_output1c), .output1d(subtractor256bit_51_output1d));  // open: inborrow, borrow
  cbuffer256bit cbuffer256bit_51 (
    .buffer1(output1[13]), .input1a({64{1'b0}}), .input1b({input2[50:0], {13{1'b0}}}),
    .input1c({{51{1'b0}}, input2[63:51]}), .input1d({64{1'b0}}), .output1a(cbuffer256bit_51_output1a),
    .output1b(cbuffer256bit_51_output1b), .output1c(cbuffer256bit_51_output1c),
    .output1d(cbuffer256bit_51_output1d));
  and and_51 (output1[13], not_1_out, or_51_out);
  or or_51 (or_51_out, comparatoru256bit_51_greater1, comparatoru256bit_51_equal1);
  comparatoru256bit comparatoru256bit_51 (
    .input1a(subtractor256bit_50_output1a), .input1b(subtractor256bit_50_output1b),
    .input1c(subtractor256bit_50_output1c), .input1d(subtractor256bit_50_output1d), .input2a({64{1'b0}}),
    .input2b({input2[50:0], {13{1'b0}}}), .input2c({{51{1'b0}}, input2[63:51]}), .input2d({64{1'b0}}),
    .greater1(comparatoru256bit_51_greater1), .equal1(comparatoru256bit_51_equal1));  // open: less1
  subtractor256bit subtractor256bit_52 (
    .input1a(subtractor256bit_51_output1a), .input1b(subtractor256bit_51_output1b),
    .input1c(subtractor256bit_51_output1c), .input1d(subtractor256bit_51_output1d),
    .input2a(cbuffer256bit_52_output1a), .input2b(cbuffer256bit_52_output1b),
    .input2c(cbuffer256bit_52_output1c), .input2d(cbuffer256bit_52_output1d),
    .output1a(subtractor256bit_52_output1a), .output1b(subtractor256bit_52_output1b),
    .output1c(subtractor256bit_52_output1c), .output1d(subtractor256bit_52_output1d));  // open: inborrow, borrow
  cbuffer256bit cbuffer256bit_52 (
    .buffer1(output1[12]), .input1a({64{1'b0}}), .input1b({input2[51:0], {12{1'b0}}}),
    .input1c({{52{1'b0}}, input2[63:52]}), .input1d({64{1'b0}}), .output1a(cbuffer256bit_52_output1a),
    .output1b(cbuffer256bit_52_output1b), .output1c(cbuffer256bit_52_output1c),
    .output1d(cbuffer256bit_52_output1d));
  and and_52 (output1[12], not_1_out, or_52_out);
  or or_52 (or_52_out, comparatoru256bit_52_greater1, comparatoru256bit_52_equal1);
  comparatoru256bit comparatoru256bit_52 (
    .input1a(subtractor256bit_51_output1a), .input1b(subtractor256bit_51_output1b),
    .input1c(subtractor256bit_51_output1c), .input1d(subtractor256bit_51_output1d), .input2a({64{1'b0}}),
    .input2b({input2[51:0], {12{1'b0}}}), .input2c({{52{1'b0}}, input2[63:52]}), .input2d({64{1'b0}}),
    .greater1(comparatoru256bit_52_greater1), .equal1(comparatoru256bit_52_equal1));  // open: less1
  subtractor256bit subtractor256bit_53 (
    .input1a(subtractor256bit_52_output1a), .input1b(subtractor256bit_52_output1b),
    .input1c(subtractor256bit_52_output1c), .input1d(subtractor256bit_52_output1d),
    .input2a(cbuffer256bit_53_output1a), .input2b(cbuffer256bit_53_output1b),
    .input2c(cbuffer256bit_53_output1c), .input2d(cbuffer256bit_53_output1d),
    .output1a(subtractor256bit_53_output1a), .output1b(subtractor256bit_53_output1b),
    .output1c(subtractor256bit_53_output1c), .output1d(subtractor256bit_53_output1d));  // open: inborrow, borrow
  cbuffer256bit cbuffer256bit_53 (
    .buffer1(output1[11]), .input1a({64{1'b0}}), .input1b({input2[52:0], {11{1'b0}}}),
    .input1c({{53{1'b0}}, input2[63:53]}), .input1d({64{1'b0}}), .output1a(cbuffer256bit_53_output1a),
    .output1b(cbuffer256bit_53_output1b), .output1c(cbuffer256bit_53_output1c),
    .output1d(cbuffer256bit_53_output1d));
  and and_53 (output1[11], not_1_out, or_53_out);
  or or_53 (or_53_out, comparatoru256bit_53_greater1, comparatoru256bit_53_equal1);
  comparatoru256bit comparatoru256bit_53 (
    .input1a(subtractor256bit_52_output1a), .input1b(subtractor256bit_52_output1b),
    .input1c(subtractor256bit_52_output1c), .input1d(subtractor256bit_52_output1d), .input2a({64{1'b0}}),
    .input2b({input2[52:0], {11{1'b0}}}), .input2c({{53{1'b0}}, input2[63:53]}), .input2d({64{1'b0}}),
    .greater1(comparatoru256bit_53_greater1), .equal1(comparatoru256bit_53_equal1));  // open: less1
  subtractor256bit subtractor256bit_54 (
    .input1a(subtractor256bit_53_output1a), .input1b(subtractor256bit_53_output1b),
    .input1c(subtractor256bit_53_output1c), .input1d(subtractor256bit_53_output1d),
    .input2a(cbuffer256bit_54_output1a), .input2b(cbuffer256bit_54_output1b),
    .input2c(cbuffer256bit_54_output1c), .input2d(cbuffer256bit_54_output1d),
    .output1a(subtractor256bit_54_output1a), .output1b(subtractor256bit_54_output1b),
    .output1c(subtractor256bit_54_output1c), .output1d(subtractor256bit_54_output1d));  // open: inborrow, borrow
  cbuffer256bit cbuffer256bit_54 (
    .buffer1(output1[10]), .input1a({64{1'b0}}), .input1b({input2[53:0], {10{1'b0}}}),
    .input1c({{54{1'b0}}, input2[63:54]}), .input1d({64{1'b0}}), .output1a(cbuffer256bit_54_output1a),
    .output1b(cbuffer256bit_54_output1b), .output1c(cbuffer256bit_54_output1c),
    .output1d(cbuffer256bit_54_output1d));
  and and_54 (output1[10], not_1_out, or_54_out);
  or or_54 (or_54_out, comparatoru256bit_54_greater1, comparatoru256bit_54_equal1);
  comparatoru256bit comparatoru256bit_54 (
    .input1a(subtractor256bit_53_output1a), .input1b(subtractor256bit_53_output1b),
    .input1c(subtractor256bit_53_output1c), .input1d(subtractor256bit_53_output1d), .input2a({64{1'b0}}),
    .input2b({input2[53:0], {10{1'b0}}}), .input2c({{54{1'b0}}, input2[63:54]}), .input2d({64{1'b0}}),
    .greater1(comparatoru256bit_54_greater1), .equal1(comparatoru256bit_54_equal1));  // open: less1
  subtractor256bit subtractor256bit_55 (
    .input1a(subtractor256bit_54_output1a), .input1b(subtractor256bit_54_output1b),
    .input1c(subtractor256bit_54_output1c), .input1d(subtractor256bit_54_output1d),
    .input2a(cbuffer256bit_55_output1a), .input2b(cbuffer256bit_55_output1b),
    .input2c(cbuffer256bit_55_output1c), .input2d(cbuffer256bit_55_output1d),
    .output1a(subtractor256bit_55_output1a), .output1b(subtractor256bit_55_output1b),
    .output1c(subtractor256bit_55_output1c), .output1d(subtractor256bit_55_output1d));  // open: inborrow, borrow
  cbuffer256bit cbuffer256bit_55 (
    .buffer1(output1[9]), .input1a({64{1'b0}}), .input1b({input2[54:0], {9{1'b0}}}),
    .input1c({{55{1'b0}}, input2[63:55]}), .input1d({64{1'b0}}), .output1a(cbuffer256bit_55_output1a),
    .output1b(cbuffer256bit_55_output1b), .output1c(cbuffer256bit_55_output1c),
    .output1d(cbuffer256bit_55_output1d));
  and and_55 (output1[9], not_1_out, or_55_out);
  comparatoru256bit comparatoru256bit_55 (
    .input1a(subtractor256bit_54_output1a), .input1b(subtractor256bit_54_output1b),
    .input1c(subtractor256bit_54_output1c), .input1d(subtractor256bit_54_output1d), .input2a({64{1'b0}}),
    .input2b({input2[54:0], {9{1'b0}}}), .input2c({{55{1'b0}}, input2[63:55]}), .input2d({64{1'b0}}),
    .greater1(comparatoru256bit_55_greater1), .equal1(comparatoru256bit_55_equal1));  // open: less1
  or or_55 (or_55_out, comparatoru256bit_55_greater1, comparatoru256bit_55_equal1);
  subtractor256bit subtractor256bit_56 (
    .input1a(subtractor256bit_55_output1a), .input1b(subtractor256bit_55_output1b),
    .input1c(subtractor256bit_55_output1c), .input1d(subtractor256bit_55_output1d),
    .input2a(cbuffer256bit_56_output1a), .input2b(cbuffer256bit_56_output1b),
    .input2c(cbuffer256bit_56_output1c), .input2d(cbuffer256bit_56_output1d),
    .output1a(subtractor256bit_56_output1a), .output1b(subtractor256bit_56_output1b),
    .output1c(subtractor256bit_56_output1c), .output1d(subtractor256bit_56_output1d));  // open: inborrow, borrow
  cbuffer256bit cbuffer256bit_56 (
    .buffer1(output1[8]), .input1a({64{1'b0}}), .input1b({input2[55:0], {8{1'b0}}}),
    .input1c({{56{1'b0}}, input2[63:56]}), .input1d({64{1'b0}}), .output1a(cbuffer256bit_56_output1a),
    .output1b(cbuffer256bit_56_output1b), .output1c(cbuffer256bit_56_output1c),
    .output1d(cbuffer256bit_56_output1d));
  and and_56 (output1[8], not_1_out, or_56_out);
  or or_56 (or_56_out, comparatoru256bit_56_greater1, comparatoru256bit_56_equal1);
  comparatoru256bit comparatoru256bit_56 (
    .input1a(subtractor256bit_55_output1a), .input1b(subtractor256bit_55_output1b),
    .input1c(subtractor256bit_55_output1c), .input1d(subtractor256bit_55_output1d), .input2a({64{1'b0}}),
    .input2b({input2[55:0], {8{1'b0}}}), .input2c({{56{1'b0}}, input2[63:56]}), .input2d({64{1'b0}}),
    .greater1(comparatoru256bit_56_greater1), .equal1(comparatoru256bit_56_equal1));  // open: less1
  subtractor256bit subtractor256bit_57 (
    .input1a(subtractor256bit_56_output1a), .input1b(subtractor256bit_56_output1b),
    .input1c(subtractor256bit_56_output1c), .input1d(subtractor256bit_56_output1d),
    .input2a(cbuffer256bit_57_output1a), .input2b(cbuffer256bit_57_output1b),
    .input2c(cbuffer256bit_57_output1c), .input2d(cbuffer256bit_57_output1d),
    .output1a(subtractor256bit_57_output1a), .output1b(subtractor256bit_57_output1b),
    .output1c(subtractor256bit_57_output1c), .output1d(subtractor256bit_57_output1d));  // open: inborrow, borrow
  cbuffer256bit cbuffer256bit_57 (
    .buffer1(output1[7]), .input1a({64{1'b0}}), .input1b({input2[56:0], {7{1'b0}}}),
    .input1c({{57{1'b0}}, input2[63:57]}), .input1d({64{1'b0}}), .output1a(cbuffer256bit_57_output1a),
    .output1b(cbuffer256bit_57_output1b), .output1c(cbuffer256bit_57_output1c),
    .output1d(cbuffer256bit_57_output1d));
  and and_57 (output1[7], not_1_out, or_57_out);
  or or_57 (or_57_out, comparatoru256bit_57_greater1, comparatoru256bit_57_equal1);
  comparatoru256bit comparatoru256bit_57 (
    .input1a(subtractor256bit_56_output1a), .input1b(subtractor256bit_56_output1b),
    .input1c(subtractor256bit_56_output1c), .input1d(subtractor256bit_56_output1d), .input2a({64{1'b0}}),
    .input2b({input2[56:0], {7{1'b0}}}), .input2c({{57{1'b0}}, input2[63:57]}), .input2d({64{1'b0}}),
    .greater1(comparatoru256bit_57_greater1), .equal1(comparatoru256bit_57_equal1));  // open: less1
  subtractor256bit subtractor256bit_58 (
    .input1a(subtractor256bit_57_output1a), .input1b(subtractor256bit_57_output1b),
    .input1c(subtractor256bit_57_output1c), .input1d(subtractor256bit_57_output1d),
    .input2a(cbuffer256bit_58_output1a), .input2b(cbuffer256bit_58_output1b),
    .input2c(cbuffer256bit_58_output1c), .input2d(cbuffer256bit_58_output1d),
    .output1a(subtractor256bit_58_output1a), .output1b(subtractor256bit_58_output1b),
    .output1c(subtractor256bit_58_output1c), .output1d(subtractor256bit_58_output1d));  // open: inborrow, borrow
  cbuffer256bit cbuffer256bit_58 (
    .buffer1(output1[6]), .input1a({64{1'b0}}), .input1b({input2[57:0], {6{1'b0}}}),
    .input1c({{58{1'b0}}, input2[63:58]}), .input1d({64{1'b0}}), .output1a(cbuffer256bit_58_output1a),
    .output1b(cbuffer256bit_58_output1b), .output1c(cbuffer256bit_58_output1c),
    .output1d(cbuffer256bit_58_output1d));
  and and_58 (output1[6], not_1_out, or_58_out);
  or or_58 (or_58_out, comparatoru256bit_58_greater1, comparatoru256bit_58_equal1);
  comparatoru256bit comparatoru256bit_58 (
    .input1a(subtractor256bit_57_output1a), .input1b(subtractor256bit_57_output1b),
    .input1c(subtractor256bit_57_output1c), .input1d(subtractor256bit_57_output1d), .input2a({64{1'b0}}),
    .input2b({input2[57:0], {6{1'b0}}}), .input2c({{58{1'b0}}, input2[63:58]}), .input2d({64{1'b0}}),
    .greater1(comparatoru256bit_58_greater1), .equal1(comparatoru256bit_58_equal1));  // open: less1
  subtractor256bit subtractor256bit_59 (
    .input1a(subtractor256bit_58_output1a), .input1b(subtractor256bit_58_output1b),
    .input1c(subtractor256bit_58_output1c), .input1d(subtractor256bit_58_output1d),
    .input2a(cbuffer256bit_59_output1a), .input2b(cbuffer256bit_59_output1b),
    .input2c(cbuffer256bit_59_output1c), .input2d(cbuffer256bit_59_output1d),
    .output1a(subtractor256bit_59_output1a), .output1b(subtractor256bit_59_output1b),
    .output1c(subtractor256bit_59_output1c), .output1d(subtractor256bit_59_output1d));  // open: inborrow, borrow
  cbuffer256bit cbuffer256bit_59 (
    .buffer1(output1[5]), .input1a({64{1'b0}}), .input1b({input2[58:0], {5{1'b0}}}),
    .input1c({{59{1'b0}}, input2[63:59]}), .input1d({64{1'b0}}), .output1a(cbuffer256bit_59_output1a),
    .output1b(cbuffer256bit_59_output1b), .output1c(cbuffer256bit_59_output1c),
    .output1d(cbuffer256bit_59_output1d));
  and and_59 (output1[5], not_1_out, or_59_out);
  or or_59 (or_59_out, comparatoru256bit_59_greater1, comparatoru256bit_59_equal1);
  comparatoru256bit comparatoru256bit_59 (
    .input1a(subtractor256bit_58_output1a), .input1b(subtractor256bit_58_output1b),
    .input1c(subtractor256bit_58_output1c), .input1d(subtractor256bit_58_output1d), .input2a({64{1'b0}}),
    .input2b({input2[58:0], {5{1'b0}}}), .input2c({{59{1'b0}}, input2[63:59]}), .input2d({64{1'b0}}),
    .greater1(comparatoru256bit_59_greater1), .equal1(comparatoru256bit_59_equal1));  // open: less1
  subtractor256bit subtractor256bit_60 (
    .input1a(subtractor256bit_59_output1a), .input1b(subtractor256bit_59_output1b),
    .input1c(subtractor256bit_59_output1c), .input1d(subtractor256bit_59_output1d),
    .input2a(cbuffer256bit_60_output1a), .input2b(cbuffer256bit_60_output1b),
    .input2c(cbuffer256bit_60_output1c), .input2d(cbuffer256bit_60_output1d),
    .output1a(subtractor256bit_60_output1a), .output1b(subtractor256bit_60_output1b),
    .output1c(subtractor256bit_60_output1c), .output1d(subtractor256bit_60_output1d));  // open: inborrow, borrow
  cbuffer256bit cbuffer256bit_60 (
    .buffer1(output1[4]), .input1a({64{1'b0}}), .input1b({input2[59:0], 4'b0000}),
    .input1c({{60{1'b0}}, input2[63:60]}), .input1d({64{1'b0}}), .output1a(cbuffer256bit_60_output1a),
    .output1b(cbuffer256bit_60_output1b), .output1c(cbuffer256bit_60_output1c),
    .output1d(cbuffer256bit_60_output1d));
  and and_60 (output1[4], not_1_out, or_60_out);
  or or_60 (or_60_out, comparatoru256bit_60_greater1, comparatoru256bit_60_equal1);
  comparatoru256bit comparatoru256bit_60 (
    .input1a(subtractor256bit_59_output1a), .input1b(subtractor256bit_59_output1b),
    .input1c(subtractor256bit_59_output1c), .input1d(subtractor256bit_59_output1d), .input2a({64{1'b0}}),
    .input2b({input2[59:0], 4'b0000}), .input2c({{60{1'b0}}, input2[63:60]}), .input2d({64{1'b0}}),
    .greater1(comparatoru256bit_60_greater1), .equal1(comparatoru256bit_60_equal1));  // open: less1
  subtractor256bit subtractor256bit_61 (
    .input1a(subtractor256bit_60_output1a), .input1b(subtractor256bit_60_output1b),
    .input1c(subtractor256bit_60_output1c), .input1d(subtractor256bit_60_output1d),
    .input2a(cbuffer256bit_61_output1a), .input2b(cbuffer256bit_61_output1b),
    .input2c(cbuffer256bit_61_output1c), .input2d(cbuffer256bit_61_output1d),
    .output1a(subtractor256bit_61_output1a), .output1b(subtractor256bit_61_output1b),
    .output1c(subtractor256bit_61_output1c), .output1d(subtractor256bit_61_output1d));  // open: inborrow, borrow
  cbuffer256bit cbuffer256bit_61 (
    .buffer1(output1[3]), .input1a({64{1'b0}}), .input1b({input2[60:0], 3'b000}),
    .input1c({{61{1'b0}}, input2[63:61]}), .input1d({64{1'b0}}), .output1a(cbuffer256bit_61_output1a),
    .output1b(cbuffer256bit_61_output1b), .output1c(cbuffer256bit_61_output1c),
    .output1d(cbuffer256bit_61_output1d));
  and and_61 (output1[3], not_1_out, or_61_out);
  or or_61 (or_61_out, comparatoru256bit_61_greater1, comparatoru256bit_61_equal1);
  comparatoru256bit comparatoru256bit_61 (
    .input1a(subtractor256bit_60_output1a), .input1b(subtractor256bit_60_output1b),
    .input1c(subtractor256bit_60_output1c), .input1d(subtractor256bit_60_output1d), .input2a({64{1'b0}}),
    .input2b({input2[60:0], 3'b000}), .input2c({{61{1'b0}}, input2[63:61]}), .input2d({64{1'b0}}),
    .greater1(comparatoru256bit_61_greater1), .equal1(comparatoru256bit_61_equal1));  // open: less1
  subtractor256bit subtractor256bit_62 (
    .input1a(subtractor256bit_61_output1a), .input1b(subtractor256bit_61_output1b),
    .input1c(subtractor256bit_61_output1c), .input1d(subtractor256bit_61_output1d),
    .input2a(cbuffer256bit_62_output1a), .input2b(cbuffer256bit_62_output1b),
    .input2c(cbuffer256bit_62_output1c), .input2d(cbuffer256bit_62_output1d),
    .output1a(subtractor256bit_62_output1a), .output1b(subtractor256bit_62_output1b),
    .output1c(subtractor256bit_62_output1c), .output1d(subtractor256bit_62_output1d));  // open: inborrow, borrow
  cbuffer256bit cbuffer256bit_62 (
    .buffer1(output1[2]), .input1a({64{1'b0}}), .input1b({input2[61:0], 2'b00}),
    .input1c({{62{1'b0}}, input2[63:62]}), .input1d({64{1'b0}}), .output1a(cbuffer256bit_62_output1a),
    .output1b(cbuffer256bit_62_output1b), .output1c(cbuffer256bit_62_output1c),
    .output1d(cbuffer256bit_62_output1d));
  and and_62 (output1[2], not_1_out, or_62_out);
  or or_62 (or_62_out, comparatoru256bit_62_greater1, comparatoru256bit_62_equal1);
  comparatoru256bit comparatoru256bit_62 (
    .input1a(subtractor256bit_61_output1a), .input1b(subtractor256bit_61_output1b),
    .input1c(subtractor256bit_61_output1c), .input1d(subtractor256bit_61_output1d), .input2a({64{1'b0}}),
    .input2b({input2[61:0], 2'b00}), .input2c({{62{1'b0}}, input2[63:62]}), .input2d({64{1'b0}}),
    .greater1(comparatoru256bit_62_greater1), .equal1(comparatoru256bit_62_equal1));  // open: less1
  subtractor256bit subtractor256bit_63 (
    .input1a(subtractor256bit_62_output1a), .input1b(subtractor256bit_62_output1b),
    .input1c(subtractor256bit_62_output1c), .input1d(subtractor256bit_62_output1d),
    .input2a(cbuffer256bit_63_output1a), .input2b(cbuffer256bit_63_output1b),
    .input2c(cbuffer256bit_63_output1c), .input2d(cbuffer256bit_63_output1d),
    .output1a(subtractor256bit_63_output1a), .output1b(subtractor256bit_63_output1b),
    .output1c(subtractor256bit_63_output1c), .output1d(subtractor256bit_63_output1d));  // open: inborrow, borrow
  cbuffer256bit cbuffer256bit_63 (
    .buffer1(output1[1]), .input1a({64{1'b0}}), .input1b({input2[62:0], 1'b0}),
    .input1c({{63{1'b0}}, input2[63]}), .input1d({64{1'b0}}), .output1a(cbuffer256bit_63_output1a),
    .output1b(cbuffer256bit_63_output1b), .output1c(cbuffer256bit_63_output1c),
    .output1d(cbuffer256bit_63_output1d));
  and and_63 (output1[1], not_1_out, or_63_out);
  comparatoru256bit comparatoru256bit_63 (
    .input1a(subtractor256bit_62_output1a), .input1b(subtractor256bit_62_output1b),
    .input1c(subtractor256bit_62_output1c), .input1d(subtractor256bit_62_output1d), .input2a({64{1'b0}}),
    .input2b({input2[62:0], 1'b0}), .input2c({{63{1'b0}}, input2[63]}), .input2d({64{1'b0}}),
    .greater1(comparatoru256bit_63_greater1), .equal1(comparatoru256bit_63_equal1));  // open: less1
  or or_63 (or_63_out, comparatoru256bit_63_greater1, comparatoru256bit_63_equal1);
  subtractor256bit subtractor256bit_64 (
    .input1a(subtractor256bit_63_output1a), .input1b(subtractor256bit_63_output1b),
    .input1c(subtractor256bit_63_output1c), .input1d(subtractor256bit_63_output1d),
    .input2a(cbuffer256bit_64_output1a), .input2b(cbuffer256bit_64_output1b),
    .input2c(cbuffer256bit_64_output1c), .input2d(cbuffer256bit_64_output1d), .output1a(remainder),
    .output1b(subtractor256bit_64_output1b), .output1c(subtractor256bit_64_output1c),
    .output1d(subtractor256bit_64_output1d));  // open: inborrow, borrow
  cbuffer256bit cbuffer256bit_64 (
    .buffer1(output1[0]), .input1a({64{1'b0}}), .input1b(input2), .input1c({64{1'b0}}), .input1d({64{1'b0}}),
    .output1a(cbuffer256bit_64_output1a), .output1b(cbuffer256bit_64_output1b),
    .output1c(cbuffer256bit_64_output1c), .output1d(cbuffer256bit_64_output1d));
  and and_64 (output1[0], not_1_out, or_64_out);
  or or_64 (or_64_out, comparatoru256bit_64_greater1, comparatoru256bit_64_equal1);
  comparatoru256bit comparatoru256bit_64 (
    .input1a(subtractor256bit_63_output1a), .input1b(subtractor256bit_63_output1b),
    .input1c(subtractor256bit_63_output1c), .input1d(subtractor256bit_63_output1d), .input2a({64{1'b0}}),
    .input2b(input2), .input2c({64{1'b0}}), .input2d({64{1'b0}}), .greater1(comparatoru256bit_64_greater1),
    .equal1(comparatoru256bit_64_equal1));  // open: less1
  // Probe on remainder
  // Probe on remainder
  // Probe on output1
  // Probe on output1
  // Probe on output1
  // Probe on output1

  // Notes on the sheet:
  //   inupper: initial=0xffbbddaa3b5afedc
  //   input2: initial=0xfed14b7a
  //   input1: initial=0xeeddaabb26ebfa3d
endmodule

module cbuffer256bit (
  input  buffer1,
  input  [63:0] input1a,
  input  [63:0] input1b,
  input  [63:0] input1c,
  input  [63:0] input1d,
  output [63:0] output1a,
  output [63:0] output1b,
  output [63:0] output1c,
  output [63:0] output1d
);

  assign output1a = {64{buffer1}} & input1a;  // AND_Gate and_1, 64 bits wide
  assign output1b = {64{buffer1}} & input1b;  // AND_Gate and_2, 64 bits wide
  assign output1c = {64{buffer1}} & input1c;  // AND_Gate and_3, 64 bits wide
  assign output1d = {64{buffer1}} & input1d;  // AND_Gate and_4, 64 bits wide
endmodule

module subtractor256bit (
  input  inborrow,
  input  [63:0] input1a,
  input  [63:0] input1b,
  input  [63:0] input1c,
  input  [63:0] input1d,
  input  [63:0] input2a,
  input  [63:0] input2b,
  input  [63:0] input2c,
  input  [63:0] input2d,
  output borrow,
  output [63:0] output1a,
  output [63:0] output1b,
  output [63:0] output1c,
  output [63:0] output1d
);

  wire subtractor128bit_1_borrow;

  subtractor128bit subtractor128bit_1 (
    .inborrow(inborrow), .input1a(input1a), .input1b(input1b), .input2a(input2a), .input2b(input2b),
    .borrow(subtractor128bit_1_borrow), .output1a(output1a), .output1b(output1b));
  subtractor128bit subtractor128bit_2 (
    .inborrow(subtractor128bit_1_borrow), .input1a(input1c), .input1b(input1d), .input2a(input2c),
    .input2b(input2d), .borrow(borrow), .output1a(output1c), .output1b(output1d));
endmodule

module negate256bit (
  input  [63:0] input1a,
  input  [63:0] input1b,
  output [63:0] output1a,
  output [63:0] output1b
);

  wire [63:0] not_1_out, not_2_out;

  assign not_1_out = ~input1a;  // NOT_Gate not_1, 64 bits wide
  assign not_2_out = ~input1b;  // NOT_Gate not_2, 64 bits wide
endmodule

module adder256bit (
  input  inflow,
  input  [63:0] input1a,
  input  [63:0] input1b,
  input  [63:0] input1c,
  input  [63:0] input1d,
  input  [63:0] input2a,
  input  [63:0] input2b,
  input  [63:0] input2c,
  input  [63:0] input2d,
  output overflow,
  output [63:0] output1a,
  output [63:0] output1b,
  output [63:0] output1c,
  output [63:0] output1d
);

  wire adder128bit_1_overflow;

  adder128bit adder128bit_1 (
    .inflow(inflow), .input1a(input1a), .input1b(input1b), .input2a(input2a), .input2b(input2b),
    .overflow(adder128bit_1_overflow), .output1a(output1a), .output1b(output1b));
  adder128bit adder128bit_2 (
    .inflow(adder128bit_1_overflow), .input1a(input1c), .input1b(input1d), .input2a(input2c),
    .input2b(input2d), .overflow(overflow), .output1a(output1c), .output1b(output1d));
endmodule

module shiftleft64bit (
  input  [63:0] input1,
  input  [7:0] shiftleft1,
  output [63:0] output1
);

  mux6x64bit mux6x64bit_1 (
    .select1(shiftleft1), .input0(input1), .input1({input1[62:0], 1'b0}), .input2({input1[61:0], 2'b00}),
    .input3({input1[60:0], 3'b000}), .input4({input1[59:0], 4'b0000}), .input5({input1[58:0], {5{1'b0}}}),
    .input6({input1[57:0], {6{1'b0}}}), .input7({input1[56:0], {7{1'b0}}}),
    .input8({input1[55:0], {8{1'b0}}}), .input9({input1[54:0], {9{1'b0}}}),
    .input10({input1[53:0], {10{1'b0}}}), .input11({input1[52:0], {11{1'b0}}}),
    .input12({input1[51:0], {12{1'b0}}}), .input13({input1[50:0], {13{1'b0}}}),
    .input14({input1[49:0], {14{1'b0}}}), .input15({input1[48:0], {15{1'b0}}}),
    .input16({input1[47:0], {16{1'b0}}}), .input17({input1[46:0], {17{1'b0}}}),
    .input18({input1[45:0], {18{1'b0}}}), .input19({input1[44:0], {19{1'b0}}}),
    .input20({input1[43:0], {20{1'b0}}}), .input21({input1[42:0], {21{1'b0}}}),
    .input22({input1[41:0], {22{1'b0}}}), .input23({input1[40:0], {23{1'b0}}}),
    .input24({input1[39:0], {24{1'b0}}}), .input25({input1[38:0], {25{1'b0}}}),
    .input26({input1[37:0], {26{1'b0}}}), .input27({input1[36:0], {27{1'b0}}}),
    .input28({input1[35:0], {28{1'b0}}}), .input29({input1[34:0], {29{1'b0}}}),
    .input30({input1[33:0], {30{1'b0}}}), .input31({input1[32:0], {31{1'b0}}}),
    .input32({input1[31:0], {32{1'b0}}}), .input33({input1[30:0], {33{1'b0}}}),
    .input34({input1[29:0], {34{1'b0}}}), .input35({input1[28:0], {35{1'b0}}}),
    .input36({input1[27:0], {36{1'b0}}}), .input37({input1[26:0], {37{1'b0}}}),
    .input38({input1[25:0], {38{1'b0}}}), .input39({input1[24:0], {39{1'b0}}}),
    .input40({input1[23:0], {40{1'b0}}}), .input41({input1[22:0], {41{1'b0}}}),
    .input42({input1[21:0], {42{1'b0}}}), .input43({input1[20:0], {43{1'b0}}}),
    .input44({input1[19:0], {44{1'b0}}}), .input45({input1[18:0], {45{1'b0}}}),
    .input46({input1[17:0], {46{1'b0}}}), .input47({input1[16:0], {47{1'b0}}}),
    .input48({input1[15:0], {48{1'b0}}}), .input49({input1[14:0], {49{1'b0}}}),
    .input50({input1[13:0], {50{1'b0}}}), .input51({input1[12:0], {51{1'b0}}}),
    .input52({input1[11:0], {52{1'b0}}}), .input53({input1[10:0], {53{1'b0}}}),
    .input54({input1[9:0], {54{1'b0}}}), .input55({input1[8:0], {55{1'b0}}}),
    .input56({input1[7:0], {56{1'b0}}}), .input57({input1[6:0], {57{1'b0}}}),
    .input58({input1[5:0], {58{1'b0}}}), .input59({input1[4:0], {59{1'b0}}}),
    .input60({input1[3:0], {60{1'b0}}}), .input61({input1[2:0], {61{1'b0}}}),
    .input62({input1[1:0], {62{1'b0}}}), .input63({input1[0], {63{1'b0}}}), .output1(output1));

  // Notes on the sheet:
  //   shiftleft1: initial=0x30
  //   input1: initial=0xcafebabecafebabe
endmodule

module mux6x64bit (
  input  [7:0] select1,
  input  [63:0] input0,
  input  [63:0] input1,
  input  [63:0] input2,
  input  [63:0] input3,
  input  [63:0] input4,
  input  [63:0] input5,
  input  [63:0] input6,
  input  [63:0] input7,
  input  [63:0] input8,
  input  [63:0] input9,
  input  [63:0] input10,
  input  [63:0] input11,
  input  [63:0] input12,
  input  [63:0] input13,
  input  [63:0] input14,
  input  [63:0] input15,
  input  [63:0] input16,
  input  [63:0] input17,
  input  [63:0] input18,
  input  [63:0] input19,
  input  [63:0] input20,
  input  [63:0] input21,
  input  [63:0] input22,
  input  [63:0] input23,
  input  [63:0] input24,
  input  [63:0] input25,
  input  [63:0] input26,
  input  [63:0] input27,
  input  [63:0] input28,
  input  [63:0] input29,
  input  [63:0] input30,
  input  [63:0] input31,
  input  [63:0] input32,
  input  [63:0] input33,
  input  [63:0] input34,
  input  [63:0] input35,
  input  [63:0] input36,
  input  [63:0] input37,
  input  [63:0] input38,
  input  [63:0] input39,
  input  [63:0] input40,
  input  [63:0] input41,
  input  [63:0] input42,
  input  [63:0] input43,
  input  [63:0] input44,
  input  [63:0] input45,
  input  [63:0] input46,
  input  [63:0] input47,
  input  [63:0] input48,
  input  [63:0] input49,
  input  [63:0] input50,
  input  [63:0] input51,
  input  [63:0] input52,
  input  [63:0] input53,
  input  [63:0] input54,
  input  [63:0] input55,
  input  [63:0] input56,
  input  [63:0] input57,
  input  [63:0] input58,
  input  [63:0] input59,
  input  [63:0] input60,
  input  [63:0] input61,
  input  [63:0] input62,
  input  [63:0] input63,
  output [63:0] output1
);

  wire comparatoru8bit_1_equal1, comparatoru8bit_2_equal1, comparatoru8bit_3_equal1,
       comparatoru8bit_4_equal1, comparatoru8bit_5_equal1, comparatoru8bit_6_equal1,
       comparatoru8bit_7_equal1, comparatoru8bit_8_equal1, comparatoru8bit_9_equal1,
       comparatoru8bit_10_equal1, comparatoru8bit_11_equal1, comparatoru8bit_12_equal1,
       comparatoru8bit_13_equal1, comparatoru8bit_14_equal1, comparatoru8bit_15_equal1,
       comparatoru8bit_16_equal1, comparatoru8bit_17_equal1, comparatoru8bit_18_equal1,
       comparatoru8bit_19_equal1, comparatoru8bit_20_equal1, comparatoru8bit_21_equal1,
       comparatoru8bit_22_equal1, comparatoru8bit_23_equal1, comparatoru8bit_24_equal1,
       comparatoru8bit_25_equal1, comparatoru8bit_26_equal1, comparatoru8bit_27_equal1,
       comparatoru8bit_28_equal1, comparatoru8bit_29_equal1, comparatoru8bit_30_equal1,
       comparatoru8bit_31_equal1, comparatoru8bit_32_equal1, comparatoru8bit_33_equal1,
       comparatoru8bit_34_equal1, comparatoru8bit_35_equal1, comparatoru8bit_36_equal1,
       comparatoru8bit_37_equal1, comparatoru8bit_38_equal1, comparatoru8bit_39_equal1,
       comparatoru8bit_40_equal1, comparatoru8bit_41_equal1, comparatoru8bit_42_equal1,
       comparatoru8bit_43_equal1, comparatoru8bit_44_equal1, comparatoru8bit_45_equal1,
       comparatoru8bit_46_equal1, comparatoru8bit_47_equal1, comparatoru8bit_48_equal1,
       comparatoru8bit_49_equal1, comparatoru8bit_50_equal1, comparatoru8bit_51_equal1,
       comparatoru8bit_52_equal1, comparatoru8bit_53_equal1, comparatoru8bit_54_equal1,
       comparatoru8bit_55_equal1, comparatoru8bit_56_equal1, comparatoru8bit_57_equal1,
       comparatoru8bit_58_equal1, comparatoru8bit_59_equal1, comparatoru8bit_60_equal1,
       comparatoru8bit_61_equal1, comparatoru8bit_62_equal1, comparatoru8bit_63_equal1,
       comparatoru8bit_64_equal1;
  wire [63:0] cbuffer64bit_1_output1, cbuffer64bit_2_output1, cbuffer64bit_3_output1, cbuffer64bit_4_output1,
       cbuffer64bit_5_output1, cbuffer64bit_6_output1, cbuffer64bit_7_output1, cbuffer64bit_8_output1,
       cbuffer64bit_9_output1, cbuffer64bit_10_output1, cbuffer64bit_11_output1, cbuffer64bit_12_output1,
       cbuffer64bit_13_output1, cbuffer64bit_14_output1, cbuffer64bit_15_output1, cbuffer64bit_16_output1,
       cbuffer64bit_17_output1, cbuffer64bit_18_output1, cbuffer64bit_19_output1, cbuffer64bit_20_output1,
       cbuffer64bit_21_output1, cbuffer64bit_22_output1, cbuffer64bit_23_output1, cbuffer64bit_24_output1,
       cbuffer64bit_25_output1, cbuffer64bit_26_output1, cbuffer64bit_27_output1, cbuffer64bit_28_output1,
       cbuffer64bit_29_output1, cbuffer64bit_30_output1, cbuffer64bit_31_output1, cbuffer64bit_32_output1,
       cbuffer64bit_33_output1, cbuffer64bit_34_output1, cbuffer64bit_35_output1, cbuffer64bit_36_output1,
       cbuffer64bit_37_output1, cbuffer64bit_38_output1, cbuffer64bit_39_output1, cbuffer64bit_40_output1,
       cbuffer64bit_41_output1, cbuffer64bit_42_output1, cbuffer64bit_43_output1, cbuffer64bit_44_output1,
       cbuffer64bit_45_output1, cbuffer64bit_46_output1, cbuffer64bit_47_output1, cbuffer64bit_48_output1,
       cbuffer64bit_49_output1, cbuffer64bit_50_output1, cbuffer64bit_51_output1, cbuffer64bit_52_output1,
       cbuffer64bit_53_output1, cbuffer64bit_54_output1, cbuffer64bit_55_output1, cbuffer64bit_56_output1,
       cbuffer64bit_57_output1, cbuffer64bit_58_output1, cbuffer64bit_59_output1, cbuffer64bit_60_output1,
       cbuffer64bit_61_output1, cbuffer64bit_62_output1, cbuffer64bit_63_output1, cbuffer64bit_64_output1;

  comparatoru8bit comparatoru8bit_1 (
    .input1(select1), .input2({8{1'b0}}), .equal1(comparatoru8bit_1_equal1));  // open: greater1, less1
  comparatoru8bit comparatoru8bit_2 (
    .input1(select1), .input2(8'h1), .equal1(comparatoru8bit_2_equal1));  // open: greater1, less1
  comparatoru8bit comparatoru8bit_3 (
    .input1(select1), .input2(8'h2), .equal1(comparatoru8bit_3_equal1));  // open: greater1, less1
  comparatoru8bit comparatoru8bit_4 (
    .input1(select1), .input2(8'h3), .equal1(comparatoru8bit_4_equal1));  // open: greater1, less1
  comparatoru8bit comparatoru8bit_5 (
    .input1(select1), .input2(8'h4), .equal1(comparatoru8bit_5_equal1));  // open: greater1, less1
  comparatoru8bit comparatoru8bit_6 (
    .input1(select1), .input2(8'h5), .equal1(comparatoru8bit_6_equal1));  // open: greater1, less1
  comparatoru8bit comparatoru8bit_7 (
    .input1(select1), .input2(8'h6), .equal1(comparatoru8bit_7_equal1));  // open: greater1, less1
  comparatoru8bit comparatoru8bit_8 (
    .input1(select1), .input2(8'h7), .equal1(comparatoru8bit_8_equal1));  // open: greater1, less1
  comparatoru8bit comparatoru8bit_9 (
    .input1(select1), .input2(8'h8), .equal1(comparatoru8bit_9_equal1));  // open: greater1, less1
  comparatoru8bit comparatoru8bit_10 (
    .input1(select1), .input2(8'h9), .equal1(comparatoru8bit_10_equal1));  // open: greater1, less1
  comparatoru8bit comparatoru8bit_11 (
    .input1(select1), .input2(8'ha), .equal1(comparatoru8bit_11_equal1));  // open: greater1, less1
  comparatoru8bit comparatoru8bit_12 (
    .input1(select1), .input2(8'hb), .equal1(comparatoru8bit_12_equal1));  // open: greater1, less1
  comparatoru8bit comparatoru8bit_13 (
    .input1(select1), .input2(8'hc), .equal1(comparatoru8bit_13_equal1));  // open: greater1, less1
  comparatoru8bit comparatoru8bit_14 (
    .input1(select1), .input2(8'hd), .equal1(comparatoru8bit_14_equal1));  // open: greater1, less1
  comparatoru8bit comparatoru8bit_15 (
    .input1(select1), .input2(8'he), .equal1(comparatoru8bit_15_equal1));  // open: greater1, less1
  comparatoru8bit comparatoru8bit_16 (
    .input1(select1), .input2(8'hf), .equal1(comparatoru8bit_16_equal1));  // open: greater1, less1
  comparatoru8bit comparatoru8bit_17 (
    .input1(select1), .input2(8'h10), .equal1(comparatoru8bit_17_equal1));  // open: greater1, less1
  comparatoru8bit comparatoru8bit_18 (
    .input1(select1), .input2(8'h11), .equal1(comparatoru8bit_18_equal1));  // open: greater1, less1
  comparatoru8bit comparatoru8bit_19 (
    .input1(select1), .input2(8'h12), .equal1(comparatoru8bit_19_equal1));  // open: greater1, less1
  comparatoru8bit comparatoru8bit_20 (
    .input1(select1), .input2(8'h13), .equal1(comparatoru8bit_20_equal1));  // open: greater1, less1
  comparatoru8bit comparatoru8bit_21 (
    .input1(select1), .input2(8'h14), .equal1(comparatoru8bit_21_equal1));  // open: greater1, less1
  comparatoru8bit comparatoru8bit_22 (
    .input1(select1), .input2(8'h15), .equal1(comparatoru8bit_22_equal1));  // open: greater1, less1
  comparatoru8bit comparatoru8bit_23 (
    .input1(select1), .input2(8'h16), .equal1(comparatoru8bit_23_equal1));  // open: greater1, less1
  comparatoru8bit comparatoru8bit_24 (
    .input1(select1), .input2(8'h17), .equal1(comparatoru8bit_24_equal1));  // open: greater1, less1
  comparatoru8bit comparatoru8bit_25 (
    .input1(select1), .input2(8'h18), .equal1(comparatoru8bit_25_equal1));  // open: greater1, less1
  comparatoru8bit comparatoru8bit_26 (
    .input1(select1), .input2(8'h19), .equal1(comparatoru8bit_26_equal1));  // open: greater1, less1
  comparatoru8bit comparatoru8bit_27 (
    .input1(select1), .input2(8'h1a), .equal1(comparatoru8bit_27_equal1));  // open: greater1, less1
  comparatoru8bit comparatoru8bit_28 (
    .input1(select1), .input2(8'h1b), .equal1(comparatoru8bit_28_equal1));  // open: greater1, less1
  comparatoru8bit comparatoru8bit_29 (
    .input1(select1), .input2(8'h1c), .equal1(comparatoru8bit_29_equal1));  // open: greater1, less1
  comparatoru8bit comparatoru8bit_30 (
    .input1(select1), .input2(8'h1d), .equal1(comparatoru8bit_30_equal1));  // open: greater1, less1
  comparatoru8bit comparatoru8bit_31 (
    .input1(select1), .input2(8'h1e), .equal1(comparatoru8bit_31_equal1));  // open: greater1, less1
  comparatoru8bit comparatoru8bit_32 (
    .input1(select1), .input2(8'h1f), .equal1(comparatoru8bit_32_equal1));  // open: greater1, less1
  comparatoru8bit comparatoru8bit_33 (
    .input1(select1), .input2(8'h20), .equal1(comparatoru8bit_33_equal1));  // open: greater1, less1
  comparatoru8bit comparatoru8bit_34 (
    .input1(select1), .input2(8'h21), .equal1(comparatoru8bit_34_equal1));  // open: greater1, less1
  comparatoru8bit comparatoru8bit_35 (
    .input1(select1), .input2(8'h22), .equal1(comparatoru8bit_35_equal1));  // open: greater1, less1
  comparatoru8bit comparatoru8bit_36 (
    .input1(select1), .input2(8'h23), .equal1(comparatoru8bit_36_equal1));  // open: greater1, less1
  comparatoru8bit comparatoru8bit_37 (
    .input1(select1), .input2(8'h24), .equal1(comparatoru8bit_37_equal1));  // open: greater1, less1
  comparatoru8bit comparatoru8bit_38 (
    .input1(select1), .input2(8'h25), .equal1(comparatoru8bit_38_equal1));  // open: greater1, less1
  comparatoru8bit comparatoru8bit_39 (
    .input1(select1), .input2(8'h26), .equal1(comparatoru8bit_39_equal1));  // open: greater1, less1
  comparatoru8bit comparatoru8bit_40 (
    .input1(select1), .input2(8'h27), .equal1(comparatoru8bit_40_equal1));  // open: greater1, less1
  comparatoru8bit comparatoru8bit_41 (
    .input1(select1), .input2(8'h28), .equal1(comparatoru8bit_41_equal1));  // open: greater1, less1
  comparatoru8bit comparatoru8bit_42 (
    .input1(select1), .input2(8'h29), .equal1(comparatoru8bit_42_equal1));  // open: greater1, less1
  comparatoru8bit comparatoru8bit_43 (
    .input1(select1), .input2(8'h2a), .equal1(comparatoru8bit_43_equal1));  // open: greater1, less1
  comparatoru8bit comparatoru8bit_44 (
    .input1(select1), .input2(8'h2b), .equal1(comparatoru8bit_44_equal1));  // open: greater1, less1
  comparatoru8bit comparatoru8bit_45 (
    .input1(select1), .input2(8'h2c), .equal1(comparatoru8bit_45_equal1));  // open: greater1, less1
  comparatoru8bit comparatoru8bit_46 (
    .input1(select1), .input2(8'h2d), .equal1(comparatoru8bit_46_equal1));  // open: greater1, less1
  comparatoru8bit comparatoru8bit_47 (
    .input1(select1), .input2(8'h2e), .equal1(comparatoru8bit_47_equal1));  // open: greater1, less1
  comparatoru8bit comparatoru8bit_48 (
    .input1(select1), .input2(8'h2f), .equal1(comparatoru8bit_48_equal1));  // open: greater1, less1
  comparatoru8bit comparatoru8bit_49 (
    .input1(select1), .input2(8'h30), .equal1(comparatoru8bit_49_equal1));  // open: greater1, less1
  comparatoru8bit comparatoru8bit_50 (
    .input1(select1), .input2(8'h31), .equal1(comparatoru8bit_50_equal1));  // open: greater1, less1
  comparatoru8bit comparatoru8bit_51 (
    .input1(select1), .input2(8'h32), .equal1(comparatoru8bit_51_equal1));  // open: greater1, less1
  comparatoru8bit comparatoru8bit_52 (
    .input1(select1), .input2(8'h33), .equal1(comparatoru8bit_52_equal1));  // open: greater1, less1
  comparatoru8bit comparatoru8bit_53 (
    .input1(select1), .input2(8'h34), .equal1(comparatoru8bit_53_equal1));  // open: greater1, less1
  comparatoru8bit comparatoru8bit_54 (
    .input1(select1), .input2(8'h35), .equal1(comparatoru8bit_54_equal1));  // open: greater1, less1
  comparatoru8bit comparatoru8bit_55 (
    .input1(select1), .input2(8'h36), .equal1(comparatoru8bit_55_equal1));  // open: greater1, less1
  comparatoru8bit comparatoru8bit_56 (
    .input1(select1), .input2(8'h37), .equal1(comparatoru8bit_56_equal1));  // open: greater1, less1
  comparatoru8bit comparatoru8bit_57 (
    .input1(select1), .input2(8'h38), .equal1(comparatoru8bit_57_equal1));  // open: greater1, less1
  comparatoru8bit comparatoru8bit_58 (
    .input1(select1), .input2(8'h39), .equal1(comparatoru8bit_58_equal1));  // open: greater1, less1
  comparatoru8bit comparatoru8bit_59 (
    .input1(select1), .input2(8'h3a), .equal1(comparatoru8bit_59_equal1));  // open: greater1, less1
  comparatoru8bit comparatoru8bit_60 (
    .input1(select1), .input2(8'h3b), .equal1(comparatoru8bit_60_equal1));  // open: greater1, less1
  comparatoru8bit comparatoru8bit_61 (
    .input1(select1), .input2(8'h3c), .equal1(comparatoru8bit_61_equal1));  // open: greater1, less1
  comparatoru8bit comparatoru8bit_62 (
    .input1(select1), .input2(8'h3d), .equal1(comparatoru8bit_62_equal1));  // open: greater1, less1
  comparatoru8bit comparatoru8bit_63 (
    .input1(select1), .input2(8'h3e), .equal1(comparatoru8bit_63_equal1));  // open: greater1, less1
  comparatoru8bit comparatoru8bit_64 (
    .input1(select1), .input2(8'h3f), .equal1(comparatoru8bit_64_equal1));  // open: greater1, less1
  cbuffer64bit cbuffer64bit_1 (.buffer1(comparatoru8bit_1_equal1), .input1(input0), .output1(cbuffer64bit_1_output1));
  cbuffer64bit cbuffer64bit_2 (.buffer1(comparatoru8bit_2_equal1), .input1(input1), .output1(cbuffer64bit_2_output1));
  cbuffer64bit cbuffer64bit_3 (.buffer1(comparatoru8bit_3_equal1), .input1(input2), .output1(cbuffer64bit_3_output1));
  cbuffer64bit cbuffer64bit_4 (.buffer1(comparatoru8bit_4_equal1), .input1(input3), .output1(cbuffer64bit_4_output1));
  cbuffer64bit cbuffer64bit_5 (.buffer1(comparatoru8bit_5_equal1), .input1(input4), .output1(cbuffer64bit_5_output1));
  cbuffer64bit cbuffer64bit_6 (.buffer1(comparatoru8bit_6_equal1), .input1(input5), .output1(cbuffer64bit_6_output1));
  cbuffer64bit cbuffer64bit_7 (.buffer1(comparatoru8bit_7_equal1), .input1(input6), .output1(cbuffer64bit_7_output1));
  cbuffer64bit cbuffer64bit_8 (.buffer1(comparatoru8bit_8_equal1), .input1(input7), .output1(cbuffer64bit_8_output1));
  cbuffer64bit cbuffer64bit_9 (.buffer1(comparatoru8bit_9_equal1), .input1(input8), .output1(cbuffer64bit_9_output1));
  cbuffer64bit cbuffer64bit_10 (
    .buffer1(comparatoru8bit_10_equal1), .input1(input9), .output1(cbuffer64bit_10_output1));
  cbuffer64bit cbuffer64bit_11 (
    .buffer1(comparatoru8bit_11_equal1), .input1(input10), .output1(cbuffer64bit_11_output1));
  cbuffer64bit cbuffer64bit_12 (
    .buffer1(comparatoru8bit_12_equal1), .input1(input11), .output1(cbuffer64bit_12_output1));
  cbuffer64bit cbuffer64bit_13 (
    .buffer1(comparatoru8bit_13_equal1), .input1(input12), .output1(cbuffer64bit_13_output1));
  cbuffer64bit cbuffer64bit_14 (
    .buffer1(comparatoru8bit_14_equal1), .input1(input13), .output1(cbuffer64bit_14_output1));
  cbuffer64bit cbuffer64bit_15 (
    .buffer1(comparatoru8bit_15_equal1), .input1(input14), .output1(cbuffer64bit_15_output1));
  cbuffer64bit cbuffer64bit_16 (
    .buffer1(comparatoru8bit_16_equal1), .input1(input15), .output1(cbuffer64bit_16_output1));
  cbuffer64bit cbuffer64bit_17 (
    .buffer1(comparatoru8bit_17_equal1), .input1(input16), .output1(cbuffer64bit_17_output1));
  cbuffer64bit cbuffer64bit_18 (
    .buffer1(comparatoru8bit_18_equal1), .input1(input17), .output1(cbuffer64bit_18_output1));
  cbuffer64bit cbuffer64bit_19 (
    .buffer1(comparatoru8bit_19_equal1), .input1(input18), .output1(cbuffer64bit_19_output1));
  cbuffer64bit cbuffer64bit_20 (
    .buffer1(comparatoru8bit_20_equal1), .input1(input19), .output1(cbuffer64bit_20_output1));
  cbuffer64bit cbuffer64bit_21 (
    .buffer1(comparatoru8bit_21_equal1), .input1(input20), .output1(cbuffer64bit_21_output1));
  cbuffer64bit cbuffer64bit_22 (
    .buffer1(comparatoru8bit_22_equal1), .input1(input21), .output1(cbuffer64bit_22_output1));
  cbuffer64bit cbuffer64bit_23 (
    .buffer1(comparatoru8bit_23_equal1), .input1(input22), .output1(cbuffer64bit_23_output1));
  cbuffer64bit cbuffer64bit_24 (
    .buffer1(comparatoru8bit_24_equal1), .input1(input23), .output1(cbuffer64bit_24_output1));
  cbuffer64bit cbuffer64bit_25 (
    .buffer1(comparatoru8bit_25_equal1), .input1(input24), .output1(cbuffer64bit_25_output1));
  cbuffer64bit cbuffer64bit_26 (
    .buffer1(comparatoru8bit_26_equal1), .input1(input25), .output1(cbuffer64bit_26_output1));
  cbuffer64bit cbuffer64bit_27 (
    .buffer1(comparatoru8bit_27_equal1), .input1(input26), .output1(cbuffer64bit_27_output1));
  cbuffer64bit cbuffer64bit_28 (
    .buffer1(comparatoru8bit_28_equal1), .input1(input27), .output1(cbuffer64bit_28_output1));
  cbuffer64bit cbuffer64bit_29 (
    .buffer1(comparatoru8bit_29_equal1), .input1(input28), .output1(cbuffer64bit_29_output1));
  cbuffer64bit cbuffer64bit_30 (
    .buffer1(comparatoru8bit_30_equal1), .input1(input29), .output1(cbuffer64bit_30_output1));
  cbuffer64bit cbuffer64bit_31 (
    .buffer1(comparatoru8bit_31_equal1), .input1(input30), .output1(cbuffer64bit_31_output1));
  cbuffer64bit cbuffer64bit_32 (
    .buffer1(comparatoru8bit_32_equal1), .input1(input31), .output1(cbuffer64bit_32_output1));
  cbuffer64bit cbuffer64bit_33 (
    .buffer1(comparatoru8bit_33_equal1), .input1(input32), .output1(cbuffer64bit_33_output1));
  cbuffer64bit cbuffer64bit_34 (
    .buffer1(comparatoru8bit_34_equal1), .input1(input33), .output1(cbuffer64bit_34_output1));
  cbuffer64bit cbuffer64bit_35 (
    .buffer1(comparatoru8bit_35_equal1), .input1(input34), .output1(cbuffer64bit_35_output1));
  cbuffer64bit cbuffer64bit_36 (
    .buffer1(comparatoru8bit_36_equal1), .input1(input35), .output1(cbuffer64bit_36_output1));
  cbuffer64bit cbuffer64bit_37 (
    .buffer1(comparatoru8bit_37_equal1), .input1(input36), .output1(cbuffer64bit_37_output1));
  cbuffer64bit cbuffer64bit_38 (
    .buffer1(comparatoru8bit_38_equal1), .input1(input37), .output1(cbuffer64bit_38_output1));
  cbuffer64bit cbuffer64bit_39 (
    .buffer1(comparatoru8bit_39_equal1), .input1(input38), .output1(cbuffer64bit_39_output1));
  cbuffer64bit cbuffer64bit_40 (
    .buffer1(comparatoru8bit_40_equal1), .input1(input39), .output1(cbuffer64bit_40_output1));
  cbuffer64bit cbuffer64bit_41 (
    .buffer1(comparatoru8bit_41_equal1), .input1(input40), .output1(cbuffer64bit_41_output1));
  cbuffer64bit cbuffer64bit_42 (
    .buffer1(comparatoru8bit_42_equal1), .input1(input41), .output1(cbuffer64bit_42_output1));
  cbuffer64bit cbuffer64bit_43 (
    .buffer1(comparatoru8bit_43_equal1), .input1(input42), .output1(cbuffer64bit_43_output1));
  cbuffer64bit cbuffer64bit_44 (
    .buffer1(comparatoru8bit_44_equal1), .input1(input43), .output1(cbuffer64bit_44_output1));
  cbuffer64bit cbuffer64bit_45 (
    .buffer1(comparatoru8bit_45_equal1), .input1(input44), .output1(cbuffer64bit_45_output1));
  cbuffer64bit cbuffer64bit_46 (
    .buffer1(comparatoru8bit_46_equal1), .input1(input45), .output1(cbuffer64bit_46_output1));
  cbuffer64bit cbuffer64bit_47 (
    .buffer1(comparatoru8bit_47_equal1), .input1(input46), .output1(cbuffer64bit_47_output1));
  cbuffer64bit cbuffer64bit_48 (
    .buffer1(comparatoru8bit_48_equal1), .input1(input47), .output1(cbuffer64bit_48_output1));
  cbuffer64bit cbuffer64bit_49 (
    .buffer1(comparatoru8bit_49_equal1), .input1(input48), .output1(cbuffer64bit_49_output1));
  cbuffer64bit cbuffer64bit_50 (
    .buffer1(comparatoru8bit_50_equal1), .input1(input49), .output1(cbuffer64bit_50_output1));
  cbuffer64bit cbuffer64bit_51 (
    .buffer1(comparatoru8bit_51_equal1), .input1(input50), .output1(cbuffer64bit_51_output1));
  cbuffer64bit cbuffer64bit_52 (
    .buffer1(comparatoru8bit_52_equal1), .input1(input51), .output1(cbuffer64bit_52_output1));
  cbuffer64bit cbuffer64bit_53 (
    .buffer1(comparatoru8bit_53_equal1), .input1(input52), .output1(cbuffer64bit_53_output1));
  cbuffer64bit cbuffer64bit_54 (
    .buffer1(comparatoru8bit_54_equal1), .input1(input53), .output1(cbuffer64bit_54_output1));
  cbuffer64bit cbuffer64bit_55 (
    .buffer1(comparatoru8bit_55_equal1), .input1(input54), .output1(cbuffer64bit_55_output1));
  cbuffer64bit cbuffer64bit_56 (
    .buffer1(comparatoru8bit_56_equal1), .input1(input55), .output1(cbuffer64bit_56_output1));
  cbuffer64bit cbuffer64bit_57 (
    .buffer1(comparatoru8bit_57_equal1), .input1(input56), .output1(cbuffer64bit_57_output1));
  cbuffer64bit cbuffer64bit_58 (
    .buffer1(comparatoru8bit_58_equal1), .input1(input57), .output1(cbuffer64bit_58_output1));
  cbuffer64bit cbuffer64bit_59 (
    .buffer1(comparatoru8bit_59_equal1), .input1(input58), .output1(cbuffer64bit_59_output1));
  cbuffer64bit cbuffer64bit_60 (
    .buffer1(comparatoru8bit_60_equal1), .input1(input59), .output1(cbuffer64bit_60_output1));
  cbuffer64bit cbuffer64bit_61 (
    .buffer1(comparatoru8bit_61_equal1), .input1(input60), .output1(cbuffer64bit_61_output1));
  cbuffer64bit cbuffer64bit_62 (
    .buffer1(comparatoru8bit_62_equal1), .input1(input61), .output1(cbuffer64bit_62_output1));
  cbuffer64bit cbuffer64bit_63 (
    .buffer1(comparatoru8bit_63_equal1), .input1(input62), .output1(cbuffer64bit_63_output1));
  cbuffer64bit cbuffer64bit_64 (
    .buffer1(comparatoru8bit_64_equal1), .input1(input63), .output1(cbuffer64bit_64_output1));
  assign output1 = cbuffer64bit_1_output1 | cbuffer64bit_2_output1 | cbuffer64bit_3_output1 | cbuffer64bit_4_output1 | cbuffer64bit_5_output1 | cbuffer64bit_6_output1 | cbuffer64bit_7_output1 | cbuffer64bit_8_output1 | cbuffer64bit_9_output1 | cbuffer64bit_10_output1 | cbuffer64bit_11_output1 | cbuffer64bit_12_output1 | cbuffer64bit_13_output1 | cbuffer64bit_14_output1 | cbuffer64bit_15_output1 | cbuffer64bit_16_output1 | cbuffer64bit_17_output1 | cbuffer64bit_18_output1 | cbuffer64bit_19_output1 | cbuffer64bit_20_output1 | cbuffer64bit_21_output1 | cbuffer64bit_22_output1 | cbuffer64bit_23_output1 | cbuffer64bit_24_output1 | cbuffer64bit_25_output1 | cbuffer64bit_26_output1 | cbuffer64bit_27_output1 | cbuffer64bit_28_output1 | cbuffer64bit_29_output1 | cbuffer64bit_30_output1 | cbuffer64bit_31_output1 | cbuffer64bit_32_output1 | cbuffer64bit_33_output1 | cbuffer64bit_34_output1 | cbuffer64bit_35_output1 | cbuffer64bit_36_output1 | cbuffer64bit_37_output1 | cbuffer64bit_38_output1 | cbuffer64bit_39_output1 | cbuffer64bit_40_output1 | cbuffer64bit_41_output1 | cbuffer64bit_42_output1 | cbuffer64bit_43_output1 | cbuffer64bit_44_output1 | cbuffer64bit_45_output1 | cbuffer64bit_46_output1 | cbuffer64bit_47_output1 | cbuffer64bit_48_output1 | cbuffer64bit_49_output1 | cbuffer64bit_50_output1 | cbuffer64bit_51_output1 | cbuffer64bit_52_output1 | cbuffer64bit_53_output1 | cbuffer64bit_54_output1 | cbuffer64bit_55_output1 | cbuffer64bit_56_output1 | cbuffer64bit_57_output1 | cbuffer64bit_58_output1 | cbuffer64bit_59_output1 | cbuffer64bit_60_output1 | cbuffer64bit_61_output1 | cbuffer64bit_62_output1 | cbuffer64bit_63_output1 | cbuffer64bit_64_output1;  // OR_Gate or_1, 64 bits wide
endmodule

module shiftright64bit (
  input  [63:0] input1,
  input  [7:0] shiftright1,
  output [63:0] output1
);

  mux6x64bit mux6x64bit_1 (
    .select1(shiftright1), .input0(input1), .input1({1'b0, input1[63:1]}), .input2({2'b00, input1[63:2]}),
    .input3({3'b000, input1[63:3]}), .input4({4'b0000, input1[63:4]}), .input5({{5{1'b0}}, input1[63:5]}),
    .input6({{6{1'b0}}, input1[63:6]}), .input7({{7{1'b0}}, input1[63:7]}),
    .input8({{8{1'b0}}, input1[63:8]}), .input9({{9{1'b0}}, input1[63:9]}),
    .input10({{10{1'b0}}, input1[63:10]}), .input11({{11{1'b0}}, input1[63:11]}),
    .input12({{12{1'b0}}, input1[63:12]}), .input13({{13{1'b0}}, input1[63:13]}),
    .input14({{14{1'b0}}, input1[63:14]}), .input15({{15{1'b0}}, input1[63:15]}),
    .input16({{16{1'b0}}, input1[63:16]}), .input17({{17{1'b0}}, input1[63:17]}),
    .input18({{18{1'b0}}, input1[63:18]}), .input19({{19{1'b0}}, input1[63:19]}),
    .input20({{20{1'b0}}, input1[63:20]}), .input21({{21{1'b0}}, input1[63:21]}),
    .input22({{22{1'b0}}, input1[63:22]}), .input23({{23{1'b0}}, input1[63:23]}),
    .input24({{24{1'b0}}, input1[63:24]}), .input25({{25{1'b0}}, input1[63:25]}),
    .input26({{26{1'b0}}, input1[63:26]}), .input27({{27{1'b0}}, input1[63:27]}),
    .input28({{28{1'b0}}, input1[63:28]}), .input29({{29{1'b0}}, input1[63:29]}),
    .input30({{30{1'b0}}, input1[63:30]}), .input31({{31{1'b0}}, input1[63:31]}),
    .input32({{32{1'b0}}, input1[63:32]}), .input33({{33{1'b0}}, input1[63:33]}),
    .input34({{34{1'b0}}, input1[63:34]}), .input35({{35{1'b0}}, input1[63:35]}),
    .input36({{36{1'b0}}, input1[63:36]}), .input37({{37{1'b0}}, input1[63:37]}),
    .input38({{38{1'b0}}, input1[63:38]}), .input39({{39{1'b0}}, input1[63:39]}),
    .input40({{40{1'b0}}, input1[63:40]}), .input41({{41{1'b0}}, input1[63:41]}),
    .input42({{42{1'b0}}, input1[63:42]}), .input43({{43{1'b0}}, input1[63:43]}),
    .input44({{44{1'b0}}, input1[63:44]}), .input45({{45{1'b0}}, input1[63:45]}),
    .input46({{46{1'b0}}, input1[63:46]}), .input47({{47{1'b0}}, input1[63:47]}),
    .input48({{48{1'b0}}, input1[63:48]}), .input49({{49{1'b0}}, input1[63:49]}),
    .input50({{50{1'b0}}, input1[63:50]}), .input51({{51{1'b0}}, input1[63:51]}),
    .input52({{52{1'b0}}, input1[63:52]}), .input53({{53{1'b0}}, input1[63:53]}),
    .input54({{54{1'b0}}, input1[63:54]}), .input55({{55{1'b0}}, input1[63:55]}),
    .input56({{56{1'b0}}, input1[63:56]}), .input57({{57{1'b0}}, input1[63:57]}),
    .input58({{58{1'b0}}, input1[63:58]}), .input59({{59{1'b0}}, input1[63:59]}),
    .input60({{60{1'b0}}, input1[63:60]}), .input61({{61{1'b0}}, input1[63:61]}),
    .input62({{62{1'b0}}, input1[63:62]}), .input63({{63{1'b0}}, input1[63]}), .output1(output1));

  // Notes on the sheet:
  //   shiftright1: initial=0x30
  //   input1: initial=0xcafebabecafebabe
endmodule

module ashiftright64bit (
  input  [63:0] input1,
  input  [7:0] ashiftright1,
  output [63:0] output1
);

  mux6x64bit mux6x64bit_1 (
    .select1(ashiftright1), .input0(input1), .input1({1'b1, input1[63:1]}), .input2({2'b11, input1[63:2]}),
    .input3({3'b111, input1[63:3]}), .input4({4'b1111, input1[63:4]}), .input5({{5{1'b1}}, input1[63:5]}),
    .input6({{6{1'b1}}, input1[63:6]}), .input7({{7{1'b1}}, input1[63:7]}),
    .input8({{8{1'b1}}, input1[63:8]}), .input9({{9{1'b1}}, input1[63:9]}),
    .input10({{10{1'b1}}, input1[63:10]}), .input11({{11{1'b1}}, input1[63:11]}),
    .input12({{12{1'b1}}, input1[63:12]}), .input13({{13{1'b1}}, input1[63:13]}),
    .input14({{14{1'b1}}, input1[63:14]}), .input15({{15{1'b1}}, input1[63:15]}),
    .input16({{16{1'b1}}, input1[63:16]}), .input17({{17{1'b1}}, input1[63:17]}),
    .input18({{18{1'b1}}, input1[63:18]}), .input19({{19{1'b1}}, input1[63:19]}),
    .input20({{20{1'b1}}, input1[63:20]}), .input21({{21{1'b1}}, input1[63:21]}),
    .input22({{22{1'b1}}, input1[63:22]}), .input23({{23{1'b1}}, input1[63:23]}),
    .input24({{24{1'b1}}, input1[63:24]}), .input25({{25{1'b1}}, input1[63:25]}),
    .input26({{26{1'b1}}, input1[63:26]}), .input27({{27{1'b1}}, input1[63:27]}),
    .input28({{28{1'b1}}, input1[63:28]}), .input29({{29{1'b1}}, input1[63:29]}),
    .input30({{30{1'b1}}, input1[63:30]}), .input31({{31{1'b1}}, input1[63:31]}),
    .input32({{32{1'b1}}, input1[63:32]}), .input33({{33{1'b1}}, input1[63:33]}),
    .input34({{34{1'b1}}, input1[63:34]}), .input35({{35{1'b1}}, input1[63:35]}),
    .input36({{36{1'b1}}, input1[63:36]}), .input37({{37{1'b1}}, input1[63:37]}),
    .input38({{38{1'b1}}, input1[63:38]}), .input39({{39{1'b1}}, input1[63:39]}),
    .input40({{40{1'b1}}, input1[63:40]}), .input41({{41{1'b1}}, input1[63:41]}),
    .input42({{42{1'b1}}, input1[63:42]}), .input43({{43{1'b1}}, input1[63:43]}),
    .input44({{44{1'b1}}, input1[63:44]}), .input45({{45{1'b1}}, input1[63:45]}),
    .input46({{46{1'b1}}, input1[63:46]}), .input47({{47{1'b1}}, input1[63:47]}),
    .input48({{48{1'b1}}, input1[63:48]}), .input49({{49{1'b1}}, input1[63:49]}),
    .input50({{50{1'b1}}, input1[63:50]}), .input51({{51{1'b1}}, input1[63:51]}),
    .input52({{52{1'b1}}, input1[63:52]}), .input53({{53{1'b1}}, input1[63:53]}),
    .input54({{54{1'b1}}, input1[63:54]}), .input55({{55{1'b1}}, input1[63:55]}),
    .input56({{56{1'b1}}, input1[63:56]}), .input57({{57{1'b1}}, input1[63:57]}),
    .input58({{58{1'b1}}, input1[63:58]}), .input59({{59{1'b1}}, input1[63:59]}),
    .input60({{60{1'b1}}, input1[63:60]}), .input61({{61{1'b1}}, input1[63:61]}),
    .input62({{62{1'b1}}, input1[63:62]}), .input63({{63{1'b1}}, input1[63]}), .output1(output1));

  // Notes on the sheet:
  //   ashiftright1: initial=0x30
  //   input1: initial=0xcafebabecafebabe
endmodule

module rotateleft64bit (
  input  [63:0] input1,
  input  [7:0] rotateleft1,
  output [63:0] output1
);

  mux6x64bit mux6x64bit_1 (
    .select1(rotateleft1), .input0(input1), .input1({input1[62:0], input1[63]}),
    .input2({input1[61:0], input1[63:62]}), .input3({input1[60:0], input1[63:61]}),
    .input4({input1[59:0], input1[63:60]}), .input5({input1[58:0], input1[63:59]}),
    .input6({input1[57:0], input1[63:58]}), .input7({input1[56:0], input1[63:57]}),
    .input8({input1[55:0], input1[63:56]}), .input9({input1[54:0], input1[63:55]}),
    .input10({input1[53:0], input1[63:54]}), .input11({input1[52:0], input1[63:53]}),
    .input12({input1[51:0], input1[63:52]}), .input13({input1[50:0], input1[63:51]}),
    .input14({input1[49:0], input1[63:50]}), .input15({input1[48:0], input1[63:49]}),
    .input16({input1[47:0], input1[63:48]}), .input17({input1[46:0], input1[63:47]}),
    .input18({input1[45:0], input1[63:46]}), .input19({input1[44:0], input1[63:45]}),
    .input20({input1[43:0], input1[63:44]}), .input21({input1[42:0], input1[63:43]}),
    .input22({input1[41:0], input1[63:42]}), .input23({input1[40:0], input1[63:41]}),
    .input24({input1[39:0], input1[63:40]}), .input25({input1[38:0], input1[63:39]}),
    .input26({input1[37:0], input1[63:38]}), .input27({input1[36:0], input1[63:37]}),
    .input28({input1[35:0], input1[63:36]}), .input29({input1[34:0], input1[63:35]}),
    .input30({input1[33:0], input1[63:34]}), .input31({input1[32:0], input1[63:33]}),
    .input32({input1[31:0], input1[63:32]}), .input33({input1[30:0], input1[63:31]}),
    .input34({input1[29:0], input1[63:30]}), .input35({input1[28:0], input1[63:29]}),
    .input36({input1[27:0], input1[63:28]}), .input37({input1[26:0], input1[63:27]}),
    .input38({input1[25:0], input1[63:26]}), .input39({input1[24:0], input1[63:25]}),
    .input40({input1[23:0], input1[63:24]}), .input41({input1[22:0], input1[63:23]}),
    .input42({input1[21:0], input1[63:22]}), .input43({input1[20:0], input1[63:21]}),
    .input44({input1[19:0], input1[63:20]}), .input45({input1[18:0], input1[63:19]}),
    .input46({input1[17:0], input1[63:18]}), .input47({input1[16:0], input1[63:17]}),
    .input48({input1[15:0], input1[63:16]}), .input49({input1[14:0], input1[63:15]}),
    .input50({input1[13:0], input1[63:14]}), .input51({input1[12:0], input1[63:13]}),
    .input52({input1[11:0], input1[63:12]}), .input53({input1[10:0], input1[63:11]}),
    .input54({input1[9:0], input1[63:10]}), .input55({input1[8:0], input1[63:9]}),
    .input56({input1[7:0], input1[63:8]}), .input57({input1[6:0], input1[63:7]}),
    .input58({input1[5:0], input1[63:6]}), .input59({input1[4:0], input1[63:5]}),
    .input60({input1[3:0], input1[63:4]}), .input61({input1[2:0], input1[63:3]}),
    .input62({input1[1:0], input1[63:2]}), .input63({input1[0], input1[63:1]}), .output1(output1));

  // Notes on the sheet:
  //   rotateleft1: initial=0x30
  //   input1: initial=0xcafebabecafebabe
endmodule

module rotateright64bit (
  input  [63:0] input1,
  input  [7:0] rotateright1,
  output [63:0] output1
);

  mux6x64bit mux6x64bit_1 (
    .select1(rotateright1), .input0(input1), .input1({input1[0], input1[63:1]}),
    .input2({input1[1:0], input1[63:2]}), .input3({input1[2:0], input1[63:3]}),
    .input4({input1[3:0], input1[63:4]}), .input5({input1[4:0], input1[63:5]}),
    .input6({input1[5:0], input1[63:6]}), .input7({input1[6:0], input1[63:7]}),
    .input8({input1[7:0], input1[63:8]}), .input9({input1[8:0], input1[63:9]}),
    .input10({input1[9:0], input1[63:10]}), .input11({input1[10:0], input1[63:11]}),
    .input12({input1[11:0], input1[63:12]}), .input13({input1[12:0], input1[63:13]}),
    .input14({input1[13:0], input1[63:14]}), .input15({input1[14:0], input1[63:15]}),
    .input16({input1[15:0], input1[63:16]}), .input17({input1[16:0], input1[63:17]}),
    .input18({input1[17:0], input1[63:18]}), .input19({input1[18:0], input1[63:19]}),
    .input20({input1[19:0], input1[63:20]}), .input21({input1[20:0], input1[63:21]}),
    .input22({input1[21:0], input1[63:22]}), .input23({input1[22:0], input1[63:23]}),
    .input24({input1[23:0], input1[63:24]}), .input25({input1[24:0], input1[63:25]}),
    .input26({input1[25:0], input1[63:26]}), .input27({input1[26:0], input1[63:27]}),
    .input28({input1[27:0], input1[63:28]}), .input29({input1[28:0], input1[63:29]}),
    .input30({input1[29:0], input1[63:30]}), .input31({input1[30:0], input1[63:31]}),
    .input32({input1[31:0], input1[63:32]}), .input33({input1[32:0], input1[63:33]}),
    .input34({input1[33:0], input1[63:34]}), .input35({input1[34:0], input1[63:35]}),
    .input36({input1[35:0], input1[63:36]}), .input37({input1[36:0], input1[63:37]}),
    .input38({input1[37:0], input1[63:38]}), .input39({input1[38:0], input1[63:39]}),
    .input40({input1[39:0], input1[63:40]}), .input41({input1[40:0], input1[63:41]}),
    .input42({input1[41:0], input1[63:42]}), .input43({input1[42:0], input1[63:43]}),
    .input44({input1[43:0], input1[63:44]}), .input45({input1[44:0], input1[63:45]}),
    .input46({input1[45:0], input1[63:46]}), .input47({input1[46:0], input1[63:47]}),
    .input48({input1[47:0], input1[63:48]}), .input49({input1[48:0], input1[63:49]}),
    .input50({input1[49:0], input1[63:50]}), .input51({input1[50:0], input1[63:51]}),
    .input52({input1[51:0], input1[63:52]}), .input53({input1[52:0], input1[63:53]}),
    .input54({input1[53:0], input1[63:54]}), .input55({input1[54:0], input1[63:55]}),
    .input56({input1[55:0], input1[63:56]}), .input57({input1[56:0], input1[63:57]}),
    .input58({input1[57:0], input1[63:58]}), .input59({input1[58:0], input1[63:59]}),
    .input60({input1[59:0], input1[63:60]}), .input61({input1[60:0], input1[63:61]}),
    .input62({input1[61:0], input1[63:62]}), .input63({input1[62:0], input1[63]}), .output1(output1));

  // Notes on the sheet:
  //   rotateright1: initial=0x30
  //   input1: initial=0xcafebabecafebabe
endmodule
