// Logisim project fpcomp.circ as structural Verilog
module fneg64 (
  input  [63:0] inval1,
  output [63:0] outval1,
  output isnan1
);

  wire fpnegator_1_p2;

  // Probe on inval1
  // FPNegator #(.fpwidth(64)) fpnegator_1: pin names not known; wires that end beside it: inval1, fpnegator_1_p2
  not not_1 (outval1[63], inval1[63]);
  Comparator #(.width(11)) comparator_1 (.a(inval1[62:52]), .b({11{1'b1}}), .eq(isnan1));  // open: gt, lt
  // Probe on fpnegator_1_p2
  // Probe on {outval1[63], inval1[62:0]}

  assign outval1[62:0] = inval1[62:0];

  // Notes on the sheet:
  //   inval1: initial=0x4040152bd3c36113
endmodule

module fadd64 (
  input  [63:0] in_1,
  input  [63:0] in_2,
  input  [63:0] in_3,
  input  [63:0] inval1,
  input  [63:0] inval2,
  output [63:0] outval1,
  output isnan1
);

  wire comparator_1_eq, comparator_2_eq, comparator_3_gt, subtractor_1_bout;
  wire [5:0] hone64_1_outval1, multiplexer_3_out, subtractor_4_out, subtractor_5_out;
  wire [10:0] bit_extender_3_out, multiplexer_7_out;
  wire [15:0] bit_extender_1_out, bit_extender_2_out, negator_1_out, subtractor_1_out, subtractor_2_out,
       subtractor_3_out;
  wire [15:6] multiplexer_3_out_2;
  wire [63:0] adder_1_out, adder_2_out, fpadder_1_out, multiplexer_1_out, multiplexer_2_out,
       multiplexer_4_out, multiplexer_5_out, multiplexer_6_out, multiplexer_8_out, multiplexer_9_out,
       multiplexer_10_out, multiplexer_11_out, negator_2_out, negator_3_out, negator_4_out, shifter_1_out,
       shifter_2_out;

  // Probe on inval1
  // Probe on inval2
  Comparator #(.width(11)) comparator_1 (.a(inval1[62:52]), .b({11{1'b1}}), .eq(comparator_1_eq));  // open: gt, lt
  Comparator #(.width(11)) comparator_2 (.a(inval2[62:52]), .b({11{1'b1}}), .eq(comparator_2_eq));  // open: gt, lt
  Multiplexer #(.width(64)) multiplexer_1 (
    .in0({3'b001, inval1[51:0], {9{1'b0}}}), .in1({3'b001, inval2[51:0], {9{1'b0}}}),
    .out(multiplexer_1_out), .sel(subtractor_1_bout));
  Multiplexer #(.width(64)) multiplexer_2 (
    .in0({3'b001, inval2[51:0], {9{1'b0}}}), .in1({3'b001, inval1[51:0], {9{1'b0}}}),
    .out(multiplexer_2_out), .sel(subtractor_1_bout));
  Subtractor #(.width(16)) subtractor_1 (
    .a(subtractor_2_out), .b(subtractor_3_out), .out(subtractor_1_out), .bout(subtractor_1_bout));  // open: bin
  Subtractor #(.width(16)) subtractor_2 (
    .a(bit_extender_1_out), .b(16'h3ff), .out(subtractor_2_out));  // open: bin, bout
  assign bit_extender_1_out = {{5{1'b0}}, inval1[62:52]};  // Bit_Extender bit_extender_1
  or or_1 (isnan1, comparator_1_eq, comparator_2_eq);
  FPAdder #(.fpwidth(64)) fpadder_1 (.a(inval1), .b(inval2), .out(fpadder_1_out));
  Shifter #(.shift("lr"), .width(64)) shifter_1 (
    .in(multiplexer_2_out), .\dist (multiplexer_3_out), .out(shifter_1_out));
  Multiplexer #(.width(16)) multiplexer_3 (
    .in0(subtractor_1_out), .in1(negator_1_out), .out({multiplexer_3_out_2, multiplexer_3_out}),
    .sel(subtractor_1_bout));
  Negator #(.width(16)) negator_1 (.in(subtractor_1_out), .out(negator_1_out));
  Subtractor #(.width(16)) subtractor_3 (
    .a(bit_extender_2_out), .b(16'h3ff), .out(subtractor_3_out));  // open: bin, bout
  assign bit_extender_2_out = {{5{1'b0}}, inval2[62:52]};  // Bit_Extender bit_extender_2
  Comparator #(.width(16)) comparator_3 (
    .a({multiplexer_3_out_2, multiplexer_3_out}), .b(16'h3f), .gt(comparator_3_gt));  // open: eq, lt
  Multiplexer #(.width(64)) multiplexer_4 (
    .in0(shifter_1_out), .in1({64{1'b0}}), .out(multiplexer_4_out), .sel(comparator_3_gt));
  Multiplexer #(.width(64)) multiplexer_5 (
    .in0(multiplexer_1_out), .in1(multiplexer_4_out), .out(multiplexer_5_out), .sel(subtractor_1_bout));
  Multiplexer #(.width(64)) multiplexer_6 (
    .in0(multiplexer_4_out), .in1(multiplexer_1_out), .out(multiplexer_6_out), .sel(subtractor_1_bout));
  Multiplexer #(.width(11)) multiplexer_7 (
    .in0(inval1[62:52]), .in1(inval2[62:52]), .out(multiplexer_7_out), .sel(subtractor_1_bout));
  Negator #(.width(64)) negator_2 (.in(multiplexer_6_out), .out(negator_2_out));
  Negator #(.width(64)) negator_3 (.in(multiplexer_5_out), .out(negator_3_out));
  Multiplexer #(.width(64)) multiplexer_8 (
    .in0(multiplexer_6_out), .in1(negator_2_out), .out(multiplexer_8_out), .sel(inval2[63]));
  Multiplexer #(.width(64)) multiplexer_9 (
    .in0(multiplexer_5_out), .in1(negator_3_out), .out(multiplexer_9_out), .sel(inval1[63]));
  Adder #(.width(64)) adder_1 (.a(multiplexer_9_out), .b(multiplexer_8_out), .out(adder_1_out));  // open: cin, cout
  Negator #(.width(64)) negator_4 (.in(adder_1_out), .out(negator_4_out));
  Comparator #(.width(64)) comparator_4 (.a(adder_1_out), .b({64{1'b0}}), .lt(outval1[63]));  // open: gt, eq
  Multiplexer #(.width(64)) multiplexer_10 (
    .in0(adder_1_out), .in1(negator_4_out), .out(multiplexer_10_out), .sel(outval1[63]));
  Shifter #(.width(64)) shifter_2 (.in(multiplexer_10_out), .\dist (subtractor_4_out), .out(shifter_2_out));
  Subtractor #(.width(6)) subtractor_4 (
    .a({6{1'b1}}), .b(hone64_1_outval1), .out(subtractor_4_out));  // open: bin, bout
  Subtractor #(.width(6)) subtractor_5 (
    .a(subtractor_4_out), .b(6'b000010), .out(subtractor_5_out));  // open: bin, bout
  hone64 hone64_1 (.inval1(multiplexer_10_out), .outval1(hone64_1_outval1));  // open: contains1
  assign bit_extender_3_out = {{5{subtractor_5_out[5]}}, subtractor_5_out};  // Bit_Extender bit_extender_3
  Subtractor #(.width(11)) subtractor_6 (
    .a(multiplexer_7_out), .b(bit_extender_3_out), .out(outval1[62:52]));  // open: bin, bout
  Multiplexer #(.width(64)) multiplexer_11 (
    .in0(shifter_2_out), .in1(adder_2_out),
    .out({multiplexer_11_out[63], outval1[51:0], multiplexer_11_out[10:0]}), .sel(shifter_2_out[10]));
  Adder #(.width(64)) adder_2 (.a(64'h800), .b(shifter_2_out), .out(adder_2_out));  // open: cin, cout
  // Probe on fpadder_1_out
  // Probe on fpadder_1_out
  // Probe on outval1

  // Notes on the sheet:
  //   in_1: initial=0x4040152bd3c36113
  //   in_2: initial=0x4061d93f7ced9168
  //   in_3: initial=0xc056ef0d844d013b
  //   inval1: initial=0x4040152bd3c36113
  //   inval2: initial=0x4061d93f7ced9168
endmodule

module fsub64 (
  input  [63:0] inval1,
  input  [63:0] inval2,
  output [63:0] outval1
);
endmodule

module fmul64 (
  input  [63:0] inval1,
  input  [63:0] inval2,
  output [63:0] outval1
);
endmodule

module fdiv64 (
  input  [63:0] inval1,
  input  [63:0] inval2,
  output [63:0] outval1
);
endmodule

module hone64 (
  input  [63:0] inval1,
  output [5:0] outval1,
  output contains1
);

  wire bitfinder_1_found, not_1_out;
  wire [5:0] bitfinder_1_index, priority_encoder_1_out;

  // Probe on priority_encoder_1_out
  Priority_Encoder #(.select(6)) priority_encoder_1 (
    .in0(inval1[0]), .in1(inval1[1]), .in2(inval1[2]), .in3(inval1[3]), .in4(inval1[4]), .in5(inval1[5]),
    .in6(inval1[6]), .in7(inval1[7]), .in8(inval1[8]), .in9(inval1[9]), .in10(inval1[10]), .in11(inval1[11]),
    .in12(inval1[12]), .in13(inval1[13]), .in14(inval1[14]), .in15(inval1[15]), .in16(inval1[16]),
    .in17(inval1[17]), .in18(inval1[18]), .in19(inval1[19]), .in20(inval1[20]), .in21(inval1[21]),
    .in22(inval1[22]), .in23(inval1[23]), .in24(inval1[24]), .in25(inval1[25]), .in26(inval1[26]),
    .in27(inval1[27]), .in28(inval1[28]), .in29(inval1[29]), .in30(inval1[30]), .in31(inval1[31]),
    .in32(inval1[32]), .in33(inval1[33]), .in34(inval1[34]), .in35(inval1[35]), .in36(inval1[36]),
    .in37(inval1[37]), .in38(inval1[38]), .in39(inval1[39]), .in40(inval1[40]), .in41(inval1[41]),
    .in42(inval1[42]), .in43(inval1[43]), .in44(inval1[44]), .in45(inval1[45]), .in46(inval1[46]),
    .in47(inval1[47]), .in48(inval1[48]), .in49(inval1[49]), .in50(inval1[50]), .in51(inval1[51]),
    .in52(inval1[52]), .in53(inval1[53]), .in54(inval1[54]), .in55(inval1[55]), .in56(inval1[56]),
    .in57(inval1[57]), .in58(inval1[58]), .in59(inval1[59]), .in60(inval1[60]), .in61(inval1[61]),
    .in62(inval1[62]), .in63(inval1[63]), .out(priority_encoder_1_out), .gs(contains1));  // open: en_out, en_in
  BitFinder #(.\type ("high1"), .width(64)) bitfinder_1 (
    .in(inval1), .index(bitfinder_1_index), .found(bitfinder_1_found));
  Multiplexer #(.width(6)) multiplexer_1 (
    .in0(priority_encoder_1_out), .in1({6{1'b0}}), .out(outval1), .sel(not_1_out));
  not not_1 (not_1_out, contains1);
  // Probe on bitfinder_1_index
  // Probe on bitfinder_1_found
  // Probe on outval1

  // Notes on the sheet:
  //   inval1: initial=0xb000000003ff
endmodule

module add128 (
  input  [63:0] inval1a,
  input  [63:0] inval1b,
  input  [63:0] inval2a,
  input  [63:0] inval2b,
  input  carryin1,
  output [63:0] outval1a,
  output [63:0] outval1b,
  output carryout1
);

  wire adder_1_cout;

  Adder #(.width(64)) adder_1 (.a(inval1a), .b(inval2a), .out(outval1a), .cin(carryin1), .cout(adder_1_cout));
  Adder #(.width(64)) adder_2 (.a(inval1b), .b(inval2b), .out(outval1b), .cin(adder_1_cout), .cout(carryout1));

  // Notes on the sheet:
  //   inval1a: initial=0xf000b000000003ff
  //   inval1b: initial=0xfff0000bff
  //   inval2a: initial=0x8321000000001234
  //   inval2b: initial=0xb0000a4b2
endmodule

module neg128 (
  input  [63:0] inval1a,
  input  [63:0] inval1b,
  output [63:0] outval1a,
  output [63:0] outval1b
);

  wire adder_1_cout;
  wire [63:0] not_1_out, not_2_out;

  assign not_1_out = ~inval1a;  // NOT_Gate not_1, 64 bits wide
  assign not_2_out = ~inval1b;  // NOT_Gate not_2, 64 bits wide
  Adder #(.width(64)) adder_1 (.a(not_1_out), .b(64'h1), .out(outval1a), .cout(adder_1_cout));  // open: cin
  Adder #(.width(64)) adder_2 (.a(not_2_out), .b({64{1'b0}}), .out(outval1b), .cin(adder_1_cout));  // open: cout

  // Notes on the sheet:
  //   inval1a: initial=0x8000000000000000
  //   inval1b: initial=0xb000000003ff
endmodule

module shl128 (
  input  [63:0] inval1a,
  input  [63:0] inval1b,
  input  [6:0] shift1a,
  output [63:0] outval1a,
  output [63:0] outval1b
);

  wire [63:0] and_1_out, and_2_out, not_1_out, or_1_out, shifter_1_out, shifter_2_out, shifter_3_out,
       shifter_4_out;

  Shifter #(.width(64)) shifter_1 (.in({64{1'b1}}), .\dist (shift1a[5:0]), .out(shifter_1_out));
  Shifter #(.shift("rl"), .width(64)) shifter_2 (.in(inval1a), .\dist (shift1a[5:0]), .out(shifter_2_out));
  Shifter #(.width(64)) shifter_3 (.in(inval1b), .\dist (shift1a[5:0]), .out(shifter_3_out));
  Shifter #(.width(64)) shifter_4 (.in(inval1a), .\dist (shift1a[5:0]), .out(shifter_4_out));
  assign not_1_out = ~shifter_1_out;  // NOT_Gate not_1, 64 bits wide
  assign and_1_out = not_1_out & shifter_2_out;  // AND_Gate and_1, 64 bits wide
  assign and_2_out = shifter_1_out & shifter_2_out;  // AND_Gate and_2, 64 bits wide
  assign or_1_out = and_1_out | shifter_3_out;  // OR_Gate or_1, 64 bits wide
  Multiplexer #(.width(64)) multiplexer_1 (.in0(and_2_out), .in1({64{1'b0}}), .out(outval1a), .sel(shift1a[6]));
  Multiplexer #(.width(64)) multiplexer_2 (.in0(or_1_out), .in1(shifter_4_out), .out(outval1b), .sel(shift1a[6]));

  // Notes on the sheet:
  //   inval1a: initial=0xffff000000000000
  //   inval1b: initial=0xf00000000fff
  //   shift1a: initial=0x10
endmodule

module shr128 (
  input  [63:0] inval1a,
  input  [63:0] inval1b,
  input  [6:0] shift1a,
  output [63:0] outval1a,
  output [63:0] outval1b
);

  wire [63:0] and_1_out, and_2_out, not_1_out, or_1_out, shifter_1_out, shifter_2_out, shifter_3_out,
       shifter_4_out;

  Shifter #(.shift("lr"), .width(64)) shifter_1 (.in(inval1b), .\dist (shift1a[5:0]), .out(shifter_1_out));
  Shifter #(.shift("lr"), .width(64)) shifter_2 (.in(inval1a), .\dist (shift1a[5:0]), .out(shifter_2_out));
  Shifter #(.shift("lr"), .width(64)) shifter_3 (.in({64{1'b1}}), .\dist (shift1a[5:0]), .out(shifter_3_out));
  Shifter #(.shift("rr"), .width(64)) shifter_4 (.in(inval1b), .\dist (shift1a[5:0]), .out(shifter_4_out));
  assign not_1_out = ~shifter_3_out;  // NOT_Gate not_1, 64 bits wide
  assign and_1_out = not_1_out & shifter_4_out;  // AND_Gate and_1, 64 bits wide
  assign and_2_out = shifter_3_out & shifter_4_out;  // AND_Gate and_2, 64 bits wide
  assign or_1_out = shifter_2_out | and_1_out;  // OR_Gate or_1, 64 bits wide
  Multiplexer #(.width(64)) multiplexer_1 (.in0(or_1_out), .in1(shifter_1_out), .out(outval1a), .sel(shift1a[6]));
  Multiplexer #(.width(64)) multiplexer_2 (.in0(and_2_out), .in1({64{1'b0}}), .out(outval1b), .sel(shift1a[6]));

  // Notes on the sheet:
  //   inval1a: initial=0xffff000000000000
  //   inval1b: initial=0xf00000000fff
  //   shift1a: initial=0x10
endmodule

module lone64 (
  input  [63:0] inval1,
  output [5:0] outval1,
  output contains1
);

  wire bitfinder_1_found, not_1_out;
  wire [5:0] bitfinder_1_index, priority_encoder_1_p1, subtractor_1_out;

  BitFinder #(.width(64)) bitfinder_1 (.in(inval1), .index(bitfinder_1_index), .found(bitfinder_1_found));
  // Probe on priority_encoder_1_p1
  // Priority_Encoder #(.select(6)) priority_encoder_1: pin names not known; wires that end beside it: priority_encoder_1_p1, contains1
  Subtractor #(.width(6)) subtractor_1 (
    .a({6{1'b1}}), .b(priority_encoder_1_p1), .out(subtractor_1_out));  // open: bin, bout
  Multiplexer #(.width(6)) multiplexer_1 (.in0(subtractor_1_out), .in1({6{1'b0}}), .out(outval1), .sel(not_1_out));
  not not_1 (not_1_out, contains1);
  // Probe on bitfinder_1_index
  // Probe on bitfinder_1_found
  // Probe on outval1

  // Notes on the sheet:
  //   inval1: initial=0xb0000003ff80
endmodule

module hzero64 (
  input  [63:0] inval1,
  output [5:0] outval1,
  output contains1
);

  wire bitfinder_1_found, not_2_out;
  wire [5:0] bitfinder_1_index, priority_encoder_1_out;
  wire [63:0] not_1_out;

  assign not_1_out = ~inval1;  // NOT_Gate not_1, 64 bits wide
  // Probe on priority_encoder_1_out
  Priority_Encoder #(.select(6)) priority_encoder_1 (
    .in0(not_1_out[0]), .in1(not_1_out[1]), .in2(not_1_out[2]), .in3(not_1_out[3]), .in4(not_1_out[4]),
    .in5(not_1_out[5]), .in6(not_1_out[6]), .in7(not_1_out[7]), .in8(not_1_out[8]), .in9(not_1_out[9]),
    .in10(not_1_out[10]), .in11(not_1_out[11]), .in12(not_1_out[12]), .in13(not_1_out[13]),
    .in14(not_1_out[14]), .in15(not_1_out[15]), .in16(not_1_out[16]), .in17(not_1_out[17]),
    .in18(not_1_out[18]), .in19(not_1_out[19]), .in20(not_1_out[20]), .in21(not_1_out[21]),
    .in22(not_1_out[22]), .in23(not_1_out[23]), .in24(not_1_out[24]), .in25(not_1_out[25]),
    .in26(not_1_out[26]), .in27(not_1_out[27]), .in28(not_1_out[28]), .in29(not_1_out[29]),
    .in30(not_1_out[30]), .in31(not_1_out[31]), .in32(not_1_out[32]), .in33(not_1_out[33]),
    .in34(not_1_out[34]), .in35(not_1_out[35]), .in36(not_1_out[36]), .in37(not_1_out[37]),
    .in38(not_1_out[38]), .in39(not_1_out[39]), .in40(not_1_out[40]), .in41(not_1_out[41]),
    .in42(not_1_out[42]), .in43(not_1_out[43]), .in44(not_1_out[44]), .in45(not_1_out[45]),
    .in46(not_1_out[46]), .in47(not_1_out[47]), .in48(not_1_out[48]), .in49(not_1_out[49]),
    .in50(not_1_out[50]), .in51(not_1_out[51]), .in52(not_1_out[52]), .in53(not_1_out[53]),
    .in54(not_1_out[54]), .in55(not_1_out[55]), .in56(not_1_out[56]), .in57(not_1_out[57]),
    .in58(not_1_out[58]), .in59(not_1_out[59]), .in60(not_1_out[60]), .in61(not_1_out[61]),
    .in62(not_1_out[62]), .in63(not_1_out[63]), .out(priority_encoder_1_out), .gs(contains1));  // open: en_out, en_in
  BitFinder #(.\type ("high0"), .width(64)) bitfinder_1 (
    .in(inval1), .index(bitfinder_1_index), .found(bitfinder_1_found));
  Multiplexer #(.width(6)) multiplexer_1 (
    .in0(priority_encoder_1_out), .in1({6{1'b0}}), .out(outval1), .sel(not_2_out));
  not not_2 (not_2_out, contains1);
  // Probe on bitfinder_1_index
  // Probe on bitfinder_1_found
  // Probe on outval1

  // Notes on the sheet:
  //   inval1: initial=0xffffb000003fffff
endmodule

module lzero64 (
  input  [63:0] inval1,
  output [5:0] outval1,
  output contains1
);

  wire bitfinder_1_found, not_2_out;
  wire [5:0] bitfinder_1_index, priority_encoder_1_p1, subtractor_1_out;
  wire [63:0] not_1_out;

  assign not_1_out = ~inval1;  // NOT_Gate not_1, 64 bits wide
  BitFinder #(.\type ("low0"), .width(64)) bitfinder_1 (
    .in(inval1), .index(bitfinder_1_index), .found(bitfinder_1_found));
  // Probe on priority_encoder_1_p1
  // Priority_Encoder #(.select(6)) priority_encoder_1: pin names not known; wires that end beside it: priority_encoder_1_p1, contains1
  Subtractor #(.width(6)) subtractor_1 (
    .a({6{1'b1}}), .b(priority_encoder_1_p1), .out(subtractor_1_out));  // open: bin, bout
  Multiplexer #(.width(6)) multiplexer_1 (.in0(subtractor_1_out), .in1({6{1'b0}}), .out(outval1), .sel(not_2_out));
  not not_2 (not_2_out, contains1);
  // Probe on bitfinder_1_index
  // Probe on bitfinder_1_found
  // Probe on outval1

  // Notes on the sheet:
  //   inval1: initial=0xffffb0000003ffff
endmodule

module ones64 (
  input  [63:0] inval1,
  output [6:0] outval1
);

  wire [1:0] adder_1_out, adder_2_out, adder_3_out, adder_4_out, adder_5_out, adder_6_out, adder_7_out,
       adder_8_out, adder_9_out, adder_10_out, adder_11_out, adder_12_out, adder_13_out, adder_14_out,
       adder_15_out, adder_16_out, adder_17_out, adder_18_out, adder_19_out, adder_20_out, adder_21_out,
       adder_22_out, adder_23_out, adder_24_out, adder_25_out, adder_26_out, adder_27_out, adder_28_out,
       adder_29_out, adder_30_out, adder_31_out, adder_32_out, bit_extender_1_out, bit_extender_2_out,
       bit_extender_3_out, bit_extender_4_out, bit_extender_5_out, bit_extender_6_out, bit_extender_7_out,
       bit_extender_8_out, bit_extender_9_out, bit_extender_10_out, bit_extender_11_out, bit_extender_12_out,
       bit_extender_13_out, bit_extender_14_out, bit_extender_15_out, bit_extender_16_out,
       bit_extender_17_out, bit_extender_18_out, bit_extender_19_out, bit_extender_20_out,
       bit_extender_21_out, bit_extender_22_out, bit_extender_23_out, bit_extender_24_out,
       bit_extender_25_out, bit_extender_26_out, bit_extender_27_out, bit_extender_28_out,
       bit_extender_29_out, bit_extender_30_out, bit_extender_31_out, bit_extender_32_out,
       bit_extender_33_out, bit_extender_34_out, bit_extender_35_out, bit_extender_36_out,
       bit_extender_37_out, bit_extender_38_out, bit_extender_39_out, bit_extender_40_out,
       bit_extender_41_out, bit_extender_42_out, bit_extender_43_out, bit_extender_44_out,
       bit_extender_45_out, bit_extender_46_out, bit_extender_47_out, bit_extender_48_out,
       bit_extender_49_out, bit_extender_50_out, bit_extender_51_out, bit_extender_52_out,
       bit_extender_53_out, bit_extender_54_out, bit_extender_55_out, bit_extender_56_out,
       bit_extender_57_out, bit_extender_58_out, bit_extender_59_out, bit_extender_60_out,
       bit_extender_61_out, bit_extender_62_out, bit_extender_63_out, bit_extender_64_out;
  wire [2:0] adder_33_out, adder_34_out, adder_35_out, adder_36_out, adder_37_out, adder_38_out,
       adder_39_out, adder_40_out, adder_41_out, adder_42_out, adder_43_out, adder_44_out, adder_45_out,
       adder_46_out, adder_47_out, adder_48_out, bit_extender_65_out, bit_extender_66_out,
       bit_extender_67_out, bit_extender_68_out, bit_extender_69_out, bit_extender_70_out,
       bit_extender_71_out, bit_extender_72_out, bit_extender_73_out, bit_extender_74_out,
       bit_extender_75_out, bit_extender_76_out, bit_extender_77_out, bit_extender_78_out,
       bit_extender_79_out, bit_extender_80_out, bit_extender_81_out, bit_extender_82_out,
       bit_extender_83_out, bit_extender_84_out, bit_extender_85_out, bit_extender_86_out,
       bit_extender_87_out, bit_extender_88_out, bit_extender_89_out, bit_extender_90_out,
       bit_extender_91_out, bit_extender_92_out, bit_extender_93_out, bit_extender_94_out,
       bit_extender_95_out, bit_extender_96_out;
  wire [3:0] adder_49_out, adder_50_out, adder_51_out, adder_52_out, adder_53_out, adder_54_out,
       adder_55_out, adder_56_out, bit_extender_97_out, bit_extender_98_out, bit_extender_99_out,
       bit_extender_100_out, bit_extender_101_out, bit_extender_102_out, bit_extender_103_out,
       bit_extender_104_out, bit_extender_105_out, bit_extender_106_out, bit_extender_107_out,
       bit_extender_108_out, bit_extender_109_out, bit_extender_110_out, bit_extender_111_out,
       bit_extender_112_out;
  wire [4:0] adder_57_out, adder_58_out, adder_59_out, adder_60_out, bit_extender_113_out,
       bit_extender_114_out, bit_extender_115_out, bit_extender_116_out, bit_extender_117_out,
       bit_extender_118_out, bit_extender_119_out, bit_extender_120_out;
  wire [5:0] adder_61_out, adder_62_out, bit_extender_121_out, bit_extender_122_out, bit_extender_123_out,
       bit_extender_124_out;
  wire [6:0] bit_extender_125_out, bit_extender_126_out, bitadder_1_out;

  BitAdder #(.width(64)) bitadder_1 (.in0(inval1), .out(bitadder_1_out));
  assign bit_extender_1_out = {{1{1'b0}}, inval1[0]};  // Bit_Extender bit_extender_1
  assign bit_extender_2_out = {{1{1'b0}}, inval1[1]};  // Bit_Extender bit_extender_2
  assign bit_extender_3_out = {{1{1'b0}}, inval1[2]};  // Bit_Extender bit_extender_3
  assign bit_extender_4_out = {{1{1'b0}}, inval1[3]};  // Bit_Extender bit_extender_4
  assign bit_extender_5_out = {{1{1'b0}}, inval1[4]};  // Bit_Extender bit_extender_5
  assign bit_extender_6_out = {{1{1'b0}}, inval1[5]};  // Bit_Extender bit_extender_6
  assign bit_extender_7_out = {{1{1'b0}}, inval1[6]};  // Bit_Extender bit_extender_7
  assign bit_extender_8_out = {{1{1'b0}}, inval1[7]};  // Bit_Extender bit_extender_8
  assign bit_extender_9_out = {{1{1'b0}}, inval1[8]};  // Bit_Extender bit_extender_9
  assign bit_extender_10_out = {{1{1'b0}}, inval1[9]};  // Bit_Extender bit_extender_10
  assign bit_extender_11_out = {{1{1'b0}}, inval1[10]};  // Bit_Extender bit_extender_11
  assign bit_extender_12_out = {{1{1'b0}}, inval1[11]};  // Bit_Extender bit_extender_12
  assign bit_extender_13_out = {{1{1'b0}}, inval1[12]};  // Bit_Extender bit_extender_13
  assign bit_extender_14_out = {{1{1'b0}}, inval1[13]};  // Bit_Extender bit_extender_14
  assign bit_extender_15_out = {{1{1'b0}}, inval1[14]};  // Bit_Extender bit_extender_15
  assign bit_extender_16_out = {{1{1'b0}}, inval1[15]};  // Bit_Extender bit_extender_16
  assign bit_extender_17_out = {{1{1'b0}}, inval1[16]};  // Bit_Extender bit_extender_17
  assign bit_extender_18_out = {{1{1'b0}}, inval1[17]};  // Bit_Extender bit_extender_18
  assign bit_extender_19_out = {{1{1'b0}}, inval1[18]};  // Bit_Extender bit_extender_19
  assign bit_extender_20_out = {{1{1'b0}}, inval1[19]};  // Bit_Extender bit_extender_20
  assign bit_extender_21_out = {{1{1'b0}}, inval1[20]};  // Bit_Extender bit_extender_21
  assign bit_extender_22_out = {{1{1'b0}}, inval1[21]};  // Bit_Extender bit_extender_22
  assign bit_extender_23_out = {{1{1'b0}}, inval1[22]};  // Bit_Extender bit_extender_23
  assign bit_extender_24_out = {{1{1'b0}}, inval1[23]};  // Bit_Extender bit_extender_24
  assign bit_extender_25_out = {{1{1'b0}}, inval1[24]};  // Bit_Extender bit_extender_25
  assign bit_extender_26_out = {{1{1'b0}}, inval1[25]};  // Bit_Extender bit_extender_26
  assign bit_extender_27_out = {{1{1'b0}}, inval1[26]};  // Bit_Extender bit_extender_27
  assign bit_extender_28_out = {{1{1'b0}}, inval1[27]};  // Bit_Extender bit_extender_28
  assign bit_extender_29_out = {{1{1'b0}}, inval1[28]};  // Bit_Extender bit_extender_29
  assign bit_extender_30_out = {{1{1'b0}}, inval1[29]};  // Bit_Extender bit_extender_30
  assign bit_extender_31_out = {{1{1'b0}}, inval1[30]};  // Bit_Extender bit_extender_31
  assign bit_extender_32_out = {{1{1'b0}}, inval1[31]};  // Bit_Extender bit_extender_32
  assign bit_extender_33_out = {{1{1'b0}}, inval1[32]};  // Bit_Extender bit_extender_33
  assign bit_extender_34_out = {{1{1'b0}}, inval1[33]};  // Bit_Extender bit_extender_34
  assign bit_extender_35_out = {{1{1'b0}}, inval1[34]};  // Bit_Extender bit_extender_35
  assign bit_extender_36_out = {{1{1'b0}}, inval1[35]};  // Bit_Extender bit_extender_36
  assign bit_extender_37_out = {{1{1'b0}}, inval1[36]};  // Bit_Extender bit_extender_37
  assign bit_extender_38_out = {{1{1'b0}}, inval1[37]};  // Bit_Extender bit_extender_38
  assign bit_extender_39_out = {{1{1'b0}}, inval1[38]};  // Bit_Extender bit_extender_39
  assign bit_extender_40_out = {{1{1'b0}}, inval1[39]};  // Bit_Extender bit_extender_40
  assign bit_extender_41_out = {{1{1'b0}}, inval1[40]};  // Bit_Extender bit_extender_41
  assign bit_extender_42_out = {{1{1'b0}}, inval1[41]};  // Bit_Extender bit_extender_42
  assign bit_extender_43_out = {{1{1'b0}}, inval1[42]};  // Bit_Extender bit_extender_43
  assign bit_extender_44_out = {{1{1'b0}}, inval1[43]};  // Bit_Extender bit_extender_44
  assign bit_extender_45_out = {{1{1'b0}}, inval1[44]};  // Bit_Extender bit_extender_45
  assign bit_extender_46_out = {{1{1'b0}}, inval1[45]};  // Bit_Extender bit_extender_46
  assign bit_extender_47_out = {{1{1'b0}}, inval1[46]};  // Bit_Extender bit_extender_47
  assign bit_extender_48_out = {{1{1'b0}}, inval1[47]};  // Bit_Extender bit_extender_48
  assign bit_extender_49_out = {{1{1'b0}}, inval1[48]};  // Bit_Extender bit_extender_49
  assign bit_extender_50_out = {{1{1'b0}}, inval1[49]};  // Bit_Extender bit_extender_50
  assign bit_extender_51_out = {{1{1'b0}}, inval1[50]};  // Bit_Extender bit_extender_51
  assign bit_extender_52_out = {{1{1'b0}}, inval1[51]};  // Bit_Extender bit_extender_52
  assign bit_extender_53_out = {{1{1'b0}}, inval1[52]};  // Bit_Extender bit_extender_53
  assign bit_extender_54_out = {{1{1'b0}}, inval1[53]};  // Bit_Extender bit_extender_54
  assign bit_extender_55_out = {{1{1'b0}}, inval1[54]};  // Bit_Extender bit_extender_55
  assign bit_extender_56_out = {{1{1'b0}}, inval1[55]};  // Bit_Extender bit_extender_56
  assign bit_extender_57_out = {{1{1'b0}}, inval1[56]};  // Bit_Extender bit_extender_57
  assign bit_extender_58_out = {{1{1'b0}}, inval1[57]};  // Bit_Extender bit_extender_58
  assign bit_extender_59_out = {{1{1'b0}}, inval1[58]};  // Bit_Extender bit_extender_59
  assign bit_extender_60_out = {{1{1'b0}}, inval1[59]};  // Bit_Extender bit_extender_60
  assign bit_extender_61_out = {{1{1'b0}}, inval1[60]};  // Bit_Extender bit_extender_61
  assign bit_extender_62_out = {{1{1'b0}}, inval1[61]};  // Bit_Extender bit_extender_62
  assign bit_extender_63_out = {{1{1'b0}}, inval1[62]};  // Bit_Extender bit_extender_63
  assign bit_extender_64_out = {{1{1'b0}}, inval1[63]};  // Bit_Extender bit_extender_64
  assign bit_extender_65_out = {{1{1'b0}}, adder_1_out};  // Bit_Extender bit_extender_65
  Adder #(.width(2)) adder_1 (.a(bit_extender_1_out), .b(bit_extender_2_out), .out(adder_1_out));  // open: cin, cout
  assign bit_extender_66_out = {{1{1'b0}}, adder_2_out};  // Bit_Extender bit_extender_66
  Adder #(.width(2)) adder_2 (.a(bit_extender_3_out), .b(bit_extender_4_out), .out(adder_2_out));  // open: cin, cout
  assign bit_extender_67_out = {{1{1'b0}}, adder_3_out};  // Bit_Extender bit_extender_67
  Adder #(.width(2)) adder_3 (.a(bit_extender_5_out), .b(bit_extender_6_out), .out(adder_3_out));  // open: cin, cout
  assign bit_extender_68_out = {{1{1'b0}}, adder_4_out};  // Bit_Extender bit_extender_68
  Adder #(.width(2)) adder_4 (.a(bit_extender_7_out), .b(bit_extender_8_out), .out(adder_4_out));  // open: cin, cout
  assign bit_extender_69_out = {{1{1'b0}}, adder_5_out};  // Bit_Extender bit_extender_69
  Adder #(.width(2)) adder_5 (.a(bit_extender_9_out), .b(bit_extender_10_out), .out(adder_5_out));  // open: cin, cout
  assign bit_extender_70_out = {{1{1'b0}}, adder_6_out};  // Bit_Extender bit_extender_70
  Adder #(.width(2)) adder_6 (.a(bit_extender_11_out), .b(bit_extender_12_out), .out(adder_6_out));  // open: cin, cout
  assign bit_extender_71_out = {{1{1'b0}}, adder_7_out};  // Bit_Extender bit_extender_71
  Adder #(.width(2)) adder_7 (.a(bit_extender_13_out), .b(bit_extender_14_out), .out(adder_7_out));  // open: cin, cout
  assign bit_extender_72_out = {{1{1'b0}}, adder_8_out};  // Bit_Extender bit_extender_72
  Adder #(.width(2)) adder_8 (.a(bit_extender_15_out), .b(bit_extender_16_out), .out(adder_8_out));  // open: cin, cout
  assign bit_extender_73_out = {{1{1'b0}}, adder_9_out};  // Bit_Extender bit_extender_73
  Adder #(.width(2)) adder_9 (.a(bit_extender_17_out), .b(bit_extender_18_out), .out(adder_9_out));  // open: cin, cout
  assign bit_extender_74_out = {{1{1'b0}}, adder_10_out};  // Bit_Extender bit_extender_74
  Adder #(.width(2)) adder_10 (
    .a(bit_extender_19_out), .b(bit_extender_20_out), .out(adder_10_out));  // open: cin, cout
  assign bit_extender_75_out = {{1{1'b0}}, adder_11_out};  // Bit_Extender bit_extender_75
  Adder #(.width(2)) adder_11 (
    .a(bit_extender_21_out), .b(bit_extender_22_out), .out(adder_11_out));  // open: cin, cout
  assign bit_extender_76_out = {{1{1'b0}}, adder_12_out};  // Bit_Extender bit_extender_76
  Adder #(.width(2)) adder_12 (
    .a(bit_extender_23_out), .b(bit_extender_24_out), .out(adder_12_out));  // open: cin, cout
  assign bit_extender_77_out = {{1{1'b0}}, adder_13_out};  // Bit_Extender bit_extender_77
  Adder #(.width(2)) adder_13 (
    .a(bit_extender_25_out), .b(bit_extender_26_out), .out(adder_13_out));  // open: cin, cout
  assign bit_extender_78_out = {{1{1'b0}}, adder_14_out};  // Bit_Extender bit_extender_78
  Adder #(.width(2)) adder_14 (
    .a(bit_extender_27_out), .b(bit_extender_28_out), .out(adder_14_out));  // open: cin, cout
  assign bit_extender_79_out = {{1{1'b0}}, adder_15_out};  // Bit_Extender bit_extender_79
  Adder #(.width(2)) adder_15 (
    .a(bit_extender_29_out), .b(bit_extender_30_out), .out(adder_15_out));  // open: cin, cout
  assign bit_extender_80_out = {{1{1'b0}}, adder_16_out};  // Bit_Extender bit_extender_80
  Adder #(.width(2)) adder_16 (
    .a(bit_extender_31_out), .b(bit_extender_32_out), .out(adder_16_out));  // open: cin, cout
  assign bit_extender_81_out = {{1{1'b0}}, adder_17_out};  // Bit_Extender bit_extender_81
  Adder #(.width(2)) adder_17 (
    .a(bit_extender_33_out), .b(bit_extender_34_out), .out(adder_17_out));  // open: cin, cout
  assign bit_extender_82_out = {{1{1'b0}}, adder_18_out};  // Bit_Extender bit_extender_82
  Adder #(.width(2)) adder_18 (
    .a(bit_extender_35_out), .b(bit_extender_36_out), .out(adder_18_out));  // open: cin, cout
  assign bit_extender_83_out = {{1{1'b0}}, adder_19_out};  // Bit_Extender bit_extender_83
  Adder #(.width(2)) adder_19 (
    .a(bit_extender_37_out), .b(bit_extender_38_out), .out(adder_19_out));  // open: cin, cout
  assign bit_extender_84_out = {{1{1'b0}}, adder_20_out};  // Bit_Extender bit_extender_84
  Adder #(.width(2)) adder_20 (
    .a(bit_extender_39_out), .b(bit_extender_40_out), .out(adder_20_out));  // open: cin, cout
  assign bit_extender_85_out = {{1{1'b0}}, adder_21_out};  // Bit_Extender bit_extender_85
  Adder #(.width(2)) adder_21 (
    .a(bit_extender_41_out), .b(bit_extender_42_out), .out(adder_21_out));  // open: cin, cout
  assign bit_extender_86_out = {{1{1'b0}}, adder_22_out};  // Bit_Extender bit_extender_86
  Adder #(.width(2)) adder_22 (
    .a(bit_extender_43_out), .b(bit_extender_44_out), .out(adder_22_out));  // open: cin, cout
  assign bit_extender_87_out = {{1{1'b0}}, adder_23_out};  // Bit_Extender bit_extender_87
  Adder #(.width(2)) adder_23 (
    .a(bit_extender_45_out), .b(bit_extender_46_out), .out(adder_23_out));  // open: cin, cout
  assign bit_extender_88_out = {{1{1'b0}}, adder_24_out};  // Bit_Extender bit_extender_88
  Adder #(.width(2)) adder_24 (
    .a(bit_extender_47_out), .b(bit_extender_48_out), .out(adder_24_out));  // open: cin, cout
  assign bit_extender_89_out = {{1{1'b0}}, adder_25_out};  // Bit_Extender bit_extender_89
  Adder #(.width(2)) adder_25 (
    .a(bit_extender_49_out), .b(bit_extender_50_out), .out(adder_25_out));  // open: cin, cout
  assign bit_extender_90_out = {{1{1'b0}}, adder_26_out};  // Bit_Extender bit_extender_90
  Adder #(.width(2)) adder_26 (
    .a(bit_extender_51_out), .b(bit_extender_52_out), .out(adder_26_out));  // open: cin, cout
  assign bit_extender_91_out = {{1{1'b0}}, adder_27_out};  // Bit_Extender bit_extender_91
  Adder #(.width(2)) adder_27 (
    .a(bit_extender_53_out), .b(bit_extender_54_out), .out(adder_27_out));  // open: cin, cout
  assign bit_extender_92_out = {{1{1'b0}}, adder_28_out};  // Bit_Extender bit_extender_92
  Adder #(.width(2)) adder_28 (
    .a(bit_extender_55_out), .b(bit_extender_56_out), .out(adder_28_out));  // open: cin, cout
  assign bit_extender_93_out = {{1{1'b0}}, adder_29_out};  // Bit_Extender bit_extender_93
  Adder #(.width(2)) adder_29 (
    .a(bit_extender_57_out), .b(bit_extender_58_out), .out(adder_29_out));  // open: cin, cout
  assign bit_extender_94_out = {{1{1'b0}}, adder_30_out};  // Bit_Extender bit_extender_94
  Adder #(.width(2)) adder_30 (
    .a(bit_extender_59_out), .b(bit_extender_60_out), .out(adder_30_out));  // open: cin, cout
  assign bit_extender_95_out = {{1{1'b0}}, adder_31_out};  // Bit_Extender bit_extender_95
  Adder #(.width(2)) adder_31 (
    .a(bit_extender_61_out), .b(bit_extender_62_out), .out(adder_31_out));  // open: cin, cout
  assign bit_extender_96_out = {{1{1'b0}}, adder_32_out};  // Bit_Extender bit_extender_96
  Adder #(.width(2)) adder_32 (
    .a(bit_extender_63_out), .b(bit_extender_64_out), .out(adder_32_out));  // open: cin, cout
  Adder #(.width(3)) adder_33 (
    .a(bit_extender_65_out), .b(bit_extender_66_out), .out(adder_33_out));  // open: cin, cout
  Adder #(.width(3)) adder_34 (
    .a(bit_extender_67_out), .b(bit_extender_68_out), .out(adder_34_out));  // open: cin, cout
  Adder #(.width(3)) adder_35 (
    .a(bit_extender_69_out), .b(bit_extender_70_out), .out(adder_35_out));  // open: cin, cout
  Adder #(.width(3)) adder_36 (
    .a(bit_extender_71_out), .b(bit_extender_72_out), .out(adder_36_out));  // open: cin, cout
  Adder #(.width(3)) adder_37 (
    .a(bit_extender_73_out), .b(bit_extender_74_out), .out(adder_37_out));  // open: cin, cout
  Adder #(.width(3)) adder_38 (
    .a(bit_extender_75_out), .b(bit_extender_76_out), .out(adder_38_out));  // open: cin, cout
  Adder #(.width(3)) adder_39 (
    .a(bit_extender_77_out), .b(bit_extender_78_out), .out(adder_39_out));  // open: cin, cout
  Adder #(.width(3)) adder_40 (
    .a(bit_extender_79_out), .b(bit_extender_80_out), .out(adder_40_out));  // open: cin, cout
  Adder #(.width(3)) adder_41 (
    .a(bit_extender_81_out), .b(bit_extender_82_out), .out(adder_41_out));  // open: cin, cout
  Adder #(.width(3)) adder_42 (
    .a(bit_extender_83_out), .b(bit_extender_84_out), .out(adder_42_out));  // open: cin, cout
  Adder #(.width(3)) adder_43 (
    .a(bit_extender_85_out), .b(bit_extender_86_out), .out(adder_43_out));  // open: cin, cout
  Adder #(.width(3)) adder_44 (
    .a(bit_extender_87_out), .b(bit_extender_88_out), .out(adder_44_out));  // open: cin, cout
  Adder #(.width(3)) adder_45 (
    .a(bit_extender_89_out), .b(bit_extender_90_out), .out(adder_45_out));  // open: cin, cout
  Adder #(.width(3)) adder_46 (
    .a(bit_extender_91_out), .b(bit_extender_92_out), .out(adder_46_out));  // open: cin, cout
  Adder #(.width(3)) adder_47 (
    .a(bit_extender_93_out), .b(bit_extender_94_out), .out(adder_47_out));  // open: cin, cout
  Adder #(.width(3)) adder_48 (
    .a(bit_extender_95_out), .b(bit_extender_96_out), .out(adder_48_out));  // open: cin, cout
  assign bit_extender_97_out = {{1{1'b0}}, adder_33_out};  // Bit_Extender bit_extender_97
  assign bit_extender_98_out = {{1{1'b0}}, adder_34_out};  // Bit_Extender bit_extender_98
  assign bit_extender_99_out = {{1{1'b0}}, adder_35_out};  // Bit_Extender bit_extender_99
  assign bit_extender_100_out = {{1{1'b0}}, adder_36_out};  // Bit_Extender bit_extender_100
  assign bit_extender_101_out = {{1{1'b0}}, adder_37_out};  // Bit_Extender bit_extender_101
  assign bit_extender_102_out = {{1{1'b0}}, adder_38_out};  // Bit_Extender bit_extender_102
  assign bit_extender_103_out = {{1{1'b0}}, adder_39_out};  // Bit_Extender bit_extender_103
  assign bit_extender_104_out = {{1{1'b0}}, adder_40_out};  // Bit_Extender bit_extender_104
  assign bit_extender_105_out = {{1{1'b0}}, adder_41_out};  // Bit_Extender bit_extender_105
  assign bit_extender_106_out = {{1{1'b0}}, adder_42_out};  // Bit_Extender bit_extender_106
  assign bit_extender_107_out = {{1{1'b0}}, adder_43_out};  // Bit_Extender bit_extender_107
  assign bit_extender_108_out = {{1{1'b0}}, adder_44_out};  // Bit_Extender bit_extender_108
  assign bit_extender_109_out = {{1{1'b0}}, adder_45_out};  // Bit_Extender bit_extender_109
  assign bit_extender_110_out = {{1{1'b0}}, adder_46_out};  // Bit_Extender bit_extender_110
  assign bit_extender_111_out = {{1{1'b0}}, adder_47_out};  // Bit_Extender bit_extender_111
  assign bit_extender_112_out = {{1{1'b0}}, adder_48_out};  // Bit_Extender bit_extender_112
  assign bit_extender_113_out = {{1{1'b0}}, adder_49_out};  // Bit_Extender bit_extender_113
  Adder #(.width(4)) adder_49 (
    .a(bit_extender_97_out), .b(bit_extender_98_out), .out(adder_49_out));  // open: cin, cout
  assign bit_extender_114_out = {{1{1'b0}}, adder_50_out};  // Bit_Extender bit_extender_114
  Adder #(.width(4)) adder_50 (
    .a(bit_extender_99_out), .b(bit_extender_100_out), .out(adder_50_out));  // open: cin, cout
  assign bit_extender_115_out = {{1{1'b0}}, adder_51_out};  // Bit_Extender bit_extender_115
  Adder #(.width(4)) adder_51 (
    .a(bit_extender_101_out), .b(bit_extender_102_out), .out(adder_51_out));  // open: cin, cout
  assign bit_extender_116_out = {{1{1'b0}}, adder_52_out};  // Bit_Extender bit_extender_116
  Adder #(.width(4)) adder_52 (
    .a(bit_extender_103_out), .b(bit_extender_104_out), .out(adder_52_out));  // open: cin, cout
  assign bit_extender_117_out = {{1{1'b0}}, adder_53_out};  // Bit_Extender bit_extender_117
  Adder #(.width(4)) adder_53 (
    .a(bit_extender_105_out), .b(bit_extender_106_out), .out(adder_53_out));  // open: cin, cout
  assign bit_extender_118_out = {{1{1'b0}}, adder_54_out};  // Bit_Extender bit_extender_118
  Adder #(.width(4)) adder_54 (
    .a(bit_extender_107_out), .b(bit_extender_108_out), .out(adder_54_out));  // open: cin, cout
  assign bit_extender_119_out = {{1{1'b0}}, adder_55_out};  // Bit_Extender bit_extender_119
  Adder #(.width(4)) adder_55 (
    .a(bit_extender_109_out), .b(bit_extender_110_out), .out(adder_55_out));  // open: cin, cout
  assign bit_extender_120_out = {{1{1'b0}}, adder_56_out};  // Bit_Extender bit_extender_120
  Adder #(.width(4)) adder_56 (
    .a(bit_extender_111_out), .b(bit_extender_112_out), .out(adder_56_out));  // open: cin, cout
  Adder #(.width(5)) adder_57 (
    .a(bit_extender_113_out), .b(bit_extender_114_out), .out(adder_57_out));  // open: cin, cout
  Adder #(.width(5)) adder_58 (
    .a(bit_extender_115_out), .b(bit_extender_116_out), .out(adder_58_out));  // open: cin, cout
  Adder #(.width(5)) adder_59 (
    .a(bit_extender_117_out), .b(bit_extender_118_out), .out(adder_59_out));  // open: cin, cout
  Adder #(.width(5)) adder_60 (
    .a(bit_extender_119_out), .b(bit_extender_120_out), .out(adder_60_out));  // open: cin, cout
  assign bit_extender_121_out = {{1{1'b0}}, adder_57_out};  // Bit_Extender bit_extender_121
  Adder #(.width(6)) adder_61 (
    .a(bit_extender_121_out), .b(bit_extender_122_out), .out(adder_61_out));  // open: cin, cout
  assign bit_extender_122_out = {{1{1'b0}}, adder_58_out};  // Bit_Extender bit_extender_122
  assign bit_extender_123_out = {{1{1'b0}}, adder_59_out};  // Bit_Extender bit_extender_123
  Adder #(.width(6)) adder_62 (
    .a(bit_extender_123_out), .b(bit_extender_124_out), .out(adder_62_out));  // open: cin, cout
  assign bit_extender_124_out = {{1{1'b0}}, adder_60_out};  // Bit_Extender bit_extender_124
  assign bit_extender_125_out = {{1{1'b0}}, adder_61_out};  // Bit_Extender bit_extender_125
  assign bit_extender_126_out = {{1{1'b0}}, adder_62_out};  // Bit_Extender bit_extender_126
  Adder #(.width(7)) adder_63 (.a(bit_extender_125_out), .b(bit_extender_126_out), .out(outval1));  // open: cin, cout
  // Probe on bitadder_1_out
  // Probe on outval1

  // Notes on the sheet:
  //   inval1: initial=0xbfaff5f000ff1dff
endmodule
