// Logisim project muxflpalu.circ as structural Verilog: 2 circuits, main circuit main
module main (
);

  wire fpcomparator_1_p3;
  wire [63:0] flpadd64_1_output1, fpadder_1_out;

  // Probe on 64'h400921fb54442d18
  // Probe on 64'h4005bf0a8b145769
  FPAdder #(.fpwidth(64)) fpadder_1 (.a(64'h400921fb54442d18), .b(64'h4005bf0a8b145769), .out(fpadder_1_out));
  flpadd64 flpadd64_1 (.input1(64'h400921fb54442d18), .input2(64'h4005bf0a8b145769), .output1(flpadd64_1_output1));
  // Probe on fpadder_1_out
  // Probe on flpadd64_1_output1
  // FPComparator #(.fpwidth(64)) fpcomparator_1: pin names not known; wires that end beside it: fpadder_1_out, flpadd64_1_output1, fpcomparator_1_p3
  LED led_1 (.in(fpcomparator_1_p3));
endmodule

module flpadd64 (
  input  [63:0] input1,
  input  [63:0] input2,
  output [63:0] output1
);

  wire bitselector_3_out, comparator_1_lt, not_1_out;
  wire [5:0] bitselector_1_out, bitselector_2_out;
  wire [10:0] adder_2_out, multiplexer_3_out, subtractor_1_out, subtractor_2_out;
  wire [52:0] multiplexer_1_out, multiplexer_2_out, shifter_1_out, shifter_2_out;
  wire [53:0] adder_1_out, bit_extender_1_out, bit_extender_2_out, multiplexer_4_out, multiplexer_5_out,
       multiplexer_6_out, multiplexer_7_out, negator_1_out, negator_2_out, negator_3_out, shifter_4_out;

  // Probe on input1
  // Probe on input2
  BitSelector #(.group(6), .width(11)) bitselector_1 (.in(subtractor_1_out), .out(bitselector_1_out), .sel(1'b0));
  Subtractor #(.width(11)) subtractor_1 (
    .a(input1[62:52]), .b(input2[62:52]), .out(subtractor_1_out));  // open: bin, bout
  Comparator #(.mode("unsigned"), .width(11)) comparator_1 (
    .a(input1[62:52]), .b(input2[62:52]), .lt(comparator_1_lt));  // open: gt, eq
  Subtractor #(.width(11)) subtractor_2 (
    .a(input2[62:52]), .b(input1[62:52]), .out(subtractor_2_out));  // open: bin, bout
  BitSelector #(.group(6), .width(11)) bitselector_2 (.in(subtractor_2_out), .out(bitselector_2_out), .sel(1'b0));
  Multiplexer #(.width(53)) multiplexer_1 (
    .in0({1'b1, input1[51:0]}), .in1(shifter_1_out), .out(multiplexer_1_out), .sel(not_1_out));
  Shifter #(.shift("lr"), .width(53)) shifter_1 (
    .in({1'b1, input1[51:0]}), .\dist (bitselector_1_out), .out(shifter_1_out));
  not not_1 (not_1_out, comparator_1_lt);
  Shifter #(.shift("lr"), .width(53)) shifter_2 (
    .in({1'b1, input2[51:0]}), .\dist (bitselector_2_out), .out(shifter_2_out));
  Multiplexer #(.width(53)) multiplexer_2 (
    .in0(shifter_2_out), .in1({1'b1, input2[51:0]}), .out(multiplexer_2_out), .sel(comparator_1_lt));
  assign bit_extender_1_out = {{1{1'b0}}, multiplexer_1_out};  // Bit_Extender bit_extender_1
  Multiplexer #(.width(11)) multiplexer_3 (
    .in0(input1[62:52]), .in1(input2[62:52]), .out(multiplexer_3_out), .sel(comparator_1_lt));
  assign bit_extender_2_out = {{1{1'b0}}, multiplexer_2_out};  // Bit_Extender bit_extender_2
  Negator #(.width(54)) negator_1 (.in(bit_extender_1_out), .out(negator_1_out));
  Negator #(.width(54)) negator_2 (.in(bit_extender_2_out), .out(negator_2_out));
  Multiplexer #(.width(54)) multiplexer_4 (
    .in0(bit_extender_1_out), .in1(negator_1_out), .out(multiplexer_4_out), .sel(input1[63]));
  Multiplexer #(.width(54)) multiplexer_5 (
    .in0(bit_extender_2_out), .in1(negator_2_out), .out(multiplexer_5_out), .sel(input2[63]));
  Adder #(.width(54)) adder_1 (.a(multiplexer_4_out), .b(multiplexer_5_out), .out(adder_1_out));  // open: cin, cout
  Multiplexer #(.width(54)) multiplexer_6 (
    .in0(adder_1_out), .in1(negator_3_out), .out(multiplexer_6_out), .sel(output1[63]));
  Negator #(.width(54)) negator_3 (.in(adder_1_out), .out(negator_3_out));
  Comparator #(.mode("unsigned"), .width(54)) comparator_2 (
    .a(adder_1_out), .b({54{1'b0}}), .lt(output1[63]));  // open: gt, eq
  BitSelector #(.width(54)) bitselector_3 (.in(multiplexer_6_out), .out(bitselector_3_out), .sel(6'b110101));
  BitSelector #(.width(54)) bitselector_4 (.in(multiplexer_6_out), .sel(6'b110100));  // open: out
  BitSelector #(.width(54)) bitselector_5 (.in(multiplexer_6_out), .sel(6'b110011));  // open: out
  Shifter #(.width(54)) shifter_3 ();  // open: in, dist, out
  Shifter #(.shift("lr"), .width(54)) shifter_4 (.in(multiplexer_6_out), .\dist (6'b000001), .out(shifter_4_out));
  Adder #(.width(11)) adder_2 (.a(multiplexer_3_out), .b(11'h1), .out(adder_2_out));  // open: cin, cout
  Multiplexer #(.width(54)) multiplexer_7 (
    .in1(shifter_4_out), .out(multiplexer_7_out), .sel(bitselector_3_out));  // open: in0
  BitSelector #(.group(52), .width(54)) bitselector_6 (.in(multiplexer_7_out), .out(output1[51:0]), .sel(1'b0));
  Multiplexer #(.width(11)) multiplexer_8 (
    .in0(multiplexer_3_out), .in1(adder_2_out), .out(output1[62:52]), .sel(bitselector_3_out));
  // Probe on output1
endmodule
