// Logisim project muxfpga.circ as structural Verilog: 2 circuits, main circuit main
module main (
);

  wire clock_1_out;
  wire [3:0] bitselector_1_out, bitselector_2_out, bitselector_3_out, bitselector_4_out, bitselector_5_out,
       bitselector_6_out, bitselector_7_out, bitselector_8_out, bitselector_9_out, bitselector_10_out,
       bitselector_11_out, bitselector_12_out;
  wire [63:0] D00, D01, D02, D03, E0_ax, E0_ay, E0_az, E1_ax, E1_ay, E1_az, E2_ax, E2_ay, E2_az, E3_ax,
       E3_ay, E3_az, multiplexer_1_out, multiplexer_2_out, multiplexer_3_out, multiplexer_4_out,
       multiplexer_5_out, multiplexer_6_out, multiplexer_7_out, multiplexer_8_out, multiplexer_9_out,
       multiplexer_10_out, multiplexer_11_out, multiplexer_12_out;

  Clock clock_1 (.out(clock_1_out));
  logicelement E0 (
    .DX(multiplexer_1_out), .DY(multiplexer_5_out), .DZ(multiplexer_9_out), .CLK(clock_1_out), .AX(E0_ax),
    .AY(E0_ay), .AZ(E0_az), .D(D00));  // open: regX, regY, regZ, AE, OP, PE, WE, LE
  logicelement E1 (
    .DX(multiplexer_2_out), .DY(multiplexer_6_out), .DZ(multiplexer_10_out), .CLK(clock_1_out), .AX(E1_ax),
    .AY(E1_ay), .AZ(E1_az), .D(D01));  // open: regX, regY, regZ, AE, OP, PE, WE, LE
  logicelement E2 (
    .DX(multiplexer_3_out), .DY(multiplexer_7_out), .DZ(multiplexer_11_out), .CLK(clock_1_out), .AX(E2_ax),
    .AY(E2_ay), .AZ(E2_az), .D(D02));  // open: regX, regY, regZ, AE, OP, PE, WE, LE
  logicelement E3 (
    .DX(multiplexer_4_out), .DY(multiplexer_8_out), .DZ(multiplexer_12_out), .CLK(clock_1_out), .AX(E3_ax),
    .AY(E3_ay), .AZ(E3_az), .D(D03));  // open: regX, regY, regZ, AE, OP, PE, WE, LE
  Multiplexer #(.select(4), .width(64)) multiplexer_1 (
    .in0(D00), .in1(D01), .in2(D02), .in3(D03), .out(multiplexer_1_out), .sel(bitselector_1_out));  // open: in4, in5, in6, in7, in8, in9, in10, in11, in12, in13, in14, in15
  BitSelector #(.group(4), .width(64)) bitselector_1 (.in(E0_ax), .out(bitselector_1_out), .sel(4'b0000));
  Multiplexer #(.select(4), .width(64)) multiplexer_2 (
    .in0(D00), .in1(D01), .in2(D02), .in3(D03), .out(multiplexer_2_out), .sel(bitselector_2_out));  // open: in4, in5, in6, in7, in8, in9, in10, in11, in12, in13, in14, in15
  BitSelector #(.group(4), .width(64)) bitselector_2 (.in(E1_ax), .out(bitselector_2_out), .sel(4'b0000));
  Multiplexer #(.select(4), .width(64)) multiplexer_3 (
    .in0(D00), .in1(D01), .in2(D02), .in3(D03), .out(multiplexer_3_out), .sel(bitselector_3_out));  // open: in4, in5, in6, in7, in8, in9, in10, in11, in12, in13, in14, in15
  BitSelector #(.group(4), .width(64)) bitselector_3 (.in(E2_ax), .out(bitselector_3_out), .sel(4'b0000));
  Multiplexer #(.select(4), .width(64)) multiplexer_4 (
    .in0(D00), .in1(D01), .in2(D02), .in3(D03), .out(multiplexer_4_out), .sel(bitselector_4_out));  // open: in4, in5, in6, in7, in8, in9, in10, in11, in12, in13, in14, in15
  BitSelector #(.group(4), .width(64)) bitselector_4 (.in(E3_ax), .out(bitselector_4_out), .sel(4'b0000));
  Multiplexer #(.select(4), .width(64)) multiplexer_5 (
    .in0(D00), .in1(D01), .in2(D02), .in3(D03), .out(multiplexer_5_out), .sel(bitselector_5_out));  // open: in4, in5, in6, in7, in8, in9, in10, in11, in12, in13, in14, in15
  BitSelector #(.group(4), .width(64)) bitselector_5 (.in(E0_ay), .out(bitselector_5_out), .sel(4'b0000));
  Multiplexer #(.select(4), .width(64)) multiplexer_6 (
    .in0(D00), .in1(D01), .in2(D02), .in3(D03), .out(multiplexer_6_out), .sel(bitselector_6_out));  // open: in4, in5, in6, in7, in8, in9, in10, in11, in12, in13, in14, in15
  BitSelector #(.group(4), .width(64)) bitselector_6 (.in(E1_ay), .out(bitselector_6_out), .sel(4'b0000));
  Multiplexer #(.select(4), .width(64)) multiplexer_7 (
    .in0(D00), .in1(D01), .in2(D02), .in3(D03), .out(multiplexer_7_out), .sel(bitselector_7_out));  // open: in4, in5, in6, in7, in8, in9, in10, in11, in12, in13, in14, in15
  BitSelector #(.group(4), .width(64)) bitselector_7 (.in(E2_ay), .out(bitselector_7_out), .sel(4'b0000));
  Multiplexer #(.select(4), .width(64)) multiplexer_8 (
    .in0(D00), .in1(D01), .in2(D02), .in3(D03), .out(multiplexer_8_out), .sel(bitselector_8_out));  // open: in4, in5, in6, in7, in8, in9, in10, in11, in12, in13, in14, in15
  BitSelector #(.group(4), .width(64)) bitselector_8 (.in(E3_ay), .out(bitselector_8_out), .sel(4'b0000));
  Multiplexer #(.select(4), .width(64)) multiplexer_9 (
    .in0(D00), .in1(D01), .in2(D02), .in3(D03), .out(multiplexer_9_out), .sel(bitselector_9_out));  // open: in4, in5, in6, in7, in8, in9, in10, in11, in12, in13, in14, in15
  BitSelector #(.group(4), .width(64)) bitselector_9 (.in(E0_az), .out(bitselector_9_out), .sel(4'b0000));
  Multiplexer #(.select(4), .width(64)) multiplexer_10 (
    .in0(D00), .in1(D01), .in2(D02), .in3(D03), .out(multiplexer_10_out), .sel(bitselector_10_out));  // open: in4, in5, in6, in7, in8, in9, in10, in11, in12, in13, in14, in15
  BitSelector #(.group(4), .width(64)) bitselector_10 (.in(E1_az), .out(bitselector_10_out), .sel(4'b0000));
  Multiplexer #(.select(4), .width(64)) multiplexer_11 (
    .in0(D00), .in1(D01), .in2(D02), .in3(D03), .out(multiplexer_11_out), .sel(bitselector_11_out));  // open: in4, in5, in6, in7, in8, in9, in10, in11, in12, in13, in14, in15
  BitSelector #(.group(4), .width(64)) bitselector_11 (.in(E2_az), .out(bitselector_11_out), .sel(4'b0000));
  Multiplexer #(.select(4), .width(64)) multiplexer_12 (
    .in0(D00), .in1(D01), .in2(D02), .in3(D03), .out(multiplexer_12_out), .sel(bitselector_12_out));  // open: in4, in5, in6, in7, in8, in9, in10, in11, in12, in13, in14, in15
  BitSelector #(.group(4), .width(64)) bitselector_12 (.in(E3_az), .out(bitselector_12_out), .sel(4'b0000));
endmodule

module logicelement (
  input  [63:0] regX,
  input  [63:0] regY,
  input  [63:0] regZ,
  input  AE,
  input  [63:0] DX,
  input  [63:0] DY,
  input  [63:0] DZ,
  input  [63:0] OP,
  input  PE,
  input  WE,
  input  LE,
  input  CLK,
  output [63:0] AX,
  output [63:0] AY,
  output [63:0] AZ,
  output [63:0] D
);

  wire WX_q;
  wire [63:0] and_1_out, and_2_out, multiplexer_1_out, multiplexer_2_out, multiplexer_3_out,
       multiplexer_4_out, multiplexer_5_out, multiplexer_6_out, multiplexer_7_out, multiplexer_8_out,
       multiplexer_9_out, multiplexer_10_out, multiplexer_11_out, nand_1_out, nor_1_out, not_1_out, or_1_out,
       register_1_q, register_2_q, xnor_1_out, xor_1_out;

  Register #(.width(64)) register_1 (.D(OP), .en(PE), .clk(CLK), .Q(register_1_q));  // open: clr
  Multiplexer #(.width(64)) multiplexer_1 (.in0(DY), .in1(64'h1), .out(multiplexer_1_out), .sel(register_1_q[10]));
  Multiplexer #(.width(64)) multiplexer_2 (
    .in0(multiplexer_1_out), .in1({64{1'b0}}), .out(multiplexer_2_out), .sel(register_1_q[9]));
  assign xnor_1_out = ~(multiplexer_2_out ^ DZ);  // XNOR_Gate xnor_1, 64 bits wide
  Multiplexer #(.width(64)) multiplexer_3 (
    .in0(multiplexer_2_out), .in1(xnor_1_out), .out(multiplexer_3_out), .sel(register_1_q[8]));
  Multiplexer #(.width(64)) multiplexer_4 (
    .in0(multiplexer_3_out), .in1(xor_1_out), .out(multiplexer_4_out), .sel(register_1_q[7]));
  assign xor_1_out = multiplexer_3_out ^ DZ;  // XOR_Gate xor_1, 64 bits wide
  Multiplexer #(.width(64)) multiplexer_5 (
    .in0(multiplexer_4_out), .in1(nor_1_out), .out(multiplexer_5_out), .sel(register_1_q[6]));
  assign nor_1_out = ~(multiplexer_4_out | DZ);  // NOR_Gate nor_1, 64 bits wide
  assign nand_1_out = ~(multiplexer_5_out & DZ);  // NAND_Gate nand_1, 64 bits wide
  Multiplexer #(.width(64)) multiplexer_6 (
    .in0(multiplexer_5_out), .in1(nand_1_out), .out(multiplexer_6_out), .sel(register_1_q[5]));
  assign or_1_out = multiplexer_6_out | DZ;  // OR_Gate or_1, 64 bits wide
  Multiplexer #(.width(64)) multiplexer_7 (
    .in0(multiplexer_6_out), .in1(or_1_out), .out(multiplexer_7_out), .sel(register_1_q[4]));
  assign and_1_out = multiplexer_7_out & DZ;  // AND_Gate and_1, 64 bits wide
  Multiplexer #(.width(64)) multiplexer_8 (
    .in0(multiplexer_7_out), .in1(and_1_out), .out(multiplexer_8_out), .sel(register_1_q[3]));
  Multiplexer #(.width(64)) multiplexer_9 (
    .in0(multiplexer_8_out), .in1(and_2_out), .out(multiplexer_9_out), .sel(register_1_q[2]));
  assign and_2_out = multiplexer_8_out & DZ;  // AND_Gate and_2, 64 bits wide
  Multiplexer #(.width(64)) multiplexer_10 (
    .in0(multiplexer_9_out), .in1(not_1_out), .out(multiplexer_10_out), .sel(register_1_q[1]));
  assign not_1_out = ~multiplexer_9_out;  // NOT_Gate not_1, 64 bits wide
  Register #(.width(64)) register_2 (.D(multiplexer_10_out), .en(1'b1), .clk(CLK), .Q(register_2_q));  // open: clr
  Multiplexer #(.width(64)) multiplexer_11 (
    .in0(multiplexer_10_out), .in1(register_2_q), .out(multiplexer_11_out), .sel(register_1_q[0]));
  Register #(.width(64)) X (.D(regX), .en(AE), .clk(CLK), .Q(AX));  // open: clr
  Register #(.width(64)) Y (.D(regY), .en(AE), .clk(CLK), .Q(AY));  // open: clr
  Register #(.width(64)) Z (.D(regZ), .en(AE), .clk(CLK), .Q(AZ));  // open: clr
  Register #(.trigger("high"), .width(64)) O (.D(multiplexer_11_out), .en(1'b1), .clk(WX_q), .Q(D));  // open: clr
  Register #(.width(1)) WX (.D(WE), .en(LE), .clk(CLK), .Q(WX_q));  // open: clr
endmodule
